// Logisim project 1DigitDecimalIn8421Adder.circ as structural Verilog: 1 circuit, main circuit 1DigitDecimalIn8421Adder
module _1DigitDecimalIn8421Adder (
  input  in_1,
  input  [3:0] in_2,
  input  [3:0] in_3,
  output [4:0] out_4
);

  wire nand_2_out, nand_3_out, not_1_out, \先行进位并行加法器_1_p1 , \先行进位并行加法器_1_p3 , \先行进位并行加法器_1_p4 ,
       \先行进位并行加法器_1_p6 , \先行进位并行加法器_2_p1 ;

  nand nand_1 (out_4[4], nand_2_out, nand_3_out, not_1_out);
  nand nand_2 (nand_2_out, \先行进位并行加法器_1_p4 , \先行进位并行加法器_1_p1 );
  nand nand_3 (nand_3_out, \先行进位并行加法器_1_p1 , \先行进位并行加法器_1_p3 );
  not not_1 (not_1_out, \先行进位并行加法器_2_p1 );
  // 先行进位并行加法器 先行进位并行加法器_1: pin names not known; wires that end beside it: \先行进位并行加法器_1_p1 , out_4[3], \先行进位并行加法器_1_p3 , \先行进位并行加法器_1_p4 , out_4[2], \先行进位并行加法器_1_p6 , 1'b0, out_4[1], out_4[4], out_4[4], out_4[0], 1'b0, 1'b0
  // 先行进位并行加法器 先行进位并行加法器_2: pin names not known; wires that end beside it: \先行进位并行加法器_2_p1 , in_2[3], \先行进位并行加法器_1_p1 , in_2[2], in_2[1], \先行进位并行加法器_1_p3 , in_2[0], in_3[3], \先行进位并行加法器_1_p4 , in_3[2], in_3[1], \先行进位并行加法器_1_p6 , in_3[0], in_1
endmodule
