// Logisim project 2DigitDecimalIn8421ToBinary.circ as structural Verilog: 1 circuit, main circuit 2DigitDecimalIn8421ToBinary
module _2DigitDecimalIn8421ToBinary (
  input  [7:0] in_1,
  output [7:0] out_2
);

  wire \先行进位并行加法器_1_p10 , \先行进位并行加法器_1_p11 , \先行进位并行加法器_2_p1 ;

  // 先行进位并行加法器 先行进位并行加法器_1: pin names not known; wires that end beside it: out_2[7], in_1[7], out_2[6], in_1[6], in_1[5], out_2[5], in_1[4], 1'b0, out_2[4], \先行进位并行加法器_1_p10 , \先行进位并行加法器_1_p11 , out_2[3], 1'b0
  // 先行进位并行加法器 先行进位并行加法器_2: pin names not known; wires that end beside it: \先行进位并行加法器_2_p1 , \先行进位并行加法器_1_p10 , in_1[7], \先行进位并行加法器_1_p11 , in_1[6], in_1[5], \先行进位并行加法器_2_p1 , in_1[4], 1'b0, out_2[2], in_1[3], in_1[2], out_2[1], in_1[1], 1'b0

  assign out_2[0] = in_1[0];
endmodule
