// Logisim project 实验1.circ as structural Verilog: 5 circuits, main circuit 一位二进制半加器
module \一位二进制半加器  (
  input  A,
  input  B,
  output S,
  output C
);

  xor xor_1 (S, A, B);
  and and_1 (C, A, B);

  // Notes on the sheet:
  //   一位二进制半加器
  //   逻辑表达式：
  //   S = A ^ B
  //   C = A & B
endmodule

module \一位二进制全加器  (
  input  A,
  input  B,
  input  Ci,
  output C,
  output S
);

  wire and_1_out, and_2_out, and_3_out, xor_1_out;

  xor xor_1 (xor_1_out, A, B);
  and and_1 (and_1_out, A, Ci);
  and and_2 (and_2_out, A, B);
  and and_3 (and_3_out, B, Ci);
  or or_1 (C, and_1_out, and_2_out, and_3_out);
  xor xor_2 (S, xor_1_out, Ci);

  // Notes on the sheet:
  //   逻辑表达式：
  //   一位二进制全加器
  //   C = AB + BCi + ACi
  //   S = A ^ B ^ Ci
endmodule

module \串行进位并行加法器  (
  input  A3,
  input  B3,
  input  A2,
  input  B2,
  input  A1,
  input  B1,
  input  A0,
  input  B0,
  input  C0,
  output C4,
  output S3,
  output S2,
  output S1,
  output S0
);

  wire \一位二进制全加器_2_c , \一位二进制全加器_3_c , \一位二进制全加器_4_c ;

  \一位二进制全加器  \u_一位二进制全加器_1  (.A(A3), .B(B3), .Ci(\一位二进制全加器_2_c ), .C(C4), .S(S3));
  \一位二进制全加器  \u_一位二进制全加器_2  (.A(A2), .B(B2), .Ci(\一位二进制全加器_3_c ), .C(\一位二进制全加器_2_c ), .S(S2));
  \一位二进制全加器  \u_一位二进制全加器_3  (.A(A1), .B(B1), .Ci(\一位二进制全加器_4_c ), .C(\一位二进制全加器_3_c ), .S(S1));
  \一位二进制全加器  \u_一位二进制全加器_4  (.A(A0), .B(B0), .Ci(C0), .C(\一位二进制全加器_4_c ), .S(S0));

  // Notes on the sheet:
  //   四位二进制
  //   串行进位并行加法器
  //   构成：由四个一位二进制全加器串行连接构成
  //   C3
  //   C2
  //   C1
endmodule

module \先行进位并行加法器  (
  input  A3,
  input  B3,
  input  A2,
  input  B2,
  input  A1,
  input  B1,
  input  A0,
  input  B0,
  input  C0,
  output C4,
  output S3,
  output S2,
  output S1,
  output S0
);

  wire and_1_out, and_2_out, and_3_out, and_4_out, and_5_out, and_6_out, and_7_out, and_8_out, and_9_out,
       and_10_out, or_2_out, or_3_out, or_4_out;
  wire [3:0] \一位二进制半加器_4_c , \一位二进制半加器_4_s ;

  \一位二进制半加器  \u_一位二进制半加器_1  (.A(A3), .B(B3), .S(\一位二进制半加器_4_s [3]), .C(\一位二进制半加器_4_c [3]));
  \一位二进制半加器  \u_一位二进制半加器_2  (.A(A2), .B(B2), .S(\一位二进制半加器_4_s [2]), .C(\一位二进制半加器_4_c [2]));
  \一位二进制半加器  \u_一位二进制半加器_3  (.A(A1), .B(B1), .S(\一位二进制半加器_4_s [1]), .C(\一位二进制半加器_4_c [1]));
  \一位二进制半加器  \u_一位二进制半加器_4  (.A(A0), .B(B0), .S(\一位二进制半加器_4_s [0]), .C(\一位二进制半加器_4_c [0]));
  and and_1 (and_1_out, \一位二进制半加器_4_c [1], \一位二进制半加器_4_s [2], \一位二进制半加器_4_s [3]);
  and and_2 (and_2_out, \一位二进制半加器_4_c [2], \一位二进制半加器_4_s [3]);
  and and_3 (and_3_out, \一位二进制半加器_4_s [1], \一位二进制半加器_4_s [2], \一位二进制半加器_4_c [0]);
  and and_4 (and_4_out, \一位二进制半加器_4_s [2], \一位二进制半加器_4_c [1]);
  and and_5 (and_5_out, C0, \一位二进制半加器_4_s [0], \一位二进制半加器_4_s [1]);
  and and_6 (and_6_out, \一位二进制半加器_4_s [1], \一位二进制半加器_4_c [0]);
  and and_7 (and_7_out, \一位二进制半加器_4_s [0], C0);
  and and_8 (and_8_out, C0, \一位二进制半加器_4_s [0], \一位二进制半加器_4_s [1], \一位二进制半加器_4_s [2], \一位二进制半加器_4_s [3]);
  and and_9 (and_9_out, \一位二进制半加器_4_s [1], \一位二进制半加器_4_s [2], \一位二进制半加器_4_s [3], \一位二进制半加器_4_c [0]);
  and and_10 (and_10_out, C0, \一位二进制半加器_4_s [0], \一位二进制半加器_4_s [1], \一位二进制半加器_4_s [2]);
  or or_1 (C4, and_8_out, and_9_out, and_1_out, and_2_out, \一位二进制半加器_4_c [3]);
  or or_2 (or_2_out, and_10_out, and_3_out, and_4_out, \一位二进制半加器_4_c [2]);
  or or_3 (or_3_out, and_5_out, and_6_out, \一位二进制半加器_4_c [1]);
  or or_4 (or_4_out, and_7_out, \一位二进制半加器_4_c [0]);
  xor xor_1 (S3, or_2_out, \一位二进制半加器_4_s [3]);
  xor xor_2 (S2, or_3_out, \一位二进制半加器_4_s [2]);
  xor xor_3 (S1, or_4_out, \一位二进制半加器_4_s [1]);
  xor xor_4 (S0, C0, \一位二进制半加器_4_s [0]);

  // Notes on the sheet:
  //   进位函数与一位二进制半加器相同
  //   这里选择直接调用
  //   四位二进制
  //   先行进位并行加法器
  //   P3
  //   G3
  //   P2
  //   G2
  //   P1
  //   G1
  //   P0
  //   G0
  //   逻辑表达式：
  //   C1 = C0 & P0 + G0
  //   Si = Ci ^ Pi
  //   P
  //   C2 = C0 & P1 & P0 + G0 & P1 + G1 
  //   G
  //   C3 = C0 & P2 & P1 & P0 + G0 & P2 & P1 + G1 & P2 + G2 
  //   C4 = C0 & P3 & P2 & P1 & P0 + G0 & P3 & P2 & P1 + G1 & P3 & P2 + G2 & P3 + G3
  //   C3
  //   C2
  //   C1
endmodule

module \先行进位并行加法器测试电路  (
  input  C0,
  input  [3:0] A,
  input  [3:0] B,
  output [4:0] S
);

  \先行进位并行加法器  \u_先行进位并行加法器_1  (
    .A3(A[3]), .B3(B[3]), .A2(A[2]), .B2(B[2]), .A1(A[1]), .B1(B[1]), .A0(A[0]), .B0(B[0]), .C4(S[4]),
    .S3(S[3]), .S2(S[2]), .S1(S[1]), .S0(S[0]), .C0(C0));

  // Notes on the sheet:
  //   四位二进制先行进位并行加法器测试电路
endmodule
