// Logisim project 实验2.circ as structural Verilog: 11 circuits, main circuit 小型实验室门禁系统
module \四位二进制可逆计数器  (
  input  CLR,
  input  CPu,
  input  CPd,
  input  nLD,
  input  A,
  input  B,
  input  C,
  input  D,
  output Qa,
  output Qb,
  output Qc,
  output Qd
);

  wire and_1_out, and_2_out, and_3_out, and_4_out, and_5_out, and_6_out, and_7_out, and_8_out, and_9_out,
       and_10_out, d_ff_1_qn, d_ff_2_qn, d_ff_3_qn, d_ff_4_qn, not_1_out, or_1_out, or_2_out, or_3_out,
       or_4_out;

  not not_1 (not_1_out, nLD);
  and and_1 (and_1_out, not_1_out, A);
  and and_2 (and_2_out, not_1_out, B);
  and and_3 (and_3_out, not_1_out, C);
  and and_4 (and_4_out, not_1_out, D);
  and and_5 (and_5_out, Qa, CPu);
  and and_6 (and_6_out, d_ff_1_qn, CPd);
  and and_7 (and_7_out, Qb, and_5_out);
  and and_8 (and_8_out, d_ff_2_qn, and_6_out);
  and and_9 (and_9_out, Qc, and_7_out);
  and and_10 (and_10_out, d_ff_3_qn, and_8_out);
  or or_1 (or_1_out, CPu, CPd);
  or or_2 (or_2_out, and_5_out, and_6_out);
  or or_3 (or_3_out, and_7_out, and_8_out);
  or or_4 (or_4_out, and_9_out, and_10_out);
  D_Flip_Flop #(.trigger("falling")) d_ff_1 (
    .clk(or_1_out), .D(d_ff_1_qn), .Q(Qa), .Qn(d_ff_1_qn), .preset(and_1_out), .en(1'b1), .reset(CLR));
  D_Flip_Flop #(.trigger("falling")) d_ff_2 (
    .clk(or_2_out), .D(d_ff_2_qn), .Q(Qb), .Qn(d_ff_2_qn), .preset(and_2_out), .en(1'b1), .reset(CLR));
  D_Flip_Flop #(.trigger("falling")) d_ff_3 (
    .clk(or_3_out), .D(d_ff_3_qn), .Q(Qc), .Qn(d_ff_3_qn), .preset(and_3_out), .en(1'b1), .reset(CLR));
  D_Flip_Flop #(.trigger("falling")) d_ff_4 (
    .clk(or_4_out), .D(d_ff_4_qn), .Q(Qd), .Qn(d_ff_4_qn), .preset(and_4_out), .en(1'b1), .reset(CLR));

  // Notes on the sheet:
  //   四位二进制可逆计数器
  //   预置控制：nLD
  //   预制位：DCBA
  //   清零：CLS
  //   减法计数：CPd
  //   加法计数：CPu
  //   输出：QdQcQbQa
  //   所有D触发器全部调整为下降沿，上升沿无法保证从零计数
  //   逻辑表达式：
  //   Di = ~ Qi
  //   C0 = CPd + CPu
  //   C2 = CPd & ~Qb & ~ Qa + CPu & Qb & Qa
  //   C1 = CPd & ~Qa + CPu & Qa
  //   C0
  //   D0
  //   C1
  //   D1
  //   C2
  //   D2
  //   C3
  //   D3
  //   C3 = CPd & ~Qc & ~Qb & ~Qa + CPu & Qc & Qb & Qa
endmodule

module \四位二进制可逆计数器测试电路  (
  input  [3:0] in_1,
  input  in_2
);

  wire button_1_out, button_2_out, button_3_out;
  wire [3:0] \四位二进制可逆计数器_1_qa ;

  Button button_1 (.out(button_1_out));
  Button button_2 (.out(button_2_out));
  Button button_3 (.out(button_3_out));
  // Probe on \四位二进制可逆计数器_1_qa 
  \四位二进制可逆计数器  \u_四位二进制可逆计数器_1  (
    .CPu(button_1_out), .CPd(button_3_out), .nLD(in_2), .A(in_1[0]), .B(in_1[1]), .C(in_1[2]), .D(in_1[3]),
    .Qa(\四位二进制可逆计数器_1_qa [0]), .Qb(\四位二进制可逆计数器_1_qa [1]), .Qc(\四位二进制可逆计数器_1_qa [2]),
    .Qd(\四位二进制可逆计数器_1_qa [3]), .CLR(button_2_out));
endmodule

module \二进制转8421码电路  (
  input  P3,
  input  P2,
  input  P1,
  input  P0,
  output C0,
  output Q3,
  output Q2,
  output Q1,
  output Q0,
  output C3,
  output C2,
  output C1
);

  wire and_1_out, or_1_out;

  \先行进位并行加法器  \u_先行进位并行加法器_1  (
    .A3(P3), .B3(1'b0), .A2(P2), .B2(and_1_out), .A1(P1), .B1(and_1_out), .A0(P0), .B0(1'b0), .C4(C0),
    .S3(Q3), .S2(Q2), .S1(Q1), .S0(Q0), .C0(1'b0));
  or or_1 (or_1_out, P1, P2);
  and and_1 (and_1_out, or_1_out, P3);

  assign C1 = 1'b0;
  assign C2 = 1'b0;
  assign C3 = 1'b0;

  // Notes on the sheet:
  //   输入：P3P2P1P0
  //   输出：C3C2C1C0Q3Q2Q1Q0
  //   K = P3 & (P2 + P1)
  //   仅当超过10时需要向C0进位，这时只需将原输入加6即可
  //   K
endmodule

module \二进制转8421码测试电路  (
  input  [3:0] in_1
);

  wire [3:0] \二进制转8421码电路_1_c0 , \二进制转8421码电路_1_q0 ;

  \二进制转8421码电路  \u_二进制转8421码电路_1  (
    .C0(\二进制转8421码电路_1_c0 [0]), .Q3(\二进制转8421码电路_1_q0 [3]), .Q2(\二进制转8421码电路_1_q0 [2]),
    .Q1(\二进制转8421码电路_1_q0 [1]), .Q0(\二进制转8421码电路_1_q0 [0]), .P3(in_1[3]), .P2(in_1[2]), .P1(in_1[1]),
    .P0(in_1[0]), .C1(\二进制转8421码电路_1_c0 [3]), .C2(\二进制转8421码电路_1_c0 [2]), .C3(\二进制转8421码电路_1_c0 [1]));
  // Probe on \二进制转8421码电路_1_c0 
  // Probe on \二进制转8421码电路_1_q0 
endmodule

module \显示电路  (
  input  A3,
  input  A2,
  input  A1,
  input  A0,
  output d,
  output a,
  output e,
  output b,
  output f,
  output c,
  output g
);

  wire or_1_out, or_2_out, or_3_out, or_4_out, or_5_out, or_6_out, or_7_out, or_8_out, or_9_out, or_10_out,
       or_11_out, or_12_out, or_13_out, or_14_out, or_15_out, or_16_out, or_17_out;

  or or_1 (or_1_out, ~A1, ~A3);  // OR_Gate
  or or_2 (or_2_out, A3, A2, A1, ~A0);  // OR_Gate
  or or_3 (or_3_out, A0, ~A2);  // OR_Gate
  or or_4 (or_4_out, ~A3, ~A1);  // OR_Gate
  or or_5 (or_5_out, ~A2, ~A1, A0);  // OR_Gate
  or or_6 (or_6_out, ~A2, ~A0, A1);  // OR_Gate
  or or_7 (or_7_out, ~A3, ~A2);  // OR_Gate
  or or_8 (or_8_out, A2, ~A1, A0);  // OR_Gate
  and and_1 (a, or_1_out, or_2_out, or_3_out);
  and and_2 (b, or_4_out, or_5_out, or_6_out);
  and and_3 (c, or_7_out, or_8_out);
  or or_9 (or_9_out, A2, A1, ~A0);  // OR_Gate
  or or_10 (or_10_out, ~A2, A1, A0);  // OR_Gate
  or or_11 (or_11_out, ~A0, ~A1, ~A2);  // OR_Gate
  or or_12 (or_12_out, ~A2, A1);  // OR_Gate
  or or_13 (or_13_out, A3, A2, ~A0);  // OR_Gate
  or or_14 (or_14_out, A2, ~A1);  // OR_Gate
  or or_15 (or_15_out, ~A1, ~A0);  // OR_Gate
  or or_16 (or_16_out, A3, A2, A1);
  or or_17 (or_17_out, ~A1, ~A2, ~A0);  // OR_Gate
  and and_4 (d, or_9_out, or_10_out, or_11_out);
  and and_5 (e, or_12_out, ~A0);  // AND_Gate
  and and_6 (f, or_13_out, or_14_out, or_15_out);
  and and_7 (g, or_16_out, or_17_out);
endmodule

module \显示电路测试电路  (
  input  [3:0] in_1
);

  wire \显示电路_1_a , \显示电路_1_b , \显示电路_1_c , \显示电路_1_d , \显示电路_1_e , \显示电路_1_f , \显示电路_1_g ;

  \显示电路  \u_显示电路_1  (
    .A3(in_1[3]), .A2(in_1[2]), .A1(in_1[1]), .A0(in_1[0]), .a(\显示电路_1_a ), .b(\显示电路_1_b ), .c(\显示电路_1_c ),
    .d(\显示电路_1_d ), .e(\显示电路_1_e ), .f(\显示电路_1_f ), .g(\显示电路_1_g ));
  _7_Segment_Display u_7_segment_display_1 (
    .g(\显示电路_1_g ), .f(\显示电路_1_f ), .a(\显示电路_1_a ), .b(\显示电路_1_b ), .e(\显示电路_1_e ), .d(\显示电路_1_d ),
    .c(\显示电路_1_c ), .dp(1'b0));
endmodule

module \报警电路  (
  input  CPu,
  input  CLR,
  input  CPd,
  output out_4,
  output out_5,
  output out_6,
  output out_7,
  output Warning
);

  wire and_2_out, and_3_out, not_1_out, \人满F_out , \无人E_out ;

  and and_1 (Warning, \人满F_out , CPu);
  not not_1 (not_1_out, \人满F_out );
  and \u_人满F  (\人满F_out , out_4, out_5, out_6, out_7);
  or \u_无人E  (\无人E_out , out_4, out_5, out_6, out_7);
  and and_2 (and_2_out, not_1_out, CPu);
  and and_3 (and_3_out, \无人E_out , CPd);
  \四位二进制可逆计数器  \u_四位二进制可逆计数器_1  (
    .CPu(and_2_out), .CPd(and_3_out), .nLD(1'b1), .A(1'b0), .B(1'b0), .C(1'b0), .D(1'b0), .Qa(out_7),
    .Qb(out_6), .Qc(out_5), .Qd(out_4), .CLR(CLR));

  // Notes on the sheet:
  //   人满F = Qd & Qc & Qb & Qa
  //   无人E = Qd + Qc + Qb + Qa
  //   Warning = CPu & F
  //   无预置
endmodule

module \小型实验室门禁系统  (
  input  CPu,
  input  CLS,
  input  CPd,
  output a,
  output b,
  output c,
  output d,
  output e,
  output f,
  output g,
  output a_2,
  output b_2,
  output c_2,
  output d_2,
  output e_2,
  output f_2,
  output g_2,
  output Warning
);

  wire \二进制转8421码电路_1_c0 , \二进制转8421码电路_1_c1 , \二进制转8421码电路_1_c2 , \二进制转8421码电路_1_c3 , \二进制转8421码电路_1_q0 ,
       \二进制转8421码电路_1_q1 , \二进制转8421码电路_1_q2 , \二进制转8421码电路_1_q3 , \报警电路_1_out_4 , \报警电路_1_out_5 ,
       \报警电路_1_out_6 , \报警电路_1_out_7 ;

  \显示电路  \u_显示电路_1  (
    .A3(\二进制转8421码电路_1_c1 ), .A2(\二进制转8421码电路_1_c2 ), .A1(\二进制转8421码电路_1_c3 ), .A0(\二进制转8421码电路_1_c0 ),
    .a(a_2), .b(b_2), .c(c_2), .d(d_2), .e(e_2), .f(f_2), .g(g_2));
  \二进制转8421码电路  \u_二进制转8421码电路_1  (
    .C0(\二进制转8421码电路_1_c0 ), .Q3(\二进制转8421码电路_1_q3 ), .Q2(\二进制转8421码电路_1_q2 ), .Q1(\二进制转8421码电路_1_q1 ),
    .Q0(\二进制转8421码电路_1_q0 ), .P3(\报警电路_1_out_4 ), .P2(\报警电路_1_out_5 ), .P1(\报警电路_1_out_6 ),
    .P0(\报警电路_1_out_7 ), .C1(\二进制转8421码电路_1_c1 ), .C2(\二进制转8421码电路_1_c2 ), .C3(\二进制转8421码电路_1_c3 ));
  \报警电路  \u_报警电路_1  (
    .Warning(Warning), .CPu(CPu), .CLR(CLS), .CPd(CPd), .out_4(\报警电路_1_out_4 ), .out_5(\报警电路_1_out_5 ),
    .out_6(\报警电路_1_out_6 ), .out_7(\报警电路_1_out_7 ));
  \显示电路  \u_显示电路_2  (
    .A3(\二进制转8421码电路_1_q3 ), .A2(\二进制转8421码电路_1_q2 ), .A1(\二进制转8421码电路_1_q1 ), .A0(\二进制转8421码电路_1_q0 ),
    .a(a), .b(b), .c(c), .d(d), .e(e), .f(f), .g(g));

  // Notes on the sheet:
  //   十位
  //   个位
endmodule

module \小型门禁系统测试电路  (
);

  wire button_1_out, button_2_out, button_3_out, \小型实验室门禁系统_1_a , \小型实验室门禁系统_1_a_2 , \小型实验室门禁系统_1_b ,
       \小型实验室门禁系统_1_b_2 , \小型实验室门禁系统_1_c , \小型实验室门禁系统_1_c_2 , \小型实验室门禁系统_1_d , \小型实验室门禁系统_1_d_2 ,
       \小型实验室门禁系统_1_e , \小型实验室门禁系统_1_e_2 , \小型实验室门禁系统_1_f , \小型实验室门禁系统_1_f_2 , \小型实验室门禁系统_1_g ,
       \小型实验室门禁系统_1_g_2 , \小型实验室门禁系统_1_warning ;

  Button button_1 (.out(button_1_out));
  Button button_2 (.out(button_2_out));
  Button button_3 (.out(button_3_out));
  _7_Segment_Display u_7_segment_display_1 (
    .g(\小型实验室门禁系统_1_g_2 ), .f(\小型实验室门禁系统_1_f_2 ), .a(\小型实验室门禁系统_1_a_2 ), .b(\小型实验室门禁系统_1_b_2 ),
    .e(\小型实验室门禁系统_1_e_2 ), .d(\小型实验室门禁系统_1_d_2 ), .c(\小型实验室门禁系统_1_c_2 ), .dp(1'b0));
  _7_Segment_Display u_7_segment_display_2 (
    .g(\小型实验室门禁系统_1_g ), .f(\小型实验室门禁系统_1_f ), .a(\小型实验室门禁系统_1_a ), .b(\小型实验室门禁系统_1_b ), .e(\小型实验室门禁系统_1_e ),
    .d(\小型实验室门禁系统_1_d ), .c(\小型实验室门禁系统_1_c ), .dp(1'b0));
  LED led_1 (.in(\小型实验室门禁系统_1_warning ));
  \小型实验室门禁系统  \u_小型实验室门禁系统_1  (
    .CPu(button_1_out), .CLS(button_2_out), .CPd(button_3_out), .Warning(\小型实验室门禁系统_1_warning ),
    .a_2(\小型实验室门禁系统_1_a_2 ), .b_2(\小型实验室门禁系统_1_b_2 ), .c_2(\小型实验室门禁系统_1_c_2 ), .d_2(\小型实验室门禁系统_1_d_2 ),
    .e_2(\小型实验室门禁系统_1_e_2 ), .f_2(\小型实验室门禁系统_1_f_2 ), .g_2(\小型实验室门禁系统_1_g_2 ), .a(\小型实验室门禁系统_1_a ),
    .b(\小型实验室门禁系统_1_b ), .c(\小型实验室门禁系统_1_c ), .d(\小型实验室门禁系统_1_d ), .e(\小型实验室门禁系统_1_e ), .f(\小型实验室门禁系统_1_f ),
    .g(\小型实验室门禁系统_1_g ));
endmodule

module \一位二进制半加器  (
  input  A,
  input  B,
  output S,
  output C
);

  xor xor_1 (S, A, B);
  and and_1 (C, A, B);

  // Notes on the sheet:
  //   一位二进制半加器
  //   逻辑表达式：
  //   S = A ^ B
  //   C = A & B
endmodule

module \先行进位并行加法器  (
  input  A3,
  input  B3,
  input  A2,
  input  B2,
  input  A1,
  input  B1,
  input  A0,
  input  B0,
  input  C0,
  output C4,
  output S3,
  output S2,
  output S1,
  output S0
);

  wire and_1_out, and_2_out, and_3_out, and_4_out, and_5_out, and_6_out, and_7_out, and_8_out, and_9_out,
       and_10_out, or_2_out, or_3_out, or_4_out;
  wire [3:0] \一位二进制半加器_4_c , \一位二进制半加器_4_s ;

  \一位二进制半加器  \u_一位二进制半加器_1  (.A(A3), .B(B3), .S(\一位二进制半加器_4_s [3]), .C(\一位二进制半加器_4_c [3]));
  \一位二进制半加器  \u_一位二进制半加器_2  (.A(A2), .B(B2), .S(\一位二进制半加器_4_s [2]), .C(\一位二进制半加器_4_c [2]));
  \一位二进制半加器  \u_一位二进制半加器_3  (.A(A1), .B(B1), .S(\一位二进制半加器_4_s [1]), .C(\一位二进制半加器_4_c [1]));
  \一位二进制半加器  \u_一位二进制半加器_4  (.A(A0), .B(B0), .S(\一位二进制半加器_4_s [0]), .C(\一位二进制半加器_4_c [0]));
  and and_1 (and_1_out, \一位二进制半加器_4_c [1], \一位二进制半加器_4_s [2], \一位二进制半加器_4_s [3]);
  and and_2 (and_2_out, \一位二进制半加器_4_c [2], \一位二进制半加器_4_s [3]);
  and and_3 (and_3_out, \一位二进制半加器_4_s [1], \一位二进制半加器_4_s [2], \一位二进制半加器_4_c [0]);
  and and_4 (and_4_out, \一位二进制半加器_4_s [2], \一位二进制半加器_4_c [1]);
  and and_5 (and_5_out, C0, \一位二进制半加器_4_s [0], \一位二进制半加器_4_s [1]);
  and and_6 (and_6_out, \一位二进制半加器_4_s [1], \一位二进制半加器_4_c [0]);
  and and_7 (and_7_out, \一位二进制半加器_4_s [0], C0);
  and and_8 (and_8_out, C0, \一位二进制半加器_4_s [0], \一位二进制半加器_4_s [1], \一位二进制半加器_4_s [2], \一位二进制半加器_4_s [3]);
  and and_9 (and_9_out, \一位二进制半加器_4_s [1], \一位二进制半加器_4_s [2], \一位二进制半加器_4_s [3], \一位二进制半加器_4_c [0]);
  and and_10 (and_10_out, C0, \一位二进制半加器_4_s [0], \一位二进制半加器_4_s [1], \一位二进制半加器_4_s [2]);
  or or_1 (C4, and_8_out, and_9_out, and_1_out, and_2_out, \一位二进制半加器_4_c [3]);
  or or_2 (or_2_out, and_10_out, and_3_out, and_4_out, \一位二进制半加器_4_c [2]);
  or or_3 (or_3_out, and_5_out, and_6_out, \一位二进制半加器_4_c [1]);
  or or_4 (or_4_out, and_7_out, \一位二进制半加器_4_c [0]);
  xor xor_1 (S3, or_2_out, \一位二进制半加器_4_s [3]);
  xor xor_2 (S2, or_3_out, \一位二进制半加器_4_s [2]);
  xor xor_3 (S1, or_4_out, \一位二进制半加器_4_s [1]);
  xor xor_4 (S0, C0, \一位二进制半加器_4_s [0]);

  // Notes on the sheet:
  //   进位函数与一位二进制半加器相同
  //   这里选择直接调用
  //   四位二进制
  //   先行进位并行加法器
  //   P3
  //   G3
  //   P2
  //   G2
  //   P1
  //   G1
  //   P0
  //   G0
  //   逻辑表达式：
  //   C1 = C0 & P0 + G0
  //   Si = Ci ^ Pi
  //   P
  //   C2 = C0 & P1 & P0 + G0 & P1 + G1 
  //   G
  //   C3 = C0 & P2 & P1 & P0 + G0 & P2 & P1 + G1 & P2 + G2 
  //   C4 = C0 & P3 & P2 & P1 & P0 + G0 & P3 & P2 & P1 + G1 & P3 & P2 + G2 & P3 + G3
  //   C3
  //   C2
  //   C1
endmodule
