// Logisim project 实验3.circ as structural Verilog: 6 circuits, main circuit 四位乘法器
module \四位乘法器  (
  input  [3:0] A,
  input  [3:0] B,
  output [7:0] out_3
);

  wire [7:0] adder_1_out, adder_2_out, adder_3_out, adder_4_out, multiplexer_1_out, multiplexer_2_out,
       multiplexer_3_out, shifter_1_out, shifter_2_out, shifter_3_out;

  Adder adder_1 (.a({8{1'b0}}), .b({4'b0000, B}), .out(adder_1_out), .cin(1'b0));  // open: cout
  Shifter shifter_1 (.in({4'b0000, B}), .\dist (3'b001), .out(shifter_1_out));
  Multiplexer #(.width(8), .enable("false")) multiplexer_1 (
    .in0({8{1'b0}}), .in1(adder_1_out), .out(multiplexer_1_out), .sel(A[0]));
  Adder adder_2 (.a(multiplexer_1_out), .b(shifter_1_out), .out(adder_2_out), .cin(1'b0));  // open: cout
  Shifter shifter_2 (.in(shifter_1_out), .\dist (3'b001), .out(shifter_2_out));
  Multiplexer #(.width(8), .enable("false")) multiplexer_2 (
    .in0(multiplexer_1_out), .in1(adder_2_out), .out(multiplexer_2_out), .sel(A[1]));
  Adder adder_3 (.a(multiplexer_2_out), .b(shifter_2_out), .out(adder_3_out), .cin(1'b0));  // open: cout
  Shifter shifter_3 (.in(shifter_2_out), .\dist (3'b001), .out(shifter_3_out));
  Multiplexer #(.width(8), .enable("false")) multiplexer_3 (
    .in0(multiplexer_2_out), .in1(adder_3_out), .out(multiplexer_3_out), .sel(A[2]));
  Adder adder_4 (.a(multiplexer_3_out), .b(shifter_3_out), .out(adder_4_out), .cin(1'b0));  // open: cout
  Multiplexer #(.width(8), .enable("false")) multiplexer_4 (
    .in0(multiplexer_3_out), .in1(adder_4_out), .out(out_3), .sel(A[3]));

  // Notes on the sheet:
  //   P
endmodule

module \四位乘法器测试电路  (
  input  [3:0] in_1,
  input  [3:0] in_2
);

  wire [7:0] \四位乘法器_1_out_3 ;

  // Probe on in_1
  // Probe on in_2
  \四位乘法器  \u_四位乘法器_1  (.A(in_1), .B(in_2), .out_3(\四位乘法器_1_out_3 ));
  // Probe on \四位乘法器_1_out_3 
endmodule

module \_32X4乘法器  (
  input  [3:0] A,
  input  [31:0] in_2,
  output [31:0] out_3,
  output [31:0] out_4
);

  wire adder_5_cout;
  wire [7:0] \四位乘法器_1_out_3 ;
  wire [31:0] adder_1_out, adder_2_out, adder_3_out, adder_4_out, multiplexer_1_out, multiplexer_2_out,
       multiplexer_3_out, shifter_1_out, shifter_2_out, shifter_3_out;
  wire [31:28] multiplexer_4_out;

  Adder #(.width(32)) adder_1 (.a({32{1'b0}}), .b({4'b0000, in_2[27:0]}), .out(adder_1_out), .cin(1'b0));  // open: cout
  Shifter #(.width(32)) shifter_1 (.in({4'b0000, in_2[27:0]}), .\dist (5'b00001), .out(shifter_1_out));
  Multiplexer #(.width(32), .enable("false")) multiplexer_1 (
    .in0({32{1'b0}}), .in1(adder_1_out), .out(multiplexer_1_out), .sel(A[0]));
  Adder #(.width(32)) adder_2 (.a(multiplexer_1_out), .b(shifter_1_out), .out(adder_2_out), .cin(1'b0));  // open: cout
  Shifter #(.width(32)) shifter_2 (.in(shifter_1_out), .\dist (5'b00001), .out(shifter_2_out));
  Multiplexer #(.width(32), .enable("false")) multiplexer_2 (
    .in0(multiplexer_1_out), .in1(adder_2_out), .out(multiplexer_2_out), .sel(A[1]));
  Adder #(.width(32)) adder_3 (.a(multiplexer_2_out), .b(shifter_2_out), .out(adder_3_out), .cin(1'b0));  // open: cout
  Shifter #(.width(32)) shifter_3 (.in(shifter_2_out), .\dist (5'b00001), .out(shifter_3_out));
  Multiplexer #(.width(32), .enable("false")) multiplexer_3 (
    .in0(multiplexer_2_out), .in1(adder_3_out), .out(multiplexer_3_out), .sel(A[2]));
  Adder #(.width(32)) adder_4 (.a(multiplexer_3_out), .b(shifter_3_out), .out(adder_4_out), .cin(1'b0));  // open: cout
  \四位乘法器  \u_四位乘法器_1  (.A(A), .B(in_2[31:28]), .out_3(\四位乘法器_1_out_3 ));
  Multiplexer #(.width(32), .enable("false")) multiplexer_4 (
    .in0(multiplexer_3_out), .in1(adder_4_out), .out({multiplexer_4_out, out_3[27:0]}), .sel(A[3]));
  Adder #(.width(4)) adder_5 (
    .a(multiplexer_4_out), .b(\四位乘法器_1_out_3 [3:0]), .out(out_3[31:28]), .cin(1'b0), .cout(adder_5_cout));
  Adder #(.width(4)) adder_6 (
    .a(4'b0000), .b(\四位乘法器_1_out_3 [7:4]), .out(out_4[3:0]), .cin(adder_5_cout), .cout(out_4[4]));

  assign out_4[31:5] = {27{1'b0}};

  // Notes on the sheet:
  //   B
  //   设计思想
  //   高4位参与4X4的乘法运算
  //   低28位参与28X4的乘法运算，数据通路为32
  //   28X4的结果的低28位为32X4的结果的低28位
  //   28X4的结果的高4位与4X4的结果的低4位的和为32X4的结果的28-31位
  //   4X4的结果的高4位为32X4的结果的高4位
  //   P
  //   Q
endmodule

module \_32X4乘法器测试电路  (
  input  [3:0] in_1,
  input  [31:0] in_2
);

  wire [31:0] \n32x4乘法器_1_out_3 , \n32x4乘法器_1_out_4 ;

  // Probe on in_1
  \_32X4乘法器  \u_32x4乘法器_1  (.A(in_1), .in_2(in_2), .out_3(\n32x4乘法器_1_out_3 ), .out_4(\n32x4乘法器_1_out_4 ));
  // Probe on in_2
  // Probe on \n32x4乘法器_1_out_3 
  // Probe on \n32x4乘法器_1_out_3 
  // Probe on \n32x4乘法器_1_out_4 
  // Probe on \n32x4乘法器_1_out_4 
endmodule

module \_32X32乘法器  (
  input  [31:0] in_1,
  input  [31:0] in_2,
  output [31:0] out_3,
  output [31:0] out_4
);

  wire C0, C1, C2, C3, C4, C5, C6;
  wire [31:0] adder_1_out, adder_2_out, adder_3_out, adder_4_out, adder_5_out, adder_6_out, adder_7_out,
       adder_8_out, adder_9_out, adder_10_out, adder_11_out, adder_12_out, P0, Q0, Q1, Q2, Q3, Q4, Q5, Q6, Q7;
  wire [31:4] \n32x4乘法器_1_out_4 , P1;
  wire [31:8] \n32x4乘法器_2_out_4 , P2;
  wire [31:12] \n32x4乘法器_3_out_4 , P3;
  wire [31:16] \n32x4乘法器_4_out_4 , P4;
  wire [31:20] \n32x4乘法器_5_out_4 , P5;
  wire [31:24] \n32x4乘法器_6_out_4 , P6;
  wire [31:28] \n32x4乘法器_7_out_4 , P7;

  \_32X4乘法器  \u_32x4乘法器_1  (
    .A(in_1[31:28]), .in_2(in_2), .out_3({Q7[27:0], P7}), .out_4({\n32x4乘法器_1_out_4 , Q7[31:28]}));
  \_32X4乘法器  \u_32x4乘法器_2  (
    .A(in_1[27:24]), .in_2(in_2), .out_3({Q6[23:0], P6}), .out_4({\n32x4乘法器_2_out_4 , Q6[31:24]}));
  \_32X4乘法器  \u_32x4乘法器_3  (
    .A(in_1[23:20]), .in_2(in_2), .out_3({Q5[19:0], P5}), .out_4({\n32x4乘法器_3_out_4 , Q5[31:20]}));
  \_32X4乘法器  \u_32x4乘法器_4  (
    .A(in_1[19:16]), .in_2(in_2), .out_3({Q4[15:0], P4}), .out_4({\n32x4乘法器_4_out_4 , Q4[31:16]}));
  \_32X4乘法器  \u_32x4乘法器_5  (
    .A(in_1[15:12]), .in_2(in_2), .out_3({Q3[11:0], P3}), .out_4({\n32x4乘法器_5_out_4 , Q3[31:12]}));
  \_32X4乘法器  \u_32x4乘法器_6  (.A(in_1[11:8]), .in_2(in_2), .out_3({Q2[7:0], P2}), .out_4({\n32x4乘法器_6_out_4 , Q2[31:8]}));
  \_32X4乘法器  \u_32x4乘法器_7  (.A(in_1[7:4]), .in_2(in_2), .out_3({Q1[3:0], P1}), .out_4({\n32x4乘法器_7_out_4 , Q1[31:4]}));
  \_32X4乘法器  \u_32x4乘法器_8  (.A(in_1[3:0]), .in_2(in_2), .out_3(P0), .out_4(Q0));
  Adder #(.width(32)) adder_1 (.a({P7, {28{1'b0}}}), .b({P6, {24{1'b0}}}), .out(adder_1_out), .cin(1'b0), .cout(C3));
  Adder #(.width(32)) adder_2 (.a({P5, {20{1'b0}}}), .b({P4, {16{1'b0}}}), .out(adder_2_out), .cin(1'b0), .cout(C2));
  Adder #(.width(32)) adder_3 (.a({P3, {12{1'b0}}}), .b({P2, {8{1'b0}}}), .out(adder_3_out), .cin(1'b0), .cout(C1));
  Adder #(.width(32)) adder_4 (.a({P1, 4'b0000}), .b(P0), .out(adder_4_out), .cin(1'b0), .cout(C0));
  Adder #(.width(32)) adder_5 (.a(Q7), .b(Q6), .out(adder_5_out), .cin(C3));  // open: cout
  Adder #(.width(32)) adder_6 (.a(Q5), .b(Q4), .out(adder_6_out), .cin(C2));  // open: cout
  Adder #(.width(32)) adder_7 (.a(Q3), .b(Q2), .out(adder_7_out), .cin(C1));  // open: cout
  Adder #(.width(32)) adder_8 (.a(Q1), .b(Q0), .out(adder_8_out), .cin(C0));  // open: cout
  Adder #(.width(32)) adder_9 (.a(adder_1_out), .b(adder_2_out), .out(adder_9_out), .cin(1'b0), .cout(C4));
  Adder #(.width(32)) adder_10 (.a(adder_3_out), .b(adder_4_out), .out(adder_10_out), .cin(1'b0), .cout(C5));
  Adder #(.width(32)) adder_11 (.a(adder_5_out), .b(adder_6_out), .out(adder_11_out), .cin(C4));  // open: cout
  Adder #(.width(32)) adder_12 (.a(adder_7_out), .b(adder_8_out), .out(adder_12_out), .cin(C5));  // open: cout
  Adder #(.width(32)) adder_13 (.a(adder_9_out), .b(adder_10_out), .out(out_3), .cin(1'b0), .cout(C6));
  Adder #(.width(32)) adder_14 (.a(adder_11_out), .b(adder_12_out), .out(out_4), .cin(C6));  // open: cout

  // Notes on the sheet:
  //   A
  //   B
  //   P
  //   Q
endmodule

module \_32X32乘法器测试电路  (
  input  [31:0] in_1,
  input  [31:0] in_2
);

  wire [31:0] \n32x32乘法器_1_out_3 , \n32x32乘法器_1_out_4 ;

  // Probe on in_1
  \_32X32乘法器  \u_32x32乘法器_1  (.in_1(in_1), .in_2(in_2), .out_3(\n32x32乘法器_1_out_3 ), .out_4(\n32x32乘法器_1_out_4 ));
  // Probe on in_2
  // Probe on \n32x32乘法器_1_out_3 
  // Probe on \n32x32乘法器_1_out_3 
  // Probe on \n32x32乘法器_1_out_4 
  // Probe on \n32x32乘法器_1_out_4 
endmodule
