// Logisim project 实验4.circ as structural Verilog: 5 circuits, main circuit 四位除法器
module \四位除法器  (
  input  [3:0] d,
  input  [3:0] n,
  output [3:0] r,
  output [3:0] q
);

  wire comparator_1_gt, comparator_2_gt, comparator_3_gt, comparator_4_gt, comparator_5_eq, not_1_out,
       not_2_out, not_3_out, not_4_out;
  wire [3:0] multiplexer_1_out, multiplexer_2_out, multiplexer_3_out, multiplexer_4_out, multiplexer_6_out,
       multiplexer_7_out, multiplexer_8_out, subtractor_1_out, subtractor_2_out, subtractor_3_out,
       subtractor_4_out;
  wire [7:0] shifter_1_out, shifter_2_out, shifter_3_out, shifter_4_out;
  wire [7:4] multiplexer_5_out;

  Shifter shifter_1 (.in({4'b0000, n}), .\dist (3'b001), .out(shifter_1_out));
  not not_1 (not_1_out, comparator_1_gt);
  Comparator #(.width(4), .mode("unsigned")) comparator_1 (
    .a(d), .b(shifter_1_out[7:4]), .gt(comparator_1_gt));  // open: eq, lt
  Subtractor #(.width(4)) subtractor_1 (
    .a(shifter_1_out[7:4]), .b(d), .out(subtractor_1_out), .bin(1'b0));  // open: bout
  Multiplexer #(.width(4), .enable("false")) multiplexer_1 (
    .in0(shifter_1_out[7:4]), .in1(subtractor_1_out), .out(multiplexer_1_out), .sel(not_1_out));
  Multiplexer #(.width(4), .enable("false")) multiplexer_2 (
    .in0(shifter_1_out[3:0]), .in1({shifter_1_out[3:1], 1'b1}), .out(multiplexer_2_out), .sel(not_1_out));
  Shifter shifter_2 (.in({multiplexer_1_out, multiplexer_2_out}), .\dist (3'b001), .out(shifter_2_out));
  Comparator #(.width(4), .mode("unsigned")) comparator_2 (
    .a(d), .b(shifter_2_out[7:4]), .gt(comparator_2_gt));  // open: eq, lt
  Subtractor #(.width(4)) subtractor_2 (
    .a(shifter_2_out[7:4]), .b(d), .out(subtractor_2_out), .bin(1'b0));  // open: bout
  not not_2 (not_2_out, comparator_2_gt);
  Multiplexer #(.width(4), .enable("false")) multiplexer_3 (
    .in0(shifter_2_out[7:4]), .in1(subtractor_2_out), .out(multiplexer_3_out), .sel(not_2_out));
  Multiplexer #(.width(4), .enable("false")) multiplexer_4 (
    .in0(shifter_2_out[3:0]), .in1({shifter_2_out[3:1], 1'b1}), .out(multiplexer_4_out), .sel(not_2_out));
  Shifter shifter_3 (.in({multiplexer_3_out, multiplexer_4_out}), .\dist (3'b001), .out(shifter_3_out));
  not not_3 (not_3_out, comparator_3_gt);
  Comparator #(.width(4), .mode("unsigned")) comparator_3 (
    .a(d), .b(shifter_3_out[7:4]), .gt(comparator_3_gt));  // open: eq, lt
  Subtractor #(.width(4)) subtractor_3 (
    .a(shifter_3_out[7:4]), .b(d), .out(subtractor_3_out), .bin(1'b0));  // open: bout
  Multiplexer #(.width(4), .enable("false")) multiplexer_5 (
    .in0(shifter_3_out[7:4]), .in1(subtractor_3_out), .out(multiplexer_5_out), .sel(not_3_out));
  Multiplexer #(.width(4), .enable("false")) multiplexer_6 (
    .in0(shifter_3_out[3:0]), .in1({shifter_3_out[3:1], 1'b1}), .out(multiplexer_6_out), .sel(not_3_out));
  Shifter shifter_4 (.in({multiplexer_5_out, multiplexer_6_out}), .\dist (3'b001), .out(shifter_4_out));
  Comparator #(.width(4), .mode("unsigned")) comparator_4 (
    .a(d), .b(shifter_4_out[7:4]), .gt(comparator_4_gt));  // open: eq, lt
  Subtractor #(.width(4)) subtractor_4 (
    .a(shifter_4_out[7:4]), .b(d), .out(subtractor_4_out), .bin(1'b0));  // open: bout
  not not_4 (not_4_out, comparator_4_gt);
  Multiplexer #(.width(4), .enable("false")) multiplexer_7 (
    .in0(shifter_4_out[7:4]), .in1(subtractor_4_out), .out(multiplexer_7_out), .sel(not_4_out));
  Multiplexer #(.width(4), .enable("false")) multiplexer_8 (
    .in0(shifter_4_out[3:0]), .in1({shifter_4_out[3:1], 1'b1}), .out(multiplexer_8_out), .sel(not_4_out));
  Comparator #(.width(4), .mode("unsigned")) comparator_5 (.a(d), .b(4'b0000), .eq(comparator_5_eq));  // open: gt, lt
  Multiplexer #(.width(4), .enable("false")) multiplexer_9 (
    .in0(multiplexer_7_out), .in1(d), .out(r), .sel(comparator_5_eq));
  Multiplexer #(.width(4), .enable("false")) multiplexer_10 (
    .in0(multiplexer_8_out), .in1(d), .out(q), .sel(comparator_5_eq));
endmodule

module \四位除法器测试电路  (
  input  [3:0] \除数d ,
  input  [3:0] \被除数n 
);

  wire [3:0] \四位除法器_1_q , \四位除法器_1_r ;

  // Probe on \除数d 
  // Probe on \被除数n 
  // Probe on \四位除法器_1_r 
  \四位除法器  \u_四位除法器_1  (.d(\除数d ), .n(\被除数n ), .r(\四位除法器_1_r ), .q(\四位除法器_1_q ));
  // Probe on \四位除法器_1_q 
endmodule

module \_32位除法器  (
  input  [31:0] d,
  input  [31:0] n,
  output [31:0] r,
  output [31:0] q
);

  wire comparator_1_eq;
  wire [31:0] \n32位一次除法器_1_qn , \n32位一次除法器_1_rn , \n32位一次除法器_2_qn , \n32位一次除法器_2_rn , \n32位一次除法器_3_qn ,
       \n32位一次除法器_3_rn , \n32位一次除法器_4_qn , \n32位一次除法器_4_rn , \n32位一次除法器_5_qn , \n32位一次除法器_5_rn ,
       \n32位一次除法器_6_qn , \n32位一次除法器_6_rn , \n32位一次除法器_7_qn , \n32位一次除法器_7_rn , \n32位一次除法器_8_qn ,
       \n32位一次除法器_8_rn , \n32位一次除法器_9_qn , \n32位一次除法器_9_rn , \n32位一次除法器_10_qn , \n32位一次除法器_10_rn ,
       \n32位一次除法器_11_qn , \n32位一次除法器_11_rn , \n32位一次除法器_12_qn , \n32位一次除法器_12_rn , \n32位一次除法器_13_qn ,
       \n32位一次除法器_13_rn , \n32位一次除法器_14_qn , \n32位一次除法器_14_rn , \n32位一次除法器_15_qn , \n32位一次除法器_15_rn ,
       \n32位一次除法器_16_qn , \n32位一次除法器_16_rn , \n32位一次除法器_17_qn , \n32位一次除法器_17_rn , \n32位一次除法器_20_qn ,
       \n32位一次除法器_20_rn , \n32位一次除法器_22_qn , \n32位一次除法器_22_rn , \n32位一次除法器_23_qn , \n32位一次除法器_23_rn ,
       \n32位一次除法器_25_qn , \n32位一次除法器_25_rn , \n32位一次除法器_27_qn , \n32位一次除法器_27_rn , \n32位一次除法器_30_qn ,
       \n32位一次除法器_30_rn , \n32位一次除法器_31_qn , \n32位一次除法器_31_rn , q0, q1, q2, q3, q4, q5, q6, q7, r0, r1, r2,
       r3, r4, r5, r6, r7;

  // Probe on d
  // Probe on n
  \_32位一次除法器  \u_32位一次除法器_1  (.d(d), .r({32{1'b0}}), .q(n), .rn(\n32位一次除法器_1_rn ), .qn(\n32位一次除法器_1_qn ));
  \_32位一次除法器  \u_32位一次除法器_2  (.d(d), .r(r0), .q(q0), .rn(\n32位一次除法器_2_rn ), .qn(\n32位一次除法器_2_qn ));
  \_32位一次除法器  \u_32位一次除法器_3  (.d(d), .r(r1), .q(q1), .rn(\n32位一次除法器_3_rn ), .qn(\n32位一次除法器_3_qn ));
  \_32位一次除法器  \u_32位一次除法器_4  (.d(d), .r(r2), .q(q2), .rn(\n32位一次除法器_4_rn ), .qn(\n32位一次除法器_4_qn ));
  \_32位一次除法器  \u_32位一次除法器_5  (.d(d), .r(r3), .q(q3), .rn(\n32位一次除法器_5_rn ), .qn(\n32位一次除法器_5_qn ));
  \_32位一次除法器  \u_32位一次除法器_6  (.d(d), .r(r4), .q(q4), .rn(\n32位一次除法器_6_rn ), .qn(\n32位一次除法器_6_qn ));
  \_32位一次除法器  \u_32位一次除法器_7  (.d(d), .r(r5), .q(q5), .rn(\n32位一次除法器_7_rn ), .qn(\n32位一次除法器_7_qn ));
  \_32位一次除法器  \u_32位一次除法器_8  (.d(d), .r(r6), .q(q6), .rn(\n32位一次除法器_8_rn ), .qn(\n32位一次除法器_8_qn ));
  \_32位一次除法器  \u_32位一次除法器_9  (
    .d(d), .r(\n32位一次除法器_1_rn ), .q(\n32位一次除法器_1_qn ), .rn(\n32位一次除法器_9_rn ), .qn(\n32位一次除法器_9_qn ));
  \_32位一次除法器  \u_32位一次除法器_10  (
    .d(d), .r(\n32位一次除法器_2_rn ), .q(\n32位一次除法器_2_qn ), .rn(\n32位一次除法器_10_rn ), .qn(\n32位一次除法器_10_qn ));
  \_32位一次除法器  \u_32位一次除法器_11  (
    .d(d), .r(\n32位一次除法器_3_rn ), .q(\n32位一次除法器_3_qn ), .rn(\n32位一次除法器_11_rn ), .qn(\n32位一次除法器_11_qn ));
  \_32位一次除法器  \u_32位一次除法器_12  (
    .d(d), .r(\n32位一次除法器_4_rn ), .q(\n32位一次除法器_4_qn ), .rn(\n32位一次除法器_12_rn ), .qn(\n32位一次除法器_12_qn ));
  \_32位一次除法器  \u_32位一次除法器_13  (
    .d(d), .r(\n32位一次除法器_5_rn ), .q(\n32位一次除法器_5_qn ), .rn(\n32位一次除法器_13_rn ), .qn(\n32位一次除法器_13_qn ));
  \_32位一次除法器  \u_32位一次除法器_14  (
    .d(d), .r(\n32位一次除法器_6_rn ), .q(\n32位一次除法器_6_qn ), .rn(\n32位一次除法器_14_rn ), .qn(\n32位一次除法器_14_qn ));
  \_32位一次除法器  \u_32位一次除法器_15  (
    .d(d), .r(\n32位一次除法器_7_rn ), .q(\n32位一次除法器_7_qn ), .rn(\n32位一次除法器_15_rn ), .qn(\n32位一次除法器_15_qn ));
  \_32位一次除法器  \u_32位一次除法器_16  (
    .d(d), .r(\n32位一次除法器_8_rn ), .q(\n32位一次除法器_8_qn ), .rn(\n32位一次除法器_16_rn ), .qn(\n32位一次除法器_16_qn ));
  Comparator #(.width(32), .mode("unsigned")) comparator_1 (
    .a({32{1'b0}}), .b(d), .eq(comparator_1_eq));  // open: gt, lt
  // Probe on r7
  // Probe on q7
  \_32位一次除法器  \u_32位一次除法器_17  (
    .d(d), .r(\n32位一次除法器_9_rn ), .q(\n32位一次除法器_9_qn ), .rn(\n32位一次除法器_17_rn ), .qn(\n32位一次除法器_17_qn ));
  \_32位一次除法器  \u_32位一次除法器_18  (.d(d), .r(\n32位一次除法器_17_rn ), .q(\n32位一次除法器_17_qn ), .rn(r0), .qn(q0));
  \_32位一次除法器  \u_32位一次除法器_19  (.d(d), .r(\n32位一次除法器_20_rn ), .q(\n32位一次除法器_20_qn ), .rn(r1), .qn(q1));
  \_32位一次除法器  \u_32位一次除法器_20  (
    .d(d), .r(\n32位一次除法器_10_rn ), .q(\n32位一次除法器_10_qn ), .rn(\n32位一次除法器_20_rn ), .qn(\n32位一次除法器_20_qn ));
  \_32位一次除法器  \u_32位一次除法器_21  (.d(d), .r(\n32位一次除法器_22_rn ), .q(\n32位一次除法器_22_qn ), .rn(r2), .qn(q2));
  \_32位一次除法器  \u_32位一次除法器_22  (
    .d(d), .r(\n32位一次除法器_11_rn ), .q(\n32位一次除法器_11_qn ), .rn(\n32位一次除法器_22_rn ), .qn(\n32位一次除法器_22_qn ));
  \_32位一次除法器  \u_32位一次除法器_23  (
    .d(d), .r(\n32位一次除法器_12_rn ), .q(\n32位一次除法器_12_qn ), .rn(\n32位一次除法器_23_rn ), .qn(\n32位一次除法器_23_qn ));
  \_32位一次除法器  \u_32位一次除法器_24  (.d(d), .r(\n32位一次除法器_23_rn ), .q(\n32位一次除法器_23_qn ), .rn(r3), .qn(q3));
  \_32位一次除法器  \u_32位一次除法器_25  (
    .d(d), .r(\n32位一次除法器_13_rn ), .q(\n32位一次除法器_13_qn ), .rn(\n32位一次除法器_25_rn ), .qn(\n32位一次除法器_25_qn ));
  \_32位一次除法器  \u_32位一次除法器_26  (.d(d), .r(\n32位一次除法器_25_rn ), .q(\n32位一次除法器_25_qn ), .rn(r4), .qn(q4));
  \_32位一次除法器  \u_32位一次除法器_27  (
    .d(d), .r(\n32位一次除法器_14_rn ), .q(\n32位一次除法器_14_qn ), .rn(\n32位一次除法器_27_rn ), .qn(\n32位一次除法器_27_qn ));
  \_32位一次除法器  \u_32位一次除法器_28  (.d(d), .r(\n32位一次除法器_27_rn ), .q(\n32位一次除法器_27_qn ), .rn(r5), .qn(q5));
  \_32位一次除法器  \u_32位一次除法器_29  (.d(d), .r(\n32位一次除法器_30_rn ), .q(\n32位一次除法器_30_qn ), .rn(r6), .qn(q6));
  \_32位一次除法器  \u_32位一次除法器_30  (
    .d(d), .r(\n32位一次除法器_15_rn ), .q(\n32位一次除法器_15_qn ), .rn(\n32位一次除法器_30_rn ), .qn(\n32位一次除法器_30_qn ));
  \_32位一次除法器  \u_32位一次除法器_31  (
    .d(d), .r(\n32位一次除法器_16_rn ), .q(\n32位一次除法器_16_qn ), .rn(\n32位一次除法器_31_rn ), .qn(\n32位一次除法器_31_qn ));
  \_32位一次除法器  \u_32位一次除法器_32  (.d(d), .r(\n32位一次除法器_31_rn ), .q(\n32位一次除法器_31_qn ), .rn(r7), .qn(q7));
  Multiplexer #(.width(32), .enable("false")) multiplexer_1 (.in0(r7), .in1(d), .out(r), .sel(comparator_1_eq));
  Multiplexer #(.width(32), .enable("false")) multiplexer_2 (.in0(q7), .in1(d), .out(q), .sel(comparator_1_eq));
endmodule

module \_32位除法器测试电路  (
  input  [31:0] in_1,
  input  [31:0] in_2
);

  wire [31:0] \n32位除法器_1_q , \n32位除法器_1_r ;

  // Probe on in_1
  // Probe on in_2
  \_32位除法器  \u_32位除法器_1  (.d(in_1), .n(in_2), .r(\n32位除法器_1_r ), .q(\n32位除法器_1_q ));
  // Probe on \n32位除法器_1_r 
  // Probe on \n32位除法器_1_q 

  // Notes on the sheet:
  //   除数d
  //   被除数n
  //   余数r
  //   商q
endmodule

module \_32位一次除法器  (
  input  [31:0] d,
  input  [31:0] r,
  input  [31:0] q,
  output [31:0] rn,
  output [31:0] qn
);

  wire not_1_out, subtractor_1_bout;
  wire [31:0] subtractor_1_out;

  Subtractor #(.width(32)) subtractor_1 (
    .a({r[30:0], q[31]}), .b(d), .out(subtractor_1_out), .bin(1'b0), .bout(subtractor_1_bout));
  not not_1 (not_1_out, subtractor_1_bout);
  Multiplexer #(.width(32), .enable("false")) multiplexer_1 (
    .in0({r[30:0], q[31]}), .in1(subtractor_1_out), .out(rn), .sel(not_1_out));
  Multiplexer #(.width(32), .enable("false")) multiplexer_2 (
    .in0({q[30:0], 1'b0}), .in1({q[30:0], 1'b1}), .out(qn), .sel(not_1_out));
endmodule
