// Logisim project 实验5.circ as structural Verilog: 17 circuits, main circuit 四位二进制可逆计数器
module \四位二进制可逆计数器  (
  input  CLR,
  input  CPu,
  input  CPd,
  input  nLD,
  input  A,
  input  B,
  input  C,
  input  D,
  output Qa,
  output Qb,
  output Qc,
  output Qd
);

  wire and_1_out, and_2_out, and_3_out, and_4_out, and_5_out, and_6_out, and_7_out, and_8_out, and_9_out,
       and_10_out, d_ff_1_qn, d_ff_2_qn, d_ff_3_qn, d_ff_4_qn, not_1_out, or_1_out, or_2_out, or_3_out,
       or_4_out;

  not not_1 (not_1_out, nLD);
  and and_1 (and_1_out, not_1_out, A);
  and and_2 (and_2_out, not_1_out, B);
  and and_3 (and_3_out, not_1_out, C);
  and and_4 (and_4_out, not_1_out, D);
  and and_5 (and_5_out, Qa, CPu);
  and and_6 (and_6_out, d_ff_1_qn, CPd);
  and and_7 (and_7_out, Qa, Qb, CPu);
  and and_8 (and_8_out, d_ff_1_qn, d_ff_2_qn, CPd);
  and and_9 (and_9_out, Qa, Qb, Qc, CPu);
  and and_10 (and_10_out, d_ff_1_qn, d_ff_2_qn, d_ff_3_qn, CPd);
  or or_1 (or_1_out, CPu, CPd);
  or or_2 (or_2_out, and_5_out, and_6_out);
  or or_3 (or_3_out, and_7_out, and_8_out);
  or or_4 (or_4_out, and_9_out, and_10_out);
  D_Flip_Flop #(.trigger("falling")) d_ff_1 (
    .clk(or_1_out), .D(d_ff_1_qn), .Q(Qa), .Qn(d_ff_1_qn), .preset(and_1_out), .en(1'b1), .reset(CLR));
  D_Flip_Flop #(.trigger("falling")) d_ff_2 (
    .clk(or_2_out), .D(d_ff_2_qn), .Q(Qb), .Qn(d_ff_2_qn), .preset(and_2_out), .en(1'b1), .reset(CLR));
  D_Flip_Flop #(.trigger("falling")) d_ff_3 (
    .clk(or_3_out), .D(d_ff_3_qn), .Q(Qc), .Qn(d_ff_3_qn), .preset(and_3_out), .en(1'b1), .reset(CLR));
  D_Flip_Flop #(.trigger("falling")) d_ff_4 (
    .clk(or_4_out), .D(d_ff_4_qn), .Q(Qd), .Qn(d_ff_4_qn), .preset(and_4_out), .en(1'b1), .reset(CLR));

  // Notes on the sheet:
  //   四位二进制可逆计数器
  //   预置控制：nLD
  //   预制位：DCBA
  //   清零：CLS
  //   减法计数：CPd
  //   加法计数：CPu
  //   输出：QdQcQbQa
  //   所有D触发器全部调整为下降沿，上升沿无法保证从零计数
  //   逻辑表达式：
  //   Di = ~ Qi
  //   C1 = CPd & ~Qa + CPu & Qa
  //   C0 = CPd + CPu
  //   C0
  //   D0
  //   C1
  //   D1
  //   C2
  //   D2
  //   C3
  //   D3
  //   C3 = CPd & ~Qc & ~Qb & ~Qa + CPu & Qc & Qb & Qa
  //   C2 = CPd & ~Qb & ~ Qa + CPu & Qb & Qa
endmodule

module \十进制可逆计数器  (
  input  CPu,
  input  Clr,
  input  CPd,
  output Qcc,
  output Qd,
  output Qc,
  output Qb,
  output Qa,
  output Qcb
);

  wire not_1_out, or_1_out;

  and and_1 (Qcc, Qd, Qb);
  or or_1 (or_1_out, Qcc, Clr);
  \四位二进制可逆计数器  \u_四位二进制可逆计数器_1  (
    .CPu(CPu), .CPd(CPd), .nLD(not_1_out), .A(1'b1), .B(1'b0), .C(1'b0), .D(1'b1), .Qa(Qa), .Qb(Qb), .Qc(Qc),
    .Qd(Qd), .CLR(or_1_out));
  and and_2 (Qcb, Qa, Qb, Qc, Qd);
  not not_1 (not_1_out, Qcb);
endmodule

module \六十进制计数器  (
  input  CPu,
  input  CLS,
  input  Adj,
  input  CPd,
  output out_5,
  output out_6,
  output out_7,
  output out_8,
  output out_9,
  output out_10,
  output out_11,
  output out_12,
  output nQcc
);

  wire and_1_out, and_2_out, and_3_out, and_4_out, or_1_out, or_2_out, or_3_out, or_4_out, \十进制可逆计数器_1_qcb ,
       \十进制可逆计数器_1_qcc ;

  not not_1 (nQcc, and_2_out);
  or or_1 (or_1_out, and_3_out, CLS);
  and and_1 (and_1_out, Adj, or_4_out, CPd);
  and and_2 (and_2_out, ~Adj, and_3_out);  // AND_Gate
  \十进制可逆计数器  \u_十进制可逆计数器_1  (
    .CPu(CPu), .Clr(or_1_out), .CPd(and_1_out), .Qcb(\十进制可逆计数器_1_qcb ), .Qcc(\十进制可逆计数器_1_qcc ), .Qd(out_5),
    .Qc(out_6), .Qb(out_7), .Qa(out_8));
  and and_3 (and_3_out, out_10, out_11);
  and and_4 (and_4_out, ~\十进制可逆计数器_1_qcb , \十进制可逆计数器_1_qcc );  // AND_Gate
  or or_2 (or_2_out, out_5, out_6, out_7, out_8);
  \十进制可逆计数器  \u_十进制可逆计数器_2  (
    .CPu(and_4_out), .Clr(or_1_out), .CPd(\十进制可逆计数器_1_qcb ), .Qd(out_9), .Qc(out_10), .Qb(out_11), .Qa(out_12));  // open: Qcb, Qcc
  or or_3 (or_3_out, out_9, out_10, out_11, out_12);
  or or_4 (or_4_out, or_3_out, or_2_out);

  // Notes on the sheet:
  //   功能要求：
  //   1. 输出两位BCD码
  //   2. 清零
  //   3. 加减计数，有进位信号
  //   4. 校准功能（加法循环校准，减法仅回零，无进位信号）
  //   设计思路：
  //   基于十进制可逆计数器，分别对个位十位进行计数
endmodule

module \六十进制计数器测试电路  (
  input  in_1
);

  wire button_1_out, button_2_out, button_3_out, button_4_out, not_1_out, \六十进制计数器_1_nqcc ;
  wire [3:0] \六十进制计数器_1_out_8 , \六十进制计数器_1_out_12 , \四位二进制可逆计数器_1_qa ;

  Button button_1 (.out(button_1_out));
  Button button_2 (.out(button_2_out));
  Hex_Digit_Display hex_digit_display_1 (.value(\六十进制计数器_1_out_12 ), .dp(1'b0));
  Hex_Digit_Display hex_digit_display_2 (.value(\六十进制计数器_1_out_8 ), .dp(1'b0));
  \六十进制计数器  \u_六十进制计数器_1  (
    .CPu(button_1_out), .CLS(button_3_out), .CPd(button_2_out), .Adj(in_1), .out_5(\六十进制计数器_1_out_8 [3]),
    .out_6(\六十进制计数器_1_out_8 [2]), .out_7(\六十进制计数器_1_out_8 [1]), .out_8(\六十进制计数器_1_out_8 [0]),
    .out_9(\六十进制计数器_1_out_12 [3]), .out_10(\六十进制计数器_1_out_12 [2]), .out_11(\六十进制计数器_1_out_12 [1]),
    .out_12(\六十进制计数器_1_out_12 [0]), .nQcc(\六十进制计数器_1_nqcc ));
  not not_1 (not_1_out, \六十进制计数器_1_nqcc );
  Button button_3 (.out(button_3_out));
  Button button_4 (.out(button_4_out));
  Hex_Digit_Display hex_digit_display_3 (.value(\四位二进制可逆计数器_1_qa ), .dp(1'b0));
  \四位二进制可逆计数器  \u_四位二进制可逆计数器_1  (
    .CPu(not_1_out), .CPd(1'b0), .nLD(1'b1), .A(1'b0), .B(1'b0), .C(1'b0), .D(1'b0),
    .Qa(\四位二进制可逆计数器_1_qa [0]), .Qb(\四位二进制可逆计数器_1_qa [1]), .Qc(\四位二进制可逆计数器_1_qa [2]),
    .Qd(\四位二进制可逆计数器_1_qa [3]), .CLR(button_4_out));
endmodule

module \十二进制计数器或二十四进制的计数器电路_基于十进制计数器_废弃  (
  input  Set,
  input  Clr,
  input  Adj,
  input  CPu,
  input  CPd,
  output out_6,
  output out_7,
  output \输出 ,
  output out_9,
  output out_10,
  output out_11,
  output out_12,
  output out_13,
  output nQcc
);

  wire _12, _24, and_1_out, and_3_out, CLS, CPd_t, or_1_out, or_2_out, or_3_out, or_4_out, \十进制可逆计数器_1_qcb ,
       \十进制可逆计数器_1_qcc ;

  \十进制可逆计数器  \u_十进制可逆计数器_1  (
    .CPu(CPu), .Clr(CLS), .CPd(CPd_t), .Qcb(\十进制可逆计数器_1_qcb ), .Qcc(\十进制可逆计数器_1_qcc ), .Qd(out_10),
    .Qc(out_11), .Qb(out_12), .Qa(out_13));
  or u_CLS (CLS, _24, Clr, _12);
  and and_1 (and_1_out, ~\十进制可逆计数器_1_qcb , \十进制可逆计数器_1_qcc );  // AND_Gate
  \十进制可逆计数器  \u_十进制可逆计数器_2  (
    .CPu(and_1_out), .Clr(CLS), .CPd(\十进制可逆计数器_1_qcb ), .Qd(out_6), .Qc(out_7), .Qb(\输出 ), .Qa(out_9));  // open: Qcb, Qcc
  or or_1 (or_1_out, out_6, out_7, \输出 , out_9);
  or or_2 (or_2_out, out_10, out_11, out_12, out_13);
  and u__24 (_24, \输出 , out_11, Set);
  or or_3 (or_3_out, or_1_out, or_2_out);
  and u__12 (_12, ~Set, out_9, out_12);  // AND_Gate
  and and_2 (CPd_t, CPd, or_3_out, Adj);
  or or_4 (or_4_out, _24, _12);
  and and_3 (and_3_out, ~Adj, or_4_out);  // AND_Gate
  not not_1 (nQcc, and_3_out);

  // Other names for the same wires on the sheet: _0a = out_13; _0b = out_12; _0c = out_11; _0d = out_10; _1a = out_9;
  //   _1b = \输出 ; _1c = out_7; _1d = out_6; a = Adj; c = Clr; d = CPd; s = Set; u = CPu

  // Notes on the sheet:
  //   输入
  //   清零信号
  //   计数器耦合
  //   进位信号
  //   累减信号
endmodule

module \十二进制或二十四进制可逆计数器电路  (
  input  Set,
  input  Clr,
  input  Adj,
  input  CPu,
  input  CPd,
  output out_6,
  output out_7,
  output out_8,
  output \输出 ,
  output out_10,
  output out_11,
  output out_12,
  output out_13,
  output nQcc
);

  wire _12a, _12b, _12c, _12Clr, _12d, _24o, _CPd, and_1_out, and_2_out, and_3_out, d_ff_1_qn,
       multiplexer_3_out, not_1_out, or_1_out, or_2_out;
  wire [7:0] _12o_BCD, _24o_BCD, multiplexer_1_out, multiplexer_4_out, multiplexer_5_out;

  Multiplexer #(.width(8), .enable("false")) multiplexer_1 (
    .in0({8{1'b0}}), .in1(8'h6), .out(multiplexer_1_out), .sel(and_1_out));
  and and_1 (and_1_out, _12d, _12b);
  \四位二进制可逆计数器  \u_四位二进制可逆计数器_1  (
    .CPu(CPu), .CPd(_CPd), .nLD(not_1_out), .A(1'b1), .B(1'b1), .C(1'b0), .D(1'b1), .Qa(_12a), .Qb(_12b),
    .Qc(_12c), .Qd(_12d), .CLR(_12Clr));
  not not_1 (not_1_out, and_2_out);
  and and_2 (and_2_out, _12d, _12c, _12b, _12a);
  // Probe on _12o_BCD
  Adder adder_1 (
    .a({4'b0000, _12d, _12c, _12b, _12a}), .b(multiplexer_1_out), .out(_12o_BCD), .cin(1'b0));  // open: cout
  // Probe on {out_13, out_12, out_11, out_10, \输出 , out_8, out_7, out_6}
  Multiplexer #(.width(8), .enable("false")) multiplexer_2 (
    .in0(_12o_BCD), .in1(_24o_BCD), .out({out_13, out_12, out_11, out_10, \输出 , out_8, out_7, out_6}),
    .sel(Set));
  D_Flip_Flop d_ff_1 (.clk(nQcc), .D(d_ff_1_qn), .Q(_24o), .Qn(d_ff_1_qn), .preset(1'b0), .en(1'b1), .reset(Clr));
  or or_1 (or_1_out, _12a, _12b, _12d, _12c);
  or or_2 (or_2_out, or_1_out, _24o);
  Multiplexer #(.enable("false")) multiplexer_3 (.in0(or_1_out), .in1(or_2_out), .out(multiplexer_3_out), .sel(Set));
  and and_3 (and_3_out, _12d, ~_12c, ~_12b);  // AND_Gate
  and and_4 (_CPd, CPd, multiplexer_3_out, Adj);
  Multiplexer #(.width(8), .enable("false")) multiplexer_4 (
    .in0(8'h12), .in1(8'h18), .out(multiplexer_4_out), .sel(and_3_out));
  Multiplexer #(.width(8), .enable("false")) multiplexer_5 (
    .in0({8{1'b0}}), .in1(multiplexer_4_out), .out(multiplexer_5_out), .sel(_24o));
  and and_5 (nQcc, _12d, _12c);
  or or_3 (_12Clr, nQcc, Clr);
  // Probe on _24o_BCD
  Adder adder_2 (.a(_12o_BCD), .b(multiplexer_5_out), .out(_24o_BCD), .cin(1'b0));  // open: cout

  // Other names for the same wires on the sheet: _12o[3:0] = {_12d, _12c, _12b, _12a}; _12Qcc = nQcc

  // Notes on the sheet:
  //   输入
  //   十二进制计数器输出转换
  //   功能要求：
  //   1. 输出两位BCD码
  //   2. 清零
  //   3. 加减计数，有进位信号
  //   5. 进制转换功能
  //   十二进制可逆计数器
  //   十二进制可逆计数器接线
  //   4. 校准功能（加法循环校准，减法仅回零，无进位信号）
  //   注：这里的进制转换是直接整合了十二小时和二十四小时转换
  //   如果需要在修改为二十四进制后始终从零计数，应当将set信号同clr信号相连
  //   计数进位信号为十二进制的进位信号，这是考虑了的上下午转换的设计
  //   二十四进制可逆计数器
  //   减计数信号
  //   二十四进制计数器输出转换
  //   十二进制计数器进位及清零信号
endmodule

module \十二进制计数器或二十四进制的计数器测试电路  (
  input  Adj,
  input  Set
);

  wire button_1_out, Clr_out, CPd_out, CPu_out, not_1_out, \十二进制或二十四进制可逆计数器电路_1_nqcc ;
  wire [3:0] \十二进制或二十四进制可逆计数器电路_1_out_6 , \十二进制或二十四进制可逆计数器电路_1_out_10 , \四位二进制可逆计数器_1_qa ;

  Button CPu (.out(CPu_out));
  Button CPd (.out(CPd_out));
  Hex_Digit_Display hex_digit_display_1 (.value(\十二进制或二十四进制可逆计数器电路_1_out_10 ), .dp(1'b0));
  Hex_Digit_Display hex_digit_display_2 (.value(\十二进制或二十四进制可逆计数器电路_1_out_6 ), .dp(1'b0));
  \十二进制或二十四进制可逆计数器电路  \u_十二进制或二十四进制可逆计数器电路_1  (
    .Set(Set), .Clr(Clr_out), .Adj(Adj), .CPu(CPu_out), .CPd(CPd_out),
    .out_6(\十二进制或二十四进制可逆计数器电路_1_out_6 [0]), .out_7(\十二进制或二十四进制可逆计数器电路_1_out_6 [1]),
    .out_8(\十二进制或二十四进制可逆计数器电路_1_out_6 [2]), .\输出 (\十二进制或二十四进制可逆计数器电路_1_out_6 [3]),
    .out_10(\十二进制或二十四进制可逆计数器电路_1_out_10 [0]), .out_11(\十二进制或二十四进制可逆计数器电路_1_out_10 [1]),
    .out_12(\十二进制或二十四进制可逆计数器电路_1_out_10 [2]), .out_13(\十二进制或二十四进制可逆计数器电路_1_out_10 [3]),
    .nQcc(\十二进制或二十四进制可逆计数器电路_1_nqcc ));
  not not_1 (not_1_out, \十二进制或二十四进制可逆计数器电路_1_nqcc );
  Button Clr (.out(Clr_out));
  Hex_Digit_Display hex_digit_display_3 (.value(\四位二进制可逆计数器_1_qa ), .dp(1'b0));
  Button button_1 (.out(button_1_out));
  \四位二进制可逆计数器  \u_四位二进制可逆计数器_1  (
    .CPu(not_1_out), .CPd(1'b0), .nLD(1'b1), .A(1'b0), .B(1'b0), .C(1'b0), .D(1'b0),
    .Qa(\四位二进制可逆计数器_1_qa [0]), .Qb(\四位二进制可逆计数器_1_qa [1]), .Qc(\四位二进制可逆计数器_1_qa [2]),
    .Qd(\四位二进制可逆计数器_1_qa [3]), .CLR(button_1_out));
endmodule

module \上下午文字显示的电路  (
  input  AM_PM,
  input  TT,
  output [4:0] out_3,
  output [4:0] out_4,
  output [4:0] out_5,
  output [4:0] out_6
);

  wire not_1_out;

  not not_1 (not_1_out, TT);
  Multiplexer #(.width(20), .disabled(0)) multiplexer_1 (
    .in0(20'h97e1), .in1(20'h853f0), .out({out_6, out_5, out_4, out_3}), .sel(AM_PM), .en(not_1_out));
endmodule

module \上下午文字显示测试电路  (
  input  in_1,
  input  in_2
);

  wire [4:0] \上下午文字显示的电路_1_out_3 , \上下午文字显示的电路_1_out_4 , \上下午文字显示的电路_1_out_5 , \上下午文字显示的电路_1_out_6 ;

  DotMatrix #(.matrixcols(4), .matrixrows(5)) dotmatrix_1 (
    .col0(\上下午文字显示的电路_1_out_3 ), .col1(\上下午文字显示的电路_1_out_4 ), .col2(\上下午文字显示的电路_1_out_5 ),
    .col3(\上下午文字显示的电路_1_out_6 ));
  \上下午文字显示的电路  \u_上下午文字显示的电路_1  (
    .out_3(\上下午文字显示的电路_1_out_3 ), .out_4(\上下午文字显示的电路_1_out_4 ), .out_5(\上下午文字显示的电路_1_out_5 ),
    .out_6(\上下午文字显示的电路_1_out_6 ), .AM_PM(in_1), .TT(in_2));
endmodule

module \电子钟整点报时电路  (
  input  [3:0] in_1,
  input  [3:0] in_2,
  input  [3:0] in_3,
  input  [3:0] in_4,
  output out_5
);

  wire and_1_out, and_2_out;

  and and_1 (and_1_out, in_1[0], in_1[2], in_2[0], in_2[3]);
  and and_2 (and_2_out, in_3[0], in_3[2], in_4[0]);
  and and_3 (out_5, and_1_out, and_2_out);
endmodule

module \电子钟整点报时电路测试电路  (
);

  wire clock_1_out, \电子钟整点报时电路_1_out_5 ;
  wire [3:0] \六十进制计数器_1_out_8 , \六十进制计数器_1_out_12 ;

  Clock clock_1 (.out(clock_1_out));
  // Probe on \六十进制计数器_1_out_12 
  // Probe on \六十进制计数器_1_out_8 
  \六十进制计数器  \u_六十进制计数器_1  (
    .CPu(clock_1_out), .CLS(1'b0), .CPd(1'b0), .Adj(1'b0), .out_5(\六十进制计数器_1_out_8 [3]),
    .out_6(\六十进制计数器_1_out_8 [2]), .out_7(\六十进制计数器_1_out_8 [1]), .out_8(\六十进制计数器_1_out_8 [0]),
    .out_9(\六十进制计数器_1_out_12 [3]), .out_10(\六十进制计数器_1_out_12 [2]), .out_11(\六十进制计数器_1_out_12 [1]),
    .out_12(\六十进制计数器_1_out_12 [0]));  // open: nQcc
  \电子钟整点报时电路  \u_电子钟整点报时电路_1  (
    .in_1(4'b0101), .in_2(4'b1001), .in_3(\六十进制计数器_1_out_12 ), .in_4(\六十进制计数器_1_out_8 ),
    .out_5(\电子钟整点报时电路_1_out_5 ));
  LED led_1 (.in(\电子钟整点报时电路_1_out_5 ));
endmodule

module \秒脉冲产生电路  (
  input  in_1,
  output out_2
);

  \四位二进制可逆计数器  \u_四位二进制可逆计数器_1  (
    .CPu(in_1), .CPd(1'b0), .nLD(1'b1), .A(1'b0), .B(1'b0), .C(1'b0), .D(1'b0), .Qd(out_2), .CLR(out_2));  // open: Qa, Qb, Qc
endmodule

module \多功能数字钟  (
  input  CP,
  input  Clr,
  input  Adj0,
  input  Adj1,
  input  CPu,
  input  CPd,
  input  Set,
  output [4:0] out_8,
  output [4:0] out_9,
  output [3:0] \输出 ,
  output [4:0] out_11,
  output [3:0] \小时 ,
  output [4:0] out_13,
  output [3:0] \分钟 ,
  output \定点报时 ,
  output [3:0] out_16,
  output [3:0] \秒 ,
  output [3:0] out_18
);

  wire AM_PM, and_1_out, and_2_out, and_3_out, and_4_out, and_5_out, and_6_out, and_7_out, comparator_1_eq,
       mTh, not_4_out, or_1_out, or_2_out, sTm, t_ff_1_q, \六十进制计数器_1_nqcc , \六十进制计数器_2_nqcc ,
       \十二进制或二十四进制可逆计数器电路_1_nqcc , \秒脉冲产生电路_1_out_2 ;
  wire [3:0] H0, H1;
  wire [7:0] multiplexer_1_out;

  and and_1 (and_1_out, ~Adj0, CP);  // AND_Gate
  and and_2 (and_2_out, CPu, and_3_out);
  and and_3 (and_3_out, Adj0, Adj1);
  and and_4 (and_4_out, CPu, and_5_out);
  and and_5 (and_5_out, Adj0, ~Adj1);  // AND_Gate
  Comparator #(.mode("unsigned")) comparator_1 (.a({H1, H0}), .b({8{1'b0}}), .eq(comparator_1_eq));  // open: gt, lt
  \秒脉冲产生电路  \u_秒脉冲产生电路_1  (.in_1(and_1_out), .out_2(\秒脉冲产生电路_1_out_2 ));
  or or_1 (or_1_out, sTm, and_2_out);
  and and_6 (and_6_out, and_3_out, CPd);
  or or_2 (or_2_out, mTh, and_4_out);
  and and_7 (and_7_out, and_5_out, CPd);
  Multiplexer #(.width(8), .enable("false")) multiplexer_1 (
    .in0({H1, H0}), .in1(8'h12), .out(multiplexer_1_out), .sel(comparator_1_eq));
  Multiplexer #(.width(8), .enable("false")) multiplexer_2 (
    .in0(multiplexer_1_out), .in1({H1, H0}), .out({\输出 , \小时 }), .sel(Set));
  \六十进制计数器  \u_六十进制计数器_1  (
    .CPu(\秒脉冲产生电路_1_out_2 ), .CLS(Clr), .CPd(1'b0), .Adj(1'b0), .out_5(out_18[3]), .out_6(out_18[2]),
    .out_7(out_18[1]), .out_8(out_18[0]), .out_9(\秒 [3]), .out_10(\秒 [2]), .out_11(\秒 [1]), .out_12(\秒 [0]),
    .nQcc(\六十进制计数器_1_nqcc ));
  \六十进制计数器  \u_六十进制计数器_2  (
    .CPu(or_1_out), .CLS(Clr), .CPd(and_6_out), .Adj(and_3_out), .out_5(out_16[3]), .out_6(out_16[2]),
    .out_7(out_16[1]), .out_8(out_16[0]), .out_9(\分钟 [3]), .out_10(\分钟 [2]), .out_11(\分钟 [1]),
    .out_12(\分钟 [0]), .nQcc(\六十进制计数器_2_nqcc ));
  \十二进制或二十四进制可逆计数器电路  \u_十二进制或二十四进制可逆计数器电路_1  (
    .Set(Set), .Clr(Clr), .Adj(and_5_out), .CPu(or_2_out), .CPd(and_7_out), .out_6(H0[0]), .out_7(H0[1]),
    .out_8(H0[2]), .\输出 (H0[3]), .out_10(H1[0]), .out_11(H1[1]), .out_12(H1[2]), .out_13(H1[3]),
    .nQcc(\十二进制或二十四进制可逆计数器电路_1_nqcc ));
  not not_1 (sTm, \六十进制计数器_1_nqcc );
  not not_2 (mTh, \六十进制计数器_2_nqcc );
  not not_3 (AM_PM, \十二进制或二十四进制可逆计数器电路_1_nqcc );
  \电子钟整点报时电路  \u_电子钟整点报时电路_1  (.in_1(\分钟 ), .in_2(out_16), .in_3(\秒 ), .in_4(out_18), .out_5(\定点报时 ));
  not not_4 (not_4_out, AM_PM);
  \上下午文字显示的电路  \u_上下午文字显示的电路_1  (
    .out_3(out_8), .out_4(out_9), .out_5(out_11), .out_6(out_13), .AM_PM(t_ff_1_q), .TT(Set));
  T_Flip_Flop t_ff_1 (.clk(not_4_out), .T(1'b1), .Q(t_ff_1_q), .preset(1'b0), .reset(Clr), .en(1'b1));  // open: Qn

  // Other names for the same wires on the sheet: a0 = Adj0; a1 = Adj1; c = Clr; d = CPd;
  //   LED[19:0] = {out_13, out_11, out_9, out_8}; M0[3:0] = out_16; M1[3:0] = \分钟 ; s = Set; S0[3:0] = out_18;
  //   S1[3:0] = \秒 ; u = CPu

  // Notes on the sheet:
  //   输入
  //   秒计数输入
  //   分钟计数输入
  //   小时计数输入
  //   秒计数
  //   分钟计数
  //   小时计数
  //   秒计数输出
  //   分钟计数输出
  //   小时计数输出
  //   秒-分钟进位信号
  //   分钟-小时进位信号
  //   上下午切换信号
  //   LED输出
  //   LED
endmodule

module \多功能数字钟测试电路  (
  input  in_1,
  input  in_2,
  input  in_3
);

  wire button_1_out, button_2_out, button_3_out, clock_1_out, \多功能数字钟_1_定点报时 ;
  wire [3:0] \多功能数字钟_1_out_16 , \多功能数字钟_1_out_18 , \多功能数字钟_1_分钟 , \多功能数字钟_1_小时 , \多功能数字钟_1_秒 , \多功能数字钟_1_输出 ;
  wire [4:0] \多功能数字钟_1_out_8 , \多功能数字钟_1_out_9 , \多功能数字钟_1_out_11 , \多功能数字钟_1_out_13 ;

  DotMatrix #(.matrixcols(4), .matrixrows(5)) dotmatrix_1 (
    .col0(\多功能数字钟_1_out_8 ), .col1(\多功能数字钟_1_out_9 ), .col2(\多功能数字钟_1_out_11 ), .col3(\多功能数字钟_1_out_13 ));
  \多功能数字钟  \u_多功能数字钟_1  (
    .CP(clock_1_out), .Clr(button_3_out), .Adj0(in_1), .Adj1(in_2), .CPu(button_2_out), .CPd(button_1_out),
    .Set(in_3), .\输出 (\多功能数字钟_1_输出 ), .\小时 (\多功能数字钟_1_小时 ), .\分钟 (\多功能数字钟_1_分钟 ), .out_16(\多功能数字钟_1_out_16 ),
    .\秒 (\多功能数字钟_1_秒 ), .out_18(\多功能数字钟_1_out_18 ), .out_8(\多功能数字钟_1_out_8 ), .out_9(\多功能数字钟_1_out_9 ),
    .out_11(\多功能数字钟_1_out_11 ), .out_13(\多功能数字钟_1_out_13 ), .\定点报时 (\多功能数字钟_1_定点报时 ));
  Clock clock_1 (.out(clock_1_out));
  Hex_Digit_Display hex_digit_display_1 (.value(\多功能数字钟_1_输出 ), .dp(1'b0));
  Hex_Digit_Display hex_digit_display_2 (.value(\多功能数字钟_1_小时 ), .dp(1'b0));
  Button button_1 (.out(button_1_out));
  Button button_2 (.out(button_2_out));
  Hex_Digit_Display hex_digit_display_3 (.value(\多功能数字钟_1_分钟 ), .dp(1'b0));
  Hex_Digit_Display hex_digit_display_4 (.value(\多功能数字钟_1_out_16 ), .dp(1'b0));
  Hex_Digit_Display hex_digit_display_5 (.value(\多功能数字钟_1_秒 ), .dp(1'b0));
  Hex_Digit_Display hex_digit_display_6 (.value(\多功能数字钟_1_out_18 ), .dp(1'b0));
  LED led_1 (.in(\多功能数字钟_1_定点报时 ));
  Button button_3 (.out(button_3_out));
endmodule

module \闹钟_24小时制设置_舍弃  (
  input  CP,
  input  Clr,
  input  Adj0,
  input  Adj1,
  input  CPu,
  input  CPd,
  input  Set,
  input  Set_Alarm,
  input  Enable_Alarm,
  output \定点报时 ,
  output [3:0] \小时 ,
  output [3:0] out_12,
  output \闹钟 ,
  output [3:0] \分钟 ,
  output [4:0] out_15,
  output [3:0] out_16,
  output [4:0] out_17,
  output [4:0] out_18,
  output [4:0] out_19,
  output [3:0] \秒 ,
  output [3:0] out_21
);

  wire AM_PM, AM_PM_t, amTh, and_1_out, and_2_out, and_3_out, and_4_out, and_5_out, and_6_out, and_7_out,
       and_8_out, and_9_out, and_10_out, and_11_out, and_12_out, and_13_out, and_14_out, and_15_out,
       and_16_out, and_17_out, and_18_out, and_19_out, and_20_out, comparator_1_eq, comparator_2_eq,
       comparator_3_eq, mTh, not_4_out, or_1_out, or_2_out, or_3_out, or_4_out, sTm, \六十进制计数器_1_nqcc ,
       \六十进制计数器_2_nqcc , \六十进制计数器_3_nqcc , \十二进制或二十四进制可逆计数器电路_1_nqcc , \秒脉冲产生电路_1_out_2 ;
  wire [3:0] aH0, aH1, aM0, aM1, H0, H1, M0, M1, S0, S1;
  wire [7:0] adder_1_out, multiplexer_1_out, multiplexer_2_out, multiplexer_6_out, multiplexer_7_out,
       multiplexer_8_out;

  and and_1 (and_1_out, ~Adj0, CP);  // AND_Gate
  and and_2 (and_2_out, CPu, and_3_out);
  and and_3 (and_3_out, Adj0, Adj1);
  and and_4 (and_4_out, CPu, and_5_out);
  and and_5 (and_5_out, Adj0, ~Adj1);  // AND_Gate
  \秒脉冲产生电路  \u_秒脉冲产生电路_1  (.in_1(and_1_out), .out_2(\秒脉冲产生电路_1_out_2 ));
  or or_1 (or_1_out, sTm, and_2_out);
  and and_6 (and_6_out, and_3_out, CPd);
  or or_2 (or_2_out, mTh, and_4_out);
  and and_7 (and_7_out, and_5_out, CPd);
  Comparator #(.mode("unsigned")) comparator_1 (.a({H1, H0}), .b({8{1'b0}}), .eq(comparator_1_eq));  // open: gt, lt
  Multiplexer #(.width(8), .enable("false")) multiplexer_1 (
    .in0({H1, H0}), .in1(8'h12), .out(multiplexer_1_out), .sel(comparator_1_eq));
  \六十进制计数器  \u_六十进制计数器_1  (
    .CPu(\秒脉冲产生电路_1_out_2 ), .CLS(and_8_out), .CPd(1'b0), .Adj(1'b0), .out_5(S0[3]), .out_6(S0[2]),
    .out_7(S0[1]), .out_8(S0[0]), .out_9(S1[3]), .out_10(S1[2]), .out_11(S1[1]), .out_12(S1[0]),
    .nQcc(\六十进制计数器_1_nqcc ));
  \六十进制计数器  \u_六十进制计数器_2  (
    .CPu(or_1_out), .CLS(and_9_out), .CPd(and_6_out), .Adj(and_3_out), .out_5(M0[3]), .out_6(M0[2]),
    .out_7(M0[1]), .out_8(M0[0]), .out_9(M1[3]), .out_10(M1[2]), .out_11(M1[1]), .out_12(M1[0]),
    .nQcc(\六十进制计数器_2_nqcc ));
  Multiplexer #(.width(8), .enable("false")) multiplexer_2 (
    .in0(multiplexer_1_out), .in1({H1, H0}), .out(multiplexer_2_out), .sel(Set));
  Multiplexer #(.width(8), .enable("false")) multiplexer_3 (
    .in0(multiplexer_2_out), .in1({aH1, aH0}), .out({out_12, \小时 }), .sel(Set_Alarm));
  Multiplexer #(.width(8), .enable("false")) multiplexer_4 (
    .in0({M1, M0}), .in1({aM1, aM0}), .out({out_16, \分钟 }), .sel(Set_Alarm));
  Multiplexer #(.width(8), .enable("false")) multiplexer_5 (
    .in0({S1, S0}), .in1({8{1'b0}}), .out({out_21, \秒 }), .sel(Set_Alarm));
  and and_8 (and_8_out, Clr, ~Set_Alarm);  // AND_Gate
  \十二进制或二十四进制可逆计数器电路  \u_十二进制或二十四进制可逆计数器电路_1  (
    .Set(Set), .Clr(and_10_out), .Adj(and_5_out), .CPu(or_2_out), .CPd(and_7_out), .out_6(H0[0]),
    .out_7(H0[1]), .out_8(H0[2]), .\输出 (H0[3]), .out_10(H1[0]), .out_11(H1[1]), .out_12(H1[2]),
    .out_13(H1[3]), .nQcc(\十二进制或二十四进制可逆计数器电路_1_nqcc ));
  not not_1 (sTm, \六十进制计数器_1_nqcc );
  not not_2 (mTh, \六十进制计数器_2_nqcc );
  and and_9 (and_9_out, Clr, ~Set_Alarm);  // AND_Gate
  not not_3 (AM_PM, \十二进制或二十四进制可逆计数器电路_1_nqcc );
  and and_10 (and_10_out, Clr, ~Set_Alarm);  // AND_Gate
  \电子钟整点报时电路  \u_电子钟整点报时电路_1  (.in_1(M1), .in_2(M0), .in_3(S1), .in_4(S0), .out_5(\定点报时 ));
  Multiplexer #(.width(8), .enable("false")) multiplexer_6 (
    .in0(8'h12), .in1(8'h18), .out(multiplexer_6_out), .sel(and_11_out));
  and and_11 (and_11_out, H0[3], ~H0[2], ~H0[1]);  // AND_Gate
  Multiplexer #(.width(8), .enable("false")) multiplexer_7 (
    .in0({8{1'b0}}), .in1(multiplexer_6_out), .out(multiplexer_7_out), .sel(AM_PM_t));
  not not_4 (not_4_out, AM_PM);
  Adder adder_1 (.a({H1, H0}), .b(multiplexer_7_out), .out(adder_1_out), .cin(1'b0));  // open: cout
  Multiplexer #(.width(8), .enable("false")) multiplexer_8 (
    .in0(adder_1_out), .in1({H1, H0}), .out(multiplexer_8_out), .sel(Set));
  and and_12 (and_12_out, CPu, and_13_out);
  and and_13 (and_13_out, Adj0, Set_Alarm, Adj1);
  and and_14 (and_14_out, and_13_out, CPd);
  and and_15 (and_15_out, CPu, and_16_out);
  and and_16 (and_16_out, Adj0, Set_Alarm, ~Adj1);  // AND_Gate
  and and_17 (and_17_out, and_16_out, CPd);
  \上下午文字显示的电路  \u_上下午文字显示的电路_1  (
    .out_3(out_15), .out_4(out_17), .out_5(out_18), .out_6(out_19), .AM_PM(AM_PM_t), .TT(or_3_out));
  T_Flip_Flop t_ff_1 (.clk(not_4_out), .T(1'b1), .Q(AM_PM_t), .preset(1'b0), .reset(Clr), .en(1'b1));  // open: Qn
  or or_3 (or_3_out, Set, Set_Alarm);
  Comparator #(.mode("unsigned")) comparator_2 (
    .a(multiplexer_8_out), .b({aH1, aH0}), .eq(comparator_2_eq));  // open: gt, lt
  Comparator #(.mode("unsigned")) comparator_3 (.a({M1, M0}), .b({aM1, aM0}), .eq(comparator_3_eq));  // open: gt, lt
  \六十进制计数器  \u_六十进制计数器_3  (
    .CPu(and_12_out), .CLS(and_19_out), .CPd(and_14_out), .Adj(and_13_out), .out_5(aM0[3]), .out_6(aM0[2]),
    .out_7(aM0[1]), .out_8(aM0[0]), .out_9(aM1[3]), .out_10(aM1[2]), .out_11(aM1[1]), .out_12(aM1[0]),
    .nQcc(\六十进制计数器_3_nqcc ));
  and and_18 (and_18_out, comparator_2_eq, Enable_Alarm, comparator_3_eq);
  \十二进制或二十四进制可逆计数器电路  \u_十二进制或二十四进制可逆计数器电路_2  (
    .Set(1'b1), .Clr(and_20_out), .Adj(and_16_out), .CPu(and_15_out), .CPd(and_17_out), .out_6(aH0[0]),
    .out_7(aH0[1]), .out_8(aH0[2]), .\输出 (aH0[3]), .out_10(aH1[0]), .out_11(aH1[1]), .out_12(aH1[2]),
    .out_13(aH1[3]));  // open: nQcc
  or or_4 (or_4_out, S1[0], S1[1], S1[2], S1[3]);
  not not_5 (amTh, \六十进制计数器_3_nqcc );
  and and_19 (and_19_out, Clr, Set_Alarm);
  and and_20 (and_20_out, Clr, Set_Alarm);
  and and_21 (\闹钟 , ~or_4_out, and_18_out, S0[0]);  // AND_Gate

  // Other names for the same wires on the sheet: a0 = Adj0; a1 = Adj1; alarm = \闹钟 ; c = Clr; d = CPd;
  //   ea = Enable_Alarm; LED[19:0] = {out_19, out_18, out_17, out_15}; s = Set; sa = Set_Alarm; u = CPu

  // Notes on the sheet:
  //   输入
  //   秒计数输入
  //   分钟计数输入
  //   小时计数输入
  //   秒计数
  //   分钟计数
  //   小时计数
  //   输出
  //   秒计数输出
  //   分钟计数输出
  //   小时计数输出
  //   秒-分钟进位信号
  //   分钟-小时进位信号
  //   上下午切换信号
  //   LED输出
  //   LED
  //   闹钟输出
  //   闹钟定时
endmodule

module \闹钟_小时制随电子钟  (
  input  CP,
  input  Clr,
  input  Adj0,
  input  Adj1,
  input  CPu,
  input  CPd,
  input  Set,
  input  Set_Alarm,
  input  Enable_Alarm,
  output \定点报时 ,
  output [3:0] \小时 ,
  output [3:0] out_12,
  output \闹钟 ,
  output [3:0] \分钟 ,
  output [4:0] out_15,
  output [3:0] out_16,
  output [4:0] out_17,
  output [4:0] out_18,
  output [4:0] out_19,
  output [3:0] \秒 ,
  output [3:0] out_21
);

  wire AM_PM, AM_PM_a, amTh, and_1_out, and_2_out, and_3_out, and_4_out, and_5_out, and_6_out, and_7_out,
       and_8_out, and_9_out, and_10_out, and_11_out, and_12_out, and_13_out, and_14_out, and_15_out,
       and_16_out, and_17_out, and_18_out, and_19_out, and_21_out, comparator_1_eq, comparator_2_eq,
       comparator_3_eq, mTh, multiplexer_6_out, or_1_out, or_2_out, or_3_out, sTm, xnor_1_out,
       \六十进制计数器_1_nqcc , \六十进制计数器_2_nqcc , \六十进制计数器_3_nqcc , \十二进制或二十四进制可逆计数器电路_1_nqcc ,
       \十二进制或二十四进制可逆计数器电路_2_nqcc , \秒脉冲产生电路_1_out_2 ;
  wire [3:0] aH0, aH1, aM0, aM1, H0, H1, M0, M1, S0, S1;
  wire [7:0] multiplexer_1_out, multiplexer_2_out;

  and and_1 (and_1_out, ~Adj0, CP);  // AND_Gate
  and and_2 (and_2_out, CPu, and_3_out);
  and and_3 (and_3_out, Adj0, ~Set_Alarm, Adj1);  // AND_Gate
  and and_4 (and_4_out, CPu, and_5_out);
  and and_5 (and_5_out, Adj0, ~Set_Alarm, ~Adj1);  // AND_Gate
  \秒脉冲产生电路  \u_秒脉冲产生电路_1  (.in_1(and_1_out), .out_2(\秒脉冲产生电路_1_out_2 ));
  or or_1 (or_1_out, sTm, and_2_out);
  and and_6 (and_6_out, and_3_out, CPd);
  or or_2 (or_2_out, mTh, and_4_out);
  and and_7 (and_7_out, and_5_out, CPd);
  Comparator #(.mode("unsigned")) comparator_1 (.a({H1, H0}), .b({8{1'b0}}), .eq(comparator_1_eq));  // open: gt, lt
  Multiplexer #(.width(8), .enable("false")) multiplexer_1 (
    .in0({H1, H0}), .in1(8'h12), .out(multiplexer_1_out), .sel(comparator_1_eq));
  \六十进制计数器  \u_六十进制计数器_1  (
    .CPu(\秒脉冲产生电路_1_out_2 ), .CLS(and_8_out), .CPd(1'b0), .Adj(1'b0), .out_5(S0[3]), .out_6(S0[2]),
    .out_7(S0[1]), .out_8(S0[0]), .out_9(S1[3]), .out_10(S1[2]), .out_11(S1[1]), .out_12(S1[0]),
    .nQcc(\六十进制计数器_1_nqcc ));
  \六十进制计数器  \u_六十进制计数器_2  (
    .CPu(or_1_out), .CLS(and_9_out), .CPd(and_6_out), .Adj(and_3_out), .out_5(M0[3]), .out_6(M0[2]),
    .out_7(M0[1]), .out_8(M0[0]), .out_9(M1[3]), .out_10(M1[2]), .out_11(M1[1]), .out_12(M1[0]),
    .nQcc(\六十进制计数器_2_nqcc ));
  Multiplexer #(.width(8), .enable("false")) multiplexer_2 (
    .in0(multiplexer_1_out), .in1({H1, H0}), .out(multiplexer_2_out), .sel(Set));
  Multiplexer #(.width(8), .enable("false")) multiplexer_3 (
    .in0(multiplexer_2_out), .in1({aH1, aH0}), .out({out_12, \小时 }), .sel(Set_Alarm));
  Multiplexer #(.width(8), .enable("false")) multiplexer_4 (
    .in0({M1, M0}), .in1({aM1, aM0}), .out({out_16, \分钟 }), .sel(Set_Alarm));
  Multiplexer #(.width(8), .enable("false")) multiplexer_5 (
    .in0({S1, S0}), .in1({8{1'b0}}), .out({out_21, \秒 }), .sel(Set_Alarm));
  and and_8 (and_8_out, Clr, ~Set_Alarm);  // AND_Gate
  \十二进制或二十四进制可逆计数器电路  \u_十二进制或二十四进制可逆计数器电路_1  (
    .Set(Set), .Clr(and_10_out), .Adj(and_5_out), .CPu(or_2_out), .CPd(and_7_out), .out_6(H0[0]),
    .out_7(H0[1]), .out_8(H0[2]), .\输出 (H0[3]), .out_10(H1[0]), .out_11(H1[1]), .out_12(H1[2]),
    .out_13(H1[3]), .nQcc(\十二进制或二十四进制可逆计数器电路_1_nqcc ));
  not not_1 (sTm, \六十进制计数器_1_nqcc );
  not not_2 (mTh, \六十进制计数器_2_nqcc );
  and and_9 (and_9_out, Clr, ~Set_Alarm);  // AND_Gate
  T_Flip_Flop t_ff_1 (
    .clk(\十二进制或二十四进制可逆计数器电路_1_nqcc ), .T(1'b1), .Q(AM_PM), .preset(1'b0), .reset(and_10_out), .en(1'b1));  // open: Qn
  and and_10 (and_10_out, Clr, ~Set_Alarm);  // AND_Gate
  \电子钟整点报时电路  \u_电子钟整点报时电路_1  (.in_1(M1), .in_2(M0), .in_3(S1), .in_4(S0), .out_5(\定点报时 ));
  Multiplexer #(.enable("false")) multiplexer_6 (.in0(AM_PM), .in1(AM_PM_a), .out(multiplexer_6_out), .sel(Set_Alarm));
  xnor xnor_1 (xnor_1_out, AM_PM, AM_PM_a);
  Comparator #(.mode("unsigned")) comparator_2 (.a({H1, H0}), .b({aH1, aH0}), .eq(comparator_2_eq));  // open: gt, lt
  and and_11 (and_11_out, CPu, and_12_out);
  and and_12 (and_12_out, Adj0, Set_Alarm, Adj1);
  and and_13 (and_13_out, and_12_out, CPd);
  and and_14 (and_14_out, CPu, and_15_out);
  and and_15 (and_15_out, Adj0, Set_Alarm, ~Adj1);  // AND_Gate
  and and_16 (and_16_out, and_15_out, CPd);
  \上下午文字显示的电路  \u_上下午文字显示的电路_1  (
    .out_3(out_15), .out_4(out_17), .out_5(out_18), .out_6(out_19), .AM_PM(multiplexer_6_out), .TT(Set));
  and and_17 (and_17_out, xnor_1_out, comparator_2_eq);
  Comparator #(.mode("unsigned")) comparator_3 (.a({M1, M0}), .b({aM1, aM0}), .eq(comparator_3_eq));  // open: gt, lt
  \六十进制计数器  \u_六十进制计数器_3  (
    .CPu(and_11_out), .CLS(and_19_out), .CPd(and_13_out), .Adj(and_12_out), .out_5(aM0[3]), .out_6(aM0[2]),
    .out_7(aM0[1]), .out_8(aM0[0]), .out_9(aM1[3]), .out_10(aM1[2]), .out_11(aM1[1]), .out_12(aM1[0]),
    .nQcc(\六十进制计数器_3_nqcc ));
  and and_18 (and_18_out, and_17_out, Enable_Alarm, comparator_3_eq);
  \十二进制或二十四进制可逆计数器电路  \u_十二进制或二十四进制可逆计数器电路_2  (
    .Set(Set), .Clr(and_21_out), .Adj(and_15_out), .CPu(and_14_out), .CPd(and_16_out), .out_6(aH0[0]),
    .out_7(aH0[1]), .out_8(aH0[2]), .\输出 (aH0[3]), .out_10(aH1[0]), .out_11(aH1[1]), .out_12(aH1[2]),
    .out_13(aH1[3]), .nQcc(\十二进制或二十四进制可逆计数器电路_2_nqcc ));
  or or_3 (or_3_out, S1[0], S1[1], S1[2], S1[3]);
  not not_3 (amTh, \六十进制计数器_3_nqcc );
  and and_19 (and_19_out, Clr, Set_Alarm);
  and and_20 (\闹钟 , ~or_3_out, and_18_out, S0[0]);  // AND_Gate
  T_Flip_Flop t_ff_2 (
    .clk(\十二进制或二十四进制可逆计数器电路_2_nqcc ), .T(1'b1), .Q(AM_PM_a), .preset(1'b0), .reset(and_21_out), .en(1'b1));  // open: Qn
  and and_21 (and_21_out, Clr, Set_Alarm);

  // Other names for the same wires on the sheet: a0 = Adj0; a1 = Adj1; alarm = \闹钟 ; c = Clr; d = CPd;
  //   ea = Enable_Alarm; LED[19:0] = {out_19, out_18, out_17, out_15}; s = Set; sa = Set_Alarm; u = CPu

  // Notes on the sheet:
  //   输入
  //   秒计数输入
  //   分钟计数输入
  //   小时计数输入
  //   秒计数
  //   分钟计数
  //   小时计数
  //   输出
  //   秒计数输出
  //   分钟计数输出
  //   小时计数输出
  //   秒-分钟进位信号
  //   分钟-小时进位信号
  //   上下午切换信号
  //   LED输出
  //   LED
  //   闹钟输出
  //   闹钟定时
endmodule

module \多功能数字钟_含闹钟_测试电路  (
  input  in_1,
  input  in_2,
  input  in_3,
  input  in_4,
  input  in_5
);

  wire button_1_out, button_2_out, button_3_out, clock_1_out, \闹钟_小时制随电子钟_1_定点报时 , \闹钟_小时制随电子钟_1_闹钟 ;
  wire [3:0] \闹钟_小时制随电子钟_1_out_12 , \闹钟_小时制随电子钟_1_out_16 , \闹钟_小时制随电子钟_1_out_21 , \闹钟_小时制随电子钟_1_分钟 ,
       \闹钟_小时制随电子钟_1_小时 , \闹钟_小时制随电子钟_1_秒 ;
  wire [4:0] \闹钟_小时制随电子钟_1_out_15 , \闹钟_小时制随电子钟_1_out_17 , \闹钟_小时制随电子钟_1_out_18 , \闹钟_小时制随电子钟_1_out_19 ;

  DotMatrix #(.matrixcols(4), .matrixrows(5)) dotmatrix_1 (
    .col0(\闹钟_小时制随电子钟_1_out_15 ), .col1(\闹钟_小时制随电子钟_1_out_17 ), .col2(\闹钟_小时制随电子钟_1_out_18 ),
    .col3(\闹钟_小时制随电子钟_1_out_19 ));
  \闹钟_小时制随电子钟  \u_闹钟_小时制随电子钟_1  (
    .CP(clock_1_out), .Clr(button_3_out), .Adj0(in_1), .Adj1(in_2), .CPu(button_2_out), .CPd(button_1_out),
    .Set(in_3), .Set_Alarm(in_4), .Enable_Alarm(in_5), .\定点报时 (\闹钟_小时制随电子钟_1_定点报时 ),
    .\小时 (\闹钟_小时制随电子钟_1_小时 ), .out_12(\闹钟_小时制随电子钟_1_out_12 ), .\闹钟 (\闹钟_小时制随电子钟_1_闹钟 ),
    .\分钟 (\闹钟_小时制随电子钟_1_分钟 ), .out_15(\闹钟_小时制随电子钟_1_out_15 ), .out_16(\闹钟_小时制随电子钟_1_out_16 ),
    .out_17(\闹钟_小时制随电子钟_1_out_17 ), .out_18(\闹钟_小时制随电子钟_1_out_18 ), .out_19(\闹钟_小时制随电子钟_1_out_19 ),
    .\秒 (\闹钟_小时制随电子钟_1_秒 ), .out_21(\闹钟_小时制随电子钟_1_out_21 ));
  Clock clock_1 (.out(clock_1_out));
  Hex_Digit_Display hex_digit_display_1 (.value(\闹钟_小时制随电子钟_1_小时 ), .dp(1'b0));
  Hex_Digit_Display hex_digit_display_2 (.value(\闹钟_小时制随电子钟_1_out_12 ), .dp(1'b0));
  Button button_1 (.out(button_1_out));
  Button button_2 (.out(button_2_out));
  Hex_Digit_Display hex_digit_display_3 (.value(\闹钟_小时制随电子钟_1_out_16 ), .dp(1'b0));
  Button button_3 (.out(button_3_out));
  Hex_Digit_Display hex_digit_display_4 (.value(\闹钟_小时制随电子钟_1_out_21 ), .dp(1'b0));
  Hex_Digit_Display hex_digit_display_5 (.value(\闹钟_小时制随电子钟_1_分钟 ), .dp(1'b0));
  Hex_Digit_Display hex_digit_display_6 (.value(\闹钟_小时制随电子钟_1_秒 ), .dp(1'b0));
  LED led_1 (.in(\闹钟_小时制随电子钟_1_闹钟 ));
  LED led_2 (.in(\闹钟_小时制随电子钟_1_定点报时 ));

  // Notes on the sheet:
  //   闹钟设置：
  //   1. “设置闹钟”置1，开始设置闹钟
  //   2. Adj0 = 1 Adj1 = 0时使用CPu CPd调节小时
  //   3. Adj0 = 1 Adj1 = 1时使用CPu CPd调节分钟
  //   4. Clr 可以清零，闹钟的小时制与Set相关
  //   6. 闹钟设置和正常显示时间无关
  //   5. “设置闹钟”置0恢复原钟面，完成闹钟设置，开启闹钟后才会触发闹钟
endmodule
