// Logisim project 实验6.circ as structural Verilog: 10 circuits, main circuit sqrX
module sqrX (
  input  [31:0] a,
  input  [31:0] c,
  input  [31:0] b,
  input  [31:0] d,
  output [31:0] a_prime,
  output [31:0] b_prime,
  output [31:0] c_prime,
  output [31:0] d_prime
);

  wire [31:0] multiplier_1_out, multiplier_2_out, multiplier_3_out, multiplier_4_out, multiplier_5_out,
       multiplier_6_out, multiplier_7_out;

  Multiplier #(.width(32)) multiplier_1 (.a(a), .b(a), .out(multiplier_1_out), .cin({32{1'b0}}));  // open: cout
  Multiplier #(.width(32)) multiplier_2 (.a(b), .b(c), .out(multiplier_2_out), .cin({32{1'b0}}));  // open: cout
  Multiplier #(.width(32)) multiplier_3 (.a(d), .b(d), .out(multiplier_3_out), .cin({32{1'b0}}));  // open: cout
  Adder #(.width(32)) adder_1 (.a(multiplier_1_out), .b(multiplier_2_out), .out(a_prime), .cin(1'b0));  // open: cout
  Adder #(.width(32)) adder_2 (.a(multiplier_2_out), .b(multiplier_3_out), .out(d_prime), .cin(1'b0));  // open: cout
  Multiplier #(.width(32)) multiplier_4 (.a(a), .b(b), .out(multiplier_4_out), .cin({32{1'b0}}));  // open: cout
  Adder #(.width(32)) adder_3 (.a(multiplier_4_out), .b(multiplier_5_out), .out(b_prime), .cin(1'b0));  // open: cout
  Multiplier #(.width(32)) multiplier_5 (.a(b), .b(d), .out(multiplier_5_out), .cin({32{1'b0}}));  // open: cout
  Multiplier #(.width(32)) multiplier_6 (.a(a), .b(c), .out(multiplier_6_out), .cin({32{1'b0}}));  // open: cout
  Adder #(.width(32)) adder_4 (.a(multiplier_6_out), .b(multiplier_7_out), .out(c_prime), .cin(1'b0));  // open: cout
  Multiplier #(.width(32)) multiplier_7 (.a(d), .b(c), .out(multiplier_7_out), .cin({32{1'b0}}));  // open: cout
endmodule

module sqrX_A (
  input  [31:0] a,
  input  [31:0] c,
  input  [31:0] b,
  input  [31:0] d,
  output [31:0] a_prime,
  output [31:0] b_prime,
  output [31:0] c_prime,
  output [31:0] d_prime
);

  wire [31:0] adder_3_out, adder_4_out, multiplier_1_out, multiplier_2_out, multiplier_3_out,
       multiplier_4_out, multiplier_5_out, multiplier_6_out, multiplier_7_out, multiplier_8_out;

  Multiplier #(.width(32)) multiplier_1 (.a(a), .b(b), .out(multiplier_1_out), .cin({32{1'b0}}));  // open: cout
  Multiplier #(.width(32)) multiplier_2 (.a(b), .b(d), .out(multiplier_2_out), .cin({32{1'b0}}));  // open: cout
  Multiplier #(.width(32)) multiplier_3 (.a(c), .b(b), .out(multiplier_3_out), .cin({32{1'b0}}));  // open: cout
  Multiplier #(.width(32)) multiplier_4 (.a(d), .b(d), .out(multiplier_4_out), .cin({32{1'b0}}));  // open: cout
  Adder #(.width(32)) adder_1 (.a(multiplier_1_out), .b(multiplier_2_out), .out(a_prime), .cin(1'b0));  // open: cout
  Adder #(.width(32)) adder_2 (.a(multiplier_3_out), .b(multiplier_4_out), .out(c_prime), .cin(1'b0));  // open: cout
  Multiplier #(.width(32)) multiplier_5 (.a(a), .b(a), .out(multiplier_5_out), .cin({32{1'b0}}));  // open: cout
  Adder #(.width(32)) adder_3 (
    .a(multiplier_5_out), .b(multiplier_6_out), .out(adder_3_out), .cin(1'b0));  // open: cout
  Multiplier #(.width(32)) multiplier_6 (.a(b), .b(c), .out(multiplier_6_out), .cin({32{1'b0}}));  // open: cout
  Multiplier #(.width(32)) multiplier_7 (.a(a), .b(c), .out(multiplier_7_out), .cin({32{1'b0}}));  // open: cout
  Adder #(.width(32)) adder_4 (
    .a(multiplier_7_out), .b(multiplier_8_out), .out(adder_4_out), .cin(1'b0));  // open: cout
  Multiplier #(.width(32)) multiplier_8 (.a(d), .b(c), .out(multiplier_8_out), .cin({32{1'b0}}));  // open: cout
  Adder #(.width(32)) adder_5 (.a(a_prime), .b(adder_3_out), .out(b_prime), .cin(1'b0));  // open: cout
  Adder #(.width(32)) adder_6 (.a(c_prime), .b(adder_4_out), .out(d_prime), .cin(1'b0));  // open: cout
endmodule

module \大于4加3模块  (
  input  [3:0] in_1,
  output [3:0] out_2
);

  wire nand_1_out, or_1_out, or_2_out;
  wire [3:0] adder_1_out;

  or or_1 (or_1_out, in_1[0], in_1[1], in_1[3]);
  or or_2 (or_2_out, in_1[3], in_1[2]);
  Adder #(.width(4)) adder_1 (.a(4'b0011), .b(in_1), .out(adder_1_out), .cin(1'b0));  // open: cout
  nand nand_1 (nand_1_out, or_1_out, or_2_out);
  Multiplexer #(.width(4), .enable("false")) multiplexer_1 (
    .in0(adder_1_out), .in1(in_1), .out(out_2), .sel(nand_1_out));
endmodule

module \_64位左移模块  (
  input  [31:0] in_h32,
  input  [31:0] in_l32,
  input  shift_in,
  output [31:0] out_h32,
  output [31:0] out_l32
);


  assign out_h32 = {in_h32[30:0], in_l32[31]};
  assign out_l32 = {in_l32[30:0], shift_in};
endmodule

module \_64位左移加三模块  (
  input  [31:0] in_h32,
  input  [31:0] in_l32,
  input  shift_in,
  output [31:0] out_h32,
  output [31:0] out_l32
);

  wire [31:0] \n64位左移模块_1_out_h32 , \n64位左移模块_1_out_l32 ;

  \_64位左移模块  \u_64位左移模块_1  (
    .in_h32(in_h32), .in_l32(in_l32), .shift_in(shift_in), .out_h32(\n64位左移模块_1_out_h32 ),
    .out_l32(\n64位左移模块_1_out_l32 ));
  \大于4加3模块  \u_大于4加3模块_1  (.in_1(\n64位左移模块_1_out_h32 [3:0]), .out_2(out_h32[3:0]));
  \大于4加3模块  \u_大于4加3模块_2  (.in_1(\n64位左移模块_1_out_h32 [7:4]), .out_2(out_h32[7:4]));
  \大于4加3模块  \u_大于4加3模块_3  (.in_1(\n64位左移模块_1_out_h32 [11:8]), .out_2(out_h32[11:8]));
  \大于4加3模块  \u_大于4加3模块_4  (.in_1(\n64位左移模块_1_out_h32 [15:12]), .out_2(out_h32[15:12]));
  \大于4加3模块  \u_大于4加3模块_5  (.in_1(\n64位左移模块_1_out_l32 [3:0]), .out_2(out_l32[3:0]));
  \大于4加3模块  \u_大于4加3模块_6  (.in_1(\n64位左移模块_1_out_l32 [7:4]), .out_2(out_l32[7:4]));
  \大于4加3模块  \u_大于4加3模块_7  (.in_1(\n64位左移模块_1_out_l32 [11:8]), .out_2(out_l32[11:8]));
  \大于4加3模块  \u_大于4加3模块_8  (.in_1(\n64位左移模块_1_out_l32 [15:12]), .out_2(out_l32[15:12]));
  \大于4加3模块  \u_大于4加3模块_9  (.in_1(\n64位左移模块_1_out_h32 [19:16]), .out_2(out_h32[19:16]));
  \大于4加3模块  \u_大于4加3模块_10  (.in_1(\n64位左移模块_1_out_h32 [23:20]), .out_2(out_h32[23:20]));
  \大于4加3模块  \u_大于4加3模块_11  (.in_1(\n64位左移模块_1_out_h32 [27:24]), .out_2(out_h32[27:24]));
  \大于4加3模块  \u_大于4加3模块_12  (.in_1(\n64位左移模块_1_out_h32 [31:28]), .out_2(out_h32[31:28]));
  \大于4加3模块  \u_大于4加3模块_13  (.in_1(\n64位左移模块_1_out_l32 [19:16]), .out_2(out_l32[19:16]));
  \大于4加3模块  \u_大于4加3模块_14  (.in_1(\n64位左移模块_1_out_l32 [23:20]), .out_2(out_l32[23:20]));
  \大于4加3模块  \u_大于4加3模块_15  (.in_1(\n64位左移模块_1_out_l32 [27:24]), .out_2(out_l32[27:24]));
  \大于4加3模块  \u_大于4加3模块_16  (.in_1(\n64位左移模块_1_out_l32 [31:28]), .out_2(out_l32[31:28]));
endmodule

module \Fibonacci数显示模块  (
  input  [31:0] in,
  output [3:0] out_2,
  output [3:0] out_3,
  output [3:0] out_4,
  output [3:0] out_5,
  output [3:0] out_6,
  output [3:0] out_7,
  output [3:0] out_8,
  output [3:0] out_9,
  output [3:0] out_10,
  output [3:0] out_11
);

  wire [31:0] \n64位左移加三模块_1_out_h32 , \n64位左移加三模块_1_out_l32 , \n64位左移加三模块_2_out_h32 , \n64位左移加三模块_2_out_l32 ,
       \n64位左移加三模块_3_out_h32 , \n64位左移加三模块_3_out_l32 , \n64位左移加三模块_4_out_h32 , \n64位左移加三模块_4_out_l32 ,
       \n64位左移加三模块_5_out_h32 , \n64位左移加三模块_5_out_l32 , \n64位左移加三模块_6_out_h32 , \n64位左移加三模块_6_out_l32 ,
       \n64位左移加三模块_7_out_h32 , \n64位左移加三模块_7_out_l32 , \n64位左移加三模块_8_out_h32 , \n64位左移加三模块_8_out_l32 ,
       \n64位左移加三模块_9_out_h32 , \n64位左移加三模块_9_out_l32 , \n64位左移加三模块_10_out_h32 , \n64位左移加三模块_10_out_l32 ,
       \n64位左移加三模块_11_out_h32 , \n64位左移加三模块_11_out_l32 , \n64位左移加三模块_12_out_h32 , \n64位左移加三模块_12_out_l32 ,
       \n64位左移加三模块_13_out_h32 , \n64位左移加三模块_13_out_l32 , \n64位左移加三模块_14_out_h32 , \n64位左移加三模块_14_out_l32 ,
       \n64位左移加三模块_15_out_h32 , \n64位左移加三模块_15_out_l32 , \n64位左移加三模块_16_out_h32 , \n64位左移加三模块_16_out_l32 ,
       \n64位左移加三模块_17_out_h32 , \n64位左移加三模块_17_out_l32 , \n64位左移加三模块_18_out_h32 , \n64位左移加三模块_18_out_l32 ,
       \n64位左移加三模块_19_out_h32 , \n64位左移加三模块_19_out_l32 , \n64位左移加三模块_20_out_h32 , \n64位左移加三模块_20_out_l32 ,
       \n64位左移加三模块_21_out_h32 , \n64位左移加三模块_21_out_l32 , \n64位左移加三模块_22_out_h32 , \n64位左移加三模块_22_out_l32 ,
       \n64位左移加三模块_23_out_h32 , \n64位左移加三模块_23_out_l32 , \n64位左移加三模块_24_out_h32 , \n64位左移加三模块_24_out_l32 ,
       \n64位左移加三模块_25_out_h32 , \n64位左移加三模块_25_out_l32 , \n64位左移加三模块_26_out_h32 , \n64位左移加三模块_26_out_l32 ,
       \n64位左移加三模块_27_out_h32 , \n64位左移加三模块_27_out_l32 , \n64位左移加三模块_28_out_h32 , \n64位左移加三模块_28_out_l32 ,
       \n64位左移加三模块_29_out_h32 , \n64位左移加三模块_29_out_l32 , \n64位左移模块_1_out_h32 , \n64位左移模块_1_out_l32 ,
       \n64位左移模块_3_out_h32 , \n64位左移模块_3_out_l32 ;
  wire [31:8] \n64位左移模块_2_out_h32 ;

  \_64位左移模块  \u_64位左移模块_1  (
    .in_h32({32{1'b0}}), .in_l32({32{1'b0}}), .shift_in(in[31]), .out_h32(\n64位左移模块_1_out_h32 ),
    .out_l32(\n64位左移模块_1_out_l32 ));
  \_64位左移模块  \u_64位左移模块_2  (
    .in_h32(\n64位左移加三模块_2_out_h32 ), .in_l32(\n64位左移加三模块_2_out_l32 ), .shift_in(in[0]),
    .out_h32({\n64位左移模块_2_out_h32 , out_11, out_10}),
    .out_l32({out_9, out_8, out_7, out_6, out_5, out_4, out_3, out_2}));
  \_64位左移模块  \u_64位左移模块_3  (
    .in_h32(\n64位左移模块_1_out_h32 ), .in_l32(\n64位左移模块_1_out_l32 ), .shift_in(in[30]),
    .out_h32(\n64位左移模块_3_out_h32 ), .out_l32(\n64位左移模块_3_out_l32 ));
  \_64位左移加三模块  \u_64位左移加三模块_1  (
    .in_h32(\n64位左移模块_3_out_h32 ), .in_l32(\n64位左移模块_3_out_l32 ), .shift_in(in[29]),
    .out_h32(\n64位左移加三模块_1_out_h32 ), .out_l32(\n64位左移加三模块_1_out_l32 ));
  \_64位左移加三模块  \u_64位左移加三模块_2  (
    .in_h32(\n64位左移加三模块_5_out_h32 ), .in_l32(\n64位左移加三模块_5_out_l32 ), .shift_in(in[1]),
    .out_h32(\n64位左移加三模块_2_out_h32 ), .out_l32(\n64位左移加三模块_2_out_l32 ));
  \_64位左移加三模块  \u_64位左移加三模块_3  (
    .in_h32(\n64位左移加三模块_1_out_h32 ), .in_l32(\n64位左移加三模块_1_out_l32 ), .shift_in(in[28]),
    .out_h32(\n64位左移加三模块_3_out_h32 ), .out_l32(\n64位左移加三模块_3_out_l32 ));
  \_64位左移加三模块  \u_64位左移加三模块_4  (
    .in_h32(\n64位左移加三模块_8_out_h32 ), .in_l32(\n64位左移加三模块_8_out_l32 ), .shift_in(in[3]),
    .out_h32(\n64位左移加三模块_4_out_h32 ), .out_l32(\n64位左移加三模块_4_out_l32 ));
  \_64位左移加三模块  \u_64位左移加三模块_5  (
    .in_h32(\n64位左移加三模块_4_out_h32 ), .in_l32(\n64位左移加三模块_4_out_l32 ), .shift_in(in[2]),
    .out_h32(\n64位左移加三模块_5_out_h32 ), .out_l32(\n64位左移加三模块_5_out_l32 ));
  \_64位左移加三模块  \u_64位左移加三模块_6  (
    .in_h32(\n64位左移加三模块_3_out_h32 ), .in_l32(\n64位左移加三模块_3_out_l32 ), .shift_in(in[27]),
    .out_h32(\n64位左移加三模块_6_out_h32 ), .out_l32(\n64位左移加三模块_6_out_l32 ));
  \_64位左移加三模块  \u_64位左移加三模块_7  (
    .in_h32(\n64位左移加三模块_6_out_h32 ), .in_l32(\n64位左移加三模块_6_out_l32 ), .shift_in(in[26]),
    .out_h32(\n64位左移加三模块_7_out_h32 ), .out_l32(\n64位左移加三模块_7_out_l32 ));
  \_64位左移加三模块  \u_64位左移加三模块_8  (
    .in_h32(\n64位左移加三模块_11_out_h32 ), .in_l32(\n64位左移加三模块_11_out_l32 ), .shift_in(in[4]),
    .out_h32(\n64位左移加三模块_8_out_h32 ), .out_l32(\n64位左移加三模块_8_out_l32 ));
  \_64位左移加三模块  \u_64位左移加三模块_9  (
    .in_h32(\n64位左移加三模块_7_out_h32 ), .in_l32(\n64位左移加三模块_7_out_l32 ), .shift_in(in[25]),
    .out_h32(\n64位左移加三模块_9_out_h32 ), .out_l32(\n64位左移加三模块_9_out_l32 ));
  \_64位左移加三模块  \u_64位左移加三模块_10  (
    .in_h32(\n64位左移加三模块_15_out_h32 ), .in_l32(\n64位左移加三模块_15_out_l32 ), .shift_in(in[6]),
    .out_h32(\n64位左移加三模块_10_out_h32 ), .out_l32(\n64位左移加三模块_10_out_l32 ));
  \_64位左移加三模块  \u_64位左移加三模块_11  (
    .in_h32(\n64位左移加三模块_10_out_h32 ), .in_l32(\n64位左移加三模块_10_out_l32 ), .shift_in(in[5]),
    .out_h32(\n64位左移加三模块_11_out_h32 ), .out_l32(\n64位左移加三模块_11_out_l32 ));
  \_64位左移加三模块  \u_64位左移加三模块_12  (
    .in_h32(\n64位左移加三模块_9_out_h32 ), .in_l32(\n64位左移加三模块_9_out_l32 ), .shift_in(in[24]),
    .out_h32(\n64位左移加三模块_12_out_h32 ), .out_l32(\n64位左移加三模块_12_out_l32 ));
  \_64位左移加三模块  \u_64位左移加三模块_13  (
    .in_h32(\n64位左移加三模块_12_out_h32 ), .in_l32(\n64位左移加三模块_12_out_l32 ), .shift_in(in[23]),
    .out_h32(\n64位左移加三模块_13_out_h32 ), .out_l32(\n64位左移加三模块_13_out_l32 ));
  \_64位左移加三模块  \u_64位左移加三模块_14  (
    .in_h32(\n64位左移加三模块_18_out_h32 ), .in_l32(\n64位左移加三模块_18_out_l32 ), .shift_in(in[8]),
    .out_h32(\n64位左移加三模块_14_out_h32 ), .out_l32(\n64位左移加三模块_14_out_l32 ));
  \_64位左移加三模块  \u_64位左移加三模块_15  (
    .in_h32(\n64位左移加三模块_14_out_h32 ), .in_l32(\n64位左移加三模块_14_out_l32 ), .shift_in(in[7]),
    .out_h32(\n64位左移加三模块_15_out_h32 ), .out_l32(\n64位左移加三模块_15_out_l32 ));
  \_64位左移加三模块  \u_64位左移加三模块_16  (
    .in_h32(\n64位左移加三模块_13_out_h32 ), .in_l32(\n64位左移加三模块_13_out_l32 ), .shift_in(in[22]),
    .out_h32(\n64位左移加三模块_16_out_h32 ), .out_l32(\n64位左移加三模块_16_out_l32 ));
  \_64位左移加三模块  \u_64位左移加三模块_17  (
    .in_h32(\n64位左移加三模块_16_out_h32 ), .in_l32(\n64位左移加三模块_16_out_l32 ), .shift_in(in[21]),
    .out_h32(\n64位左移加三模块_17_out_h32 ), .out_l32(\n64位左移加三模块_17_out_l32 ));
  \_64位左移加三模块  \u_64位左移加三模块_18  (
    .in_h32(\n64位左移加三模块_20_out_h32 ), .in_l32(\n64位左移加三模块_20_out_l32 ), .shift_in(in[9]),
    .out_h32(\n64位左移加三模块_18_out_h32 ), .out_l32(\n64位左移加三模块_18_out_l32 ));
  \_64位左移加三模块  \u_64位左移加三模块_19  (
    .in_h32(\n64位左移加三模块_17_out_h32 ), .in_l32(\n64位左移加三模块_17_out_l32 ), .shift_in(in[20]),
    .out_h32(\n64位左移加三模块_19_out_h32 ), .out_l32(\n64位左移加三模块_19_out_l32 ));
  \_64位左移加三模块  \u_64位左移加三模块_20  (
    .in_h32(\n64位左移加三模块_21_out_h32 ), .in_l32(\n64位左移加三模块_21_out_l32 ), .shift_in(in[10]),
    .out_h32(\n64位左移加三模块_20_out_h32 ), .out_l32(\n64位左移加三模块_20_out_l32 ));
  \_64位左移加三模块  \u_64位左移加三模块_21  (
    .in_h32(\n64位左移加三模块_24_out_h32 ), .in_l32(\n64位左移加三模块_24_out_l32 ), .shift_in(in[11]),
    .out_h32(\n64位左移加三模块_21_out_h32 ), .out_l32(\n64位左移加三模块_21_out_l32 ));
  \_64位左移加三模块  \u_64位左移加三模块_22  (
    .in_h32(\n64位左移加三模块_23_out_h32 ), .in_l32(\n64位左移加三模块_23_out_l32 ), .shift_in(in[18]),
    .out_h32(\n64位左移加三模块_22_out_h32 ), .out_l32(\n64位左移加三模块_22_out_l32 ));
  \_64位左移加三模块  \u_64位左移加三模块_23  (
    .in_h32(\n64位左移加三模块_19_out_h32 ), .in_l32(\n64位左移加三模块_19_out_l32 ), .shift_in(in[19]),
    .out_h32(\n64位左移加三模块_23_out_h32 ), .out_l32(\n64位左移加三模块_23_out_l32 ));
  \_64位左移加三模块  \u_64位左移加三模块_24  (
    .in_h32(\n64位左移加三模块_26_out_h32 ), .in_l32(\n64位左移加三模块_26_out_l32 ), .shift_in(in[12]),
    .out_h32(\n64位左移加三模块_24_out_h32 ), .out_l32(\n64位左移加三模块_24_out_l32 ));
  \_64位左移加三模块  \u_64位左移加三模块_25  (
    .in_h32(\n64位左移加三模块_22_out_h32 ), .in_l32(\n64位左移加三模块_22_out_l32 ), .shift_in(in[17]),
    .out_h32(\n64位左移加三模块_25_out_h32 ), .out_l32(\n64位左移加三模块_25_out_l32 ));
  \_64位左移加三模块  \u_64位左移加三模块_26  (
    .in_h32(\n64位左移加三模块_27_out_h32 ), .in_l32(\n64位左移加三模块_27_out_l32 ), .shift_in(in[13]),
    .out_h32(\n64位左移加三模块_26_out_h32 ), .out_l32(\n64位左移加三模块_26_out_l32 ));
  \_64位左移加三模块  \u_64位左移加三模块_27  (
    .in_h32(\n64位左移加三模块_29_out_h32 ), .in_l32(\n64位左移加三模块_29_out_l32 ), .shift_in(in[14]),
    .out_h32(\n64位左移加三模块_27_out_h32 ), .out_l32(\n64位左移加三模块_27_out_l32 ));
  \_64位左移加三模块  \u_64位左移加三模块_28  (
    .in_h32(\n64位左移加三模块_25_out_h32 ), .in_l32(\n64位左移加三模块_25_out_l32 ), .shift_in(in[16]),
    .out_h32(\n64位左移加三模块_28_out_h32 ), .out_l32(\n64位左移加三模块_28_out_l32 ));
  \_64位左移加三模块  \u_64位左移加三模块_29  (
    .in_h32(\n64位左移加三模块_28_out_h32 ), .in_l32(\n64位左移加三模块_28_out_l32 ), .shift_in(in[15]),
    .out_h32(\n64位左移加三模块_29_out_h32 ), .out_l32(\n64位左移加三模块_29_out_l32 ));
endmodule

module \矩阵快速幂模块  (
  input  clk,
  input  clr,
  input  start,
  input  n_i_1,
  output [31:0] Fn
);

  wire and_1_out;
  wire [31:0] multiplexer_1_out, multiplexer_2_out, multiplexer_3_out, multiplexer_4_out, multiplexer_5_out,
       multiplexer_6_out, multiplexer_7_out, multiplexer_8_out, register_1_q, register_3_q, register_4_q,
       sqrx_1_a_prime, sqrx_1_b_prime, sqrx_1_c_prime, sqrx_1_d_prime, sqrx_a_1_a_prime, sqrx_a_1_b_prime,
       sqrx_a_1_c_prime, sqrx_a_1_d_prime;

  and and_1 (and_1_out, ~clr, start);  // AND_Gate
  Multiplexer #(.width(32), .enable("false")) multiplexer_1 (
    .in0({32{1'b0}}), .in1(multiplexer_5_out), .out(multiplexer_1_out), .sel(and_1_out));
  Multiplexer #(.width(32), .enable("false")) multiplexer_2 (
    .in0(32'h1), .in1(multiplexer_6_out), .out(multiplexer_2_out), .sel(and_1_out));
  Multiplexer #(.width(32), .enable("false")) multiplexer_3 (
    .in0(32'h1), .in1(multiplexer_7_out), .out(multiplexer_3_out), .sel(and_1_out));
  Multiplexer #(.width(32), .enable("false")) multiplexer_4 (
    .in0(32'h1), .in1(multiplexer_8_out), .out(multiplexer_4_out), .sel(and_1_out));
  Register #(.width(32), .trigger("falling")) register_1 (
    .D(multiplexer_1_out), .en(1'b1), .Q(register_1_q), .clk(clk), .clr(clr));
  Register #(.width(32), .trigger("falling")) register_2 (
    .D(multiplexer_2_out), .en(1'b1), .Q(Fn), .clk(clk), .clr(clr));
  Register #(.width(32), .trigger("falling")) register_3 (
    .D(multiplexer_3_out), .en(1'b1), .Q(register_3_q), .clk(clk), .clr(clr));
  Register #(.width(32), .trigger("falling")) register_4 (
    .D(multiplexer_4_out), .en(1'b1), .Q(register_4_q), .clk(clk), .clr(clr));
  sqrX sqrx_1 (
    .a(register_1_q), .c(register_3_q), .b(Fn), .d(register_4_q), .a_prime(sqrx_1_a_prime),
    .b_prime(sqrx_1_b_prime), .c_prime(sqrx_1_c_prime), .d_prime(sqrx_1_d_prime));
  sqrX_A sqrx_a_1 (
    .a(register_1_q), .c(register_3_q), .b(Fn), .d(register_4_q), .a_prime(sqrx_a_1_a_prime),
    .b_prime(sqrx_a_1_b_prime), .c_prime(sqrx_a_1_c_prime), .d_prime(sqrx_a_1_d_prime));
  Multiplexer #(.width(32), .enable("false")) multiplexer_5 (
    .in0(sqrx_1_a_prime), .in1(sqrx_a_1_a_prime), .out(multiplexer_5_out), .sel(n_i_1));
  Multiplexer #(.width(32), .enable("false")) multiplexer_6 (
    .in0(sqrx_1_b_prime), .in1(sqrx_a_1_b_prime), .out(multiplexer_6_out), .sel(n_i_1));
  Multiplexer #(.width(32), .enable("false")) multiplexer_7 (
    .in0(sqrx_1_c_prime), .in1(sqrx_a_1_c_prime), .out(multiplexer_7_out), .sel(n_i_1));
  Multiplexer #(.width(32), .enable("false")) multiplexer_8 (
    .in0(sqrx_1_d_prime), .in1(sqrx_a_1_d_prime), .out(multiplexer_8_out), .sel(n_i_1));
endmodule

module \控制模块  (
  input  [5:0] n,
  input  clk,
  input  clr,
  output start,
  output clr_2,
  output n_i_1,
  output clk_2
);

  wire comparator_1_gt, not_1_out, or_1_out, or_2_out, shift_register_1_out;
  wire [7:0] counter_1_q;

  Counter counter_1 (.load(1'b0), .D({8{1'b0}}), .count(1'b1), .Q(counter_1_q), .clk(clk_2), .clr(clr));  // open: carry
  Comparator comparator_1 (.a(8'h6), .b(counter_1_q), .gt(comparator_1_gt));  // open: eq, lt
  and and_1 (clk_2, comparator_1_gt, clk);
  not not_1 (not_1_out, clr);
  Shift_Register #(.length(7)) shift_register_1 (
    .shift(not_1_out), .in(1'b0), .clk(or_1_out), .out(shift_register_1_out), .load(clr), .clr(1'b0),
    .d0(n[0]), .d1(n[1]), .d2(n[2]), .d3(n[3]), .d4(n[4]), .d5(n[5]), .d6(1'b0), .q6(n_i_1));  // open: q0, q1, q2, q3, q4, q5
  or or_1 (or_1_out, clr, clk_2);
  D_Flip_Flop d_ff_1 (.clk(clk_2), .D(or_2_out), .Q(start), .preset(1'b0), .en(1'b1), .reset(clr));  // open: Qn
  or or_2 (or_2_out, start, shift_register_1_out);

  assign clr_2 = clr;
endmodule

module \斐波那契_Fibonacci_数列计算器  (
  input  [5:0] in_1,
  input  in_2,
  input  in_3,
  output [3:0] out_4,
  output [3:0] out_5,
  output [3:0] out_6,
  output [3:0] out_7,
  output [3:0] out_8,
  output [3:0] out_9,
  output [3:0] out_10,
  output [3:0] out_11,
  output [3:0] out_12,
  output [3:0] out_13
);

  wire \控制模块_1_clk_2 , \控制模块_1_clr_2 , \控制模块_1_n_i_1 , \控制模块_1_start ;
  wire [31:0] \矩阵快速幂模块_1_fn ;

  \控制模块  \u_控制模块_1  (
    .clk(in_2), .clr(in_3), .start(\控制模块_1_start ), .clr_2(\控制模块_1_clr_2 ), .n(in_1), .clk_2(\控制模块_1_clk_2 ),
    .n_i_1(\控制模块_1_n_i_1 ));
  \矩阵快速幂模块  \u_矩阵快速幂模块_1  (
    .start(\控制模块_1_start ), .clr(\控制模块_1_clr_2 ), .clk(\控制模块_1_clk_2 ), .n_i_1(\控制模块_1_n_i_1 ),
    .Fn(\矩阵快速幂模块_1_fn ));
  \Fibonacci数显示模块  \fibonacci数显示模块_1  (
    .in(\矩阵快速幂模块_1_fn ), .out_2(out_13), .out_3(out_12), .out_4(out_11), .out_5(out_10), .out_6(out_9),
    .out_7(out_8), .out_8(out_7), .out_9(out_6), .out_10(out_5), .out_11(out_4));
endmodule

module \斐波那契_Fibonacci_数列计算器验证电路  (
  input  [5:0] in_1
);

  wire button_1_out, button_2_out;
  wire [3:0] \斐波那契_fibonacci_数列计算器_1_out_4 , \斐波那契_fibonacci_数列计算器_1_out_5 , \斐波那契_fibonacci_数列计算器_1_out_6 ,
       \斐波那契_fibonacci_数列计算器_1_out_7 , \斐波那契_fibonacci_数列计算器_1_out_8 , \斐波那契_fibonacci_数列计算器_1_out_9 ,
       \斐波那契_fibonacci_数列计算器_1_out_10 , \斐波那契_fibonacci_数列计算器_1_out_11 , \斐波那契_fibonacci_数列计算器_1_out_12 ,
       \斐波那契_fibonacci_数列计算器_1_out_13 ;

  Button button_1 (.out(button_1_out));
  Button button_2 (.out(button_2_out));
  // Probe on in_1
  Hex_Digit_Display hex_digit_display_1 (.value(\斐波那契_fibonacci_数列计算器_1_out_4 ), .dp(1'b0));
  Hex_Digit_Display hex_digit_display_2 (.value(\斐波那契_fibonacci_数列计算器_1_out_5 ), .dp(1'b0));
  \斐波那契_Fibonacci_数列计算器  \u_斐波那契_fibonacci_数列计算器_1  (
    .in_3(button_2_out), .in_1(in_1), .out_4(\斐波那契_fibonacci_数列计算器_1_out_4 ),
    .out_5(\斐波那契_fibonacci_数列计算器_1_out_5 ), .out_6(\斐波那契_fibonacci_数列计算器_1_out_6 ),
    .out_7(\斐波那契_fibonacci_数列计算器_1_out_7 ), .out_8(\斐波那契_fibonacci_数列计算器_1_out_8 ),
    .out_9(\斐波那契_fibonacci_数列计算器_1_out_9 ), .out_10(\斐波那契_fibonacci_数列计算器_1_out_10 ),
    .out_11(\斐波那契_fibonacci_数列计算器_1_out_11 ), .out_12(\斐波那契_fibonacci_数列计算器_1_out_12 ),
    .out_13(\斐波那契_fibonacci_数列计算器_1_out_13 ), .in_2(button_1_out));
  Hex_Digit_Display hex_digit_display_3 (.value(\斐波那契_fibonacci_数列计算器_1_out_7 ), .dp(1'b0));
  Hex_Digit_Display hex_digit_display_4 (.value(\斐波那契_fibonacci_数列计算器_1_out_6 ), .dp(1'b0));
  Hex_Digit_Display hex_digit_display_5 (.value(\斐波那契_fibonacci_数列计算器_1_out_8 ), .dp(1'b0));
  Hex_Digit_Display hex_digit_display_6 (.value(\斐波那契_fibonacci_数列计算器_1_out_9 ), .dp(1'b0));
  Hex_Digit_Display hex_digit_display_7 (.value(\斐波那契_fibonacci_数列计算器_1_out_10 ), .dp(1'b0));
  Hex_Digit_Display hex_digit_display_8 (.value(\斐波那契_fibonacci_数列计算器_1_out_11 ), .dp(1'b0));
  Hex_Digit_Display hex_digit_display_9 (.value(\斐波那契_fibonacci_数列计算器_1_out_12 ), .dp(1'b0));
  Hex_Digit_Display hex_digit_display_10 (.value(\斐波那契_fibonacci_数列计算器_1_out_13 ), .dp(1'b0));
endmodule
