// Logisim project cpu24.circ as structural Verilog: 24 circuits, main circuit ◇单周期MIPS
module \单周期MIPS  (
  input  IR1,
  input  IR2,
  input  IR3,
  output RegWrite,
  output MemWrite,
  output [31:0] PC,
  output [31:0] IR,
  output [31:0] RDin,
  output [31:0] MDin,
  output [31:0] LedData
);

  wire ALU_SRC, and_1_out, and_3_out, and_4_out, and_5_out, and_6_out, B, BEQ, BGEZ, BNE, CLK,
       comparator_1_eq, comparator_2_eq, comparator_2_lt, d_ff_1_q, equ, ERET, GEZ, Go, IR1_t, IR2_t, IR3_t,
       IRA, IRB, IRC, JAL, JMP, JR, LedOut, MemToReg, nand_2_out, RegDst, rst, run, sel1, sel2, sel3, sel4,
       SignedExt, SRLV, syscall, undriven, W1, W2, W3;
  wire [2:0] or_1_out;
  wire [3:0] ALU_OP, decoder_1_out0;
  wire [4:0] multiplexer_3_out, multiplexer_4_out, multiplexer_5_out, multiplexer_7_out;
  wire [7:0] demultiplexer_1_out0, demultiplexer_1_out1, demultiplexer_1_out2, demultiplexer_1_out3, MDin1,
       MDin2, MDin3, MDin4;
  wire [9:0] MemAddr;
  wire [12:0] CNT_num;
  wire [15:0] \总周期数 ;
  wire [31:0] BAddr, bit_extender_1_out, bit_extender_2_out, ExtImm, MDout, multiplexer_6_out, nextPC, PC_4,
       R, R1, shifter_1_out;

  Clock #(.highDuration(1), .lowDuration(1)) clock_1 (.out(CLK));
  Button _1 (.out(IRA));
  Button _2 (.out(IRB));
  Button _3 (.out(IRC));
  Button \u_继续运行  (.out(Go));
  LED #(.active("true")) led_1 (.in(W1));
  LED #(.active("true")) led_2 (.in(W2));
  LED #(.active("true")) led_3 (.in(W3));
  // Mips_Probe mips_probe_1: pin names not known; wires that end beside it: IR, PC[11:2]
  and and_1 (and_1_out, JAL, JMP);
  and and_2 (or_1_out[2], JR, JMP);
  Hex_Digit_Display hex_digit_display_1 (.value(LedData[31:28]));  // open: dp
  Register #(.width(32), .trigger("rising"), .Select("low")) u_PC (.D(nextPC), .en(run), .Q(PC), .clk(CLK), .clr(rst));
  and and_3 (and_3_out, GEZ, BGEZ);
  and and_4 (and_4_out, equ, BEQ);
  or or_1 (or_1_out[0], and_4_out, and_3_out, and_5_out);
  and and_5 (and_5_out, ~equ, BNE);  // AND_Gate
  and and_6 (and_6_out, ~JR, ~JAL, JMP);  // AND_Gate
  or or_2 (or_1_out[1], and_1_out, and_6_out);
  Multiplexer #(.select(3), .width(32), .disabled("Z"), .enable("false")) multiplexer_1 (
    .in0(PC_4), .in1(BAddr), .in2({PC[31:28], IR[25:0], 2'b00}), .in4(R1), .out(nextPC), .sel(or_1_out));  // open: in3, in5, in6, in7
  Hex_Digit_Display hex_digit_display_2 (.value(LedData[23:20]));  // open: dp
  Hex_Digit_Display hex_digit_display_3 (.value(LedData[27:24]));  // open: dp
  Hex_Digit_Display hex_digit_display_4 (.value(LedData[15:12]));  // open: dp
  Hex_Digit_Display hex_digit_display_5 (.value(LedData[19:16]));  // open: dp
  \单周期硬布线控制器  \u_单周期硬布线控制器_1  (
    .Func(IR[5:0]), .OP(IR[31:26]), .ALU_OP(ALU_OP), .MemToReg(MemToReg), .MemWrite(MemWrite),
    .ALU_SRC(ALU_SRC), .RegWrite(RegWrite), .SysCALL(syscall), .SignedExt(SignedExt), .RegDst(RegDst),
    .JR(JR), .JMP(JMP), .Beq(BEQ), .JAL(JAL), .Bne(BNE), .ERET(ERET), .B(B), .BGEZ(BGEZ), .SRLV(SRLV));
  ROM #(.addrWidth(10), .dataWidth(32), .Select("high")) rom_1 (.addr(PC[11:2]), .data(IR));
  Hex_Digit_Display hex_digit_display_6 (.value(LedData[11:8]));  // open: dp
  Hex_Digit_Display hex_digit_display_7 (.value(LedData[7:4]));  // open: dp
  // Probe on \总周期数 
  Hex_Digit_Display hex_digit_display_8 (.value(LedData[3:0]));  // open: dp
  assign bit_extender_1_out = {{16{1'b0}}, IR[15:0]};  // Bit_Extender bit_extender_1
  Multiplexer #(.select(1), .width(32), .disabled("Z"), .enable("false")) multiplexer_2 (
    .in0(bit_extender_1_out), .in1(bit_extender_2_out), .out(ExtImm), .sel(SignedExt));
  assign bit_extender_2_out = {{16{IR[15]}}, IR[15:0]};  // Bit_Extender bit_extender_2
  Shifter #(.width(32), .shift("ll")) shifter_1 (.in(ExtImm), .\dist (5'b00010), .out(shifter_1_out));
  Adder #(.width(32)) adder_1 (.a(shifter_1_out), .b(PC_4), .out(BAddr));  // open: cin, cout
  Adder #(.width(32)) adder_2 (.a(PC), .b(32'h4), .out(PC_4));  // open: cin, cout
  or or_3 (IR1_t, IR1, IRA);
  or or_4 (IR2_t, IR2, IRB);
  Multiplexer #(.select(1), .width(5), .disabled("Z"), .enable("false")) multiplexer_3 (
    .in0(IR[25:21]), .in1(5'b00010), .out(multiplexer_3_out), .sel(syscall));
  Multiplexer #(.select(1), .width(5), .disabled("Z"), .enable("false")) multiplexer_4 (
    .in0(IR[20:16]), .in1(5'b00100), .out(multiplexer_4_out), .sel(syscall));
  Multiplexer #(.select(2), .width(5), .disabled("Z"), .enable("false")) multiplexer_5 (
    .in0(IR[20:16]), .in1(IR[15:11]), .in2({5{1'b1}}), .in3({5{1'b1}}), .out(multiplexer_5_out),
    .sel({JAL, RegDst}));
  Counter #(.width(16), .max('hffff), .ongoal("wrap"), .trigger("rising"), .behavior("new")) counter_1 (
    .count(run), .Q(\总周期数 ), .clk(CLK), .clr(rst));  // open: load, D, carry, preset, down
  Comparator #(.width(32), .mode("twosComplement")) comparator_1 (
    .a(32'h22), .b(R1), .eq(comparator_1_eq));  // open: gt, lt
  or or_5 (IR3_t, IR3, IRC);
  MIPS_Regifile mips_regifile_1 (
    .Din(RDin), .Clk(CLK), .R1(R1), .R2(MDin), .WE(RegWrite), .W_num(multiplexer_5_out),
    .R1_num(multiplexer_3_out), .R2_num(multiplexer_4_out));
  Register #(.width(32), .trigger("rising"), .Select("low")) register_1 (
    .D(MDin), .en(LedOut), .Q(LedData), .clk(CLK), .clr(rst));
  and and_7 (LedOut, syscall, comparator_1_eq);
  nand nand_1 (run, syscall, ~comparator_1_eq);  // NAND_Gate
  Button button_1 (.out(rst));
  Multiplexer #(.select(1), .width(32), .disabled("Z"), .enable("false")) multiplexer_6 (
    .in0(MDin), .in1(ExtImm), .out(multiplexer_6_out), .sel(ALU_SRC));
  Multiplexer #(.select(1), .width(5), .disabled("Z"), .enable("false")) multiplexer_7 (
    .in0(IR[10:6]), .in1(R1[4:0]), .out(multiplexer_7_out), .sel(SRLV));
  Decoder #(.select(2), .tristate("false"), .disabled("Z"), .enable("false")) decoder_1 (
    .out0(decoder_1_out0[0]), .out1(decoder_1_out0[1]), .out2(decoder_1_out0[2]), .out3(decoder_1_out0[3]),
    .sel(R[1:0]));
  Demultiplexer #(.select(2), .width(8), .tristate("false"), .disabled("Z"), .enable("false")) demultiplexer_1 (
    .out0(demultiplexer_1_out0), .out1(demultiplexer_1_out1), .out2(demultiplexer_1_out2),
    .out3(demultiplexer_1_out3), .in(MDin[7:0]), .sel(R[1:0]));
  MIPS_ALU mips_alu_1 (
    .X(R1), .Y(multiplexer_6_out), .AluOP(ALU_OP), .Equal(equ), .Result({R[31:12], MemAddr, R[1:0]}),
    .shamt(multiplexer_7_out), .GEZ(GEZ));  // open: Result_2
  assign {sel4, sel3, sel2, sel1} = ~B ? 4'b1111 : 4'bz;  // Controlled_Buffer controlled_buffer_1
  assign {sel4, sel3, sel2, sel1} = B ? decoder_1_out0 : 4'bz;  // Controlled_Buffer controlled_buffer_2
  assign {MDin4, MDin3, MDin2, MDin1} = B ? {demultiplexer_1_out3, demultiplexer_1_out2, demultiplexer_1_out1, demultiplexer_1_out0} : 32'bz;  // Controlled_Buffer controlled_buffer_3
  assign {MDin4, MDin3, MDin2, MDin1} = ~B ? MDin : 32'bz;  // Controlled_Buffer controlled_buffer_4
  RAM #(.addrWidth(10), .dataWidth(8), .bus("separate"), .Select("high")) ram_1 (
    .addr(MemAddr), .din(MDin1), .data(MDout[7:0]), .str(MemWrite), .sel(sel1), .clk(CLK), .clr(rst));  // open: ld
  RAM #(.addrWidth(10), .dataWidth(8), .bus("separate"), .Select("high")) ram_2 (
    .addr(MemAddr), .din(MDin2), .data(MDout[15:8]), .str(MemWrite), .sel(sel2), .clk(CLK), .clr(rst));  // open: ld
  RAM #(.addrWidth(10), .dataWidth(8), .bus("separate"), .Select("high")) ram_3 (
    .addr(MemAddr), .din(MDin3), .data(MDout[23:16]), .str(MemWrite), .sel(sel3), .clk(CLK), .clr(rst));  // open: ld
  RAM #(.addrWidth(10), .dataWidth(8), .bus("separate"), .Select("high")) ram_4 (
    .addr(MemAddr), .din(MDin4), .data(MDout[31:24]), .str(MemWrite), .sel(sel4), .clk(CLK), .clr(rst));  // open: ld
  D_Flip_Flop #(.trigger("high"), .Pre_Clr_Positions("LEGACY"), .NegatePresetClear("false"), .enable("true"), .NewFFLayout("false")) d_ff_1 (.Q(d_ff_1_q));  // open: clk, D, Qn, preset, en, reset
  // Probe on 13'ha
  Comparator #(.width(13), .mode("twosComplement")) comparator_2 (
    .a(CNT_num), .b(13'ha), .eq(comparator_2_eq), .lt(comparator_2_lt));  // open: gt
  Clock #(.highDuration(1), .lowDuration(1)) clock_2 ();  // open: out
  Counter #(.width(13), .max('h1fff), .ongoal("stay"), .trigger("rising"), .behavior("old")) counter_2 (
    .count(comparator_2_lt), .Q(CNT_num), .clk(undriven));  // open: load, D, carry, clr, preset
  nand nand_2 (nand_2_out, d_ff_1_q, comparator_2_eq);
  assign CLK = nand_2_out ? undriven : 1'bz;  // Controlled_Buffer controlled_buffer_5
  Pull_Resistor #(.pull(1)) pull_resistor_1 (.node(CLK));
  Multiplexer #(.select(2), .width(32), .disabled("Z"), .enable("false")) multiplexer_8 (
    .in0({R[31:12], MemAddr, R[1:0]}), .in1(PC_4), .in2(MDout), .out(RDin), .sel({MemToReg, JAL}));  // open: in3

  // Other names for the same wires on the sheet: Func[5:0] = IR[5:0]; IAddr[31:2] = {PC[31:28], IR[25:0]};
  //   Imm16[15:0] = IR[15:0]; Imm26[25:0] = IR[25:0]; sa[4:0] = IR[10:6]; rd[4:0] = IR[15:11]; rt[4:0] = IR[20:16];
  //   rs[4:0] = IR[25:21]; OP[5:0] = IR[31:26]; R[11:2] = MemAddr; RAddr[31:0] = R1

  // Notes on the sheet:
  //   中断源
  //   中断等待指示
  //   总复位信号应将除ROM以外所有存储组件全部清零
  //   指令字
  //   指令存储器
  //   数码管输出
  //   contents of rom_1 (hex, n*v repeats v):
  //   20110001 8000c05 20110001 20120002 20130003 8000c09 20110001 20120002 20130003 8000c0d 20110001
  //   20120002 20130003 8000c11 20110001 20120002 20130003 c000cb8 20100001 20110001 118fc0 112020
  //   20020022 c 118882 12200001 8000c15 112020 20020022 c 20110001 118880 112020 20020022 c 12200001
  //   8000c1f 20110001 118fc0 112020 20020022 c 1188c3 112020 20020022 c 118903 112020 20020022 c 118903
  //   112020 20020022 c 118903 112020 20020022 c 118903 112020 20020022 c 118903 112020 20020022 c 118903
  //   112020 20020022 c 118903 112020 20020022 c 20100001 109fc0 139fc3 8021 2012000c 24160003 26100001
  //   3210000f 20080008 20090001 139900 2709825 132020 20020022 c 1094022 1500fff9 22100001 2018000f
  //   2188024 108700 20080008 20090001 139902 2709825 132021 20020022 c 1094022 1500fff9 108702 2c9b022
  //   12c00001 8000c50 4020 1084027 84400 3508ffff 82021 20020022 c 2010ffff 20110000 ae300000 22100001
  //   22310004 ae300000 22100001 22310004 ae300000 22100001 22310004 ae300000 22100001 22310004 ae300000
  //   22100001 22310004 ae300000 22100001 22310004 ae300000 22100001 22310004 ae300000 22100001 22310004
  //   ae300000 22100001 22310004 ae300000 22100001 22310004 ae300000 22100001 22310004 ae300000 22100001
  //   22310004 ae300000 22100001 22310004 ae300000 22100001 22310004 ae300000 22100001 22310004 ae300000
  //   22100001 22310004 22100001 8020 2011003c 8e130000 8e340000 274402a 11000002 ae330000 ae140000
  //   2231fffc 1611fff8 102020 20020022 c 22100004 2011003c 1611fff2 20020032 c 20100000 22100001 102020
  //   20020022 c 22100002 102020 20020022 c 22100003 102020 20020022 c 22100004 102020 20020022 c 22100005
  //   102020 20020022 c 22100006 102020 20020022 c 22100007 102020 20020022 c 22100008 102020 20020022
  //   20020022 c 3e00008
  //   数码管输出应该用寄存器锁存，否则显示数据只能一闪而过
  //   OP
  //   Func
  //   rs
  //   rt
  //   rd
  //   sa
  //   Imm16
  //   Imm26
  //   没有实现branch delay slot，因此只加4
  //   v0
  //   t0
  //   ra
  //   display
  //   为方便自动评测，需要输出PC，IR，寄存器堆写如数据RDin
  //   RAM写使能MemWrite、RAM写入数据MDin等信号
  //   差异化指令：2554
  //   控制位
  //   暂停节拍，不能为0
  //   戳工具置1进入计数暂停模式，ctrl+k时钟自动运行到对应节拍暂停
  //   ctrl+k关闭时钟连续运行，将控制位置零，进入单步调试模式调试
  //   用这个时钟源需要去掉电路中的其他时钟源
  //   可计数暂停的时钟源
endmodule

// 单周期硬布线控制器
module \单周期硬布线控制器  (
  input  [5:0] OP,
  input  [5:0] Func,
  output [3:0] ALU_OP,
  output MemToReg,
  output MemWrite,
  output ALU_SRC,
  output RegWrite,
  output SysCALL,
  output SignedExt,
  output RegDst,
  output Beq,
  output Bne,
  output JR,
  output JMP,
  output JAL,
  output ERET,
  output B,
  output BGEZ,
  output SRLV
);

  \运算控制器自动生成  \u_运算控制器自动生成_1  (
    .OP0(OP[0]), .OP1(OP[1]), .OP2(OP[2]), .OP3(OP[3]), .OP4(OP[4]), .OP5(OP[5]), .F0(Func[0]), .F1(Func[1]),
    .F2(Func[2]), .F3(Func[3]), .F4(Func[4]), .F5(Func[5]), .S0(ALU_OP[0]), .S1(ALU_OP[1]), .S2(ALU_OP[2]),
    .S3(ALU_OP[3]));
  \控制信号自动生成  \u_控制信号自动生成_1  (
    .OP0(OP[0]), .MemToReg(MemToReg), .OP1(OP[1]), .OP2(OP[2]), .OP3(OP[3]), .OP4(OP[4]),
    .MemWrite(MemWrite), .OP5(OP[5]), .F0(Func[0]), .F1(Func[1]), .F2(Func[2]), .F3(Func[3]), .F4(Func[4]),
    .F5(Func[5]), .ALU_SRC(ALU_SRC), .RegWrite(RegWrite), .SysCALL(SysCALL), .SignedExt(SignedExt),
    .RegDst(RegDst), .BEQ(Beq), .BNE(Bne), .JR(JR), .JUMP(JMP), .JAL(JAL), .ERET(ERET), .B(B), .BGEZ(BGEZ),
    .SRLV(SRLV));

  // Other names for the same wires on the sheet: OP_CODE[5:0] = OP

  // Notes on the sheet:
  //   运算器控制器，根据指令生成运算器功能选择信号
  //   控制信号生成，产生数据通路需要的其他控制信号
endmodule

// 运算器控制器
module \运算控制器自动生成  (
  input  OP0,
  input  OP1,
  input  OP2,
  input  OP3,
  input  OP4,
  input  OP5,
  input  F0,
  input  F1,
  input  F2,
  input  F3,
  input  F4,
  input  F5,
  output S0,
  output S1,
  output S2,
  output S3
);

  wire and_1_out, and_2_out, and_3_out, and_4_out, and_5_out, and_6_out, and_7_out, and_8_out, and_9_out,
       and_10_out, and_11_out, and_12_out, and_13_out, and_14_out, and_15_out, and_16_out, and_17_out,
       and_18_out, and_19_out, and_20_out, and_21_out, and_22_out, and_23_out, and_24_out, and_25_out,
       and_26_out, and_27_out, and_28_out, and_29_out, and_30_out, and_31_out, and_32_out, and_33_out,
       and_34_out, and_35_out, and_36_out, and_37_out, and_38_out, and_39_out, not_1_out, not_2_out,
       not_3_out, not_4_out, not_5_out, not_6_out, not_7_out, not_8_out, not_9_out, not_10_out, not_11_out,
       not_12_out, not_13_out, not_14_out, not_15_out, not_16_out, not_17_out, not_18_out, not_19_out,
       not_20_out, not_21_out, not_22_out, not_23_out, not_24_out, not_25_out, not_26_out, not_27_out,
       not_28_out, not_29_out, not_30_out, not_31_out, not_32_out, not_33_out, not_34_out, not_35_out,
       not_36_out, not_37_out, not_38_out, not_39_out, not_40_out, not_41_out, not_42_out, not_43_out,
       not_44_out, not_45_out, not_46_out, not_47_out, not_48_out, not_49_out, not_50_out, not_51_out,
       not_52_out, not_53_out, not_54_out, not_55_out, not_56_out, not_57_out, not_58_out, not_59_out,
       not_60_out, not_61_out, not_62_out, not_63_out, not_64_out, not_65_out, not_66_out, not_67_out,
       not_68_out, not_69_out, not_70_out, not_71_out, not_72_out, not_73_out, not_74_out, not_75_out,
       not_76_out, not_77_out, not_78_out, not_79_out, not_80_out, not_81_out, not_82_out, not_83_out,
       not_84_out, not_85_out, not_86_out, not_87_out, not_88_out, not_89_out, not_90_out, not_91_out,
       not_92_out, not_93_out, not_94_out, not_95_out, not_96_out, not_97_out, not_98_out, not_99_out,
       not_100_out, not_101_out, not_102_out, not_103_out, not_104_out, not_105_out, not_106_out,
       not_107_out, not_108_out, not_109_out, not_110_out, not_111_out, not_112_out, not_113_out,
       not_114_out, not_115_out, not_116_out, not_117_out, not_118_out, not_119_out, not_120_out,
       not_121_out, not_122_out, not_123_out, not_124_out, not_125_out, not_126_out, not_127_out,
       not_128_out, not_129_out, not_130_out, not_131_out, not_132_out, not_133_out, not_134_out,
       not_135_out, not_136_out, not_137_out, not_138_out, not_139_out, not_140_out, not_141_out,
       not_142_out, not_143_out, not_144_out, not_145_out, not_146_out, not_147_out, not_148_out,
       not_149_out, not_150_out, not_151_out, not_152_out, not_153_out, not_154_out, not_155_out,
       not_156_out, not_157_out, not_158_out, not_159_out, not_160_out, not_161_out, not_162_out,
       not_163_out, not_164_out, not_165_out, not_166_out, not_167_out, not_168_out, not_169_out,
       not_170_out, not_171_out, not_172_out, not_173_out, not_174_out, not_175_out, not_176_out,
       not_177_out, not_178_out, not_179_out, not_180_out, not_181_out, not_182_out, not_183_out,
       not_184_out, not_185_out, not_186_out, not_187_out, not_188_out, not_189_out, not_190_out,
       not_191_out, not_192_out, not_193_out, not_194_out, not_195_out, not_196_out, not_197_out,
       not_198_out, not_199_out, not_200_out, not_201_out, not_202_out, not_203_out, not_204_out,
       not_205_out, not_206_out, not_207_out, not_208_out, not_209_out, not_210_out, not_211_out,
       not_212_out, not_213_out, not_214_out, not_215_out, not_216_out, not_217_out, not_218_out,
       not_219_out, not_220_out, not_221_out, not_222_out, not_223_out, not_224_out, not_225_out,
       not_226_out, not_227_out, not_228_out, not_229_out, not_230_out, not_231_out, not_232_out,
       not_233_out, not_234_out, not_235_out, not_236_out, not_237_out, not_238_out, not_239_out,
       not_240_out, not_241_out, not_242_out, not_243_out, not_244_out, not_245_out, not_246_out,
       not_247_out, not_248_out, not_249_out, not_250_out, not_251_out, not_252_out, not_253_out,
       not_254_out, not_255_out, not_256_out, not_257_out, not_258_out, not_259_out, not_260_out,
       not_261_out, not_262_out, not_263_out, not_264_out, not_265_out, not_266_out, not_267_out,
       not_268_out, not_269_out, not_270_out, not_271_out, not_272_out;

  not not_1 (not_1_out, OP5);
  not not_2 (not_2_out, OP4);
  not not_3 (not_3_out, OP3);
  not not_4 (not_4_out, OP2);
  not not_5 (not_5_out, OP1);
  not not_6 (not_6_out, OP0);
  not not_7 (not_7_out, F5);
  not not_8 (not_8_out, F4);
  not not_9 (not_9_out, F3);
  not not_10 (not_10_out, F2);
  not not_11 (not_11_out, OP5);
  not not_12 (not_12_out, OP4);
  not not_13 (not_13_out, OP3);
  not not_14 (not_14_out, OP2);
  not not_15 (not_15_out, OP1);
  not not_16 (not_16_out, OP0);
  not not_17 (not_17_out, F4);
  not not_18 (not_18_out, F3);
  not not_19 (not_19_out, F2);
  not not_20 (not_20_out, F1);
  not not_21 (not_21_out, F0);
  not not_22 (not_22_out, OP5);
  not not_23 (not_23_out, OP4);
  not not_24 (not_24_out, OP3);
  not not_25 (not_25_out, OP2);
  not not_26 (not_26_out, OP1);
  not not_27 (not_27_out, OP0);
  not not_28 (not_28_out, F4);
  not not_29 (not_29_out, F3);
  not not_30 (not_30_out, F2);
  not not_31 (not_31_out, F1);
  not not_32 (not_32_out, OP5);
  not not_33 (not_33_out, OP4);
  not not_34 (not_34_out, OP3);
  not not_35 (not_35_out, OP2);
  not not_36 (not_36_out, OP1);
  not not_37 (not_37_out, OP0);
  not not_38 (not_38_out, F4);
  not not_39 (not_39_out, F3);
  not not_40 (not_40_out, F1);
  not not_41 (not_41_out, F0);
  not not_42 (not_42_out, OP5);
  not not_43 (not_43_out, OP4);
  not not_44 (not_44_out, OP3);
  not not_45 (not_45_out, OP2);
  not not_46 (not_46_out, OP1);
  not not_47 (not_47_out, OP0);
  not not_48 (not_48_out, F4);
  not not_49 (not_49_out, F2);
  not not_50 (not_50_out, F0);
  not not_51 (not_51_out, OP5);
  not not_52 (not_52_out, OP4);
  not not_53 (not_53_out, OP2);
  not not_54 (not_54_out, OP1);
  not not_55 (not_55_out, OP0);
  not not_56 (not_56_out, OP5);
  not not_57 (not_57_out, OP4);
  not not_58 (not_58_out, OP1);
  not not_59 (not_59_out, OP0);
  not not_60 (not_60_out, OP5);
  not not_61 (not_61_out, OP4);
  not not_62 (not_62_out, OP2);
  not not_63 (not_63_out, OP1);
  not not_64 (not_64_out, OP5);
  not not_65 (not_65_out, OP4);
  not not_66 (not_66_out, OP2);
  not not_67 (not_67_out, OP0);
  not not_68 (not_68_out, OP4);
  not not_69 (not_69_out, OP3);
  not not_70 (not_70_out, OP2);
  not not_71 (not_71_out, OP4);
  not not_72 (not_72_out, OP2);
  not not_73 (not_73_out, OP5);
  not not_74 (not_74_out, OP4);
  not not_75 (not_75_out, OP3);
  not not_76 (not_76_out, OP2);
  not not_77 (not_77_out, OP1);
  not not_78 (not_78_out, OP0);
  not not_79 (not_79_out, F4);
  not not_80 (not_80_out, F3);
  not not_81 (not_81_out, F0);
  not not_82 (not_82_out, OP4);
  not not_83 (not_83_out, OP2);
  not not_84 (not_84_out, OP1);
  not not_85 (not_85_out, OP0);
  not not_86 (not_86_out, OP5);
  not not_87 (not_87_out, OP4);
  not not_88 (not_88_out, OP3);
  not not_89 (not_89_out, OP2);
  not not_90 (not_90_out, OP1);
  not not_91 (not_91_out, OP0);
  not not_92 (not_92_out, F5);
  not not_93 (not_93_out, F4);
  not not_94 (not_94_out, F3);
  not not_95 (not_95_out, F2);
  not not_96 (not_96_out, F0);
  not not_97 (not_97_out, OP5);
  not not_98 (not_98_out, OP4);
  not not_99 (not_99_out, OP3);
  not not_100 (not_100_out, OP2);
  not not_101 (not_101_out, OP1);
  not not_102 (not_102_out, OP0);
  not not_103 (not_103_out, F4);
  not not_104 (not_104_out, F3);
  not not_105 (not_105_out, F2);
  not not_106 (not_106_out, F0);
  not not_107 (not_107_out, OP5);
  not not_108 (not_108_out, OP4);
  not not_109 (not_109_out, OP3);
  not not_110 (not_110_out, OP2);
  not not_111 (not_111_out, OP1);
  not not_112 (not_112_out, OP0);
  not not_113 (not_113_out, F4);
  not not_114 (not_114_out, F3);
  not not_115 (not_115_out, F1);
  not not_116 (not_116_out, F0);
  not not_117 (not_117_out, OP5);
  not not_118 (not_118_out, OP4);
  not not_119 (not_119_out, OP3);
  not not_120 (not_120_out, OP2);
  not not_121 (not_121_out, OP1);
  not not_122 (not_122_out, OP0);
  not not_123 (not_123_out, F4);
  not not_124 (not_124_out, F3);
  not not_125 (not_125_out, OP5);
  not not_126 (not_126_out, OP4);
  not not_127 (not_127_out, OP3);
  not not_128 (not_128_out, OP2);
  not not_129 (not_129_out, OP1);
  not not_130 (not_130_out, OP0);
  not not_131 (not_131_out, F4);
  not not_132 (not_132_out, F2);
  not not_133 (not_133_out, F0);
  not not_134 (not_134_out, OP5);
  not not_135 (not_135_out, OP4);
  not not_136 (not_136_out, OP1);
  not not_137 (not_137_out, OP0);
  not not_138 (not_138_out, OP5);
  not not_139 (not_139_out, OP4);
  not not_140 (not_140_out, OP2);
  not not_141 (not_141_out, OP0);
  not not_142 (not_142_out, OP5);
  not not_143 (not_143_out, OP4);
  not not_144 (not_144_out, OP3);
  not not_145 (not_145_out, OP2);
  not not_146 (not_146_out, OP1);
  not not_147 (not_147_out, OP0);
  not not_148 (not_148_out, F5);
  not not_149 (not_149_out, F4);
  not not_150 (not_150_out, F3);
  not not_151 (not_151_out, F0);
  not not_152 (not_152_out, OP5);
  not not_153 (not_153_out, OP4);
  not not_154 (not_154_out, OP3);
  not not_155 (not_155_out, OP2);
  not not_156 (not_156_out, OP1);
  not not_157 (not_157_out, OP0);
  not not_158 (not_158_out, F4);
  not not_159 (not_159_out, F3);
  not not_160 (not_160_out, F2);
  not not_161 (not_161_out, F1);
  not not_162 (not_162_out, F0);
  not not_163 (not_163_out, OP5);
  not not_164 (not_164_out, OP4);
  not not_165 (not_165_out, OP3);
  not not_166 (not_166_out, OP2);
  not not_167 (not_167_out, OP1);
  not not_168 (not_168_out, OP0);
  not not_169 (not_169_out, F4);
  not not_170 (not_170_out, F3);
  not not_171 (not_171_out, F2);
  not not_172 (not_172_out, F1);
  not not_173 (not_173_out, OP5);
  not not_174 (not_174_out, OP4);
  not not_175 (not_175_out, OP3);
  not not_176 (not_176_out, OP2);
  not not_177 (not_177_out, OP1);
  not not_178 (not_178_out, OP0);
  not not_179 (not_179_out, F4);
  not not_180 (not_180_out, F3);
  not not_181 (not_181_out, F2);
  not not_182 (not_182_out, F0);
  not not_183 (not_183_out, OP5);
  not not_184 (not_184_out, OP4);
  not not_185 (not_185_out, OP3);
  not not_186 (not_186_out, OP2);
  not not_187 (not_187_out, OP1);
  not not_188 (not_188_out, OP0);
  not not_189 (not_189_out, F4);
  not not_190 (not_190_out, F3);
  not not_191 (not_191_out, F1);
  not not_192 (not_192_out, F0);
  not not_193 (not_193_out, OP5);
  not not_194 (not_194_out, OP4);
  not not_195 (not_195_out, OP3);
  not not_196 (not_196_out, OP2);
  not not_197 (not_197_out, OP1);
  not not_198 (not_198_out, OP0);
  not not_199 (not_199_out, F4);
  not not_200 (not_200_out, F2);
  not not_201 (not_201_out, OP5);
  not not_202 (not_202_out, OP4);
  not not_203 (not_203_out, OP2);
  not not_204 (not_204_out, OP1);
  not not_205 (not_205_out, OP0);
  not not_206 (not_206_out, OP5);
  not not_207 (not_207_out, OP4);
  not not_208 (not_208_out, OP1);
  not not_209 (not_209_out, OP0);
  not not_210 (not_210_out, OP5);
  not not_211 (not_211_out, OP4);
  not not_212 (not_212_out, OP2);
  not not_213 (not_213_out, OP1);
  not not_214 (not_214_out, OP4);
  not not_215 (not_215_out, OP3);
  not not_216 (not_216_out, OP2);
  not not_217 (not_217_out, OP4);
  not not_218 (not_218_out, OP2);
  not not_219 (not_219_out, OP4);
  not not_220 (not_220_out, OP2);
  not not_221 (not_221_out, OP1);
  not not_222 (not_222_out, OP0);
  not not_223 (not_223_out, OP5);
  not not_224 (not_224_out, OP4);
  not not_225 (not_225_out, OP3);
  not not_226 (not_226_out, OP2);
  not not_227 (not_227_out, OP1);
  not not_228 (not_228_out, OP0);
  not not_229 (not_229_out, F4);
  not not_230 (not_230_out, F3);
  not not_231 (not_231_out, F1);
  not not_232 (not_232_out, OP5);
  not not_233 (not_233_out, OP4);
  not not_234 (not_234_out, OP3);
  not not_235 (not_235_out, OP2);
  not not_236 (not_236_out, OP1);
  not not_237 (not_237_out, OP0);
  not not_238 (not_238_out, F4);
  not not_239 (not_239_out, F3);
  not not_240 (not_240_out, OP5);
  not not_241 (not_241_out, OP4);
  not not_242 (not_242_out, OP3);
  not not_243 (not_243_out, OP2);
  not not_244 (not_244_out, OP1);
  not not_245 (not_245_out, OP0);
  not not_246 (not_246_out, F4);
  not not_247 (not_247_out, F2);
  not not_248 (not_248_out, F0);
  not not_249 (not_249_out, OP5);
  not not_250 (not_250_out, OP4);
  not not_251 (not_251_out, OP3);
  not not_252 (not_252_out, OP2);
  not not_253 (not_253_out, OP1);
  not not_254 (not_254_out, OP0);
  not not_255 (not_255_out, F4);
  not not_256 (not_256_out, F2);
  not not_257 (not_257_out, OP5);
  not not_258 (not_258_out, OP4);
  not not_259 (not_259_out, OP2);
  not not_260 (not_260_out, OP0);
  not not_261 (not_261_out, OP5);
  not not_262 (not_262_out, OP4);
  not not_263 (not_263_out, OP1);
  not not_264 (not_264_out, OP5);
  not not_265 (not_265_out, OP4);
  not not_266 (not_266_out, OP3);
  not not_267 (not_267_out, OP2);
  not not_268 (not_268_out, OP1);
  not not_269 (not_269_out, OP0);
  not not_270 (not_270_out, F4);
  not not_271 (not_271_out, F3);
  not not_272 (not_272_out, F0);
  and and_1 (and_1_out, not_1_out, not_2_out, not_3_out, not_4_out, not_5_out, not_6_out, not_7_out, not_8_out, not_9_out, not_10_out, F1, F0);
  and and_2 (and_2_out, not_11_out, not_12_out, not_13_out, not_14_out, not_15_out, not_16_out, F5, not_17_out, not_18_out, not_19_out, not_20_out, not_21_out);
  and and_3 (and_3_out, not_22_out, not_23_out, not_24_out, not_25_out, not_26_out, not_27_out, F5, not_28_out, not_29_out, not_30_out, not_31_out, F0);
  and and_4 (and_4_out, not_32_out, not_33_out, not_34_out, not_35_out, not_36_out, not_37_out, F5, not_38_out, not_39_out, F2, not_40_out, not_41_out);
  and and_5 (and_5_out, not_42_out, not_43_out, not_44_out, not_45_out, not_46_out, not_47_out, F5, not_48_out, F3, not_49_out, F1, not_50_out);
  and and_6 (and_6_out, not_51_out, not_52_out, OP3, not_53_out, not_54_out, not_55_out);
  and and_7 (and_7_out, not_56_out, not_57_out, OP3, OP2, not_58_out, not_59_out);
  and and_8 (and_8_out, not_60_out, not_61_out, OP3, not_62_out, not_63_out, OP0);
  and and_9 (and_9_out, not_64_out, not_65_out, OP3, not_66_out, OP1, not_67_out);
  and and_10 (and_10_out, OP5, not_68_out, not_69_out, not_70_out, OP1, OP0);
  and and_11 (and_11_out, OP5, not_71_out, OP3, not_72_out, OP1, OP0);
  and and_12 (and_12_out, not_73_out, not_74_out, not_75_out, not_76_out, not_77_out, not_78_out, F5, not_79_out, not_80_out, F2, F1, not_81_out);
  and and_13 (and_13_out, OP5, not_82_out, OP3, not_83_out, not_84_out, not_85_out);
  and and_14 (and_14_out, not_86_out, not_87_out, not_88_out, not_89_out, not_90_out, not_91_out, not_92_out, not_93_out, not_94_out, not_95_out, F1, not_96_out);
  and and_15 (and_15_out, not_97_out, not_98_out, not_99_out, not_100_out, not_101_out, not_102_out, F5, not_103_out, not_104_out, not_105_out, F1, not_106_out);
  and and_16 (and_16_out, not_107_out, not_108_out, not_109_out, not_110_out, not_111_out, not_112_out, F5, not_113_out, not_114_out, F2, not_115_out, not_116_out);
  and and_17 (and_17_out, not_117_out, not_118_out, not_119_out, not_120_out, not_121_out, not_122_out, F5, not_123_out, not_124_out, F2, F1, F0);
  and and_18 (and_18_out, not_125_out, not_126_out, not_127_out, not_128_out, not_129_out, not_130_out, F5, not_131_out, F3, not_132_out, F1, not_133_out);
  and and_19 (and_19_out, not_134_out, not_135_out, OP3, OP2, not_136_out, not_137_out);
  and and_20 (and_20_out, not_138_out, not_139_out, OP3, not_140_out, OP1, not_141_out);
  and and_21 (and_21_out, not_142_out, not_143_out, not_144_out, not_145_out, not_146_out, not_147_out, not_148_out, not_149_out, not_150_out, F2, F1, not_151_out);
  and and_22 (and_22_out, not_152_out, not_153_out, not_154_out, not_155_out, not_156_out, not_157_out, F5, not_158_out, not_159_out, not_160_out, not_161_out, not_162_out);
  and and_23 (and_23_out, not_163_out, not_164_out, not_165_out, not_166_out, not_167_out, not_168_out, F5, not_169_out, not_170_out, not_171_out, not_172_out, F0);
  and and_24 (and_24_out, not_173_out, not_174_out, not_175_out, not_176_out, not_177_out, not_178_out, F5, not_179_out, not_180_out, not_181_out, F1, not_182_out);
  and and_25 (and_25_out, not_183_out, not_184_out, not_185_out, not_186_out, not_187_out, not_188_out, F5, not_189_out, not_190_out, F2, not_191_out, not_192_out);
  and and_26 (and_26_out, not_193_out, not_194_out, not_195_out, not_196_out, not_197_out, not_198_out, F5, not_199_out, F3, not_200_out, F1, F0);
  and and_27 (and_27_out, not_201_out, not_202_out, OP3, not_203_out, not_204_out, not_205_out);
  and and_28 (and_28_out, not_206_out, not_207_out, OP3, OP2, not_208_out, not_209_out);
  and and_29 (and_29_out, not_210_out, not_211_out, OP3, not_212_out, not_213_out, OP0);
  and and_30 (and_30_out, OP5, not_214_out, not_215_out, not_216_out, OP1, OP0);
  and and_31 (and_31_out, OP5, not_217_out, OP3, not_218_out, OP1, OP0);
  and and_32 (and_32_out, OP5, not_219_out, OP3, not_220_out, not_221_out, not_222_out);
  and and_33 (and_33_out, not_223_out, not_224_out, not_225_out, not_226_out, not_227_out, not_228_out, F5, not_229_out, not_230_out, F2, not_231_out, F0);
  and and_34 (and_34_out, not_232_out, not_233_out, not_234_out, not_235_out, not_236_out, not_237_out, F5, not_238_out, not_239_out, F2, F1, F0);
  and and_35 (and_35_out, not_240_out, not_241_out, not_242_out, not_243_out, not_244_out, not_245_out, F5, not_246_out, F3, not_247_out, F1, not_248_out);
  and and_36 (and_36_out, not_249_out, not_250_out, not_251_out, not_252_out, not_253_out, not_254_out, F5, not_255_out, F3, not_256_out, F1, F0);
  and and_37 (and_37_out, not_257_out, not_258_out, OP3, not_259_out, OP1, not_260_out);
  and and_38 (and_38_out, not_261_out, not_262_out, OP3, OP2, not_263_out, OP0);
  and and_39 (and_39_out, not_264_out, not_265_out, not_266_out, not_267_out, not_268_out, not_269_out, F5, not_270_out, not_271_out, F2, F1, not_272_out);
  or or_1 (S1, and_14_out, and_15_out, and_16_out, and_17_out, and_18_out, and_19_out, and_20_out, and_21_out);
  or or_2 (S2, and_22_out, and_23_out, and_24_out, and_25_out, and_26_out, and_27_out, and_28_out, and_29_out, and_30_out, and_31_out, and_32_out);
  or or_3 (S3, and_33_out, and_34_out, and_35_out, and_36_out, and_37_out, and_38_out, and_39_out);
  or or_4 (S0, and_1_out, and_2_out, and_3_out, and_4_out, and_5_out, and_6_out, and_7_out, and_8_out, and_9_out, and_10_out, and_11_out, and_12_out, and_13_out);
endmodule

// 控制信号生成
module \控制信号自动生成  (
  input  OP0,
  input  OP1,
  input  OP2,
  input  OP3,
  input  OP4,
  input  OP5,
  input  F0,
  input  F1,
  input  F2,
  input  F3,
  input  F4,
  input  F5,
  output MemToReg,
  output MemWrite,
  output ALU_SRC,
  output RegWrite,
  output SysCALL,
  output SignedExt,
  output RegDst,
  output BEQ,
  output BNE,
  output JR,
  output JUMP,
  output JAL,
  output ERET,
  output B,
  output BGEZ,
  output SRLV
);

  wire and_2_out, and_3_out, and_4_out, and_5_out, and_6_out, and_7_out, and_8_out, and_9_out, and_10_out,
       and_11_out, and_12_out, and_13_out, and_14_out, and_15_out, and_16_out, and_17_out, and_18_out,
       and_19_out, and_20_out, and_21_out, and_22_out, and_23_out, and_24_out, and_25_out, and_26_out,
       and_27_out, and_28_out, and_29_out, and_30_out, and_31_out, and_33_out, and_34_out, and_35_out,
       and_36_out, and_37_out, and_38_out, and_39_out, and_40_out, and_41_out, and_42_out, and_43_out,
       and_44_out, and_45_out, and_46_out, and_47_out, and_48_out, and_49_out, and_50_out, and_51_out,
       and_52_out, and_53_out, and_57_out, and_58_out, and_59_out, not_1_out, not_2_out, not_3_out,
       not_4_out, not_5_out, not_6_out, not_7_out, not_8_out, not_9_out, not_10_out, not_11_out, not_12_out,
       not_13_out, not_14_out, not_15_out, not_16_out, not_17_out, not_18_out, not_19_out, not_20_out,
       not_21_out, not_22_out, not_23_out, not_24_out, not_25_out, not_26_out, not_27_out, not_28_out,
       not_29_out, not_30_out, not_31_out, not_32_out, not_33_out, not_34_out, not_35_out, not_36_out,
       not_37_out, not_38_out, not_39_out, not_40_out, not_41_out, not_42_out, not_43_out, not_44_out,
       not_45_out, not_46_out, not_47_out, not_48_out, not_49_out, not_50_out, not_51_out, not_52_out,
       not_53_out, not_54_out, not_55_out, not_56_out, not_57_out, not_58_out, not_59_out, not_60_out,
       not_61_out, not_62_out, not_63_out, not_64_out, not_65_out, not_66_out, not_67_out, not_68_out,
       not_69_out, not_70_out, not_71_out, not_72_out, not_73_out, not_74_out, not_75_out, not_76_out,
       not_77_out, not_78_out, not_79_out, not_80_out, not_81_out, not_82_out, not_83_out, not_84_out,
       not_85_out, not_86_out, not_87_out, not_88_out, not_89_out, not_90_out, not_91_out, not_92_out,
       not_93_out, not_94_out, not_95_out, not_96_out, not_97_out, not_98_out, not_99_out, not_100_out,
       not_101_out, not_102_out, not_103_out, not_104_out, not_105_out, not_106_out, not_107_out,
       not_108_out, not_109_out, not_110_out, not_111_out, not_112_out, not_113_out, not_114_out,
       not_115_out, not_116_out, not_117_out, not_118_out, not_119_out, not_120_out, not_121_out,
       not_122_out, not_123_out, not_124_out, not_125_out, not_126_out, not_127_out, not_128_out,
       not_129_out, not_130_out, not_131_out, not_132_out, not_133_out, not_134_out, not_135_out,
       not_136_out, not_137_out, not_138_out, not_139_out, not_140_out, not_141_out, not_142_out,
       not_143_out, not_144_out, not_145_out, not_146_out, not_147_out, not_148_out, not_149_out,
       not_150_out, not_151_out, not_152_out, not_153_out, not_154_out, not_155_out, not_156_out,
       not_157_out, not_158_out, not_159_out, not_160_out, not_161_out, not_162_out, not_163_out,
       not_164_out, not_165_out, not_166_out, not_167_out, not_168_out, not_169_out, not_170_out,
       not_171_out, not_172_out, not_173_out, not_174_out, not_175_out, not_176_out, not_177_out,
       not_178_out, not_179_out, not_180_out, not_181_out, not_182_out, not_183_out, not_184_out,
       not_185_out, not_186_out, not_187_out, not_188_out, not_189_out, not_190_out, not_191_out,
       not_192_out, not_193_out, not_194_out, not_195_out, not_196_out, not_197_out, not_198_out,
       not_199_out, not_200_out, not_201_out, not_202_out, not_203_out, not_204_out, not_205_out,
       not_206_out, not_207_out, not_208_out, not_209_out, not_210_out, not_211_out, not_212_out,
       not_213_out, not_214_out, not_215_out, not_216_out, not_217_out, not_218_out, not_219_out,
       not_220_out, not_221_out, not_222_out, not_223_out, not_224_out, not_225_out, not_226_out,
       not_227_out, not_228_out, not_229_out, not_230_out, not_231_out, not_232_out, not_233_out,
       not_234_out, not_235_out, not_236_out, not_237_out, not_238_out, not_239_out, not_240_out,
       not_241_out, not_242_out, not_243_out, not_244_out, not_245_out, not_246_out, not_247_out,
       not_248_out, not_249_out, not_250_out, not_251_out, not_252_out, not_253_out, not_254_out,
       not_255_out, not_256_out, not_257_out, not_258_out, not_259_out, not_260_out, not_261_out,
       not_262_out, not_263_out, not_264_out, not_265_out, not_266_out, not_267_out, not_268_out,
       not_269_out, not_270_out, not_271_out, not_272_out, not_273_out, not_274_out, not_275_out,
       not_276_out, not_277_out, not_278_out, not_279_out, not_280_out, not_281_out, not_282_out,
       not_283_out, not_284_out, not_285_out, not_286_out, not_287_out, not_288_out, not_289_out,
       not_290_out, not_291_out, not_292_out, not_293_out, not_294_out, not_295_out, not_296_out,
       not_297_out, not_298_out, not_299_out, not_300_out, not_301_out, not_302_out, not_303_out,
       not_304_out, not_305_out, not_306_out, not_307_out, not_308_out, not_309_out, not_310_out,
       not_311_out, not_312_out, not_313_out, not_314_out, not_315_out, not_316_out, not_317_out,
       not_318_out, not_319_out, not_320_out, not_321_out, not_322_out, not_323_out, not_324_out,
       not_325_out, not_326_out, not_327_out, not_328_out, not_329_out, not_330_out, not_331_out,
       not_332_out, not_333_out, not_334_out, not_335_out, not_336_out, not_337_out, not_338_out,
       not_339_out, not_340_out, not_341_out, not_342_out, not_343_out, not_344_out, not_345_out,
       not_346_out, not_347_out, not_348_out, not_349_out, not_350_out, not_351_out, not_352_out,
       not_353_out, not_354_out, not_355_out, not_356_out, not_357_out, not_358_out, not_359_out,
       not_360_out, not_361_out, not_362_out, not_363_out, not_364_out, not_365_out, not_366_out,
       not_367_out, not_368_out, not_369_out, not_370_out, not_371_out, not_372_out, not_373_out,
       not_374_out, not_375_out, not_376_out, not_377_out, not_378_out, not_379_out, not_380_out,
       not_381_out, not_382_out, not_383_out, not_384_out, not_385_out, not_386_out, not_387_out,
       not_388_out, not_389_out, not_390_out, not_391_out, not_392_out, not_393_out, not_394_out,
       not_395_out, not_396_out, not_397_out, not_398_out, not_399_out, not_400_out, not_401_out,
       not_402_out, not_403_out, not_404_out, not_405_out, not_406_out, not_407_out, not_408_out,
       not_409_out, not_410_out, not_411_out, not_412_out, not_413_out, not_414_out, not_415_out,
       not_416_out, not_417_out, not_418_out, not_419_out, not_420_out, not_421_out, not_422_out,
       not_423_out, not_424_out, not_425_out, not_426_out, not_427_out, not_428_out, not_429_out,
       not_430_out, not_431_out, not_432_out, not_433_out;

  not not_1 (not_1_out, OP4);
  not not_2 (not_2_out, OP3);
  not not_3 (not_3_out, OP2);
  not not_4 (not_4_out, OP4);
  not not_5 (not_5_out, OP2);
  not not_6 (not_6_out, OP4);
  not not_7 (not_7_out, OP2);
  not not_8 (not_8_out, OP1);
  not not_9 (not_9_out, OP0);
  not not_10 (not_10_out, OP5);
  not not_11 (not_11_out, OP4);
  not not_12 (not_12_out, OP2);
  not not_13 (not_13_out, OP1);
  not not_14 (not_14_out, OP0);
  not not_15 (not_15_out, OP5);
  not not_16 (not_16_out, OP4);
  not not_17 (not_17_out, OP1);
  not not_18 (not_18_out, OP0);
  not not_19 (not_19_out, OP5);
  not not_20 (not_20_out, OP4);
  not not_21 (not_21_out, OP2);
  not not_22 (not_22_out, OP1);
  not not_23 (not_23_out, OP5);
  not not_24 (not_24_out, OP4);
  not not_25 (not_25_out, OP2);
  not not_26 (not_26_out, OP0);
  not not_27 (not_27_out, OP5);
  not not_28 (not_28_out, OP4);
  not not_29 (not_29_out, OP1);
  not not_30 (not_30_out, OP4);
  not not_31 (not_31_out, OP3);
  not not_32 (not_32_out, OP2);
  not not_33 (not_33_out, OP4);
  not not_34 (not_34_out, OP2);
  not not_35 (not_35_out, OP4);
  not not_36 (not_36_out, OP2);
  not not_37 (not_37_out, OP1);
  not not_38 (not_38_out, OP0);
  not not_39 (not_39_out, OP5);
  not not_40 (not_40_out, OP4);
  not not_41 (not_41_out, OP3);
  not not_42 (not_42_out, OP2);
  not not_43 (not_43_out, OP1);
  not not_44 (not_44_out, OP0);
  not not_45 (not_45_out, F5);
  not not_46 (not_46_out, F4);
  not not_47 (not_47_out, F3);
  not not_48 (not_48_out, F2);
  not not_49 (not_49_out, F1);
  not not_50 (not_50_out, F0);
  not not_51 (not_51_out, OP5);
  not not_52 (not_52_out, OP4);
  not not_53 (not_53_out, OP3);
  not not_54 (not_54_out, OP2);
  not not_55 (not_55_out, OP1);
  not not_56 (not_56_out, OP0);
  not not_57 (not_57_out, F5);
  not not_58 (not_58_out, F4);
  not not_59 (not_59_out, F3);
  not not_60 (not_60_out, F2);
  not not_61 (not_61_out, OP5);
  not not_62 (not_62_out, OP4);
  not not_63 (not_63_out, OP3);
  not not_64 (not_64_out, OP2);
  not not_65 (not_65_out, OP1);
  not not_66 (not_66_out, OP0);
  not not_67 (not_67_out, F5);
  not not_68 (not_68_out, F4);
  not not_69 (not_69_out, F3);
  not not_70 (not_70_out, F2);
  not not_71 (not_71_out, F0);
  not not_72 (not_72_out, OP5);
  not not_73 (not_73_out, OP4);
  not not_74 (not_74_out, OP3);
  not not_75 (not_75_out, OP2);
  not not_76 (not_76_out, OP1);
  not not_77 (not_77_out, OP0);
  not not_78 (not_78_out, F4);
  not not_79 (not_79_out, F3);
  not not_80 (not_80_out, F2);
  not not_81 (not_81_out, F1);
  not not_82 (not_82_out, F0);
  not not_83 (not_83_out, OP5);
  not not_84 (not_84_out, OP4);
  not not_85 (not_85_out, OP3);
  not not_86 (not_86_out, OP2);
  not not_87 (not_87_out, OP1);
  not not_88 (not_88_out, OP0);
  not not_89 (not_89_out, F4);
  not not_90 (not_90_out, F3);
  not not_91 (not_91_out, F2);
  not not_92 (not_92_out, F1);
  not not_93 (not_93_out, OP5);
  not not_94 (not_94_out, OP4);
  not not_95 (not_95_out, OP3);
  not not_96 (not_96_out, OP2);
  not not_97 (not_97_out, OP1);
  not not_98 (not_98_out, OP0);
  not not_99 (not_99_out, F4);
  not not_100 (not_100_out, F3);
  not not_101 (not_101_out, F2);
  not not_102 (not_102_out, F0);
  not not_103 (not_103_out, OP5);
  not not_104 (not_104_out, OP4);
  not not_105 (not_105_out, OP3);
  not not_106 (not_106_out, OP2);
  not not_107 (not_107_out, OP1);
  not not_108 (not_108_out, OP0);
  not not_109 (not_109_out, F4);
  not not_110 (not_110_out, F3);
  not not_111 (not_111_out, F1);
  not not_112 (not_112_out, F0);
  not not_113 (not_113_out, OP5);
  not not_114 (not_114_out, OP4);
  not not_115 (not_115_out, OP3);
  not not_116 (not_116_out, OP2);
  not not_117 (not_117_out, OP1);
  not not_118 (not_118_out, OP0);
  not not_119 (not_119_out, F4);
  not not_120 (not_120_out, F3);
  not not_121 (not_121_out, F1);
  not not_122 (not_122_out, OP5);
  not not_123 (not_123_out, OP4);
  not not_124 (not_124_out, OP3);
  not not_125 (not_125_out, OP2);
  not not_126 (not_126_out, OP1);
  not not_127 (not_127_out, OP0);
  not not_128 (not_128_out, F4);
  not not_129 (not_129_out, F3);
  not not_130 (not_130_out, OP5);
  not not_131 (not_131_out, OP4);
  not not_132 (not_132_out, OP3);
  not not_133 (not_133_out, OP2);
  not not_134 (not_134_out, OP1);
  not not_135 (not_135_out, OP0);
  not not_136 (not_136_out, F4);
  not not_137 (not_137_out, F2);
  not not_138 (not_138_out, F0);
  not not_139 (not_139_out, OP5);
  not not_140 (not_140_out, OP4);
  not not_141 (not_141_out, OP3);
  not not_142 (not_142_out, OP2);
  not not_143 (not_143_out, OP1);
  not not_144 (not_144_out, OP0);
  not not_145 (not_145_out, F4);
  not not_146 (not_146_out, F2);
  not not_147 (not_147_out, OP5);
  not not_148 (not_148_out, OP4);
  not not_149 (not_149_out, OP3);
  not not_150 (not_150_out, OP2);
  not not_151 (not_151_out, OP5);
  not not_152 (not_152_out, OP4);
  not not_153 (not_153_out, OP2);
  not not_154 (not_154_out, OP1);
  not not_155 (not_155_out, OP0);
  not not_156 (not_156_out, OP5);
  not not_157 (not_157_out, OP4);
  not not_158 (not_158_out, OP1);
  not not_159 (not_159_out, OP0);
  not not_160 (not_160_out, OP5);
  not not_161 (not_161_out, OP4);
  not not_162 (not_162_out, OP2);
  not not_163 (not_163_out, OP1);
  not not_164 (not_164_out, OP5);
  not not_165 (not_165_out, OP4);
  not not_166 (not_166_out, OP2);
  not not_167 (not_167_out, OP0);
  not not_168 (not_168_out, OP5);
  not not_169 (not_169_out, OP4);
  not not_170 (not_170_out, OP1);
  not not_171 (not_171_out, OP4);
  not not_172 (not_172_out, OP3);
  not not_173 (not_173_out, OP2);
  not not_174 (not_174_out, OP5);
  not not_175 (not_175_out, OP4);
  not not_176 (not_176_out, OP3);
  not not_177 (not_177_out, OP2);
  not not_178 (not_178_out, OP1);
  not not_179 (not_179_out, OP0);
  not not_180 (not_180_out, F5);
  not not_181 (not_181_out, F4);
  not not_182 (not_182_out, F3);
  not not_183 (not_183_out, F0);
  not not_184 (not_184_out, OP5);
  not not_185 (not_185_out, OP4);
  not not_186 (not_186_out, OP3);
  not not_187 (not_187_out, OP2);
  not not_188 (not_188_out, OP1);
  not not_189 (not_189_out, OP0);
  not not_190 (not_190_out, F4);
  not not_191 (not_191_out, F3);
  not not_192 (not_192_out, F0);
  not not_193 (not_193_out, OP5);
  not not_194 (not_194_out, OP4);
  not not_195 (not_195_out, OP3);
  not not_196 (not_196_out, OP2);
  not not_197 (not_197_out, OP1);
  not not_198 (not_198_out, OP0);
  not not_199 (not_199_out, F5);
  not not_200 (not_200_out, F4);
  not not_201 (not_201_out, F1);
  not not_202 (not_202_out, F0);
  not not_203 (not_203_out, OP5);
  not not_204 (not_204_out, OP4);
  not not_205 (not_205_out, OP3);
  not not_206 (not_206_out, OP1);
  not not_207 (not_207_out, OP0);
  not not_208 (not_208_out, OP5);
  not not_209 (not_209_out, OP4);
  not not_210 (not_210_out, OP3);
  not not_211 (not_211_out, OP1);
  not not_212 (not_212_out, OP5);
  not not_213 (not_213_out, OP4);
  not not_214 (not_214_out, OP2);
  not not_215 (not_215_out, OP1);
  not not_216 (not_216_out, OP0);
  not not_217 (not_217_out, OP5);
  not not_218 (not_218_out, OP4);
  not not_219 (not_219_out, OP2);
  not not_220 (not_220_out, OP0);
  not not_221 (not_221_out, OP4);
  not not_222 (not_222_out, OP3);
  not not_223 (not_223_out, OP2);
  not not_224 (not_224_out, OP4);
  not not_225 (not_225_out, OP2);
  not not_226 (not_226_out, OP4);
  not not_227 (not_227_out, OP2);
  not not_228 (not_228_out, OP1);
  not not_229 (not_229_out, OP0);
  not not_230 (not_230_out, OP5);
  not not_231 (not_231_out, OP4);
  not not_232 (not_232_out, OP3);
  not not_233 (not_233_out, OP2);
  not not_234 (not_234_out, OP1);
  not not_235 (not_235_out, OP5);
  not not_236 (not_236_out, OP4);
  not not_237 (not_237_out, OP3);
  not not_238 (not_238_out, OP2);
  not not_239 (not_239_out, OP1);
  not not_240 (not_240_out, OP0);
  not not_241 (not_241_out, F5);
  not not_242 (not_242_out, F4);
  not not_243 (not_243_out, F3);
  not not_244 (not_244_out, F2);
  not not_245 (not_245_out, F1);
  not not_246 (not_246_out, F0);
  not not_247 (not_247_out, OP5);
  not not_248 (not_248_out, OP4);
  not not_249 (not_249_out, OP3);
  not not_250 (not_250_out, OP2);
  not not_251 (not_251_out, OP1);
  not not_252 (not_252_out, OP0);
  not not_253 (not_253_out, F5);
  not not_254 (not_254_out, F4);
  not not_255 (not_255_out, F3);
  not not_256 (not_256_out, F2);
  not not_257 (not_257_out, OP5);
  not not_258 (not_258_out, OP4);
  not not_259 (not_259_out, OP3);
  not not_260 (not_260_out, OP2);
  not not_261 (not_261_out, OP1);
  not not_262 (not_262_out, OP0);
  not not_263 (not_263_out, F5);
  not not_264 (not_264_out, F4);
  not not_265 (not_265_out, F3);
  not not_266 (not_266_out, F2);
  not not_267 (not_267_out, F0);
  not not_268 (not_268_out, OP5);
  not not_269 (not_269_out, OP4);
  not not_270 (not_270_out, OP3);
  not not_271 (not_271_out, OP2);
  not not_272 (not_272_out, OP1);
  not not_273 (not_273_out, OP0);
  not not_274 (not_274_out, F4);
  not not_275 (not_275_out, F3);
  not not_276 (not_276_out, F2);
  not not_277 (not_277_out, F1);
  not not_278 (not_278_out, F0);
  not not_279 (not_279_out, OP5);
  not not_280 (not_280_out, OP4);
  not not_281 (not_281_out, OP3);
  not not_282 (not_282_out, OP2);
  not not_283 (not_283_out, OP1);
  not not_284 (not_284_out, OP0);
  not not_285 (not_285_out, F4);
  not not_286 (not_286_out, F3);
  not not_287 (not_287_out, F2);
  not not_288 (not_288_out, F1);
  not not_289 (not_289_out, OP5);
  not not_290 (not_290_out, OP4);
  not not_291 (not_291_out, OP3);
  not not_292 (not_292_out, OP2);
  not not_293 (not_293_out, OP1);
  not not_294 (not_294_out, OP0);
  not not_295 (not_295_out, F4);
  not not_296 (not_296_out, F3);
  not not_297 (not_297_out, F2);
  not not_298 (not_298_out, F0);
  not not_299 (not_299_out, OP5);
  not not_300 (not_300_out, OP4);
  not not_301 (not_301_out, OP3);
  not not_302 (not_302_out, OP2);
  not not_303 (not_303_out, OP1);
  not not_304 (not_304_out, OP0);
  not not_305 (not_305_out, F4);
  not not_306 (not_306_out, F3);
  not not_307 (not_307_out, F1);
  not not_308 (not_308_out, F0);
  not not_309 (not_309_out, OP5);
  not not_310 (not_310_out, OP4);
  not not_311 (not_311_out, OP3);
  not not_312 (not_312_out, OP2);
  not not_313 (not_313_out, OP1);
  not not_314 (not_314_out, OP0);
  not not_315 (not_315_out, F4);
  not not_316 (not_316_out, F3);
  not not_317 (not_317_out, F1);
  not not_318 (not_318_out, OP5);
  not not_319 (not_319_out, OP4);
  not not_320 (not_320_out, OP3);
  not not_321 (not_321_out, OP2);
  not not_322 (not_322_out, OP1);
  not not_323 (not_323_out, OP0);
  not not_324 (not_324_out, F4);
  not not_325 (not_325_out, F3);
  not not_326 (not_326_out, OP5);
  not not_327 (not_327_out, OP4);
  not not_328 (not_328_out, OP3);
  not not_329 (not_329_out, OP2);
  not not_330 (not_330_out, OP1);
  not not_331 (not_331_out, OP0);
  not not_332 (not_332_out, F4);
  not not_333 (not_333_out, F2);
  not not_334 (not_334_out, F0);
  not not_335 (not_335_out, OP5);
  not not_336 (not_336_out, OP4);
  not not_337 (not_337_out, OP3);
  not not_338 (not_338_out, OP2);
  not not_339 (not_339_out, OP1);
  not not_340 (not_340_out, OP0);
  not not_341 (not_341_out, F4);
  not not_342 (not_342_out, F2);
  not not_343 (not_343_out, OP5);
  not not_344 (not_344_out, OP4);
  not not_345 (not_345_out, OP3);
  not not_346 (not_346_out, OP2);
  not not_347 (not_347_out, OP1);
  not not_348 (not_348_out, OP0);
  not not_349 (not_349_out, F5);
  not not_350 (not_350_out, F4);
  not not_351 (not_351_out, F3);
  not not_352 (not_352_out, F0);
  not not_353 (not_353_out, OP5);
  not not_354 (not_354_out, OP4);
  not not_355 (not_355_out, OP3);
  not not_356 (not_356_out, OP2);
  not not_357 (not_357_out, OP1);
  not not_358 (not_358_out, OP0);
  not not_359 (not_359_out, F4);
  not not_360 (not_360_out, F3);
  not not_361 (not_361_out, F0);
  not not_362 (not_362_out, OP5);
  not not_363 (not_363_out, OP4);
  not not_364 (not_364_out, OP3);
  not not_365 (not_365_out, OP1);
  not not_366 (not_366_out, OP0);
  not not_367 (not_367_out, OP5);
  not not_368 (not_368_out, OP4);
  not not_369 (not_369_out, OP3);
  not not_370 (not_370_out, OP1);
  not not_371 (not_371_out, OP5);
  not not_372 (not_372_out, OP4);
  not not_373 (not_373_out, OP3);
  not not_374 (not_374_out, OP2);
  not not_375 (not_375_out, OP1);
  not not_376 (not_376_out, OP0);
  not not_377 (not_377_out, F5);
  not not_378 (not_378_out, F4);
  not not_379 (not_379_out, F2);
  not not_380 (not_380_out, F1);
  not not_381 (not_381_out, F0);
  not not_382 (not_382_out, OP5);
  not not_383 (not_383_out, OP4);
  not not_384 (not_384_out, OP3);
  not not_385 (not_385_out, OP2);
  not not_386 (not_386_out, OP1);
  not not_387 (not_387_out, OP0);
  not not_388 (not_388_out, F5);
  not not_389 (not_389_out, F4);
  not not_390 (not_390_out, F2);
  not not_391 (not_391_out, F1);
  not not_392 (not_392_out, F0);
  not not_393 (not_393_out, OP5);
  not not_394 (not_394_out, OP4);
  not not_395 (not_395_out, OP3);
  not not_396 (not_396_out, OP2);
  not not_397 (not_397_out, OP0);
  not not_398 (not_398_out, OP5);
  not not_399 (not_399_out, OP4);
  not not_400 (not_400_out, OP3);
  not not_401 (not_401_out, OP2);
  not not_402 (not_402_out, OP5);
  not not_403 (not_403_out, OP4);
  not not_404 (not_404_out, OP3);
  not not_405 (not_405_out, OP2);
  not not_406 (not_406_out, OP5);
  not not_407 (not_407_out, OP3);
  not not_408 (not_408_out, OP2);
  not not_409 (not_409_out, OP1);
  not not_410 (not_410_out, OP0);
  not not_411 (not_411_out, F5);
  not not_412 (not_412_out, F2);
  not not_413 (not_413_out, F1);
  not not_414 (not_414_out, F0);
  not not_415 (not_415_out, OP4);
  not not_416 (not_416_out, OP2);
  not not_417 (not_417_out, OP1);
  not not_418 (not_418_out, OP0);
  not not_419 (not_419_out, OP5);
  not not_420 (not_420_out, OP4);
  not not_421 (not_421_out, OP3);
  not not_422 (not_422_out, OP2);
  not not_423 (not_423_out, OP1);
  not not_424 (not_424_out, OP5);
  not not_425 (not_425_out, OP4);
  not not_426 (not_426_out, OP3);
  not not_427 (not_427_out, OP2);
  not not_428 (not_428_out, OP1);
  not not_429 (not_429_out, OP0);
  not not_430 (not_430_out, F5);
  not not_431 (not_431_out, F4);
  not not_432 (not_432_out, F3);
  not not_433 (not_433_out, F0);
  and and_1 (MemToReg, OP5, not_1_out, not_2_out, not_3_out, OP1, OP0);
  and and_2 (and_2_out, OP5, not_4_out, OP3, not_5_out, OP1, OP0);
  and and_3 (and_3_out, OP5, not_6_out, OP3, not_7_out, not_8_out, not_9_out);
  and and_4 (and_4_out, not_10_out, not_11_out, OP3, not_12_out, not_13_out, not_14_out);
  and and_5 (and_5_out, not_15_out, not_16_out, OP3, OP2, not_17_out, not_18_out);
  and and_6 (and_6_out, not_19_out, not_20_out, OP3, not_21_out, not_22_out, OP0);
  and and_7 (and_7_out, not_23_out, not_24_out, OP3, not_25_out, OP1, not_26_out);
  and and_8 (and_8_out, not_27_out, not_28_out, OP3, OP2, not_29_out, OP0);
  and and_9 (and_9_out, OP5, not_30_out, not_31_out, not_32_out, OP1, OP0);
  and and_10 (and_10_out, OP5, not_33_out, OP3, not_34_out, OP1, OP0);
  and and_11 (and_11_out, OP5, not_35_out, OP3, not_36_out, not_37_out, not_38_out);
  and and_12 (and_12_out, not_39_out, not_40_out, not_41_out, not_42_out, not_43_out, not_44_out, not_45_out, not_46_out, not_47_out, not_48_out, not_49_out, not_50_out);
  and and_13 (and_13_out, not_51_out, not_52_out, not_53_out, not_54_out, not_55_out, not_56_out, not_57_out, not_58_out, not_59_out, not_60_out, F1, F0);
  and and_14 (and_14_out, not_61_out, not_62_out, not_63_out, not_64_out, not_65_out, not_66_out, not_67_out, not_68_out, not_69_out, not_70_out, F1, not_71_out);
  and and_15 (and_15_out, not_72_out, not_73_out, not_74_out, not_75_out, not_76_out, not_77_out, F5, not_78_out, not_79_out, not_80_out, not_81_out, not_82_out);
  and and_16 (and_16_out, not_83_out, not_84_out, not_85_out, not_86_out, not_87_out, not_88_out, F5, not_89_out, not_90_out, not_91_out, not_92_out, F0);
  and and_17 (and_17_out, not_93_out, not_94_out, not_95_out, not_96_out, not_97_out, not_98_out, F5, not_99_out, not_100_out, not_101_out, F1, not_102_out);
  and and_18 (and_18_out, not_103_out, not_104_out, not_105_out, not_106_out, not_107_out, not_108_out, F5, not_109_out, not_110_out, F2, not_111_out, not_112_out);
  and and_19 (and_19_out, not_113_out, not_114_out, not_115_out, not_116_out, not_117_out, not_118_out, F5, not_119_out, not_120_out, F2, not_121_out, F0);
  and and_20 (and_20_out, not_122_out, not_123_out, not_124_out, not_125_out, not_126_out, not_127_out, F5, not_128_out, not_129_out, F2, F1, F0);
  and and_21 (and_21_out, not_130_out, not_131_out, not_132_out, not_133_out, not_134_out, not_135_out, F5, not_136_out, F3, not_137_out, F1, not_138_out);
  and and_22 (and_22_out, not_139_out, not_140_out, not_141_out, not_142_out, not_143_out, not_144_out, F5, not_145_out, F3, not_146_out, F1, F0);
  and and_23 (and_23_out, not_147_out, not_148_out, not_149_out, not_150_out, OP1, OP0);
  and and_24 (and_24_out, not_151_out, not_152_out, OP3, not_153_out, not_154_out, not_155_out);
  and and_25 (and_25_out, not_156_out, not_157_out, OP3, OP2, not_158_out, not_159_out);
  and and_26 (and_26_out, not_160_out, not_161_out, OP3, not_162_out, not_163_out, OP0);
  and and_27 (and_27_out, not_164_out, not_165_out, OP3, not_166_out, OP1, not_167_out);
  and and_28 (and_28_out, not_168_out, not_169_out, OP3, OP2, not_170_out, OP0);
  and and_29 (and_29_out, OP5, not_171_out, not_172_out, not_173_out, OP1, OP0);
  and and_30 (and_30_out, not_174_out, not_175_out, not_176_out, not_177_out, not_178_out, not_179_out, not_180_out, not_181_out, not_182_out, F2, F1, not_183_out);
  and and_31 (and_31_out, not_184_out, not_185_out, not_186_out, not_187_out, not_188_out, not_189_out, F5, not_190_out, not_191_out, F2, F1, not_192_out);
  and and_32 (SysCALL, not_193_out, not_194_out, not_195_out, not_196_out, not_197_out, not_198_out, not_199_out, not_200_out, F3, F2, not_201_out, not_202_out);
  and and_33 (and_33_out, not_203_out, not_204_out, not_205_out, OP2, not_206_out, not_207_out);
  and and_34 (and_34_out, not_208_out, not_209_out, not_210_out, OP2, not_211_out, OP0);
  and and_35 (and_35_out, not_212_out, not_213_out, OP3, not_214_out, not_215_out, not_216_out);
  and and_36 (and_36_out, not_217_out, not_218_out, OP3, not_219_out, OP1, not_220_out);
  and and_37 (and_37_out, OP5, not_221_out, not_222_out, not_223_out, OP1, OP0);
  and and_38 (and_38_out, OP5, not_224_out, OP3, not_225_out, OP1, OP0);
  and and_39 (and_39_out, OP5, not_226_out, OP3, not_227_out, not_228_out, not_229_out);
  and and_40 (and_40_out, not_230_out, not_231_out, not_232_out, not_233_out, not_234_out, OP0);
  and and_41 (and_41_out, not_235_out, not_236_out, not_237_out, not_238_out, not_239_out, not_240_out, not_241_out, not_242_out, not_243_out, not_244_out, not_245_out, not_246_out);
  and and_42 (and_42_out, not_247_out, not_248_out, not_249_out, not_250_out, not_251_out, not_252_out, not_253_out, not_254_out, not_255_out, not_256_out, F1, F0);
  and and_43 (and_43_out, not_257_out, not_258_out, not_259_out, not_260_out, not_261_out, not_262_out, not_263_out, not_264_out, not_265_out, not_266_out, F1, not_267_out);
  and and_44 (and_44_out, not_268_out, not_269_out, not_270_out, not_271_out, not_272_out, not_273_out, F5, not_274_out, not_275_out, not_276_out, not_277_out, not_278_out);
  and and_45 (and_45_out, not_279_out, not_280_out, not_281_out, not_282_out, not_283_out, not_284_out, F5, not_285_out, not_286_out, not_287_out, not_288_out, F0);
  and and_46 (and_46_out, not_289_out, not_290_out, not_291_out, not_292_out, not_293_out, not_294_out, F5, not_295_out, not_296_out, not_297_out, F1, not_298_out);
  and and_47 (and_47_out, not_299_out, not_300_out, not_301_out, not_302_out, not_303_out, not_304_out, F5, not_305_out, not_306_out, F2, not_307_out, not_308_out);
  and and_48 (and_48_out, not_309_out, not_310_out, not_311_out, not_312_out, not_313_out, not_314_out, F5, not_315_out, not_316_out, F2, not_317_out, F0);
  and and_49 (and_49_out, not_318_out, not_319_out, not_320_out, not_321_out, not_322_out, not_323_out, F5, not_324_out, not_325_out, F2, F1, F0);
  and and_50 (and_50_out, not_326_out, not_327_out, not_328_out, not_329_out, not_330_out, not_331_out, F5, not_332_out, F3, not_333_out, F1, not_334_out);
  and and_51 (and_51_out, not_335_out, not_336_out, not_337_out, not_338_out, not_339_out, not_340_out, F5, not_341_out, F3, not_342_out, F1, F0);
  and and_52 (and_52_out, not_343_out, not_344_out, not_345_out, not_346_out, not_347_out, not_348_out, not_349_out, not_350_out, not_351_out, F2, F1, not_352_out);
  and and_53 (and_53_out, not_353_out, not_354_out, not_355_out, not_356_out, not_357_out, not_358_out, F5, not_359_out, not_360_out, F2, F1, not_361_out);
  and and_54 (BEQ, not_362_out, not_363_out, not_364_out, OP2, not_365_out, not_366_out);
  and and_55 (BNE, not_367_out, not_368_out, not_369_out, OP2, not_370_out, OP0);
  and and_56 (JR, not_371_out, not_372_out, not_373_out, not_374_out, not_375_out, not_376_out, not_377_out, not_378_out, F3, not_379_out, not_380_out, not_381_out);
  and and_57 (and_57_out, not_382_out, not_383_out, not_384_out, not_385_out, not_386_out, not_387_out, not_388_out, not_389_out, F3, not_390_out, not_391_out, not_392_out);
  and and_58 (and_58_out, not_393_out, not_394_out, not_395_out, not_396_out, OP1, not_397_out);
  and and_59 (and_59_out, not_398_out, not_399_out, not_400_out, not_401_out, OP1, OP0);
  and and_60 (JAL, not_402_out, not_403_out, not_404_out, not_405_out, OP1, OP0);
  and and_61 (ERET, not_406_out, OP4, not_407_out, not_408_out, not_409_out, not_410_out, not_411_out, F4, F3, not_412_out, not_413_out, not_414_out);
  and and_62 (B, OP5, not_415_out, OP3, not_416_out, not_417_out, not_418_out);
  and and_63 (BGEZ, not_419_out, not_420_out, not_421_out, not_422_out, not_423_out, OP0);
  and and_64 (SRLV, not_424_out, not_425_out, not_426_out, not_427_out, not_428_out, not_429_out, not_430_out, not_431_out, not_432_out, F2, F1, not_433_out);
  or or_1 (MemWrite, and_2_out, and_3_out);
  or or_2 (ALU_SRC, and_4_out, and_5_out, and_6_out, and_7_out, and_8_out, and_9_out, and_10_out, and_11_out);
  or or_3 (SignedExt, and_33_out, and_34_out, and_35_out, and_36_out, and_37_out, and_38_out, and_39_out, and_40_out);
  or or_4 (JUMP, and_57_out, and_58_out, and_59_out);
  or or_5 (RegWrite, and_12_out, and_13_out, and_14_out, and_15_out, and_16_out, and_17_out, and_18_out, and_19_out, and_20_out, and_21_out, and_22_out, and_23_out, and_24_out, and_25_out, and_26_out, and_27_out, and_28_out, and_29_out, and_30_out, and_31_out);
  or or_6 (RegDst, and_41_out, and_42_out, and_43_out, and_44_out, and_45_out, and_46_out, and_47_out, and_48_out, and_49_out, and_50_out, and_51_out, and_52_out, and_53_out);
endmodule

// ALU
module MIPS_ALU (
  input  [4:0] shamt,
  input  [31:0] X,
  input  [31:0] Y,
  input  [3:0] AluOP,
  output Equal,
  output GEZ,
  output [31:0] Result,
  output [31:0] Result_2
);

  wire comparator_3_eq, comparator_3_gt;
  wire [0:0] comparator_1_lt, comparator_2_lt;
  wire [31:0] adder_1_out, AND_out, divider_1_out, divider_1_rem, multiplier_1_cout, multiplier_1_out,
       NOR_out, OR_out, shifter_1_out, shifter_2_out, shifter_3_out, subtractor_1_out, XOR_out;

  assign AND_out = X & Y;  // AND_Gate AND, 32 bits wide
  assign OR_out = X | Y;  // OR_Gate OR, 32 bits wide
  Shifter #(.width(32), .shift("ll")) shifter_1 (.in(Y), .\dist (shamt), .out(shifter_1_out));
  Shifter #(.width(32), .shift("ar")) shifter_2 (.in(Y), .\dist (shamt), .out(shifter_2_out));
  Shifter #(.width(32), .shift("lr")) shifter_3 (.in(Y), .\dist (shamt), .out(shifter_3_out));
  Multiplier #(.width(32)) multiplier_1 (.a(X), .b(Y), .out(multiplier_1_out), .cout(multiplier_1_cout));  // open: cin
  Divider #(.width(32)) divider_1 (.a(X), .b(Y), .out(divider_1_out), .rem(divider_1_rem));  // open: upper
  Adder #(.width(32)) adder_1 (.a(X), .b(Y), .out(adder_1_out));  // open: cin, cout
  Subtractor #(.width(32)) subtractor_1 (.a(X), .b(Y), .out(subtractor_1_out));  // open: bin, bout
  assign XOR_out = X ^ Y;  // XOR_Gate XOR, 32 bits wide
  assign NOR_out = ~(X | Y);  // NOR_Gate NOR, 32 bits wide
  Comparator #(.width(32), .mode("twosComplement")) comparator_1 (
    .a(X), .b(Y), .eq(Equal), .lt(comparator_1_lt[0]));  // open: gt
  Comparator #(.width(32), .mode("unsigned")) comparator_2 (.a(X), .b(Y), .lt(comparator_2_lt[0]));  // open: gt, eq
  Comparator #(.width(32), .mode("twosComplement")) comparator_3 (
    .a(X), .b({32{1'b0}}), .gt(comparator_3_gt), .eq(comparator_3_eq));  // open: lt
  or or_2 (GEZ, comparator_3_gt, comparator_3_eq);
  Multiplexer #(.select(4), .width(32), .disabled("Z"), .enable("false")) multiplexer_1 (
    .in0(shifter_1_out), .in1(shifter_2_out), .in2(shifter_3_out), .in3(multiplier_1_out),
    .in4(divider_1_out), .in5(adder_1_out), .in6(subtractor_1_out), .in7(AND_out), .in8(OR_out),
    .in9(XOR_out), .in10(NOR_out), .in11({{31{1'b0}}, comparator_1_lt[0]}),
    .in12({{31{1'b0}}, comparator_2_lt[0]}), .in13({32{1'b0}}), .in14({32{1'b0}}), .in15({32{1'b0}}),
    .out(Result), .sel(AluOP));
  Multiplexer #(.select(4), .width(32), .disabled("Z"), .enable("false")) multiplexer_2 (
    .in0({32{1'b0}}), .in1({32{1'b0}}), .in2({32{1'b0}}), .in3(multiplier_1_cout), .in4(divider_1_rem),
    .in5({32{1'b0}}), .in6({32{1'b0}}), .in7({32{1'b0}}), .in8({32{1'b0}}), .in9({32{1'b0}}),
    .in10({32{1'b0}}), .in11({32{1'b0}}), .in12({32{1'b0}}), .in13({32{1'b0}}), .in14({32{1'b0}}),
    .in15({32{1'b0}}), .out(Result_2), .sel(AluOP));

  // Other names for the same wires on the sheet: Result2[31:0] = Result_2; S[3:0] = AluOP

  // Notes on the sheet:
  //   不要改变此引脚区域内容，也不要改变ALU封装形式
  //   输入引脚
  //   输出引脚
endmodule

module MIPS_Regifile (
  input  [31:0] Din,
  input  Clk,
  input  WE,
  input  [4:0] R1_num,
  input  [4:0] W_num,
  input  [4:0] R2_num,
  output [31:0] R1,
  output [31:0] R2
);

  // RegisterFile registerfile_1: pin names not known; wires that end beside it: Din, Clk, WE, W_num, R1_num, R2_num, R1, R2
endmodule

module \理想流水线  (
  output RegWrite,
  output MemWrite,
  output [31:0] IF_PC,
  output [31:0] ID_PC,
  output [31:0] EX_PC,
  output [31:0] M_PC,
  output [31:0] WB_PC,
  output [31:0] RDin,
  output [31:0] MDin,
  output [31:0] LedData
);

  wire and_2_out, and_4_out, and_5_out, and_6_out, and_7_out, CLK, clock_1_out, clock_2_out, comparator_1_eq,
       comparator_2_eq, comparator_2_lt, d_ff_1_q, equ, EX_ALU_SRC, EX_B, EX_BEQ, EX_BGEZ, EX_BNE, EX_ERET,
       EX_JAL, EX_JMP, EX_JR, EX_MemToReg, EX_MemWrite, EX_RegWrite, EX_SRLV, EX_Syscall, GEZ, Go,
       ID_ALU_SRC, ID_B, ID_BEQ, ID_BGEZ, ID_BNE, ID_ERET, ID_JAL, ID_JMP, ID_JR, ID_MemToReg, ID_MemWrite,
       ID_RegDst, ID_RegWrite, ID_SRLV, ID_Syscall, IR1, IR2, IR3, LedOut, MEM_B, MEM_ERET, MEM_JAL,
       MEM_MemToReg, MEM_RegWrite, MEM_Syscall, nand_2_out, RST, run, sel1, sel2, sel3, sel4, SignedExt, W1,
       W2, W3, WB_ERET, WB_JAL, WB_MemToReg, WB_Syscall;
  wire [2:0] Branch;
  wire [3:0] decoder_1_out0, EX_ALU_OP, ID_ALU_OP;
  wire [4:0] EX_sa, EX_W_num, ID_W_num, MEM_W_num, multiplexer_3_out, multiplexer_4_out, multiplexer_7_out,
       WB_W_num;
  wire [7:0] demultiplexer_1_out0, demultiplexer_1_out1, demultiplexer_1_out2, demultiplexer_1_out3, MDin1,
       MDin2, MDin3, MDin4;
  wire [12:0] CNT_num;
  wire [15:0] \LoadUse次数 , \总周期数 , \插入气泡数 , \无条件分支数 , \条件分支成功数 ;
  wire [27:2] IAddr;
  wire [31:0] adder_3_out, adder_4_out, BAddr, bit_extender_1_out, bit_extender_2_out, EX_ExtImm, EX_IR,
       EX_MDin, EX_R, EX_R1, ID_ExtImm, ID_MDin, ID_R1, IF_IR, MEM_IR, MEM_MDout, MEM_R, multiplexer_6_out,
       nextPC, PC_4, shifter_1_out, WB_IR, WB_MDout, WB_R;
  wire [31:26] ID_IR;

  Button \u_总复位  (.out(RST));
  Button _1 (.out(IR1));
  Button _2 (.out(IR2));
  Button _3 (.out(IR3));
  // Probe on \总周期数 
  // Probe on \总周期数 
  Button \u_继续运行  (.out(Go));
  LED #(.active("true")) led_1 (.in(W1));
  LED #(.active("true")) led_2 (.in(W2));
  LED #(.active("true")) led_3 (.in(W3));
  Hex_Digit_Display hex_digit_display_1 (.value(LedData[31:28]));  // open: dp
  // Probe on IF_PC[19:0]
  // Mips_Probe mips_probe_1: pin names not known; wires that end beside it: IF_IR
  Register #(.width(32), .trigger("rising"), .Select("low")) PC (.D(nextPC), .en(run), .Q(IF_PC), .clk(CLK), .clr(RST));
  Hex_Digit_Display hex_digit_display_2 (.value(LedData[27:24]));  // open: dp
  Hex_Digit_Display hex_digit_display_3 (.value(LedData[23:20]));  // open: dp
  // Probe on ID_PC[19:0]
  // Mips_Probe mips_probe_2: pin names not known; wires that end beside it: {ID_IR, IAddr}
  Hex_Digit_Display hex_digit_display_4 (.value(LedData[19:16]));  // open: dp
  Hex_Digit_Display hex_digit_display_5 (.value(LedData[15:12]));  // open: dp
  Counter #(.width(16), .max('hffff), .ongoal("wrap"), .trigger("rising"), .behavior("new")) counter_1 (
    .count(run), .Q(\总周期数 ), .clk(CLK), .clr(RST));  // open: load, D, carry, preset, down
  ROM #(.addrWidth(10), .dataWidth(32), .Select("high")) rom_1 (.addr(IF_PC[11:2]), .data(IF_IR));
  Adder #(.width(32)) adder_1 (.a(IF_PC), .b(32'h4), .out(PC_4));  // open: cin, cout
  Multiplexer #(.select(3), .width(32), .disabled("Z"), .enable("false")) multiplexer_1 (
    .in0(PC_4), .in1(BAddr), .in2({ID_PC[31:28], IAddr, 2'b00}), .in4(EX_R1), .out(nextPC), .sel(Branch));  // open: in3, in5, in6, in7
  Hex_Digit_Display hex_digit_display_6 (.value(LedData[7:4]));  // open: dp
  Hex_Digit_Display hex_digit_display_7 (.value(LedData[11:8]));  // open: dp
  Clock #(.highDuration(1), .lowDuration(1)) clock_1 (.out(clock_1_out));
  // Probe on EX_PC[19:0]
  // Mips_Probe mips_probe_3: pin names not known; wires that end beside it: clock_1_out, EX_IR, CLK
  Hex_Digit_Display hex_digit_display_8 (.value(LedData[3:0]));  // open: dp
  Register #(.width(32), .trigger("rising"), .Select("low")) register_1 (
    .D(MDin), .en(LedOut), .Q(LedData), .clk(CLK), .clr(RST));
  // IF_ID if_id_1: pin names not known; wires that end beside it: IF_IR, IF_PC, run, RST, CLK, {ID_IR, IAddr}, ID_PC
  // Probe on \总周期数 
  // Probe on M_PC[19:0]
  // Mips_Probe mips_probe_4: pin names not known; wires that end beside it: MEM_IR
  // Probe on \总周期数 
  // Probe on \无条件分支数 
  // Probe on \条件分支成功数 
  // Probe on \插入气泡数 
  // Probe on \LoadUse次数 
  // Probe on WB_R
  \单周期硬布线控制器  \u_单周期硬布线控制器_1  (
    .Func(IAddr[7:2]), .OP(ID_IR), .ALU_OP(ID_ALU_OP), .MemToReg(ID_MemToReg), .MemWrite(ID_MemWrite),
    .ALU_SRC(ID_ALU_SRC), .RegWrite(ID_RegWrite), .SysCALL(ID_Syscall), .SignedExt(SignedExt),
    .RegDst(ID_RegDst), .JR(ID_JR), .JMP(ID_JMP), .Beq(ID_BEQ), .JAL(ID_JAL), .Bne(ID_BNE), .ERET(ID_ERET),
    .B(ID_B), .BGEZ(ID_BGEZ), .SRLV(ID_SRLV));
  // Probe on IF_PC[11:0]
  // Probe on WB_PC[19:0]
  // Mips_Probe mips_probe_5: pin names not known; wires that end beside it: WB_IR
  // Probe on EX_PC[11:0]
  // Probe on ID_PC[11:0]
  Comparator #(.width(32), .mode("twosComplement")) comparator_1 (
    .a(32'h22), .b(WB_R), .eq(comparator_1_eq));  // open: gt, lt
  Multiplexer #(.select(2), .width(5), .disabled("Z"), .enable("false")) multiplexer_2 (
    .in0(IAddr[22:18]), .in1(IAddr[17:13]), .in2({5{1'b1}}), .in3({5{1'b1}}), .out(ID_W_num),
    .sel({ID_JAL, ID_RegDst}));
  // Probe on M_PC[11:0]
  D_Flip_Flop #(.trigger("high"), .Pre_Clr_Positions("LEGACY"), .NegatePresetClear("false"), .enable("true"), .NewFFLayout("false")) d_ff_1 (.Q(d_ff_1_q));  // open: clk, D, Qn, preset, en, reset
  // Probe on 13'hc
  and and_1 (LedOut, WB_Syscall, comparator_1_eq);
  nand nand_1 (run, WB_Syscall, ~comparator_1_eq);  // NAND_Gate
  Multiplexer #(.select(1), .width(5), .disabled("Z"), .enable("false")) multiplexer_3 (
    .in0(IAddr[27:23]), .in1(5'b00010), .out(multiplexer_3_out), .sel(ID_Syscall));
  Multiplexer #(.select(1), .width(5), .disabled("Z"), .enable("false")) multiplexer_4 (
    .in0(IAddr[22:18]), .in1(5'b00100), .out(multiplexer_4_out), .sel(ID_Syscall));
  // Probe on WB_PC[11:0]
  Comparator #(.width(13), .mode("twosComplement")) comparator_2 (
    .a(CNT_num), .b(13'hc), .eq(comparator_2_eq), .lt(comparator_2_lt));  // open: gt
  Clock #(.highDuration(1), .lowDuration(1)) clock_2 (.out(clock_2_out));
  assign bit_extender_1_out = {{16{1'b0}}, IAddr[17:2]};  // Bit_Extender bit_extender_1
  assign bit_extender_2_out = {{16{IAddr[17]}}, IAddr[17:2]};  // Bit_Extender bit_extender_2
  nand nand_2 (nand_2_out, d_ff_1_q, comparator_2_eq);
  Counter #(.width(13), .max('h1fff), .ongoal("stay"), .trigger("rising"), .behavior("old")) counter_2 (
    .count(comparator_2_lt), .Q(CNT_num), .clk(clock_2_out));  // open: load, D, carry, clr, preset
  MIPS_Regifile mips_regifile_1 (
    .Din(RDin), .Clk(CLK), .R1(ID_R1), .R2(ID_MDin), .WE(RegWrite), .W_num(WB_W_num),
    .R1_num(multiplexer_3_out), .R2_num(multiplexer_4_out));
  Multiplexer #(.select(1), .width(32), .disabled("Z"), .enable("false")) multiplexer_5 (
    .in0(bit_extender_1_out), .in1(bit_extender_2_out), .out(ID_ExtImm), .sel(SignedExt));
  assign CLK = nand_2_out ? clock_2_out : 1'bz;  // Controlled_Buffer controlled_buffer_1
  // ID_EX id_ex_1: pin names not known; wires that end beside it: ID_B, ID_ERET, ID_SRLV, ID_JMP, ID_JR, ID_BEQ, ID_BNE, ID_BGEZ, ID_JAL, ID_MemToReg, ID_MemWrite, ID_ALU_SRC, ID_RegWrite, ID_Syscall, ID_ALU_OP, {ID_IR, IAddr}, ID_R1, ID_MDin, ID_ExtImm, ID_W_num, IAddr[12:8], ID_PC, run, RST, CLK, EX_B, EX_ERET, EX_SRLV, EX_JMP, EX_JR, EX_BEQ, EX_BNE, EX_BGEZ, EX_JAL, EX_MemToReg, EX_MemWrite, EX_ALU_SRC, EX_RegWrite, EX_Syscall, EX_ALU_OP, EX_IR, EX_R1, EX_MDin, EX_ExtImm, EX_W_num, EX_sa, EX_PC
  Pull_Resistor #(.pull(1)) pull_resistor_1 (.node(CLK));
  and and_2 (and_2_out, EX_JAL, EX_JMP);
  and and_3 (Branch[2], EX_JR, EX_JMP);
  and and_4 (and_4_out, GEZ, EX_BGEZ);
  and and_5 (and_5_out, equ, EX_BEQ);
  or or_1 (Branch[0], and_5_out, and_4_out, and_6_out);
  and and_6 (and_6_out, ~equ, EX_BNE);  // AND_Gate
  and and_7 (and_7_out, ~EX_JR, ~EX_JAL, EX_JMP);  // AND_Gate
  or or_2 (Branch[1], and_2_out, and_7_out);
  Multiplexer #(.select(1), .width(32), .disabled("Z"), .enable("false")) multiplexer_6 (
    .in0(EX_MDin), .in1(EX_ExtImm), .out(multiplexer_6_out), .sel(EX_ALU_SRC));
  Shifter #(.width(32), .shift("ll")) shifter_1 (.in(EX_ExtImm), .\dist (5'b00010), .out(shifter_1_out));
  Adder #(.width(32)) adder_2 (.a(shifter_1_out), .b(adder_3_out), .out(BAddr));  // open: cin, cout
  Adder #(.width(32)) adder_3 (.a(32'h4), .b(EX_PC), .out(adder_3_out));  // open: cin, cout
  MIPS_ALU mips_alu_1 (
    .X(EX_R1), .Y(multiplexer_6_out), .AluOP(EX_ALU_OP), .Equal(equ), .Result(EX_R),
    .shamt(multiplexer_7_out), .GEZ(GEZ));  // open: Result_2
  Multiplexer #(.select(1), .width(5), .disabled("Z"), .enable("false")) multiplexer_7 (
    .in0(EX_sa), .in1(EX_R1[4:0]), .out(multiplexer_7_out), .sel(EX_SRLV));
  // EX_MEM ex_mem_1: pin names not known; wires that end beside it: EX_B, EX_ERET, EX_JAL, EX_MemToReg, EX_MemWrite, EX_RegWrite, EX_Syscall, EX_R, EX_IR, EX_MDin, EX_W_num, EX_PC, run, RST, CLK, MEM_B, MEM_ERET, MEM_JAL, MEM_MemToReg, MemWrite, MEM_RegWrite, MEM_Syscall, MEM_R, MEM_IR, MDin, MEM_W_num, M_PC
  Decoder #(.select(2), .tristate("false"), .disabled("Z"), .enable("false")) decoder_1 (
    .out0(decoder_1_out0[0]), .out1(decoder_1_out0[1]), .out2(decoder_1_out0[2]), .out3(decoder_1_out0[3]),
    .sel(MEM_R[1:0]));
  Demultiplexer #(.select(2), .width(8), .tristate("false"), .disabled("Z"), .enable("false")) demultiplexer_1 (
    .out0(demultiplexer_1_out0), .out1(demultiplexer_1_out1), .out2(demultiplexer_1_out2),
    .out3(demultiplexer_1_out3), .in(MDin[7:0]), .sel(MEM_R[1:0]));
  assign {sel4, sel3, sel2, sel1} = MEM_B ? decoder_1_out0 : 4'bz;  // Controlled_Buffer controlled_buffer_2
  assign {MDin4, MDin3, MDin2, MDin1} = MEM_B ? {demultiplexer_1_out3, demultiplexer_1_out2, demultiplexer_1_out1, demultiplexer_1_out0} : 32'bz;  // Controlled_Buffer controlled_buffer_3
  assign {sel4, sel3, sel2, sel1} = ~MEM_B ? 4'b1111 : 4'bz;  // Controlled_Buffer controlled_buffer_4
  assign {MDin4, MDin3, MDin2, MDin1} = ~MEM_B ? MDin : 32'bz;  // Controlled_Buffer controlled_buffer_5
  RAM #(.addrWidth(10), .dataWidth(8), .bus("separate"), .Select("high")) ram_1 (
    .addr(MEM_R[11:2]), .din(MDin1), .data(MEM_MDout[7:0]), .str(MemWrite), .sel(sel1), .clk(CLK), .clr(RST));  // open: ld
  RAM #(.addrWidth(10), .dataWidth(8), .bus("separate"), .Select("high")) ram_2 (
    .addr(MEM_R[11:2]), .din(MDin2), .data(MEM_MDout[15:8]), .str(MemWrite), .sel(sel2), .clk(CLK), .clr(RST));  // open: ld
  RAM #(.addrWidth(10), .dataWidth(8), .bus("separate"), .Select("high")) ram_3 (
    .addr(MEM_R[11:2]), .din(MDin3), .data(MEM_MDout[23:16]), .str(MemWrite), .sel(sel3), .clk(CLK), .clr(RST));  // open: ld
  RAM #(.addrWidth(10), .dataWidth(8), .bus("separate"), .Select("high")) ram_4 (
    .addr(MEM_R[11:2]), .din(MDin4), .data(MEM_MDout[31:24]), .str(MemWrite), .sel(sel4), .clk(CLK), .clr(RST));  // open: ld
  // MEM_WB mem_wb_1: pin names not known; wires that end beside it: MEM_ERET, MEM_JAL, MEM_MemToReg, MEM_RegWrite, MEM_Syscall, MEM_R, MEM_MDout, MEM_IR, MEM_W_num, M_PC, run, RST, CLK, WB_ERET, WB_JAL, WB_MemToReg, RegWrite, WB_Syscall, WB_R, WB_MDout, WB_IR, WB_W_num, WB_PC
  Adder #(.width(32)) adder_4 (.a(32'h4), .b(WB_PC), .out(adder_4_out));  // open: cin, cout
  Multiplexer #(.select(2), .width(32), .disabled("Z"), .enable("false")) multiplexer_8 (
    .in0(WB_R), .in1(adder_4_out), .in2(WB_MDout), .out(RDin), .sel({WB_MemToReg, WB_JAL}));  // open: in3

  // Other names for the same wires on the sheet: ID_IR[25:0] = IAddr; Imm16[15:0] = IAddr[17:2]; Imm26[25:0] = IAddr;
  //   ID_sa[4:0] = IAddr[12:8]; rd[4:0] = IAddr[17:13]; rt[4:0] = IAddr[22:18]; rs[4:0] = IAddr[27:23];
  //   IAddr[31:28] = ID_PC[31:28]; MEM_MDin[31:0] = MDin; MEM_MemWrite = MemWrite; MEM_PC[31:0] = M_PC;
  //   MemAddr[9:0] = MEM_R[11:2]; PC[31:0] = IF_PC; RAddr[31:0] = EX_R1; WB_RegWrite = RegWrite

  // Notes on the sheet:
  //   中断源
  //   时空图监测，可删除
  //   中断等待指示
  //   指令存储器
  //   数码管输出
  //   contents of rom_1 (hex, n*v repeats v):
  //   20100000 20110000 20120000 20130000 36100000 36310001 36520002 36730003 ae100000 ae110004 ae120008
  //   ae13000c 2002000a 20110000 20120000 20130000 c
  //   OP
  //   Func
  //   rs
  //   rt
  //   rd
  //   sa
  //   Imm16
  //   Imm26
  //   display
  //   控制位
  //   v0
  //   t0
  //   ra
  //   流水调试日志用
  //   暂停节拍，不能为0
  //   戳工具置1进入计数暂停模式，ctrl+k时钟自动运行到对应节拍暂停
  //   ctrl+k关闭时钟连续运行，将控制位置零，进入单步调试模式调试
  //   用这个时钟源需要去掉电路中的其他时钟源
  //   可计数暂停的时钟源
  //   为方便自动评测，需要输出流水线各段保存的PC值，注意是PC不是PC+4，另外ID段寄存器写入信息，Mem段内存写入信息也要输出
endmodule

module \气泡流水线  (
  output RegWrite,
  output MemWrite,
  output [31:0] IF_PC,
  output [31:0] ID_PC,
  output [31:0] EX_PC,
  output [31:0] M_PC,
  output [31:0] WB_PC,
  output [31:0] RDin,
  output [31:0] MDin,
  output [31:0] LedData
);

  wire and_1_out, and_2_out, and_3_out, and_4_out, and_5_out, and_6_out, and_7_out, and_8_out, and_9_out,
       and_10_out, and_11_out, and_14_out, CLK, clock_1_out, clock_2_out, comparator_1_eq, comparator_2_eq,
       comparator_3_eq, comparator_4_eq, comparator_5_eq, comparator_6_eq, comparator_7_eq, comparator_7_lt,
       comparator_8_eq, comparator_9_eq, d_ff_1_q, DataHazzard, equ, EX_ALU_SRC, EX_BEQ, EX_BGEZ, EX_BNE,
       EX_JAL, EX_JMP, EX_JR, EX_RegWrite, EX_SRLV, flush, GEZ, Go, ID_ALU_SRC, ID_B, ID_BEQ, ID_BGEZ,
       ID_BNE, ID_ERET, id_ex_1_ex_b, id_ex_1_ex_eret, id_ex_1_ex_memreg, id_ex_1_ex_memtoreg,
       id_ex_1_ex_syscall, ID_JAL, ID_JMP, ID_JR, ID_MemToReg, ID_MemWrite, ID_RegDst, ID_RegWrite, ID_SRLV,
       ID_Syscall, IR1, IR2, IR3, LedOut, MEM_B, MEM_ERET, MEM_JAL, MEM_MemToReg, MEM_RegWrite, MEM_Syscall,
       nand_1_out, not_1_out, not_2_out, not_3_out, not_4_out, not_5_out, not_6_out, not_7_out, or_2_out,
       Pause, RST, RsUsed, RtUsed, sel1, sel2, sel3, sel4, SignedExt, W1, W2, W3, WB_ERET, WB_JAL,
       WB_MemToReg;
  wire [2:0] Branch;
  wire [3:0] decoder_1_out0, EX_ALU_OP, ID_ALU_OP;
  wire [4:0] EX_sa, EX_W_num, ID_W_num, MEM_W_num, multiplexer_7_out, R1_num, R2_num, WB_W_num;
  wire [5:0] FUNC;
  wire [7:0] demultiplexer_1_out0, demultiplexer_1_out1, demultiplexer_1_out2, demultiplexer_1_out3, MDin1,
       MDin2, MDin3, MDin4;
  wire [12:0] CNT_num;
  wire [15:0] \LoadUse次数 , \总周期数 , \插入气泡数 , \无条件分支数 , \条件分支成功数 ;
  wire [25:0] EX_Imm26;
  wire [25:6] ID_Imm26;
  wire [31:0] adder_2_out, adder_4_out, BAddr, bit_extender_1_out, bit_extender_2_out, EX_ExtImm, EX_IR,
       EX_MDin, EX_R, EX_R1, ID_ExtImm, ID_MDin, ID_R1, IF_IR, MEM_IR, MEM_MDout, MEM_R, MEM_R1,
       multiplexer_6_out, nextPC, PC_4, shifter_1_out, WB_IR, WB_MDout, WB_R;
  wire [31:26] ID_IR;

  Button \u_总复位  (.out(RST));
  Button _1 (.out(IR1));
  Button _2 (.out(IR2));
  Button _3 (.out(IR3));
  // Probe on \总周期数 
  // Probe on \总周期数 
  Button \u_继续运行  (.out(Go));
  LED #(.active("true")) led_1 (.in(W1));
  LED #(.active("true")) led_2 (.in(W2));
  LED #(.active("true")) led_3 (.in(W3));
  // Probe on IF_PC[19:0]
  // Mips_Probe mips_probe_1: pin names not known; wires that end beside it: IF_IR
  and and_1 (and_1_out, ~Pause, ~DataHazzard);  // AND_Gate
  Hex_Digit_Display hex_digit_display_1 (.value(LedData[31:28]));  // open: dp
  Hex_Digit_Display hex_digit_display_2 (.value(LedData[27:24]));  // open: dp
  Register #(.width(32), .trigger("rising"), .Select("low")) PC (
    .D(nextPC), .en(and_1_out), .Q(IF_PC), .clk(CLK), .clr(RST));
  Hex_Digit_Display hex_digit_display_3 (.value(LedData[23:20]));  // open: dp
  Hex_Digit_Display hex_digit_display_4 (.value(LedData[19:16]));  // open: dp
  // Probe on ID_PC[19:0]
  // Mips_Probe mips_probe_2: pin names not known; wires that end beside it: {ID_IR, ID_Imm26, FUNC}
  Hex_Digit_Display hex_digit_display_5 (.value(LedData[11:8]));  // open: dp
  Hex_Digit_Display hex_digit_display_6 (.value(LedData[15:12]));  // open: dp
  ROM #(.addrWidth(10), .dataWidth(32), .Select("high")) rom_1 (.addr(IF_PC[11:2]), .data(IF_IR));
  Adder #(.width(32)) adder_1 (.a(IF_PC), .b(32'h4), .out(PC_4));  // open: cin, cout
  Multiplexer #(.select(3), .width(32), .disabled("Z"), .enable("false")) multiplexer_1 (
    .in0(PC_4), .in1(BAddr), .in2({EX_PC[31:28], EX_Imm26, 2'b00}), .in4(EX_R1), .out(nextPC), .sel(Branch));  // open: in3, in5, in6, in7
  Hex_Digit_Display hex_digit_display_7 (.value(LedData[3:0]));  // open: dp
  Hex_Digit_Display hex_digit_display_8 (.value(LedData[7:4]));  // open: dp
  Clock #(.highDuration(1), .lowDuration(1)) clock_1 (.out(clock_1_out));
  // Probe on EX_PC[19:0]
  // Mips_Probe mips_probe_3: pin names not known; wires that end beside it: clock_1_out, EX_IR, CLK
  and and_2 (and_2_out, ~Pause, ~DataHazzard);  // AND_Gate
  Rs_Rt rs_rt_1 (
    .OP0(ID_IR[26]), .OP1(ID_IR[27]), .OP2(ID_IR[28]), .OP3(ID_IR[29]), .OP4(ID_IR[30]), .OP5(ID_IR[31]),
    .F0(FUNC[0]), .F1(FUNC[1]), .F2(FUNC[2]), .F3(FUNC[3]), .F4(FUNC[4]), .F5(FUNC[5]), .RsUsed(RsUsed),
    .RtUsed(RtUsed));
  IF_ID if_id_1 (
    .IF_PC(IF_PC), .IF_IR(IF_IR), .CLK(CLK), .ID_PC(ID_PC), .ID_IR({ID_IR, ID_Imm26, FUNC}), .RST(RST),
    .RUN(and_2_out), .Bubble(flush));  // open: IF_Predict, ID_Predict, IF_Valid, ID_Valid, IF_Hit, ID_Hit
  // Probe on \总周期数 
  // Probe on M_PC[19:0]
  // Mips_Probe mips_probe_4: pin names not known; wires that end beside it: MEM_IR
  // Probe on \总周期数 
  // Probe on \无条件分支数 
  // Probe on \条件分支成功数 
  // Probe on \插入气泡数 
  // Probe on \LoadUse次数 
  // Probe on WB_PC[19:0]
  // Mips_Probe mips_probe_5: pin names not known; wires that end beside it: WB_IR
  \单周期硬布线控制器  \u_单周期硬布线控制器_1  (
    .Func(FUNC), .OP(ID_IR), .ALU_OP(ID_ALU_OP), .MemToReg(ID_MemToReg), .MemWrite(ID_MemWrite),
    .ALU_SRC(ID_ALU_SRC), .RegWrite(ID_RegWrite), .SysCALL(ID_Syscall), .SignedExt(SignedExt),
    .RegDst(ID_RegDst), .JR(ID_JR), .JMP(ID_JMP), .Beq(ID_BEQ), .JAL(ID_JAL), .Bne(ID_BNE), .ERET(ID_ERET),
    .B(ID_B), .BGEZ(ID_BGEZ), .SRLV(ID_SRLV));
  Comparator #(.width(5), .mode("unsigned")) comparator_1 (
    .a(R1_num), .b({5{1'b0}}), .eq(comparator_1_eq));  // open: gt, lt
  Comparator #(.width(5), .mode("unsigned")) comparator_2 (
    .a(R2_num), .b({5{1'b0}}), .eq(comparator_2_eq));  // open: gt, lt
  Comparator #(.width(5), .mode("unsigned")) comparator_3 (
    .a(R1_num), .b(EX_W_num), .eq(comparator_3_eq));  // open: gt, lt
  Comparator #(.width(5), .mode("unsigned")) comparator_4 (
    .a(R2_num), .b(EX_W_num), .eq(comparator_4_eq));  // open: gt, lt
  Comparator #(.width(5), .mode("unsigned")) comparator_5 (
    .a(R1_num), .b(MEM_W_num), .eq(comparator_5_eq));  // open: gt, lt
  Comparator #(.width(5), .mode("unsigned")) comparator_6 (
    .a(R2_num), .b(MEM_W_num), .eq(comparator_6_eq));  // open: gt, lt
  // Probe on IF_PC[11:0]
  not not_1 (not_1_out, comparator_1_eq);
  not not_2 (not_2_out, comparator_2_eq);
  // Probe on EX_PC[11:0]
  // Probe on ID_PC[11:0]
  D_Flip_Flop #(.trigger("high"), .Pre_Clr_Positions("LEGACY"), .NegatePresetClear("false"), .enable("true"), .NewFFLayout("false")) d_ff_1 (.Q(d_ff_1_q));  // open: clk, D, Qn, preset, en, reset
  Multiplexer #(.select(1), .width(5), .disabled("Z"), .enable("false")) multiplexer_2 (
    .in0(ID_Imm26[25:21]), .in1(5'b00010), .out(R1_num), .sel(ID_Syscall));
  Multiplexer #(.select(1), .width(5), .disabled("Z"), .enable("false")) multiplexer_3 (
    .in0(ID_Imm26[20:16]), .in1(5'b00100), .out(R2_num), .sel(ID_Syscall));
  Multiplexer #(.select(2), .width(5), .disabled("Z"), .enable("false")) multiplexer_4 (
    .in0(ID_Imm26[20:16]), .in1(ID_Imm26[15:11]), .in2({5{1'b1}}), .in3({5{1'b1}}), .out(ID_W_num),
    .sel({ID_JAL, ID_RegDst}));
  // Probe on M_PC[11:0]
  // Probe on WB_PC[11:0]
  // Probe on 13'h5b5
  and and_3 (and_3_out, not_1_out, EX_RegWrite, comparator_3_eq, RsUsed);
  and and_4 (and_4_out, not_2_out, EX_RegWrite, RtUsed, comparator_4_eq);
  and and_5 (and_5_out, not_1_out, RsUsed, MEM_RegWrite, comparator_5_eq);
  and and_6 (and_6_out, RtUsed, MEM_RegWrite, comparator_6_eq, not_2_out);
  Comparator #(.width(13), .mode("twosComplement")) comparator_7 (
    .a(CNT_num), .b(13'h5b5), .eq(comparator_7_eq), .lt(comparator_7_lt));  // open: gt
  Clock #(.highDuration(1), .lowDuration(1)) clock_2 (.out(clock_2_out));
  not not_3 (not_3_out, CLK);
  MIPS_Regifile mips_regifile_1 (
    .Din(RDin), .Clk(not_3_out), .R1(ID_R1), .R2(ID_MDin), .WE(RegWrite), .W_num(WB_W_num), .R1_num(R1_num),
    .R2_num(R2_num));
  assign bit_extender_1_out = {{16{1'b0}}, {ID_Imm26[15:6], FUNC}};  // Bit_Extender bit_extender_1
  Multiplexer #(.select(1), .width(32), .disabled("Z"), .enable("false")) multiplexer_5 (
    .in0(bit_extender_1_out), .in1(bit_extender_2_out), .out(ID_ExtImm), .sel(SignedExt));
  assign bit_extender_2_out = {{16{ID_Imm26[15]}}, {ID_Imm26[15:6], FUNC}};  // Bit_Extender bit_extender_2
  nand nand_1 (nand_1_out, d_ff_1_q, comparator_7_eq);
  Counter #(.width(13), .max('h1fff), .ongoal("stay"), .trigger("rising"), .behavior("old")) counter_1 (
    .count(comparator_7_lt), .Q(CNT_num), .clk(clock_2_out));  // open: load, D, carry, clr, preset
  not not_4 (not_4_out, Pause);
  or or_1 (DataHazzard, and_3_out, and_4_out, and_5_out, and_6_out);
  assign CLK = nand_1_out ? clock_2_out : 1'bz;  // Controlled_Buffer controlled_buffer_1
  Pull_Resistor #(.pull(1)) pull_resistor_1 (.node(CLK));
  or or_2 (or_2_out, DataHazzard, flush);
  ID_EX id_ex_1 (
    .CLK(CLK), .ID_PC(ID_PC), .ID_IR({ID_IR, ID_Imm26, FUNC}), .RST(RST), .EX_PC(EX_PC), .EX_IR(EX_IR),
    .ID_R1(ID_R1), .ID_R2(ID_MDin), .EX_R1(EX_R1), .EX_R2(EX_MDin), .ID_ExtImm(ID_ExtImm),
    .ID_W_num(ID_W_num), .EX_ExtImm(EX_ExtImm), .EX_W_num(EX_W_num), .ID_B(ID_B), .ID_ERET(ID_ERET),
    .ID_SRLV(ID_SRLV), .ID_JMP(ID_JMP), .ID_JR(ID_JR), .ID_BEQ(ID_BEQ), .ID_BNE(ID_BNE), .ID_BGEZ(ID_BGEZ),
    .ID_JAL(ID_JAL), .ID_MemToReg(ID_MemToReg), .ID_MemWrite(ID_MemWrite), .ID_ALU_SRC(ID_ALU_SRC),
    .ID_RegWrite(ID_RegWrite), .ID_Syscall(ID_Syscall), .ID_AlU_OP(ID_ALU_OP), .EX_B(id_ex_1_ex_b),
    .EX_ERET(id_ex_1_ex_eret), .EX_SRLV(EX_SRLV), .EX_JMP(EX_JMP), .EX_JR(EX_JR), .EX_BEQ(EX_BEQ),
    .EX_BNE(EX_BNE), .EX_BGEZ(EX_BGEZ), .EX_JAL(EX_JAL), .EX_MemToReg(id_ex_1_ex_memtoreg),
    .EX_MemReg(id_ex_1_ex_memreg), .EX_ALU_SRC(EX_ALU_SRC), .EX_RegWrite(EX_RegWrite),
    .EX_Syscall(id_ex_1_ex_syscall), .EX_ALU_OP(EX_ALU_OP), .ID_sa(ID_Imm26[10:6]), .EX_sa(EX_sa),
    .RUN(not_4_out), .Bubble(or_2_out), .ID_Imm26({ID_Imm26, FUNC}), .EX_Imm26(EX_Imm26));  // open: ID_rs_f, EX_rs_f, ID_rt_f, EX_rt_f, ID_Predict, EX_Predict, EX_MFC0, ID_MFC0, ID_MTC0, EX_MTC0, ID_Valid, EX_Valid, EX_Hit, in_34
  Shifter #(.width(32), .shift("ll")) shifter_1 (.in(EX_ExtImm), .\dist (5'b00010), .out(shifter_1_out));
  Adder #(.width(32)) adder_2 (.a(32'h4), .b(EX_PC), .out(adder_2_out));  // open: cin, cout
  and and_7 (and_7_out, equ, EX_BEQ);
  or or_3 (Branch[0], and_7_out, and_8_out, and_9_out);
  and and_8 (and_8_out, GEZ, EX_BGEZ);
  and and_9 (and_9_out, ~equ, EX_BNE);  // AND_Gate
  and and_10 (and_10_out, ~EX_JAL, ~EX_JR, EX_JMP);  // AND_Gate
  or or_4 (Branch[1], and_10_out, and_11_out);
  and and_11 (and_11_out, EX_JMP, EX_JAL);
  and and_12 (Branch[2], EX_JMP, EX_JR);
  Multiplexer #(.select(1), .width(32), .disabled("Z"), .enable("false")) multiplexer_6 (
    .in0(EX_MDin), .in1(EX_ExtImm), .out(multiplexer_6_out), .sel(EX_ALU_SRC));
  Multiplexer #(.select(1), .width(5), .disabled("Z"), .enable("false")) multiplexer_7 (
    .in0(EX_sa), .in1(EX_R1[4:0]), .out(multiplexer_7_out), .sel(EX_SRLV));
  Adder #(.width(32)) adder_3 (.a(shifter_1_out), .b(adder_2_out), .out(BAddr));  // open: cin, cout
  or or_5 (flush, Branch[0], Branch[1], Branch[2]);
  MIPS_ALU mips_alu_1 (
    .X(EX_R1), .Y(multiplexer_6_out), .AluOP(EX_ALU_OP), .Equal(equ), .Result(EX_R),
    .shamt(multiplexer_7_out), .GEZ(GEZ));  // open: Result_2
  not not_5 (not_5_out, Pause);
  EX_MEM ex_mem_1 (
    .CLK(CLK), .EX_PC(EX_PC), .EX_IR(EX_IR), .RST(RST), .EX_R(EX_R), .EX_MDin(EX_MDin), .EX_W_num(EX_W_num),
    .MEM_PC(M_PC), .MEM_IR(MEM_IR), .MEM_R(MEM_R), .MEM_MDin(MDin), .MEM_W_num(MEM_W_num),
    .EX_B(id_ex_1_ex_b), .EX_JAL(EX_JAL), .EX_MemToReg(id_ex_1_ex_memtoreg), .EX_MemWrite(id_ex_1_ex_memreg),
    .EX_RegWrite(EX_RegWrite), .EX_Syscall(id_ex_1_ex_syscall), .MEM_B(MEM_B), .MEM_JAL(MEM_JAL),
    .MEM_MemToReg(MEM_MemToReg), .MEM_MemWrite(MemWrite), .MEM_RegWrite(MEM_RegWrite),
    .MEM_Syscall(MEM_Syscall), .RUN(not_5_out), .MEM_R1(MEM_R1), .EX_R1(EX_R1));
  Decoder #(.select(2), .tristate("false"), .disabled("Z"), .enable("false")) decoder_1 (
    .out0(decoder_1_out0[0]), .out1(decoder_1_out0[1]), .out2(decoder_1_out0[2]), .out3(decoder_1_out0[3]),
    .sel(MEM_R[1:0]));
  Demultiplexer #(.select(2), .width(8), .tristate("false"), .disabled("Z"), .enable("false")) demultiplexer_1 (
    .out0(demultiplexer_1_out0), .out1(demultiplexer_1_out1), .out2(demultiplexer_1_out2),
    .out3(demultiplexer_1_out3), .in(MDin[7:0]), .sel(MEM_R[1:0]));
  assign {sel4, sel3, sel2, sel1} = ~MEM_B ? 4'b1111 : 4'bz;  // Controlled_Buffer controlled_buffer_2
  assign {sel4, sel3, sel2, sel1} = MEM_B ? decoder_1_out0 : 4'bz;  // Controlled_Buffer controlled_buffer_3
  assign {MDin4, MDin3, MDin2, MDin1} = MEM_B ? {demultiplexer_1_out3, demultiplexer_1_out2, demultiplexer_1_out1, demultiplexer_1_out0} : 32'bz;  // Controlled_Buffer controlled_buffer_4
  assign {MDin4, MDin3, MDin2, MDin1} = ~MEM_B ? MDin : 32'bz;  // Controlled_Buffer controlled_buffer_5
  Comparator #(.width(32), .mode("unsigned")) comparator_8 (
    .a(32'h22), .b(MEM_R1), .eq(comparator_8_eq));  // open: gt, lt
  Comparator #(.width(32), .mode("unsigned")) comparator_9 (
    .a(MEM_R1), .b(32'h32), .eq(comparator_9_eq));  // open: gt, lt
  and and_13 (LedOut, MEM_Syscall, comparator_8_eq);
  and and_14 (and_14_out, MEM_Syscall, comparator_9_eq);
  D_Flip_Flop #(.trigger("falling"), .Pre_Clr_Positions("ABOVE_BELOW"), .NegatePresetClear("false"), .enable("false"), .NewFFLayout("false")) d_ff_2 (
    .clk(and_14_out), .D(1'b1), .Q(Pause), .reset(Go));  // open: Qn, preset
  not not_6 (not_6_out, Pause);
  Counter #(.width(16), .max('hffff), .ongoal("wrap"), .trigger("rising"), .behavior("new")) counter_2 (
    .count(not_6_out), .Q(\总周期数 ), .clk(CLK), .clr(RST));  // open: load, D, carry, preset, down
  Register #(.width(32), .trigger("rising"), .Select("low")) register_1 (
    .D(MDin), .en(LedOut), .Q(LedData), .clk(CLK), .clr(RST));
  RAM #(.addrWidth(10), .dataWidth(8), .bus("separate"), .Select("high")) ram_1 (
    .addr(MEM_R[11:2]), .din(MDin1), .data(MEM_MDout[7:0]), .str(MemWrite), .sel(sel1), .clk(CLK), .clr(RST));  // open: ld
  RAM #(.addrWidth(10), .dataWidth(8), .bus("separate"), .Select("high")) ram_2 (
    .addr(MEM_R[11:2]), .din(MDin2), .data(MEM_MDout[15:8]), .str(MemWrite), .sel(sel2), .clk(CLK), .clr(RST));  // open: ld
  RAM #(.addrWidth(10), .dataWidth(8), .bus("separate"), .Select("high")) ram_3 (
    .addr(MEM_R[11:2]), .din(MDin3), .data(MEM_MDout[23:16]), .str(MemWrite), .sel(sel3), .clk(CLK), .clr(RST));  // open: ld
  RAM #(.addrWidth(10), .dataWidth(8), .bus("separate"), .Select("high")) ram_4 (
    .addr(MEM_R[11:2]), .din(MDin4), .data(MEM_MDout[31:24]), .str(MemWrite), .sel(sel4), .clk(CLK), .clr(RST));  // open: ld
  not not_7 (not_7_out, Pause);
  // MEM_WB mem_wb_1: pin names not known; wires that end beside it: MEM_ERET, MEM_JAL, MEM_MemToReg, MEM_RegWrite, MEM_R, MEM_MDout, MEM_IR, MEM_W_num, M_PC, not_7_out, RST, CLK, WB_ERET, WB_JAL, WB_MemToReg, RegWrite, WB_R, WB_MDout, WB_IR, WB_W_num, WB_PC
  Adder #(.width(32)) adder_4 (.a(32'h4), .b(WB_PC), .out(adder_4_out));  // open: cin, cout
  Multiplexer #(.select(2), .width(32), .disabled("Z"), .enable("false")) multiplexer_8 (
    .in0(WB_R), .in1(adder_4_out), .in2(WB_MDout), .out(RDin), .sel({WB_MemToReg, WB_JAL}));  // open: in3

  // Other names for the same wires on the sheet: IAddr[31:2] = {EX_PC[31:28], EX_Imm26}; ID_Imm26[5:0] = FUNC;
  //   ID_IR[25:0] = {ID_Imm26, FUNC}; Imm16[15:0] = {ID_Imm26[15:6], FUNC}; Imm26[25:0] = {ID_Imm26, FUNC};
  //   ID_sa[4:0] = ID_Imm26[10:6]; rd[4:0] = ID_Imm26[15:11]; rt[4:0] = ID_Imm26[20:16]; rs[4:0] = ID_Imm26[25:21];
  //   OP_CODE[5:0] = ID_IR; MEM_MDin[31:0] = MDin; MEM_MemWrite = MemWrite; MEM_PC[31:0] = M_PC;
  //   MemAddr[9:0] = MEM_R[11:2]; PC[31:0] = IF_PC; RAddr[31:0] = EX_R1; WB_RegWrite = RegWrite

  // Notes on the sheet:
  //   中断源
  //   时空图监测，可删除
  //   中断等待指示
  //   指令存储器
  //   数码管输出
  //   contents of rom_1 (hex, n*v repeats v):
  //   20110001 8000c05 20110001 20120002 20130003 8000c09 20110001 20120002 20130003 8000c0d 20110001
  //   20120002 20130003 8000c11 20110001 20120002 20130003 c000cf6 20100001 20110001 118fc0 112020
  //   20020022 c 118882 12200001 8000c15 112020 20020022 c 20110001 118880 112020 20020022 c 12200001
  //   8000c1f 20110001 118fc0 112020 20020022 c 1188c3 112020 20020022 c 118903 112020 20020022 c 118903
  //   112020 20020022 c 118903 112020 20020022 c 118903 112020 20020022 c 118903 112020 20020022 c 118903
  //   112020 20020022 c 118903 112020 20020022 c 20100001 109fc0 139fc3 8021 2012000c 24160003 26100001
  //   3210000f 20080008 20090001 139900 2709825 132020 20020022 c 1094022 1500fff9 22100001 2018000f
  //   2188024 108700 20080008 20090001 139902 2709825 132021 20020022 c 1094022 1500fff9 108702 2c9b022
  //   12c00001 8000c50 4020 1084027 84400 3508ffff 82021 20020022 c 2010ffff 20110000 ae300000 22100001
  //   22310004 ae300000 22100001 22310004 ae300000 22100001 22310004 ae300000 22100001 22310004 ae300000
  //   22100001 22310004 ae300000 22100001 22310004 ae300000 22100001 22310004 ae300000 22100001 22310004
  //   ae300000 22100001 22310004 ae300000 22100001 22310004 ae300000 22100001 22310004 ae300000 22100001
  //   22310004 ae300000 22100001 22310004 ae300000 22100001 22310004 ae300000 22100001 22310004 ae300000
  //   22100001 22310004 22100001 8020 2011003c 8e130000 8e340000 274402a 11000002 ae330000 ae140000
  //   2231fffc 1611fff8 102020 20020022 c 22100004 2011003c 1611fff2 20020032 c 20080001 20090003 20110876
  //   118d00 112020 20020022 c 200b0008 1118806 1318806 112020 20020022 c 216bffff 1560fff9 20020032 c
  //   2008ffff 20117777 112020 20020022 c 200b0010 2288826 112020 20020022 c 216bffff 1560fffa 20020032 c
  //   20090000 200b0020 20110000 20120001 a1310000 112020 20020022 c 2328820 21290001 216bffff 1560fff8
  //   200b0008 20090000 8d310000 112020 20020022 c 21290004 216bffff 1560fff9 20020032 c 2011000f 112020
  //   20020022 c 2231ffff 621fffb 20020032 c 20100000 22100001 102020 20020022 c 22100002 102020 20020022
  //   c 22100003 102020 20020022 c 22100004 102020 20020022 c 22100005 102020 20020022 c 22100006 102020
  //   20020022 c 22100007 102020 20020022 c 22100008 102020 20020022 20020022 c 3e00008
  //   rt
  //   sa
  //   OP
  //   Func
  //   rs
  //   rd
  //   Imm16
  //   Imm26
  //   ra
  //   控制位
  //   v0
  //   t0
  //   流水调试日志用
  //   暂停节拍，不能为0
  //   戳工具置1进入计数暂停模式，ctrl+k时钟自动运行到对应节拍暂停
  //   ctrl+k关闭时钟连续运行，将控制位置零，进入单步调试模式调试
  //   可计数暂停的时钟源
  //   为方便自动评测，需要输出流水线各段保存的PC值，注意是PC不是PC+4，另外ID段寄存器写入信息，Mem段内存写入信息也要输出
endmodule
module \重定向流水线  (
  output RegWrite,
  output MemWrite,
  output [31:0] IF_PC,
  output [31:0] ID_PC,
  output [31:0] EX_PC,
  output [31:0] M_PC,
  output [31:0] WB_PC,
  output [31:0] RDin,
  output [31:0] MDin,
  output [31:0] LedData
);

  wire and_1_out, and_2_out, and_3_out, and_4_out, and_5_out, and_6_out, and_7_out, and_8_out, and_13_out,
       and_14_out, and_15_out, and_16_out, and_17_out, and_20_out, CLK, clock_1_out, clock_2_out,
       comparator_7_eq, comparator_7_lt, comparator_8_eq, comparator_9_eq, d_ff_1_q, equ, EX_ALU_SRC, EX_BEQ,
       EX_BGEZ, EX_BNE, EX_JAL, EX_JMP, EX_JR, EX_MemToReg, EX_RegWrite, EX_SRLV, flush, GEZ, Go, ID_ALU_SRC,
       ID_B, ID_BEQ, ID_BGEZ, ID_BNE, ID_ERET, id_ex_1_ex_b, id_ex_1_ex_eret, id_ex_1_ex_memreg,
       id_ex_1_ex_syscall, ID_EX_rs, ID_EX_rt, ID_JAL, ID_JMP, ID_JR, ID_MemToReg, ID_MemWrite, ID_RegDst,
       ID_RegWrite, ID_SRLV, ID_Syscall, IR1, IR2, IR3, LedOut, LoadUse, MEM_B, MEM_ERET, MEM_EX_rs,
       MEM_EX_rt, MEM_JAL, MEM_MemToReg, MEM_RegWrite, MEM_Syscall, nand_1_out, not_1_out, not_2_out,
       not_3_out, not_4_out, not_5_out, or_2_out, Pause, rs____0, rs____EX_W_num, rs____MEM_W_num, RST,
       RsUsed, rt____0, rt____EX_W_num, rt____MEM_W_num, RtUsed, sel1, sel2, sel3, sel4, SignedExt, W1, W2,
       W3, WB_ERET, WB_JAL, WB_MemToReg;
  wire [1:0] EX_Rs_F, EX_Rt_F, ID_Rs_F, ID_Rt_F, multiplexer_6_out, multiplexer_7_out;
  wire [2:0] Branch;
  wire [3:0] decoder_1_out0, EX_ALU_OP, ID_ALU_OP;
  wire [4:0] EX_sa, EX_W_num, ID_W_num, MEM_W_num, multiplexer_11_out, multiplexer_13_out, R1_num, R2_num,
       WB_W_num;
  wire [7:0] demultiplexer_1_out0, demultiplexer_1_out1, demultiplexer_1_out2, demultiplexer_1_out3, MDin1,
       MDin2, MDin3, MDin4;
  wire [12:0] CNT_num;
  wire [15:0] \LoadUse次数 , \总周期数 , \插入气泡数 , \无条件分支数 , \条件分支成功数 ;
  wire [25:0] EX_Imm26, ID_Imm26;
  wire [31:0] adder_3_out, adder_4_out, BAddr, bit_extender_1_out, bit_extender_2_out, EX_ExtImm, EX_IR,
       EX_MDin, EX_R, EX_R1, id_ex_1_ex_r2, ID_ExtImm, ID_MDin, ID_R1, IF_IR, MEM_IR, MEM_MDout, MEM_R,
       MEM_R1, multiplexer_12_out, nextPC, PC_4, shifter_1_out, WB_IR, WB_MDout, WB_R;
  wire [31:5] multiplexer_11_out_2;
  wire [31:26] ID_IR;

  Button \u_总复位  (.out(RST));
  Button _1 (.out(IR1));
  Button _2 (.out(IR2));
  Button _3 (.out(IR3));
  // Probe on \总周期数 
  // Probe on \总周期数 
  Button \u_继续运行  (.out(Go));
  LED #(.active("true")) led_1 (.in(W1));
  LED #(.active("true")) led_2 (.in(W2));
  LED #(.active("true")) led_3 (.in(W3));
  and and_1 (and_1_out, ~Pause, ~LoadUse);  // AND_Gate
  Hex_Digit_Display hex_digit_display_1 (.value(LedData[31:28]));  // open: dp
  // Probe on IF_PC[19:0]
  // Mips_Probe mips_probe_1: pin names not known; wires that end beside it: IF_IR
  Register #(.width(32), .trigger("rising"), .Select("low")) PC (
    .D(nextPC), .en(and_1_out), .Q(IF_PC), .clk(CLK), .clr(RST));
  Hex_Digit_Display hex_digit_display_2 (.value(LedData[23:20]));  // open: dp
  Hex_Digit_Display hex_digit_display_3 (.value(LedData[27:24]));  // open: dp
  // Probe on ID_PC[19:0]
  // Mips_Probe mips_probe_2: pin names not known; wires that end beside it: {ID_IR, ID_Imm26}
  Hex_Digit_Display hex_digit_display_4 (.value(LedData[15:12]));  // open: dp
  Hex_Digit_Display hex_digit_display_5 (.value(LedData[19:16]));  // open: dp
  ROM #(.addrWidth(10), .dataWidth(32), .Select("high")) rom_1 (.addr(IF_PC[11:2]), .data(IF_IR));
  Adder #(.width(32)) adder_1 (.a(IF_PC), .b(32'h4), .out(PC_4));  // open: cin, cout
  Multiplexer #(.select(3), .width(32), .disabled("Z"), .enable("false")) multiplexer_1 (
    .in0(PC_4), .in1(BAddr), .in2({EX_PC[31:28], EX_Imm26, 2'b00}), .in4(EX_R1), .out(nextPC), .sel(Branch));  // open: in3, in5, in6, in7
  Hex_Digit_Display hex_digit_display_6 (.value(LedData[11:8]));  // open: dp
  Hex_Digit_Display hex_digit_display_7 (.value(LedData[7:4]));  // open: dp
  Clock #(.highDuration(1), .lowDuration(1)) clock_1 (.out(clock_1_out));
  // Probe on EX_PC[19:0]
  // Mips_Probe mips_probe_3: pin names not known; wires that end beside it: clock_1_out, EX_IR, CLK
  and and_2 (and_2_out, ~Pause, ~LoadUse);  // AND_Gate
  Rs_Rt rs_rt_1 (
    .OP0(ID_IR[26]), .OP1(ID_IR[27]), .OP2(ID_IR[28]), .OP3(ID_IR[29]), .OP4(ID_IR[30]), .OP5(ID_IR[31]),
    .F0(ID_Imm26[0]), .F1(ID_Imm26[1]), .F2(ID_Imm26[2]), .F3(ID_Imm26[3]), .F4(ID_Imm26[4]),
    .F5(ID_Imm26[5]), .RsUsed(RsUsed), .RtUsed(RtUsed));
  Hex_Digit_Display hex_digit_display_8 (.value(LedData[3:0]));  // open: dp
  IF_ID if_id_1 (
    .IF_PC(IF_PC), .IF_IR(IF_IR), .CLK(CLK), .ID_PC(ID_PC), .ID_IR({ID_IR, ID_Imm26}), .RST(RST),
    .RUN(and_2_out), .Bubble(flush));  // open: IF_Predict, ID_Predict, IF_Valid, ID_Valid, IF_Hit, ID_Hit
  Comparator #(.width(5), .mode("unsigned")) comparator_1 (.a(R1_num), .b({5{1'b0}}), .eq(rs____0));  // open: gt, lt
  Comparator #(.width(5), .mode("unsigned")) comparator_2 (
    .a(R1_num), .b(EX_W_num), .eq(rs____EX_W_num));  // open: gt, lt
  Comparator #(.width(5), .mode("unsigned")) comparator_3 (
    .a(EX_W_num), .b(R2_num), .eq(rt____EX_W_num));  // open: gt, lt
  Comparator #(.width(5), .mode("unsigned")) comparator_4 (.a({5{1'b0}}), .b(R2_num), .eq(rt____0));  // open: gt, lt
  Comparator #(.width(5), .mode("unsigned")) comparator_5 (
    .a(R2_num), .b(MEM_W_num), .eq(rt____MEM_W_num));  // open: gt, lt
  Comparator #(.width(5), .mode("unsigned")) comparator_6 (
    .a(MEM_W_num), .b(R1_num), .eq(rs____MEM_W_num));  // open: gt, lt
  // Probe on \总周期数 
  // Probe on M_PC[19:0]
  // Mips_Probe mips_probe_4: pin names not known; wires that end beside it: MEM_IR
  // Probe on \总周期数 
  // Probe on \无条件分支数 
  // Probe on \条件分支成功数 
  // Probe on \插入气泡数 
  // Probe on \LoadUse次数 
  \单周期硬布线控制器  \u_单周期硬布线控制器_1  (
    .Func(ID_Imm26[5:0]), .OP(ID_IR), .ALU_OP(ID_ALU_OP), .MemToReg(ID_MemToReg), .MemWrite(ID_MemWrite),
    .ALU_SRC(ID_ALU_SRC), .RegWrite(ID_RegWrite), .SysCALL(ID_Syscall), .SignedExt(SignedExt),
    .RegDst(ID_RegDst), .JR(ID_JR), .JMP(ID_JMP), .Beq(ID_BEQ), .JAL(ID_JAL), .Bne(ID_BNE), .ERET(ID_ERET),
    .B(ID_B), .BGEZ(ID_BGEZ), .SRLV(ID_SRLV));
  // Probe on IF_PC[11:0]
  // Probe on WB_PC[19:0]
  // Mips_Probe mips_probe_5: pin names not known; wires that end beside it: WB_IR, Go
  and and_3 (and_3_out, ~rs____0, RsUsed, rs____EX_W_num);  // AND_Gate
  and and_4 (and_4_out, rt____EX_W_num, RtUsed, ~rt____0);  // AND_Gate
  and and_5 (and_5_out, ~rs____0, RsUsed, rs____MEM_W_num);  // AND_Gate
  and and_6 (and_6_out, rt____MEM_W_num, RtUsed, ~rt____0);  // AND_Gate
  // Probe on ID_PC[11:0]
  // Probe on EX_PC[11:0]
  Multiplexer #(.select(2), .width(5), .disabled("Z"), .enable("false")) multiplexer_2 (
    .in0(ID_Imm26[20:16]), .in1(ID_Imm26[15:11]), .in2({5{1'b1}}), .in3({5{1'b1}}), .out(ID_W_num),
    .sel({ID_JAL, ID_RegDst}));
  // Probe on M_PC[11:0]
  D_Flip_Flop #(.trigger("high"), .Pre_Clr_Positions("LEGACY"), .NegatePresetClear("false"), .enable("true"), .NewFFLayout("false")) d_ff_1 (
    .Q(d_ff_1_q), .preset(Pause), .reset(Go));  // open: clk, D, Qn, en
  Multiplexer #(.select(1), .width(5), .disabled("Z"), .enable("false")) multiplexer_3 (
    .in0(ID_Imm26[25:21]), .in1(5'b00010), .out(R1_num), .sel(ID_Syscall));
  Multiplexer #(.select(1), .width(5), .disabled("Z"), .enable("false")) multiplexer_4 (
    .in0(ID_Imm26[20:16]), .in1(5'b00100), .out(R2_num), .sel(ID_Syscall));
  and and_7 (and_7_out, and_3_out, EX_MemToReg);
  and and_8 (and_8_out, EX_MemToReg, and_4_out);
  and and_9 (ID_EX_rt, and_4_out, EX_RegWrite);
  and and_10 (ID_EX_rs, EX_RegWrite, and_3_out);
  and and_11 (MEM_EX_rs, and_5_out, MEM_RegWrite);
  and and_12 (MEM_EX_rt, MEM_RegWrite, and_6_out);
  // Probe on WB_PC[11:0]
  // Probe on 13'h340
  Clock #(.highDuration(1), .lowDuration(1)) clock_2 (.out(clock_2_out));
  not not_1 (not_1_out, CLK);
  assign bit_extender_1_out = {{16{1'b0}}, ID_Imm26[15:0]};  // Bit_Extender bit_extender_1
  assign bit_extender_2_out = {{16{ID_Imm26[15]}}, ID_Imm26[15:0]};  // Bit_Extender bit_extender_2
  or or_1 (LoadUse, and_7_out, and_8_out);
  Comparator #(.width(13), .mode("twosComplement")) comparator_7 (
    .a(CNT_num), .b(13'h340), .eq(comparator_7_eq), .lt(comparator_7_lt));  // open: gt
  MIPS_Regifile mips_regifile_1 (
    .Din(RDin), .Clk(not_1_out), .R1(ID_R1), .R2(ID_MDin), .WE(RegWrite), .W_num(WB_W_num), .R1_num(R1_num),
    .R2_num(R2_num));
  Multiplexer #(.select(1), .width(32), .disabled("Z"), .enable("false")) multiplexer_5 (
    .in0(bit_extender_1_out), .in1(bit_extender_2_out), .out(ID_ExtImm), .sel(SignedExt));
  nand nand_1 (nand_1_out, d_ff_1_q, comparator_7_eq);
  // Probe on CNT_num
  Counter #(.width(13), .max('h1fff), .ongoal("stay"), .trigger("rising"), .behavior("old")) counter_1 (
    .count(comparator_7_lt), .Q(CNT_num), .clk(clock_2_out), .clr(RST));  // open: load, D, carry, preset
  or or_2 (or_2_out, LoadUse, flush);
  not not_2 (not_2_out, Pause);
  ID_EX id_ex_1 (
    .CLK(CLK), .ID_PC(ID_PC), .ID_IR({ID_IR, ID_Imm26}), .RST(RST), .EX_PC(EX_PC), .EX_IR(EX_IR),
    .ID_R1(ID_R1), .ID_R2(ID_MDin), .EX_R1(EX_R1), .EX_R2(id_ex_1_ex_r2), .ID_ExtImm(ID_ExtImm),
    .ID_W_num(ID_W_num), .EX_ExtImm(EX_ExtImm), .EX_W_num(EX_W_num), .ID_B(ID_B), .ID_ERET(ID_ERET),
    .ID_SRLV(ID_SRLV), .ID_JMP(ID_JMP), .ID_JR(ID_JR), .ID_BEQ(ID_BEQ), .ID_BNE(ID_BNE), .ID_BGEZ(ID_BGEZ),
    .ID_JAL(ID_JAL), .ID_MemToReg(ID_MemToReg), .ID_MemWrite(ID_MemWrite), .ID_ALU_SRC(ID_ALU_SRC),
    .ID_RegWrite(ID_RegWrite), .ID_Syscall(ID_Syscall), .ID_AlU_OP(ID_ALU_OP), .EX_B(id_ex_1_ex_b),
    .EX_ERET(id_ex_1_ex_eret), .EX_SRLV(EX_SRLV), .EX_JMP(EX_JMP), .EX_JR(EX_JR), .EX_BEQ(EX_BEQ),
    .EX_BNE(EX_BNE), .EX_BGEZ(EX_BGEZ), .EX_JAL(EX_JAL), .EX_MemToReg(EX_MemToReg),
    .EX_MemReg(id_ex_1_ex_memreg), .EX_ALU_SRC(EX_ALU_SRC), .EX_RegWrite(EX_RegWrite),
    .EX_Syscall(id_ex_1_ex_syscall), .EX_ALU_OP(EX_ALU_OP), .ID_sa(ID_Imm26[10:6]), .EX_sa(EX_sa),
    .RUN(not_2_out), .Bubble(or_2_out), .ID_Imm26(ID_Imm26), .EX_Imm26(EX_Imm26), .ID_rs_f(ID_Rs_F),
    .EX_rs_f(EX_Rs_F), .ID_rt_f(ID_Rt_F), .EX_rt_f(EX_Rt_F));  // open: ID_Predict, EX_Predict, EX_MFC0, ID_MFC0, ID_MTC0, EX_MTC0, ID_Valid, EX_Valid, EX_Hit, in_34
  Multiplexer #(.select(1), .width(2), .disabled("Z"), .enable("false")) multiplexer_6 (
    .in0(2'b00), .in1(2'b01), .out(multiplexer_6_out), .sel(MEM_EX_rs));
  Multiplexer #(.select(1), .width(2), .disabled("Z"), .enable("false")) multiplexer_7 (
    .in0(2'b00), .in1(2'b01), .out(multiplexer_7_out), .sel(MEM_EX_rt));
  assign CLK = nand_1_out ? clock_2_out : 1'bz;  // Controlled_Buffer controlled_buffer_1
  Pull_Resistor #(.pull(1)) pull_resistor_1 (.node(CLK));
  Multiplexer #(.select(1), .width(2), .disabled("Z"), .enable("false")) multiplexer_8 (
    .in0(multiplexer_6_out), .in1(2'b10), .out(ID_Rs_F), .sel(ID_EX_rs));
  Multiplexer #(.select(1), .width(2), .disabled("Z"), .enable("false")) multiplexer_9 (
    .in0(multiplexer_7_out), .in1(2'b10), .out(ID_Rt_F), .sel(ID_EX_rt));
  Multiplexer #(.select(2), .width(32), .disabled("Z"), .enable("false")) multiplexer_10 (
    .in0(id_ex_1_ex_r2), .in1(RDin), .in2(MEM_R), .out(EX_MDin), .sel(EX_Rt_F));  // open: in3
  and and_13 (and_13_out, equ, EX_BEQ);
  and and_14 (and_14_out, GEZ, EX_BGEZ);
  and and_15 (and_15_out, ~equ, EX_BNE);  // AND_Gate
  and and_16 (and_16_out, ~EX_JAL, ~EX_JR, EX_JMP);  // AND_Gate
  or or_3 (Branch[1], and_16_out, and_17_out);
  and and_17 (and_17_out, EX_JMP, EX_JAL);
  and and_18 (Branch[2], EX_JMP, EX_JR);
  Multiplexer #(.select(2), .width(32), .disabled("Z"), .enable("false")) multiplexer_11 (
    .in0(EX_R1), .in1(RDin), .in2(MEM_R), .out({multiplexer_11_out_2, multiplexer_11_out}), .sel(EX_Rs_F));  // open: in3
  Multiplexer #(.select(1), .width(32), .disabled("Z"), .enable("false")) multiplexer_12 (
    .in0(EX_MDin), .in1(EX_ExtImm), .out(multiplexer_12_out), .sel(EX_ALU_SRC));
  Shifter #(.width(32), .shift("ll")) shifter_1 (.in(EX_ExtImm), .\dist (5'b00010), .out(shifter_1_out));
  Adder #(.width(32)) adder_2 (.a(shifter_1_out), .b(adder_3_out), .out(BAddr));  // open: cin, cout
  Adder #(.width(32)) adder_3 (.a(32'h4), .b(EX_PC), .out(adder_3_out));  // open: cin, cout
  or or_4 (Branch[0], and_13_out, and_14_out, and_15_out);
  MIPS_ALU mips_alu_1 (
    .X({multiplexer_11_out_2, multiplexer_11_out}), .Y(multiplexer_12_out), .AluOP(EX_ALU_OP), .Equal(equ),
    .Result(EX_R), .shamt(multiplexer_13_out), .GEZ(GEZ));  // open: Result_2
  Multiplexer #(.select(1), .width(5), .disabled("Z"), .enable("false")) multiplexer_13 (
    .in0(EX_sa), .in1(multiplexer_11_out), .out(multiplexer_13_out), .sel(EX_SRLV));
  or or_5 (flush, Branch[0], Branch[1], Branch[2]);
  not not_3 (not_3_out, Pause);
  EX_MEM ex_mem_1 (
    .CLK(CLK), .EX_PC(EX_PC), .EX_IR(EX_IR), .RST(RST), .EX_R(EX_R), .EX_MDin(EX_MDin), .EX_W_num(EX_W_num),
    .MEM_PC(M_PC), .MEM_IR(MEM_IR), .MEM_R(MEM_R), .MEM_MDin(MDin), .MEM_W_num(MEM_W_num),
    .EX_B(id_ex_1_ex_b), .EX_JAL(EX_JAL), .EX_MemToReg(EX_MemToReg), .EX_MemWrite(id_ex_1_ex_memreg),
    .EX_RegWrite(EX_RegWrite), .EX_Syscall(id_ex_1_ex_syscall), .MEM_B(MEM_B), .MEM_JAL(MEM_JAL),
    .MEM_MemToReg(MEM_MemToReg), .MEM_MemWrite(MemWrite), .MEM_RegWrite(MEM_RegWrite),
    .MEM_Syscall(MEM_Syscall), .RUN(not_3_out), .MEM_R1(MEM_R1),
    .EX_R1({multiplexer_11_out_2, multiplexer_11_out}));
  Decoder #(.select(2), .tristate("false"), .disabled("Z"), .enable("false")) decoder_1 (
    .out0(decoder_1_out0[0]), .out1(decoder_1_out0[1]), .out2(decoder_1_out0[2]), .out3(decoder_1_out0[3]),
    .sel(MEM_R[1:0]));
  Demultiplexer #(.select(2), .width(8), .tristate("false"), .disabled("Z"), .enable("false")) demultiplexer_1 (
    .out0(demultiplexer_1_out0), .out1(demultiplexer_1_out1), .out2(demultiplexer_1_out2),
    .out3(demultiplexer_1_out3), .in(MDin[7:0]), .sel(MEM_R[1:0]));
  assign {sel4, sel3, sel2, sel1} = MEM_B ? decoder_1_out0 : 4'bz;  // Controlled_Buffer controlled_buffer_2
  assign {MDin4, MDin3, MDin2, MDin1} = MEM_B ? {demultiplexer_1_out3, demultiplexer_1_out2, demultiplexer_1_out1, demultiplexer_1_out0} : 32'bz;  // Controlled_Buffer controlled_buffer_3
  Comparator #(.width(32), .mode("unsigned")) comparator_8 (
    .a(32'h22), .b(MEM_R1), .eq(comparator_8_eq));  // open: gt, lt
  Comparator #(.width(32), .mode("unsigned")) comparator_9 (
    .a(MEM_R1), .b(32'h32), .eq(comparator_9_eq));  // open: gt, lt
  assign {sel4, sel3, sel2, sel1} = ~MEM_B ? 4'b1111 : 4'bz;  // Controlled_Buffer controlled_buffer_4
  assign {MDin4, MDin3, MDin2, MDin1} = ~MEM_B ? MDin : 32'bz;  // Controlled_Buffer controlled_buffer_5
  and and_19 (LedOut, MEM_Syscall, comparator_8_eq);
  and and_20 (and_20_out, MEM_Syscall, comparator_9_eq);
  D_Flip_Flop #(.trigger("falling"), .Pre_Clr_Positions("ABOVE_BELOW"), .NegatePresetClear("false"), .enable("false"), .NewFFLayout("false")) d_ff_2 (
    .clk(and_20_out), .D(1'b1), .Q(Pause), .reset(Go));  // open: Qn, preset
  not not_4 (not_4_out, Pause);
  Counter #(.width(16), .max('hffff), .ongoal("wrap"), .trigger("rising"), .behavior("new")) counter_2 (
    .count(not_4_out), .Q(\总周期数 ), .clk(CLK), .clr(RST));  // open: load, D, carry, preset, down
  Register #(.width(32), .trigger("rising"), .Select("low")) register_1 (
    .D(MDin), .en(LedOut), .Q(LedData), .clk(CLK), .clr(RST));
  RAM #(.addrWidth(10), .dataWidth(8), .bus("separate"), .Select("high")) ram_1 (
    .addr(MEM_R[11:2]), .din(MDin1), .data(MEM_MDout[7:0]), .str(MemWrite), .sel(sel1), .clk(CLK), .clr(RST));  // open: ld
  RAM #(.addrWidth(10), .dataWidth(8), .bus("separate"), .Select("high")) ram_2 (
    .addr(MEM_R[11:2]), .din(MDin2), .data(MEM_MDout[15:8]), .str(MemWrite), .sel(sel2), .clk(CLK), .clr(RST));  // open: ld
  RAM #(.addrWidth(10), .dataWidth(8), .bus("separate"), .Select("high")) ram_3 (
    .addr(MEM_R[11:2]), .din(MDin3), .data(MEM_MDout[23:16]), .str(MemWrite), .sel(sel3), .clk(CLK), .clr(RST));  // open: ld
  RAM #(.addrWidth(10), .dataWidth(8), .bus("separate"), .Select("high")) ram_4 (
    .addr(MEM_R[11:2]), .din(MDin4), .data(MEM_MDout[31:24]), .str(MemWrite), .sel(sel4), .clk(CLK), .clr(RST));  // open: ld
  not not_5 (not_5_out, Pause);
  // MEM_WB mem_wb_1: pin names not known; wires that end beside it: MEM_ERET, MEM_JAL, MEM_MemToReg, MEM_RegWrite, MEM_R, MEM_MDout, MEM_IR, MEM_W_num, M_PC, not_5_out, RST, CLK, WB_ERET, WB_JAL, WB_MemToReg, RegWrite, WB_R, WB_MDout, WB_IR, WB_W_num, WB_PC
  Adder #(.width(32)) adder_4 (.a(32'h4), .b(WB_PC), .out(adder_4_out));  // open: cin, cout
  Multiplexer #(.select(2), .width(32), .disabled("Z"), .enable("false")) multiplexer_14 (
    .in0(WB_R), .in1(adder_4_out), .in2(WB_MDout), .out(RDin), .sel({WB_MemToReg, WB_JAL}));  // open: in3

  // Other names for the same wires on the sheet: IAddr[31:2] = {EX_PC[31:28], EX_Imm26}; ID_IR[25:0] = ID_Imm26;
  //   Imm16[15:0] = ID_Imm26[15:0]; Imm26[25:0] = ID_Imm26; ID_sa[4:0] = ID_Imm26[10:6]; rd[4:0] = ID_Imm26[15:11];
  //   rt[4:0] = ID_Imm26[20:16]; rs[4:0] = ID_Imm26[25:21]; MEM_MDin[31:0] = MDin; MEM_MemWrite = MemWrite;
  //   MEM_PC[31:0] = M_PC; MemAddr[9:0] = MEM_R[11:2]; PC[31:0] = IF_PC; RAddr[31:0] = EX_R1; WB_RDin[31:0] = RDin;
  //   WB_RegWrite = RegWrite

  // Notes on the sheet:
  //   中断源
  //   时空图监测，可删除
  //   中断等待指示
  //   指令存储器
  //   数码管输出
  //   contents of rom_1 (hex, n*v repeats v):
  //   20110001 8000c05 20110001 20120002 20130003 8000c09 20110001 20120002 20130003 8000c0d 20110001
  //   20120002 20130003 8000c11 20110001 20120002 20130003 c000cb8 20100001 20110001 118fc0 112020
  //   20020022 c 118882 12200001 8000c15 112020 20020022 c 20110001 118880 112020 20020022 c 12200001
  //   8000c1f 20110001 118fc0 112020 20020022 c 1188c3 112020 20020022 c 118903 112020 20020022 c 118903
  //   112020 20020022 c 118903 112020 20020022 c 118903 112020 20020022 c 118903 112020 20020022 c 118903
  //   112020 20020022 c 118903 112020 20020022 c 20100001 109fc0 139fc3 8021 2012000c 24160003 26100001
  //   3210000f 20080008 20090001 139900 2709825 132020 20020022 c 1094022 1500fff9 22100001 2018000f
  //   2188024 108700 20080008 20090001 139902 2709825 132021 20020022 c 1094022 1500fff9 108702 2c9b022
  //   12c00001 8000c50 4020 1084027 84400 3508ffff 82021 20020022 c 2010ffff 20110000 ae300000 22100001
  //   22310004 ae300000 22100001 22310004 ae300000 22100001 22310004 ae300000 22100001 22310004 ae300000
  //   22100001 22310004 ae300000 22100001 22310004 ae300000 22100001 22310004 ae300000 22100001 22310004
  //   ae300000 22100001 22310004 ae300000 22100001 22310004 ae300000 22100001 22310004 ae300000 22100001
  //   22310004 ae300000 22100001 22310004 ae300000 22100001 22310004 ae300000 22100001 22310004 ae300000
  //   22100001 22310004 22100001 8020 2011003c 8e130000 8e340000 274402a 11000002 ae330000 ae140000
  //   2231fffc 1611fff8 102020 20020022 c 22100004 2011003c 1611fff2 20020032 c 20100000 22100001 102020
  //   20020022 c 22100002 102020 20020022 c 22100003 102020 20020022 c 22100004 102020 20020022 c 22100005
  //   102020 20020022 c 22100006 102020 20020022 c 22100007 102020 20020022 c 22100008 102020 20020022
  //   20020022 c 3e00008
  //   OP
  //   Func
  //   rs
  //   rt
  //   rd
  //   sa
  //   Imm16
  //   Imm26
  //   v0
  //   t0
  //   ra
  //   流水调试日志用
  //   控制位
  //   暂停节拍，不能为0
  //   戳工具置1进入计数暂停模式，ctrl+k时钟自动运行到对应节拍暂停
  //   ctrl+k关闭时钟连续运行，将控制位置零，进入单步调试模式调试
  //   可计数暂停的时钟源
  //   为方便自动评测，需要输出流水线各段保存的PC值，注意是PC不是PC+4，另外ID段寄存器写入信息，Mem段内存写入信息也要输出
endmodule

module \分支预测  (
  output RegWrite,
  output MemWrite,
  output [31:0] IF_PC,
  output [31:0] ID_PC,
  output [31:0] EX_PC,
  output [31:0] M_PC,
  output [31:0] WB_PC,
  output [31:0] RDin,
  output [31:0] MDin,
  output [31:0] LedData
);

  wire and_1_out, and_2_out, and_3_out, and_4_out, and_5_out, and_6_out, and_7_out, and_8_out, and_13_out,
       and_14_out, and_15_out, and_16_out, and_17_out, and_20_out, BJ, Branch, BranchTaken, CLK, clock_1_out,
       clock_2_out, comparator_7_eq, comparator_7_lt, comparator_8_eq, comparator_9_eq, d_ff_1_q, equ,
       EX_ALU_SRC, EX_BEQ, EX_BGEZ, EX_BNE, EX_JAL, EX_JMP, EX_JR, EX_MemToReg, EX_PredictJmp, EX_RegWrite,
       EX_SRLV, GEZ, Go, ID_ALU_SRC, ID_B, ID_BEQ, ID_BGEZ, ID_BNE, ID_ERET, id_ex_1_ex_b, id_ex_1_ex_eret,
       id_ex_1_ex_memreg, id_ex_1_ex_syscall, ID_EX_rs, ID_EX_rt, ID_JAL, ID_JMP, ID_JR, ID_MemToReg,
       ID_MemWrite, ID_PredictJmp, ID_RegDst, ID_RegWrite, ID_SRLV, ID_Syscall, IR1, IR2, IR3, JImm, JR32,
       LedOut, LoadUse, MEM_B, MEM_ERET, MEM_EX_rs, MEM_EX_rt, MEM_JAL, MEM_MemToReg, MEM_RegWrite,
       MEM_Syscall, nand_1_out, not_1_out, not_2_out, not_3_out, not_4_out, not_5_out, or_1_out, Pause,
       PredictErr, PredictJ, rs____0, rs____EX_W_num, rs____MEM_W_num, RST, RsUsed, rt____0, rt____EX_W_num,
       rt____MEM_W_num, RtUsed, sel1, sel2, sel3, sel4, SignedExt, W1, W2, W3, WB_ERET, WB_JAL, WB_MemToReg;
  wire [1:0] EX_Rs_F, EX_Rt_F, ID_Rs_F, ID_Rt_F, multiplexer_12_out, multiplexer_13_out;
  wire [3:0] decoder_1_out0, EX_ALU_OP, ID_ALU_OP;
  wire [4:0] EX_sa, EX_W_num, ID_W_num, MEM_W_num, multiplexer_14_out, multiplexer_18_out, R1_num, R2_num,
       WB_W_num;
  wire [7:0] demultiplexer_1_out0, demultiplexer_1_out1, demultiplexer_1_out2, demultiplexer_1_out3, MDin1,
       MDin2, MDin3, MDin4;
  wire [12:0] CNT_num;
  wire [15:0] \LoadUse次数 , \总周期数 , \插入气泡数 , \无条件分支数 , \条件分支成功数 ;
  wire [25:0] EX_Imm26, ID_Imm26;
  wire [31:0] adder_1_out, adder_4_out, adder_5_out, BAddr, bit_extender_1_out, bit_extender_2_out,
       EX_ExtImm, EX_IR, EX_MDin, EX_R, EX_R1, id_ex_1_ex_r2, ID_ExtImm, ID_MDin, ID_R1, IF_IR, MEM_IR,
       MEM_MDout, MEM_R, MEM_R1, multiplexer_1_out, multiplexer_2_out, multiplexer_3_out, multiplexer_4_out,
       multiplexer_6_out, multiplexer_15_out, nextPC, PC_4, PredictJmp, shifter_1_out, WB_IR, WB_MDout, WB_R;
  wire [31:5] multiplexer_14_out_2;
  wire [31:26] ID_IR;

  Button \u_总复位  (.out(RST));
  Button _1 (.out(IR1));
  Button _2 (.out(IR2));
  Button _3 (.out(IR3));
  // Probe on \总周期数 
  // Probe on \总周期数 
  Button \u_继续运行  (.out(Go));
  LED #(.active("true")) led_1 (.in(W1));
  LED #(.active("true")) led_2 (.in(W2));
  LED #(.active("true")) led_3 (.in(W3));
  Hex_Digit_Display hex_digit_display_1 (.value(LedData[31:28]));  // open: dp
  // Probe on IF_PC[19:0]
  // Mips_Probe mips_probe_1: pin names not known; wires that end beside it: IF_IR
  Multiplexer #(.select(1), .width(32), .disabled("Z"), .enable("false")) multiplexer_1 (
    .in0(PC_4), .in1({EX_PC[31:28], EX_Imm26, 2'b00}), .out(multiplexer_1_out), .sel(JImm));
  and and_1 (and_1_out, ~Pause, ~LoadUse);  // AND_Gate
  Hex_Digit_Display hex_digit_display_2 (.value(LedData[23:20]));  // open: dp
  Hex_Digit_Display hex_digit_display_3 (.value(LedData[27:24]));  // open: dp
  // Probe on ID_PC[19:0]
  // Mips_Probe mips_probe_2: pin names not known; wires that end beside it: {ID_IR, ID_Imm26}
  Multiplexer #(.select(1), .width(32), .disabled("Z"), .enable("false")) multiplexer_2 (
    .in0(multiplexer_1_out), .in1(EX_R1), .out(multiplexer_2_out), .sel(JR32));
  Register #(.width(32), .trigger("rising"), .Select("low")) PC (
    .D(nextPC), .en(and_1_out), .Q(IF_PC), .clk(CLK), .clr(RST));
  Hex_Digit_Display hex_digit_display_4 (.value(LedData[15:12]));  // open: dp
  Hex_Digit_Display hex_digit_display_5 (.value(LedData[19:16]));  // open: dp
  Adder #(.width(32)) adder_1 (.a(EX_PC), .b(32'h4), .out(adder_1_out));  // open: cin, cout
  Multiplexer #(.select(1), .width(32), .disabled("Z"), .enable("false")) multiplexer_3 (
    .in0(multiplexer_2_out), .in1(BAddr), .out(multiplexer_3_out), .sel(BJ));
  Hex_Digit_Display hex_digit_display_6 (.value(LedData[11:8]));  // open: dp
  Hex_Digit_Display hex_digit_display_7 (.value(LedData[7:4]));  // open: dp
  Clock #(.highDuration(1), .lowDuration(1)) clock_1 (.out(clock_1_out));
  // Probe on EX_PC[19:0]
  // Mips_Probe mips_probe_3: pin names not known; wires that end beside it: clock_1_out, EX_IR, CLK
  Multiplexer #(.select(1), .width(32), .disabled("Z"), .enable("false")) multiplexer_4 (
    .in0(PC_4), .in1(PredictJmp), .out(multiplexer_4_out), .sel(PredictJ));
  Multiplexer #(.select(1), .width(32), .disabled("Z"), .enable("false")) multiplexer_5 (
    .in0(multiplexer_4_out), .in1(multiplexer_6_out), .out(nextPC), .sel(PredictErr));
  Multiplexer #(.select(1), .width(32), .disabled("Z"), .enable("false")) multiplexer_6 (
    .in0(adder_1_out), .in1(multiplexer_3_out), .out(multiplexer_6_out), .sel(BranchTaken));
  ROM #(.addrWidth(10), .dataWidth(32), .Select("high")) rom_1 (.addr(IF_PC[11:2]), .data(IF_IR));
  Adder #(.width(32)) adder_2 (.a(IF_PC), .b(32'h4), .out(PC_4));  // open: cin, cout
  Hex_Digit_Display hex_digit_display_8 (.value(LedData[3:0]));  // open: dp
  // Probe on \总周期数 
  // Probe on M_PC[19:0]
  // Mips_Probe mips_probe_4: pin names not known; wires that end beside it: MEM_IR
  BTB btb_1 (
    .BTin(multiplexer_3_out), .BranchPC(EX_PC), .CLK(CLK), .J(BranchTaken), .BTout(PredictJmp),
    .PredictJmp(PredictJ), .CurrentPC(IF_PC), .Branch(Branch));  // open: Hit
  // Probe on \总周期数 
  // Probe on \无条件分支数 
  // Probe on \条件分支成功数 
  // Probe on \插入气泡数 
  // Probe on \LoadUse次数 
  // Probe on IF_PC[11:0]
  // Probe on WB_PC[19:0]
  // Mips_Probe mips_probe_5: pin names not known; wires that end beside it: WB_IR, Go
  and and_2 (and_2_out, ~Pause, ~LoadUse);  // AND_Gate
  // Probe on EX_PC[11:0]
  // Probe on ID_PC[11:0]
  IF_ID if_id_1 (
    .IF_PC(IF_PC), .IF_IR(IF_IR), .CLK(CLK), .ID_PC(ID_PC), .ID_IR({ID_IR, ID_Imm26}), .RST(RST),
    .RUN(and_2_out), .Bubble(PredictErr), .IF_Predict(PredictJ), .ID_Predict(ID_PredictJmp));  // open: IF_Valid, ID_Valid, IF_Hit, ID_Hit
  // Probe on M_PC[11:0]
  D_Flip_Flop #(.trigger("high"), .Pre_Clr_Positions("LEGACY"), .NegatePresetClear("false"), .enable("true"), .NewFFLayout("false")) d_ff_1 (
    .Q(d_ff_1_q), .preset(Pause), .reset(Go));  // open: clk, D, Qn, en
  Rs_Rt rs_rt_1 (
    .OP0(ID_IR[26]), .OP1(ID_IR[27]), .OP2(ID_IR[28]), .OP3(ID_IR[29]), .OP4(ID_IR[30]), .OP5(ID_IR[31]),
    .F0(ID_Imm26[0]), .F1(ID_Imm26[1]), .F2(ID_Imm26[2]), .F3(ID_Imm26[3]), .F4(ID_Imm26[4]),
    .F5(ID_Imm26[5]), .RsUsed(RsUsed), .RtUsed(RtUsed));
  // Probe on WB_PC[11:0]
  // Probe on 13'hfff
  Clock #(.highDuration(1), .lowDuration(1)) clock_2 (.out(clock_2_out));
  \单周期硬布线控制器  \u_单周期硬布线控制器_1  (
    .Func(ID_Imm26[5:0]), .OP(ID_IR), .ALU_OP(ID_ALU_OP), .MemToReg(ID_MemToReg), .MemWrite(ID_MemWrite),
    .ALU_SRC(ID_ALU_SRC), .RegWrite(ID_RegWrite), .SysCALL(ID_Syscall), .SignedExt(SignedExt),
    .RegDst(ID_RegDst), .JR(ID_JR), .JMP(ID_JMP), .Beq(ID_BEQ), .JAL(ID_JAL), .Bne(ID_BNE), .ERET(ID_ERET),
    .B(ID_B), .BGEZ(ID_BGEZ), .SRLV(ID_SRLV));
  Comparator #(.width(5), .mode("unsigned")) comparator_1 (.a(R1_num), .b({5{1'b0}}), .eq(rs____0));  // open: gt, lt
  Comparator #(.width(5), .mode("unsigned")) comparator_2 (
    .a(R1_num), .b(EX_W_num), .eq(rs____EX_W_num));  // open: gt, lt
  Comparator #(.width(5), .mode("unsigned")) comparator_3 (
    .a(EX_W_num), .b(R2_num), .eq(rt____EX_W_num));  // open: gt, lt
  Comparator #(.width(5), .mode("unsigned")) comparator_4 (.a({5{1'b0}}), .b(R2_num), .eq(rt____0));  // open: gt, lt
  Comparator #(.width(5), .mode("unsigned")) comparator_5 (
    .a(R2_num), .b(MEM_W_num), .eq(rt____MEM_W_num));  // open: gt, lt
  Comparator #(.width(5), .mode("unsigned")) comparator_6 (
    .a(MEM_W_num), .b(R1_num), .eq(rs____MEM_W_num));  // open: gt, lt
  Comparator #(.width(13), .mode("twosComplement")) comparator_7 (
    .a(CNT_num), .b(13'hfff), .eq(comparator_7_eq), .lt(comparator_7_lt));  // open: gt
  nand nand_1 (nand_1_out, d_ff_1_q, comparator_7_eq);
  // Probe on CNT_num
  Counter #(.width(13), .max('h1fff), .ongoal("stay"), .trigger("rising"), .behavior("old")) counter_1 (
    .count(comparator_7_lt), .Q(CNT_num), .clk(clock_2_out));  // open: load, D, carry, clr, preset
  Multiplexer #(.select(2), .width(5), .disabled("Z"), .enable("false")) multiplexer_7 (
    .in0(ID_Imm26[20:16]), .in1(ID_Imm26[15:11]), .in2({5{1'b1}}), .in3({5{1'b1}}), .out(ID_W_num),
    .sel({ID_JAL, ID_RegDst}));
  assign CLK = nand_1_out ? clock_2_out : 1'bz;  // Controlled_Buffer controlled_buffer_1
  Pull_Resistor #(.pull(1)) pull_resistor_1 (.node(CLK));
  Multiplexer #(.select(1), .width(5), .disabled("Z"), .enable("false")) multiplexer_8 (
    .in0(ID_Imm26[25:21]), .in1(5'b00010), .out(R1_num), .sel(ID_Syscall));
  Multiplexer #(.select(1), .width(5), .disabled("Z"), .enable("false")) multiplexer_9 (
    .in0(ID_Imm26[20:16]), .in1(5'b00100), .out(R2_num), .sel(ID_Syscall));
  and and_3 (and_3_out, ~rs____0, RsUsed, rs____EX_W_num);  // AND_Gate
  and and_4 (and_4_out, rt____EX_W_num, RtUsed, ~rt____0);  // AND_Gate
  and and_5 (and_5_out, ~rs____0, RsUsed, rs____MEM_W_num);  // AND_Gate
  and and_6 (and_6_out, rt____MEM_W_num, RtUsed, ~rt____0);  // AND_Gate
  not not_1 (not_1_out, CLK);
  assign bit_extender_1_out = {{16{1'b0}}, ID_Imm26[15:0]};  // Bit_Extender bit_extender_1
  assign bit_extender_2_out = {{16{ID_Imm26[15]}}, ID_Imm26[15:0]};  // Bit_Extender bit_extender_2
  MIPS_Regifile mips_regifile_1 (
    .Din(RDin), .Clk(not_1_out), .R1(ID_R1), .R2(ID_MDin), .WE(RegWrite), .W_num(WB_W_num), .R1_num(R1_num),
    .R2_num(R2_num));
  Multiplexer #(.select(1), .width(32), .disabled("Z"), .enable("false")) multiplexer_10 (
    .in0(bit_extender_1_out), .in1(bit_extender_2_out), .out(ID_ExtImm), .sel(SignedExt));
  and and_7 (and_7_out, and_3_out, EX_MemToReg);
  and and_8 (and_8_out, EX_MemToReg, and_4_out);
  and and_9 (ID_EX_rt, and_4_out, EX_RegWrite);
  and and_10 (ID_EX_rs, EX_RegWrite, and_3_out);
  and and_11 (MEM_EX_rs, and_5_out, MEM_RegWrite);
  and and_12 (MEM_EX_rt, MEM_RegWrite, and_6_out);
  or or_1 (or_1_out, LoadUse, PredictErr);
  not not_2 (not_2_out, Pause);
  ID_EX id_ex_1 (
    .CLK(CLK), .ID_PC(ID_PC), .ID_IR({ID_IR, ID_Imm26}), .RST(RST), .EX_PC(EX_PC), .EX_IR(EX_IR),
    .ID_R1(ID_R1), .ID_R2(ID_MDin), .EX_R1(EX_R1), .EX_R2(id_ex_1_ex_r2), .ID_ExtImm(ID_ExtImm),
    .ID_W_num(ID_W_num), .EX_ExtImm(EX_ExtImm), .EX_W_num(EX_W_num), .ID_B(ID_B), .ID_ERET(ID_ERET),
    .ID_SRLV(ID_SRLV), .ID_JMP(ID_JMP), .ID_JR(ID_JR), .ID_BEQ(ID_BEQ), .ID_BNE(ID_BNE), .ID_BGEZ(ID_BGEZ),
    .ID_JAL(ID_JAL), .ID_MemToReg(ID_MemToReg), .ID_MemWrite(ID_MemWrite), .ID_ALU_SRC(ID_ALU_SRC),
    .ID_RegWrite(ID_RegWrite), .ID_Syscall(ID_Syscall), .ID_AlU_OP(ID_ALU_OP), .EX_B(id_ex_1_ex_b),
    .EX_ERET(id_ex_1_ex_eret), .EX_SRLV(EX_SRLV), .EX_JMP(EX_JMP), .EX_JR(EX_JR), .EX_BEQ(EX_BEQ),
    .EX_BNE(EX_BNE), .EX_BGEZ(EX_BGEZ), .EX_JAL(EX_JAL), .EX_MemToReg(EX_MemToReg),
    .EX_MemReg(id_ex_1_ex_memreg), .EX_ALU_SRC(EX_ALU_SRC), .EX_RegWrite(EX_RegWrite),
    .EX_Syscall(id_ex_1_ex_syscall), .EX_ALU_OP(EX_ALU_OP), .ID_sa(ID_Imm26[10:6]), .EX_sa(EX_sa),
    .RUN(not_2_out), .Bubble(or_1_out), .ID_Imm26(ID_Imm26), .EX_Imm26(EX_Imm26), .ID_rs_f(ID_Rs_F),
    .EX_rs_f(EX_Rs_F), .ID_rt_f(ID_Rt_F), .EX_rt_f(EX_Rt_F), .ID_Predict(ID_PredictJmp),
    .EX_Predict(EX_PredictJmp));  // open: EX_MFC0, ID_MFC0, ID_MTC0, EX_MTC0, ID_Valid, EX_Valid, EX_Hit, in_34
  or or_2 (LoadUse, and_7_out, and_8_out);
  or or_3 (Branch, EX_BEQ, EX_BGEZ, EX_BNE, EX_JMP, EX_JAL, EX_JR);
  Multiplexer #(.select(2), .width(32), .disabled("Z"), .enable("false")) multiplexer_11 (
    .in0(id_ex_1_ex_r2), .in1(RDin), .in2(MEM_R), .out(EX_MDin), .sel(EX_Rt_F));  // open: in3
  Multiplexer #(.select(1), .width(2), .disabled("Z"), .enable("false")) multiplexer_12 (
    .in0(2'b00), .in1(2'b01), .out(multiplexer_12_out), .sel(MEM_EX_rs));
  Multiplexer #(.select(1), .width(2), .disabled("Z"), .enable("false")) multiplexer_13 (
    .in0(2'b00), .in1(2'b01), .out(multiplexer_13_out), .sel(MEM_EX_rt));
  and and_13 (and_13_out, equ, EX_BEQ);
  and and_14 (and_14_out, GEZ, EX_BGEZ);
  and and_15 (and_15_out, ~equ, EX_BNE);  // AND_Gate
  and and_16 (and_16_out, ~EX_JAL, ~EX_JR, EX_JMP);  // AND_Gate
  or or_4 (JImm, and_16_out, and_17_out);
  and and_17 (and_17_out, EX_JMP, EX_JAL);
  and and_18 (JR32, EX_JMP, EX_JR);
  Multiplexer #(.select(2), .width(32), .disabled("Z"), .enable("false")) multiplexer_14 (
    .in0(EX_R1), .in1(RDin), .in2(MEM_R), .out({multiplexer_14_out_2, multiplexer_14_out}), .sel(EX_Rs_F));  // open: in3
  Multiplexer #(.select(1), .width(32), .disabled("Z"), .enable("false")) multiplexer_15 (
    .in0(EX_MDin), .in1(EX_ExtImm), .out(multiplexer_15_out), .sel(EX_ALU_SRC));
  Shifter #(.width(32), .shift("ll")) shifter_1 (.in(EX_ExtImm), .\dist (5'b00010), .out(shifter_1_out));
  Adder #(.width(32)) adder_3 (.a(shifter_1_out), .b(adder_4_out), .out(BAddr));  // open: cin, cout
  Adder #(.width(32)) adder_4 (.a(32'h4), .b(EX_PC), .out(adder_4_out));  // open: cin, cout
  Multiplexer #(.select(1), .width(2), .disabled("Z"), .enable("false")) multiplexer_16 (
    .in0(multiplexer_12_out), .in1(2'b10), .out(ID_Rs_F), .sel(ID_EX_rs));
  Multiplexer #(.select(1), .width(2), .disabled("Z"), .enable("false")) multiplexer_17 (
    .in0(multiplexer_13_out), .in1(2'b10), .out(ID_Rt_F), .sel(ID_EX_rt));
  or or_5 (BJ, and_13_out, and_14_out, and_15_out);
  MIPS_ALU mips_alu_1 (
    .X({multiplexer_14_out_2, multiplexer_14_out}), .Y(multiplexer_15_out), .AluOP(EX_ALU_OP), .Equal(equ),
    .Result(EX_R), .shamt(multiplexer_18_out), .GEZ(GEZ));  // open: Result_2
  Multiplexer #(.select(1), .width(5), .disabled("Z"), .enable("false")) multiplexer_18 (
    .in0(EX_sa), .in1(multiplexer_14_out), .out(multiplexer_18_out), .sel(EX_SRLV));
  not not_3 (not_3_out, Pause);
  EX_MEM ex_mem_1 (
    .CLK(CLK), .EX_PC(EX_PC), .EX_IR(EX_IR), .RST(RST), .EX_R(EX_R), .EX_MDin(EX_MDin), .EX_W_num(EX_W_num),
    .MEM_PC(M_PC), .MEM_IR(MEM_IR), .MEM_R(MEM_R), .MEM_MDin(MDin), .MEM_W_num(MEM_W_num),
    .EX_B(id_ex_1_ex_b), .EX_JAL(EX_JAL), .EX_MemToReg(EX_MemToReg), .EX_MemWrite(id_ex_1_ex_memreg),
    .EX_RegWrite(EX_RegWrite), .EX_Syscall(id_ex_1_ex_syscall), .MEM_B(MEM_B), .MEM_JAL(MEM_JAL),
    .MEM_MemToReg(MEM_MemToReg), .MEM_MemWrite(MemWrite), .MEM_RegWrite(MEM_RegWrite),
    .MEM_Syscall(MEM_Syscall), .RUN(not_3_out), .MEM_R1(MEM_R1),
    .EX_R1({multiplexer_14_out_2, multiplexer_14_out}));
  or or_6 (BranchTaken, BJ, JImm, JR32);
  xor xor_1 (PredictErr, EX_PredictJmp, BranchTaken);
  Decoder #(.select(2), .tristate("false"), .disabled("Z"), .enable("false")) decoder_1 (
    .out0(decoder_1_out0[0]), .out1(decoder_1_out0[1]), .out2(decoder_1_out0[2]), .out3(decoder_1_out0[3]),
    .sel(MEM_R[1:0]));
  Demultiplexer #(.select(2), .width(8), .tristate("false"), .disabled("Z"), .enable("false")) demultiplexer_1 (
    .out0(demultiplexer_1_out0), .out1(demultiplexer_1_out1), .out2(demultiplexer_1_out2),
    .out3(demultiplexer_1_out3), .in(MDin[7:0]), .sel(MEM_R[1:0]));
  assign {sel4, sel3, sel2, sel1} = MEM_B ? decoder_1_out0 : 4'bz;  // Controlled_Buffer controlled_buffer_2
  assign {MDin4, MDin3, MDin2, MDin1} = MEM_B ? {demultiplexer_1_out3, demultiplexer_1_out2, demultiplexer_1_out1, demultiplexer_1_out0} : 32'bz;  // Controlled_Buffer controlled_buffer_3
  Comparator #(.width(32), .mode("unsigned")) comparator_8 (
    .a(32'h22), .b(MEM_R1), .eq(comparator_8_eq));  // open: gt, lt
  Comparator #(.width(32), .mode("unsigned")) comparator_9 (
    .a(MEM_R1), .b(32'h32), .eq(comparator_9_eq));  // open: gt, lt
  assign {sel4, sel3, sel2, sel1} = ~MEM_B ? 4'b1111 : 4'bz;  // Controlled_Buffer controlled_buffer_4
  assign {MDin4, MDin3, MDin2, MDin1} = ~MEM_B ? MDin : 32'bz;  // Controlled_Buffer controlled_buffer_5
  and and_19 (LedOut, MEM_Syscall, comparator_8_eq);
  and and_20 (and_20_out, MEM_Syscall, comparator_9_eq);
  D_Flip_Flop #(.trigger("falling"), .Pre_Clr_Positions("ABOVE_BELOW"), .NegatePresetClear("false"), .enable("false"), .NewFFLayout("false")) d_ff_2 (
    .clk(and_20_out), .D(1'b1), .Q(Pause), .reset(Go));  // open: Qn, preset
  not not_4 (not_4_out, Pause);
  Counter #(.width(16), .max('hffff), .ongoal("wrap"), .trigger("rising"), .behavior("new")) counter_2 (
    .count(not_4_out), .Q(\总周期数 ), .clk(CLK), .clr(RST));  // open: load, D, carry, preset, down
  Register #(.width(32), .trigger("rising"), .Select("low")) register_1 (
    .D(MDin), .en(LedOut), .Q(LedData), .clk(CLK), .clr(RST));
  RAM #(.addrWidth(10), .dataWidth(8), .bus("separate"), .Select("high")) ram_1 (
    .addr(MEM_R[11:2]), .din(MDin1), .data(MEM_MDout[7:0]), .str(MemWrite), .sel(sel1), .clk(CLK), .clr(RST));  // open: ld
  RAM #(.addrWidth(10), .dataWidth(8), .bus("separate"), .Select("high")) ram_2 (
    .addr(MEM_R[11:2]), .din(MDin2), .data(MEM_MDout[15:8]), .str(MemWrite), .sel(sel2), .clk(CLK), .clr(RST));  // open: ld
  RAM #(.addrWidth(10), .dataWidth(8), .bus("separate"), .Select("high")) ram_3 (
    .addr(MEM_R[11:2]), .din(MDin3), .data(MEM_MDout[23:16]), .str(MemWrite), .sel(sel3), .clk(CLK), .clr(RST));  // open: ld
  RAM #(.addrWidth(10), .dataWidth(8), .bus("separate"), .Select("high")) ram_4 (
    .addr(MEM_R[11:2]), .din(MDin4), .data(MEM_MDout[31:24]), .str(MemWrite), .sel(sel4), .clk(CLK), .clr(RST));  // open: ld
  not not_5 (not_5_out, Pause);
  // MEM_WB mem_wb_1: pin names not known; wires that end beside it: MEM_ERET, MEM_JAL, MEM_MemToReg, MEM_RegWrite, MEM_R, MEM_MDout, MEM_IR, MEM_W_num, M_PC, not_5_out, RST, CLK, WB_ERET, WB_JAL, WB_MemToReg, RegWrite, WB_R, WB_MDout, WB_IR, WB_W_num, WB_PC
  Adder #(.width(32)) adder_5 (.a(32'h4), .b(WB_PC), .out(adder_5_out));  // open: cin, cout
  Multiplexer #(.select(2), .width(32), .disabled("Z"), .enable("false")) multiplexer_19 (
    .in0(WB_R), .in1(adder_5_out), .in2(WB_MDout), .out(RDin), .sel({WB_MemToReg, WB_JAL}));  // open: in3

  // Other names for the same wires on the sheet: IAddr[31:2] = {EX_PC[31:28], EX_Imm26}; ID_IR[25:0] = ID_Imm26;
  //   Imm16[15:0] = ID_Imm26[15:0]; Imm26[25:0] = ID_Imm26; ID_sa[4:0] = ID_Imm26[10:6]; rd[4:0] = ID_Imm26[15:11];
  //   rt[4:0] = ID_Imm26[20:16]; rs[4:0] = ID_Imm26[25:21]; MEM_MDin[31:0] = MDin; MEM_MemWrite = MemWrite;
  //   MEM_PC[31:0] = M_PC; MemAddr[9:0] = MEM_R[11:2]; PC[31:0] = IF_PC; RAddr[31:0] = EX_R1; WB_RDin[31:0] = RDin;
  //   WB_RegWrite = RegWrite

  // Notes on the sheet:
  //   中断源
  //   时空图监测，可删除
  //   中断等待指示
  //   数码管输出
  //   指令存储器
  //   contents of rom_1 (hex, n*v repeats v):
  //   20110001 8000c05 20110001 20120002 20130003 8000c09 20110001 20120002 20130003 8000c0d 20110001
  //   20120002 20130003 8000c11 20110001 20120002 20130003 c000cf6 20100001 20110001 118fc0 112020
  //   20020022 c 118882 12200001 8000c15 112020 20020022 c 20110001 118880 112020 20020022 c 12200001
  //   8000c1f 20110001 118fc0 112020 20020022 c 1188c3 112020 20020022 c 118903 112020 20020022 c 118903
  //   112020 20020022 c 118903 112020 20020022 c 118903 112020 20020022 c 118903 112020 20020022 c 118903
  //   112020 20020022 c 118903 112020 20020022 c 20100001 109fc0 139fc3 8021 2012000c 24160003 26100001
  //   3210000f 20080008 20090001 139900 2709825 132020 20020022 c 1094022 1500fff9 22100001 2018000f
  //   2188024 108700 20080008 20090001 139902 2709825 132021 20020022 c 1094022 1500fff9 108702 2c9b022
  //   12c00001 8000c50 4020 1084027 84400 3508ffff 82021 20020022 c 2010ffff 20110000 ae300000 22100001
  //   22310004 ae300000 22100001 22310004 ae300000 22100001 22310004 ae300000 22100001 22310004 ae300000
  //   22100001 22310004 ae300000 22100001 22310004 ae300000 22100001 22310004 ae300000 22100001 22310004
  //   ae300000 22100001 22310004 ae300000 22100001 22310004 ae300000 22100001 22310004 ae300000 22100001
  //   22310004 ae300000 22100001 22310004 ae300000 22100001 22310004 ae300000 22100001 22310004 ae300000
  //   22100001 22310004 22100001 8020 2011003c 8e130000 8e340000 274402a 11000002 ae330000 ae140000
  //   2231fffc 1611fff8 102020 20020022 c 22100004 2011003c 1611fff2 20020032 c 20080001 20090003 20110876
  //   118d00 112020 20020022 c 200b0008 1118806 1318806 112020 20020022 c 216bffff 1560fff9 20020032 c
  //   2008ffff 20117777 112020 20020022 c 200b0010 2288826 112020 20020022 c 216bffff 1560fffa 20020032 c
  //   20090000 200b0020 20110000 20120001 a1310000 112020 20020022 c 2328820 21290001 216bffff 1560fff8
  //   200b0008 20090000 8d310000 112020 20020022 c 21290004 216bffff 1560fff9 20020032 c 2011000f 112020
  //   20020022 c 2231ffff 621fffb 20020032 c 20100000 22100001 102020 20020022 c 22100002 102020 20020022
  //   c 22100003 102020 20020022 c 22100004 102020 20020022 c 22100005 102020 20020022 c 22100006 102020
  //   20020022 c 22100007 102020 20020022 c 22100008 102020 20020022 20020022 c 3e00008
  //   流水调试日志用
  //   控制位
  //   OP
  //   Func
  //   rs
  //   rt
  //   rd
  //   sa
  //   Imm16
  //   Imm26
  //   暂停节拍，不能为0
  //   戳工具置1进入计数暂停模式，ctrl+k时钟自动运行到对应节拍暂停
  //   ctrl+k关闭时钟连续运行，将控制位置零，进入单步调试模式调试
  //   v0
  //   t0
  //   ra
  //   可计数暂停的时钟源
  //   为方便自动评测，需要输出流水线各段保存的PC值，注意是PC不是PC+4，另外ID段寄存器写入信息，Mem段内存写入信息也要输出
endmodule

module \流水中断  (
  output RegWrite,
  output MemWrite,
  output [31:0] IF_PC,
  output [31:0] ID_PC,
  output [31:0] EX_PC,
  output [31:0] M_PC,
  output [31:0] WB_PC,
  output [31:0] RDin,
  output [31:0] MDin,
  output [31:0] LedData
);

  wire and_1_out, and_2_out, and_3_out, and_4_out, and_5_out, and_6_out, and_9_out, and_10_out, and_15_out,
       and_16_out, and_17_out, and_21_out, and_22_out, and_23_out, and_24_out, and_25_out, and_28_out, CLK,
       clock_1_out, clock_2_out, comparator_1_eq, comparator_8_eq, comparator_9_eq, comparator_10_eq,
       comparator_11_eq, comparator_11_lt, comparator_12_eq, comparator_13_eq, d_ff_1_q, d_ff_2_q, d_ff_3_q,
       d_ff_4_q, equ, EX_ALU_SRC, EX_BEQ, EX_BGEZ, EX_BNE, EX_ERET, EX_JAL, EX_JMP, EX_JR, EX_MemToReg,
       EX_MFC0, EX_MTC0, EX_RegWrite, EX_SRLV, EX_Valid, flush, GEZ, Go, ID_ALU_SRC, ID_B, ID_BEQ, ID_BGEZ,
       ID_BNE, ID_ERET, id_ex_1_ex_b, id_ex_1_ex_memreg, id_ex_1_ex_syscall, ID_EX_rs, ID_EX_rt, ID_JAL,
       ID_JMP, ID_JR, ID_MemToReg, ID_MemWrite, ID_MFC0, ID_MTC0, ID_RegDst, ID_RegWrite, ID_SRLV,
       ID_Syscall, IE, IE_q, if_id_1_id_valid, INT_SIG, IR1, IR2, IR3, LedOut, LoadUse, MEM_B, MEM_EX_rs,
       MEM_EX_rt, MEM_JAL, MEM_MemToReg, MEM_RegWrite, MEM_Syscall, multiplexer_8_out, multiplexer_10_out,
       nand_1_out, not_1_out, not_2_out, not_3_out, not_4_out, not_6_out, not_7_out, or_1_out, or_6_out,
       or_7_out, or_8_out, or_9_out, or_10_out, or_11_out, or_12_out, or_16_out, or_17_out, Pause,
       priority_encoder_1_en_out, rs____0, rs____EX_W_num, rs____MEM_W_num, RST, RsUsed, rt____0,
       rt____EX_W_num, rt____MEM_W_num, RtUsed, sel1, sel2, sel3, sel4, SignedExt, W1, W2, W3, WB_JAL,
       WB_MemToReg;
  wire [1:0] EX_Rs_F, EX_Rt_F, ID_Rs_F, ID_Rt_F, INT, INT_TOP, multiplexer_11_out, multiplexer_12_out,
       multiplexer_15_out, multiplexer_17_out, multiplexer_22_out, register_1_q, register_2_q;
  wire [2:0] and_18_out, and_19_out, Branch, decoder_1_out1, INM, INM_q, IR1_q, multiplexer_21_out,
       multiplexer_24_out, multiplexer_27_out, multiplexer_29_out, register_4_q, register_6_q;
  wire [3:0] decoder_2_out0, EX_ALU_OP, ID_ALU_OP;
  wire [4:0] EX_sa, EX_W_num, ID_W_num, MEM_W_num, multiplexer_20_out, R1_num, R2_num, WB_W_num;
  wire [7:0] demultiplexer_1_out0, demultiplexer_1_out1, demultiplexer_1_out2, demultiplexer_1_out3, MDin1,
       MDin2, MDin3, MDin4;
  wire [12:0] CNT_num;
  wire [15:0] \LoadUse次数 , \总周期数 , \插入气泡数 , \无条件分支数 , \条件分支成功数 ;
  wire [25:0] EX_Imm26, ID_Imm26;
  wire [31:0] adder_2_out, adder_4_out, BAddr, bit_extender_1_out, bit_extender_2_out, BreakPoint, EX_ExtImm,
       EX_IR, EX_MDin, EX_R, EX_R1, id_ex_1_ex_r2, ID_ExtImm, ID_MDin, ID_R1, IF_IR, MEM_IR, MEM_MDout,
       MEM_R, MEM_R1, multiplexer_1_out, multiplexer_3_out, multiplexer_4_out, multiplexer_18_out,
       multiplexer_19_out, multiplexer_23_out, multiplexer_25_out, multiplexer_26_out, multiplexer_28_out,
       nextPC, PC_4, register_3_q, register_5_q, shifter_1_out, WB_IR, WB_MDout, WB_R;
  wire [31:26] ID_IR;

  Button \u_总复位  (.out(RST));
  Button _1 (.out(IR1));
  Button _2 (.out(IR2));
  Button _3 (.out(IR3));
  // Probe on \总周期数 
  // Probe on \总周期数 
  Button \u_继续运行  (.out(Go));
  LED #(.active("true")) led_1 (.in(W1));
  LED #(.active("true")) led_2 (.in(W2));
  LED #(.active("true")) led_3 (.in(W3));
  Multiplexer #(.select(2), .width(32), .disabled("Z"), .enable("false")) multiplexer_1 (
    .in1(32'h30ac), .in2(32'h3158), .in3(32'h3204), .out(multiplexer_1_out), .sel(INT));  // open: in0
  and and_1 (and_1_out, ~Pause, ~LoadUse);  // AND_Gate
  Hex_Digit_Display hex_digit_display_1 (.value(LedData[31:28]));  // open: dp
  // Probe on IF_PC[19:0]
  // Mips_Probe mips_probe_1: pin names not known; wires that end beside it: IF_IR
  Multiplexer #(.select(3), .width(32), .disabled("Z"), .enable("false")) multiplexer_2 (
    .in0(PC_4), .in1(BAddr), .in2({EX_PC[31:28], EX_Imm26, 2'b00}), .in4(EX_R1), .out(nextPC), .sel(Branch));  // open: in3, in5, in6, in7
  Multiplexer #(.select(1), .width(32), .disabled("Z"), .enable("false")) multiplexer_3 (
    .in0(nextPC), .in1(multiplexer_1_out), .out(multiplexer_3_out), .sel(INT_SIG));
  Register #(.width(32), .trigger("rising"), .Select("low")) PC (
    .D(multiplexer_4_out), .en(and_1_out), .Q(IF_PC), .clk(CLK), .clr(RST));
  Hex_Digit_Display hex_digit_display_2 (.value(LedData[23:20]));  // open: dp
  Hex_Digit_Display hex_digit_display_3 (.value(LedData[27:24]));  // open: dp
  // Probe on ID_PC[19:0]
  // Mips_Probe mips_probe_2: pin names not known; wires that end beside it: {ID_IR, ID_Imm26}
  Hex_Digit_Display hex_digit_display_4 (.value(LedData[15:12]));  // open: dp
  Hex_Digit_Display hex_digit_display_5 (.value(LedData[19:16]));  // open: dp
  Multiplexer #(.select(1), .width(32), .disabled("Z"), .enable("false")) multiplexer_4 (
    .in0(multiplexer_3_out), .in1(BreakPoint), .out(multiplexer_4_out), .sel(EX_ERET));
  ROM #(.addrWidth(10), .dataWidth(32), .Select("high")) rom_1 (.addr(IF_PC[11:2]), .data(IF_IR));
  Adder #(.width(32)) adder_1 (.a(IF_PC), .b(32'h4), .out(PC_4));  // open: cin, cout
  Hex_Digit_Display hex_digit_display_6 (.value(LedData[7:4]));  // open: dp
  Hex_Digit_Display hex_digit_display_7 (.value(LedData[11:8]));  // open: dp
  Clock #(.highDuration(1), .lowDuration(1)) clock_1 (.out(clock_1_out));
  // Probe on EX_PC[19:0]
  // Mips_Probe mips_probe_3: pin names not known; wires that end beside it: clock_1_out, EX_IR, CLK
  Comparator #(.width(32), .mode("twosComplement")) comparator_1 (
    .a({32{1'b0}}), .b(IF_IR), .eq(comparator_1_eq));  // open: gt, lt
  not not_1 (not_1_out, comparator_1_eq);
  and and_2 (and_2_out, ~Pause, ~LoadUse);  // AND_Gate
  Rs_Rt rs_rt_1 (
    .OP0(ID_IR[26]), .OP1(ID_IR[27]), .OP2(ID_IR[28]), .OP3(ID_IR[29]), .OP4(ID_IR[30]), .OP5(ID_IR[31]),
    .F0(ID_Imm26[0]), .F1(ID_Imm26[1]), .F2(ID_Imm26[2]), .F3(ID_Imm26[3]), .F4(ID_Imm26[4]),
    .F5(ID_Imm26[5]), .RsUsed(RsUsed), .RtUsed(RtUsed));
  Hex_Digit_Display hex_digit_display_8 (.value(LedData[3:0]));  // open: dp
  or or_1 (or_1_out, flush, EX_ERET, INT_SIG);
  IF_ID if_id_1 (
    .IF_PC(IF_PC), .IF_IR(IF_IR), .CLK(CLK), .ID_PC(ID_PC), .ID_IR({ID_IR, ID_Imm26}), .RST(RST),
    .RUN(and_2_out), .Bubble(or_1_out), .IF_Valid(not_1_out), .ID_Valid(if_id_1_id_valid));  // open: IF_Predict, ID_Predict, IF_Hit, ID_Hit
  Comparator #(.width(5), .mode("unsigned")) comparator_2 (.a(R1_num), .b({5{1'b0}}), .eq(rs____0));  // open: gt, lt
  Comparator #(.width(5), .mode("unsigned")) comparator_3 (
    .a(R1_num), .b(EX_W_num), .eq(rs____EX_W_num));  // open: gt, lt
  Comparator #(.width(5), .mode("unsigned")) comparator_4 (
    .a(EX_W_num), .b(R2_num), .eq(rt____EX_W_num));  // open: gt, lt
  Comparator #(.width(5), .mode("unsigned")) comparator_5 (.a({5{1'b0}}), .b(R2_num), .eq(rt____0));  // open: gt, lt
  Comparator #(.width(5), .mode("unsigned")) comparator_6 (
    .a(R2_num), .b(MEM_W_num), .eq(rt____MEM_W_num));  // open: gt, lt
  Comparator #(.width(5), .mode("unsigned")) comparator_7 (
    .a(MEM_W_num), .b(R1_num), .eq(rs____MEM_W_num));  // open: gt, lt
  // Probe on \总周期数 
  // Probe on M_PC[19:0]
  // Mips_Probe mips_probe_4: pin names not known; wires that end beside it: MEM_IR
  // Probe on \总周期数 
  // Probe on \无条件分支数 
  // Probe on \条件分支成功数 
  // Probe on \插入气泡数 
  // Probe on \LoadUse次数 
  \单周期硬布线控制器  \u_单周期硬布线控制器_1  (
    .Func(ID_Imm26[5:0]), .OP(ID_IR), .ALU_OP(ID_ALU_OP), .MemToReg(ID_MemToReg), .MemWrite(ID_MemWrite),
    .ALU_SRC(ID_ALU_SRC), .RegWrite(ID_RegWrite), .SysCALL(ID_Syscall), .SignedExt(SignedExt),
    .RegDst(ID_RegDst), .JR(ID_JR), .JMP(ID_JMP), .Beq(ID_BEQ), .JAL(ID_JAL), .Bne(ID_BNE), .ERET(ID_ERET),
    .B(ID_B), .BGEZ(ID_BGEZ), .SRLV(ID_SRLV));
  // Probe on IF_PC[11:0]
  // Probe on WB_PC[19:0]
  // Mips_Probe mips_probe_5: pin names not known; wires that end beside it: WB_IR, Go
  Comparator #(.width(6), .mode("unsigned")) comparator_8 (
    .a(6'b010000), .b(ID_IR), .eq(comparator_8_eq));  // open: gt, lt
  Comparator #(.width(5), .mode("unsigned")) comparator_9 (
    .a(ID_Imm26[25:21]), .b(5'b00100), .eq(comparator_9_eq));  // open: gt, lt
  Comparator #(.width(5), .mode("unsigned")) comparator_10 (
    .a(ID_Imm26[25:21]), .b({5{1'b0}}), .eq(comparator_10_eq));  // open: gt, lt
  and and_3 (and_3_out, ~rs____0, RsUsed, rs____EX_W_num);  // AND_Gate
  and and_4 (and_4_out, rt____EX_W_num, RtUsed, ~rt____0);  // AND_Gate
  and and_5 (and_5_out, ~rs____0, RsUsed, rs____MEM_W_num);  // AND_Gate
  and and_6 (and_6_out, rt____MEM_W_num, RtUsed, ~rt____0);  // AND_Gate
  // Probe on ID_PC[11:0]
  // Probe on EX_PC[11:0]
  and and_7 (ID_MTC0, comparator_8_eq, comparator_9_eq);
  and and_8 (ID_MFC0, comparator_8_eq, comparator_10_eq);
  Multiplexer #(.select(2), .width(5), .disabled("Z"), .enable("false")) multiplexer_5 (
    .in0(ID_Imm26[20:16]), .in1(ID_Imm26[15:11]), .in2({5{1'b1}}), .in3({5{1'b1}}), .out(ID_W_num),
    .sel({ID_JAL, ID_RegDst}));
  or or_2 (W1, IR1_q[0], d_ff_2_q);
  or or_3 (W2, IR1_q[1], d_ff_3_q);
  or or_4 (W3, IR1_q[2], d_ff_4_q);
  // Probe on M_PC[11:0]
  D_Flip_Flop #(.trigger("high"), .Pre_Clr_Positions("LEGACY"), .NegatePresetClear("false"), .enable("true"), .NewFFLayout("false")) d_ff_1 (
    .Q(d_ff_1_q), .preset(Pause), .reset(Go));  // open: clk, D, Qn, en
  Multiplexer #(.select(1), .width(5), .disabled("Z"), .enable("false")) multiplexer_6 (
    .in0(ID_Imm26[25:21]), .in1(5'b00010), .out(R1_num), .sel(ID_Syscall));
  Multiplexer #(.select(1), .width(5), .disabled("Z"), .enable("false")) multiplexer_7 (
    .in0(ID_Imm26[20:16]), .in1(5'b00100), .out(R2_num), .sel(ID_Syscall));
  and and_9 (and_9_out, and_3_out, EX_MemToReg);
  and and_10 (and_10_out, EX_MemToReg, and_4_out);
  and and_11 (ID_EX_rt, and_4_out, EX_RegWrite);
  and and_12 (ID_EX_rs, EX_RegWrite, and_3_out);
  and and_13 (MEM_EX_rs, and_5_out, MEM_RegWrite);
  and and_14 (MEM_EX_rt, MEM_RegWrite, and_6_out);
  D_Flip_Flop #(.trigger("rising"), .Pre_Clr_Positions("LEGACY"), .NegatePresetClear("false"), .enable("true"), .NewFFLayout("false")) d_ff_2 (
    .clk(IR1), .D(1'b1), .Q(d_ff_2_q), .reset(IR1_q[0]));  // open: Qn, preset, en
  D_Flip_Flop #(.trigger("rising"), .Pre_Clr_Positions("LEGACY"), .NegatePresetClear("false"), .enable("true"), .NewFFLayout("false")) d_ff_3 (
    .clk(IR2), .D(1'b1), .Q(d_ff_3_q), .reset(IR1_q[1]));  // open: Qn, preset, en
  D_Flip_Flop #(.trigger("rising"), .Pre_Clr_Positions("LEGACY"), .NegatePresetClear("false"), .enable("true"), .NewFFLayout("false")) d_ff_4 (
    .clk(IR3), .D(1'b1), .Q(d_ff_4_q), .reset(IR1_q[2]));  // open: Qn, preset, en
  // Probe on WB_PC[11:0]
  // Probe on 13'h340
  Clock #(.highDuration(1), .lowDuration(1)) clock_2 (.out(clock_2_out));
  not not_2 (not_2_out, CLK);
  assign bit_extender_1_out = {{16{1'b0}}, ID_Imm26[15:0]};  // Bit_Extender bit_extender_1
  assign bit_extender_2_out = {{16{ID_Imm26[15]}}, ID_Imm26[15:0]};  // Bit_Extender bit_extender_2
  or or_5 (LoadUse, and_9_out, and_10_out);
  or or_6 (or_6_out, EX_MTC0, INT_SIG);
  Multiplexer #(.select(1), .width(1), .disabled("Z"), .enable("false")) multiplexer_8 (
    .in0(IE_q), .in1(1'b1), .out(multiplexer_8_out), .sel(or_6_out));
  or or_7 (or_7_out, d_ff_2_q, IR1_q[0]);
  or or_8 (or_8_out, d_ff_3_q, IR1_q[1]);
  or or_9 (or_9_out, d_ff_4_q, IR1_q[2]);
  Comparator #(.width(13), .mode("twosComplement")) comparator_11 (
    .a(CNT_num), .b(13'h340), .eq(comparator_11_eq), .lt(comparator_11_lt));  // open: gt
  MIPS_Regifile mips_regifile_1 (
    .Din(RDin), .Clk(not_2_out), .R1(ID_R1), .R2(ID_MDin), .WE(RegWrite), .W_num(WB_W_num), .R1_num(R1_num),
    .R2_num(R2_num));
  Multiplexer #(.select(1), .width(32), .disabled("Z"), .enable("false")) multiplexer_9 (
    .in0(bit_extender_1_out), .in1(bit_extender_2_out), .out(ID_ExtImm), .sel(SignedExt));
  Multiplexer #(.select(1), .width(1), .disabled("Z"), .enable("false")) multiplexer_10 (
    .in0(multiplexer_8_out), .in1(1'b0), .out(multiplexer_10_out), .sel(EX_MFC0));
  and and_15 (and_15_out, or_7_out, ~and_19_out[0]);  // AND_Gate
  and and_16 (and_16_out, or_8_out, ~and_19_out[1]);  // AND_Gate
  and and_17 (and_17_out, or_9_out, ~and_19_out[2]);  // AND_Gate
  nand nand_1 (nand_1_out, d_ff_1_q, comparator_11_eq);
  // Probe on CNT_num
  Counter #(.width(13), .max('h1fff), .ongoal("stay"), .trigger("rising"), .behavior("old")) counter_1 (
    .count(comparator_11_lt), .Q(CNT_num), .clk(clock_2_out), .clr(RST));  // open: load, D, carry, preset
  not not_3 (not_3_out, Pause);
  Multiplexer #(.select(1), .width(2), .disabled("Z"), .enable("false")) multiplexer_11 (
    .in0(2'b00), .in1(2'b01), .out(multiplexer_11_out), .sel(MEM_EX_rs));
  Multiplexer #(.select(1), .width(2), .disabled("Z"), .enable("false")) multiplexer_12 (
    .in0(2'b00), .in1(2'b01), .out(multiplexer_12_out), .sel(MEM_EX_rt));
  D_Flip_Flop #(.trigger("rising"), .Pre_Clr_Positions("ABOVE_BELOW"), .NegatePresetClear("false"), .enable("false"), .NewFFLayout("false")) u_IE (
    .clk(CLK), .D(multiplexer_10_out), .Q(IE_q), .Qn(IE), .reset(or_10_out));  // open: preset
  or or_10 (or_10_out, RST, EX_ERET);
  D_Flip_Flop #(.trigger("rising"), .Pre_Clr_Positions("LEGACY"), .NegatePresetClear("false"), .enable("true"), .NewFFLayout("false")) u_IR1 (
    .clk(CLK), .D(and_15_out), .Q(IR1_q[0]), .reset(RST));  // open: Qn, preset, en
  assign and_18_out = IR1_q & INM;  // AND_Gate and_18, 3 bits wide
  D_Flip_Flop #(.trigger("rising"), .Pre_Clr_Positions("LEGACY"), .NegatePresetClear("false"), .enable("true"), .NewFFLayout("false")) u_IR2 (
    .clk(CLK), .D(and_16_out), .Q(IR1_q[1]), .reset(RST));  // open: Qn, preset, en
  D_Flip_Flop #(.trigger("rising"), .Pre_Clr_Positions("LEGACY"), .NegatePresetClear("false"), .enable("true"), .NewFFLayout("false")) u_IR3 (
    .clk(CLK), .D(and_17_out), .Q(IR1_q[2]), .reset(RST));  // open: Qn, preset, en
  assign and_19_out = decoder_1_out1 & {3{EX_ERET}};  // AND_Gate and_19, 3 bits wide
  assign CLK = nand_1_out ? clock_2_out : 1'bz;  // Controlled_Buffer controlled_buffer_1
  Pull_Resistor #(.pull(1)) pull_resistor_1 (.node(CLK));
  or or_11 (or_11_out, INT_SIG, LoadUse, flush, EX_ERET);
  ID_EX id_ex_1 (
    .CLK(CLK), .ID_PC(ID_PC), .ID_IR({ID_IR, ID_Imm26}), .RST(RST), .EX_PC(EX_PC), .EX_IR(EX_IR),
    .ID_R1(ID_R1), .ID_R2(ID_MDin), .EX_R1(EX_R1), .EX_R2(id_ex_1_ex_r2), .ID_ExtImm(ID_ExtImm),
    .ID_W_num(ID_W_num), .EX_ExtImm(EX_ExtImm), .EX_W_num(EX_W_num), .ID_B(ID_B), .ID_ERET(ID_ERET),
    .ID_SRLV(ID_SRLV), .ID_JMP(ID_JMP), .ID_JR(ID_JR), .ID_BEQ(ID_BEQ), .ID_BNE(ID_BNE), .ID_BGEZ(ID_BGEZ),
    .ID_JAL(ID_JAL), .ID_MemToReg(ID_MemToReg), .ID_MemWrite(ID_MemWrite), .ID_ALU_SRC(ID_ALU_SRC),
    .ID_RegWrite(ID_RegWrite), .ID_Syscall(ID_Syscall), .ID_AlU_OP(ID_ALU_OP), .EX_B(id_ex_1_ex_b),
    .EX_ERET(EX_ERET), .EX_SRLV(EX_SRLV), .EX_JMP(EX_JMP), .EX_JR(EX_JR), .EX_BEQ(EX_BEQ), .EX_BNE(EX_BNE),
    .EX_BGEZ(EX_BGEZ), .EX_JAL(EX_JAL), .EX_MemToReg(EX_MemToReg), .EX_MemReg(id_ex_1_ex_memreg),
    .EX_ALU_SRC(EX_ALU_SRC), .EX_RegWrite(EX_RegWrite), .EX_Syscall(id_ex_1_ex_syscall),
    .EX_ALU_OP(EX_ALU_OP), .ID_sa(ID_Imm26[10:6]), .EX_sa(EX_sa), .RUN(not_3_out), .Bubble(or_11_out),
    .ID_Imm26(ID_Imm26), .EX_Imm26(EX_Imm26), .ID_rs_f(ID_Rs_F), .EX_rs_f(EX_Rs_F), .ID_rt_f(ID_Rt_F),
    .EX_rt_f(EX_Rt_F), .EX_MFC0(EX_MFC0), .ID_MFC0(ID_MFC0), .ID_MTC0(ID_MTC0), .EX_MTC0(EX_MTC0),
    .ID_Valid(if_id_1_id_valid), .EX_Valid(EX_Valid));  // open: ID_Predict, EX_Predict, EX_Hit, in_34
  Multiplexer #(.select(1), .width(2), .disabled("Z"), .enable("false")) multiplexer_13 (
    .in0(multiplexer_11_out), .in1(2'b10), .out(ID_Rs_F), .sel(ID_EX_rs));
  Multiplexer #(.select(1), .width(2), .disabled("Z"), .enable("false")) multiplexer_14 (
    .in0(multiplexer_12_out), .in1(2'b10), .out(ID_Rt_F), .sel(ID_EX_rt));
  and and_20 (INT_SIG, IE, EX_Valid, ~priority_encoder_1_en_out);  // AND_Gate
  Priority_Encoder #(.select(2), .disabled("Z")) priority_encoder_1 (
    .in1(and_18_out[0]), .in2(and_18_out[1]), .in3(and_18_out[2]), .out(INT),
    .en_out(priority_encoder_1_en_out));  // open: in0, gs, en_in
  Decoder #(.select(2), .tristate("false"), .disabled("Z"), .enable("false")) decoder_1 (
    .out1(decoder_1_out1[0]), .out2(decoder_1_out1[1]), .out3(decoder_1_out1[2]), .sel(INT_TOP));  // open: out0
  or or_12 (or_12_out, INT_SIG, EX_ERET);
  Multiplexer #(.select(1), .width(2), .disabled("Z"), .enable("false")) multiplexer_15 (
    .in0(INT), .in1(register_1_q), .out(multiplexer_15_out), .sel(EX_ERET));
  Register #(.width(2), .trigger("rising"), .Select("low")) u_INT (
    .D(multiplexer_15_out), .en(or_12_out), .Q(INT_TOP), .clk(CLK), .clr(RST));
  and and_21 (and_21_out, equ, EX_BEQ);
  and and_22 (and_22_out, GEZ, EX_BGEZ);
  and and_23 (and_23_out, ~equ, EX_BNE);  // AND_Gate
  and and_24 (and_24_out, ~EX_JAL, ~EX_JR, EX_JMP);  // AND_Gate
  or or_13 (Branch[1], and_24_out, and_25_out);
  and and_25 (and_25_out, EX_JMP, EX_JAL);
  and and_26 (Branch[2], EX_JMP, EX_JR);
  Multiplexer #(.select(2), .width(32), .disabled("Z"), .enable("false")) multiplexer_16 (
    .in0(id_ex_1_ex_r2), .in1(RDin), .in2(MEM_R), .out(EX_MDin), .sel(EX_Rt_F));  // open: in3
  Multiplexer #(.select(1), .width(2), .disabled("Z"), .enable("false")) multiplexer_17 (
    .in0(INT_TOP), .in1(register_2_q), .out(multiplexer_17_out), .sel(EX_ERET));
  or or_14 (Branch[0], and_21_out, and_22_out, and_23_out);
  Shifter #(.width(32), .shift("ll")) shifter_1 (.in(EX_ExtImm), .\dist (5'b00010), .out(shifter_1_out));
  Adder #(.width(32)) adder_2 (.a(32'h4), .b(EX_PC), .out(adder_2_out));  // open: cin, cout
  Register #(.width(2), .trigger("rising"), .Select("low")) register_1 (
    .D(multiplexer_17_out), .en(or_12_out), .Q(register_1_q), .clk(CLK), .clr(RST));
  or or_15 (flush, Branch[0], Branch[1], Branch[2]);
  Multiplexer #(.select(2), .width(32), .disabled("Z"), .enable("false")) multiplexer_18 (
    .in0(EX_R1), .in1(RDin), .in2(MEM_R), .out(multiplexer_18_out), .sel(EX_Rs_F));  // open: in3
  Multiplexer #(.select(1), .width(32), .disabled("Z"), .enable("false")) multiplexer_19 (
    .in0(EX_MDin), .in1(EX_ExtImm), .out(multiplexer_19_out), .sel(EX_ALU_SRC));
  Multiplexer #(.select(1), .width(5), .disabled("Z"), .enable("false")) multiplexer_20 (
    .in0(EX_sa), .in1(multiplexer_18_out[4:0]), .out(multiplexer_20_out), .sel(EX_SRLV));
  Adder #(.width(32)) adder_3 (.a(shifter_1_out), .b(adder_2_out), .out(BAddr));  // open: cin, cout
  Multiplexer #(.select(2), .width(3), .disabled("Z"), .enable("false")) multiplexer_21 (
    .in0(3'b000), .in1(3'b001), .in2(3'b011), .in3(3'b111), .out(multiplexer_21_out), .sel(INT));
  Register #(.width(2), .trigger("rising"), .Select("low")) register_2 (
    .D(multiplexer_22_out), .en(or_12_out), .Q(register_2_q), .clk(CLK), .clr(RST));
  Multiplexer #(.select(1), .width(2), .disabled("Z"), .enable("false")) multiplexer_22 (
    .in0(register_1_q), .in1(2'b00), .out(multiplexer_22_out), .sel(EX_ERET));
  MIPS_ALU mips_alu_1 (
    .X(multiplexer_18_out), .Y(multiplexer_19_out), .AluOP(EX_ALU_OP), .Equal(equ), .Result(EX_R),
    .shamt(multiplexer_20_out), .GEZ(GEZ));  // open: Result_2
  Multiplexer #(.select(1), .width(32), .disabled("Z"), .enable("false")) multiplexer_23 (
    .in0(multiplexer_25_out), .in1(register_3_q), .out(multiplexer_23_out), .sel(EX_ERET));
  or or_16 (or_16_out, INT_SIG, EX_ERET);
  Multiplexer #(.select(1), .width(3), .disabled("Z"), .enable("false")) multiplexer_24 (
    .in0(multiplexer_21_out), .in1(register_4_q), .out(multiplexer_24_out), .sel(EX_ERET));
  or or_17 (or_17_out, INT_SIG, EX_ERET);
  not not_4 (not_4_out, Pause);
  EX_MEM ex_mem_1 (
    .CLK(CLK), .EX_PC(EX_PC), .EX_IR(EX_IR), .RST(RST), .EX_R(EX_R), .EX_MDin(EX_MDin), .EX_W_num(EX_W_num),
    .MEM_PC(M_PC), .MEM_IR(MEM_IR), .MEM_R(MEM_R), .MEM_MDin(MDin), .MEM_W_num(MEM_W_num),
    .EX_B(id_ex_1_ex_b), .EX_JAL(EX_JAL), .EX_MemToReg(EX_MemToReg), .EX_MemWrite(id_ex_1_ex_memreg),
    .EX_RegWrite(EX_RegWrite), .EX_Syscall(id_ex_1_ex_syscall), .MEM_B(MEM_B), .MEM_JAL(MEM_JAL),
    .MEM_MemToReg(MEM_MemToReg), .MEM_MemWrite(MemWrite), .MEM_RegWrite(MEM_RegWrite),
    .MEM_Syscall(MEM_Syscall), .RUN(not_4_out), .MEM_R1(MEM_R1), .EX_R1(multiplexer_18_out));
  Multiplexer #(.select(3), .width(32), .disabled("Z"), .enable("false")) multiplexer_25 (
    .in0(adder_2_out), .in1(BAddr), .in2({EX_PC[31:28], EX_Imm26, 2'b00}), .in4(EX_R1),
    .out(multiplexer_25_out), .sel(Branch));  // open: in3, in5, in6, in7
  Register #(.width(32), .trigger("rising"), .Select("low")) EPC_Top (
    .D(multiplexer_23_out), .en(or_16_out), .Q(BreakPoint), .clk(CLK), .clr(RST));
  assign INM = ~INM_q;  // NOT_Gate not_5, 3 bits wide
  Register #(.width(3), .trigger("rising"), .Select("low")) u_INM (
    .D(multiplexer_24_out), .en(or_17_out), .Q(INM_q), .clk(CLK), .clr(RST));
  Multiplexer #(.select(1), .width(32), .disabled("Z"), .enable("false")) multiplexer_26 (
    .in0(BreakPoint), .in1(register_5_q), .out(multiplexer_26_out), .sel(EX_ERET));
  Register #(.width(32), .trigger("rising"), .Select("low")) register_3 (
    .D(multiplexer_26_out), .en(or_16_out), .Q(register_3_q), .clk(CLK), .clr(RST));
  Multiplexer #(.select(1), .width(3), .disabled("Z"), .enable("false")) multiplexer_27 (
    .in0(INM_q), .in1(register_6_q), .out(multiplexer_27_out), .sel(EX_ERET));
  Register #(.width(3), .trigger("rising"), .Select("low")) register_4 (
    .D(multiplexer_27_out), .en(or_17_out), .Q(register_4_q), .clk(CLK), .clr(RST));
  Comparator #(.width(32), .mode("unsigned")) comparator_12 (
    .a(32'h22), .b(MEM_R1), .eq(comparator_12_eq));  // open: gt, lt
  Comparator #(.width(32), .mode("unsigned")) comparator_13 (
    .a(MEM_R1), .b(32'h32), .eq(comparator_13_eq));  // open: gt, lt
  Decoder #(.select(2), .tristate("false"), .disabled("Z"), .enable("false")) decoder_2 (
    .out0(decoder_2_out0[0]), .out1(decoder_2_out0[1]), .out2(decoder_2_out0[2]), .out3(decoder_2_out0[3]),
    .sel(MEM_R[1:0]));
  Demultiplexer #(.select(2), .width(8), .tristate("false"), .disabled("Z"), .enable("false")) demultiplexer_1 (
    .out0(demultiplexer_1_out0), .out1(demultiplexer_1_out1), .out2(demultiplexer_1_out2),
    .out3(demultiplexer_1_out3), .in(MDin[7:0]), .sel(MEM_R[1:0]));
  Multiplexer #(.select(1), .width(32), .disabled("Z"), .enable("false")) multiplexer_28 (
    .in0(register_3_q), .in1({32{1'b0}}), .out(multiplexer_28_out), .sel(EX_ERET));
  Multiplexer #(.select(1), .width(3), .disabled("Z"), .enable("false")) multiplexer_29 (
    .in0(register_4_q), .in1(3'b000), .out(multiplexer_29_out), .sel(EX_ERET));
  and and_27 (LedOut, MEM_Syscall, comparator_12_eq);
  and and_28 (and_28_out, MEM_Syscall, comparator_13_eq);
  D_Flip_Flop #(.trigger("falling"), .Pre_Clr_Positions("ABOVE_BELOW"), .NegatePresetClear("false"), .enable("false"), .NewFFLayout("false")) d_ff_5 (
    .clk(and_28_out), .D(1'b1), .Q(Pause), .reset(Go));  // open: Qn, preset
  assign {sel4, sel3, sel2, sel1} = MEM_B ? decoder_2_out0 : 4'bz;  // Controlled_Buffer controlled_buffer_2
  assign {MDin4, MDin3, MDin2, MDin1} = MEM_B ? {demultiplexer_1_out3, demultiplexer_1_out2, demultiplexer_1_out1, demultiplexer_1_out0} : 32'bz;  // Controlled_Buffer controlled_buffer_3
  Register #(.width(32), .trigger("rising"), .Select("low")) register_5 (
    .D(multiplexer_28_out), .en(or_16_out), .Q(register_5_q), .clk(CLK), .clr(RST));
  Register #(.width(3), .trigger("rising"), .Select("low")) register_6 (
    .D(multiplexer_29_out), .en(or_17_out), .Q(register_6_q), .clk(CLK), .clr(RST));
  not not_6 (not_6_out, Pause);
  Counter #(.width(16), .max('hffff), .ongoal("wrap"), .trigger("rising"), .behavior("new")) counter_2 (
    .count(not_6_out), .Q(\总周期数 ), .clk(CLK), .clr(RST));  // open: load, D, carry, preset, down
  assign {sel4, sel3, sel2, sel1} = ~MEM_B ? 4'b1111 : 4'bz;  // Controlled_Buffer controlled_buffer_4
  assign {MDin4, MDin3, MDin2, MDin1} = ~MEM_B ? MDin : 32'bz;  // Controlled_Buffer controlled_buffer_5
  Register #(.width(32), .trigger("rising"), .Select("low")) register_7 (
    .D(MDin), .en(LedOut), .Q(LedData), .clk(CLK), .clr(RST));
  RAM #(.addrWidth(10), .dataWidth(8), .bus("separate"), .Select("high")) ram_1 (
    .addr(MEM_R[11:2]), .din(MDin1), .data(MEM_MDout[7:0]), .str(MemWrite), .sel(sel1), .clk(CLK), .clr(RST));  // open: ld
  RAM #(.addrWidth(10), .dataWidth(8), .bus("separate"), .Select("high")) ram_2 (
    .addr(MEM_R[11:2]), .din(MDin2), .data(MEM_MDout[15:8]), .str(MemWrite), .sel(sel2), .clk(CLK), .clr(RST));  // open: ld
  RAM #(.addrWidth(10), .dataWidth(8), .bus("separate"), .Select("high")) ram_3 (
    .addr(MEM_R[11:2]), .din(MDin3), .data(MEM_MDout[23:16]), .str(MemWrite), .sel(sel3), .clk(CLK), .clr(RST));  // open: ld
  RAM #(.addrWidth(10), .dataWidth(8), .bus("separate"), .Select("high")) ram_4 (
    .addr(MEM_R[11:2]), .din(MDin4), .data(MEM_MDout[31:24]), .str(MemWrite), .sel(sel4), .clk(CLK), .clr(RST));  // open: ld
  not not_7 (not_7_out, Pause);
  MEM_WB mem_wb_1 (
    .WB_PC(WB_PC), .WB_IR(WB_IR), .WB_MDout(WB_MDout), .CLK(CLK), .RST(RST), .WB_R(WB_R), .MEM_PC(M_PC),
    .MEM_IR(MEM_IR), .MEM_MDout(MEM_MDout), .MEM_R(MEM_R), .MEM_W_num(MEM_W_num), .WB_W_num(WB_W_num),
    .MEM_JAL(MEM_JAL), .MEM_MemToReg(MEM_MemToReg), .MEM_RegWrite(MEM_RegWrite), .WB_JAL(WB_JAL),
    .WB_MemToReg(WB_MemToReg), .WB_RegWrite(RegWrite), .RUN(not_7_out));  // open: MEM_Syscall, WB_Syscall, MEM_R1, WB_R1, MEM_MDin, WB_MDin
  Adder #(.width(32)) adder_4 (.a(32'h4), .b(WB_PC), .out(adder_4_out));  // open: cin, cout
  Multiplexer #(.select(2), .width(32), .disabled("Z"), .enable("false")) multiplexer_30 (
    .in0(WB_R), .in1(adder_4_out), .in2(WB_MDout), .out(RDin), .sel({WB_MemToReg, WB_JAL}));  // open: in3

  // Other names for the same wires on the sheet: IAddr[31:2] = {EX_PC[31:28], EX_Imm26}; ID_IR[25:0] = ID_Imm26;
  //   Imm16[15:0] = ID_Imm26[15:0]; Imm26[25:0] = ID_Imm26; ID_sa[4:0] = ID_Imm26[10:6]; rd[4:0] = ID_Imm26[15:11];
  //   rt[4:0] = ID_Imm26[20:16]; rs[4:0] = ID_Imm26[25:21]; OP[5:0] = ID_IR; MEM_MDin[31:0] = MDin;
  //   MEM_MemWrite = MemWrite; MEM_PC[31:0] = M_PC; MemAddr[9:0] = MEM_R[11:2]; PC[31:0] = IF_PC; RAddr[31:0] = EX_R1;
  //   WB_RDin[31:0] = RDin; WB_RegWrite = RegWrite

  // Notes on the sheet:
  //   中断源
  //   时空图监测，可删除
  //   中断等待指示
  //   指令存储器
  //   数码管输出
  //   contents of rom_1 (hex, n*v repeats v):
  //   201d07d0 20100001 109fc0 139fc3 8021 2012000c 24160008 26100001 3210000f 20080008 20090001 139900
  //   2709825 132020 20020022 c 1094022 1500fff9 22100001 2018000f 2188024 108700 20080008 20090001 139902
  //   2709825 132021 20020022 c 1094022 1500fff9 108702 2c9b022 12c00001 8000c07 4020 1084027 84400
  //   3508ffff 82021 20020022 c 8000c01 afa20000 23bd0004 afa40000 23bd0004 afb00000 23bd0004 afb30000
  //   23bd0004 afb40000 23bd0004 afb50000 23bd0004 afb60000 23bd0004 40000000 20160001 20140003 20150001
  //   168020 108100 2149825 132020 20020022 c 1600fffa 295a022 1680fff7 40800000 23bdfffc 8fb60000
  //   23bdfffc 8fb50000 23bdfffc 8fb40000 23bdfffc 8fb30000 23bdfffc 8fb00000 23bdfffc 8fa40000 23bdfffc
  //   8fa20000 42000018 afa20000 23bd0004 afa40000 23bd0004 afb00000 23bd0004 afb30000 23bd0004 afb40000
  //   23bd0004 afb50000 23bd0004 afb60000 23bd0004 40000000 20160002 20140003 20150001 168020 108100
  //   2149825 132020 20020022 c 1600fffa 295a022 1680fff7 40800000 23bdfffc 8fb60000 23bdfffc 8fb50000
  //   23bdfffc 8fb40000 23bdfffc 8fb30000 23bdfffc 8fb00000 23bdfffc 8fa40000 23bdfffc 8fa20000 42000018
  //   afa20000 23bd0004 afa40000 23bd0004 afb00000 23bd0004 afb30000 23bd0004 afb40000 23bd0004 afb50000
  //   23bd0004 afb60000 23bd0004 40000000 20160003 20140003 20150001 168020 108100 2149825 132020 20020022
  //   c 1600fffa 295a022 1680fff7 40800000 23bdfffc 8fb60000 23bdfffc 8fb50000 23bdfffc 8fb40000 23bdfffc
  //   8fb30000 23bdfffc 8fb00000 23bdfffc 8fa40000 23bdfffc 8fa20000 42000018
  //   OP
  //   Func
  //   rs
  //   rt
  //   rd
  //   sa
  //   Imm16
  //   Imm26
  //   v0
  //   t0
  //   ra
  //   流水调试日志用
  //   控制位
  //   暂停节拍，不能为0
  //   戳工具置1进入计数暂停模式，ctrl+k时钟自动运行到对应节拍暂停
  //   ctrl+k关闭时钟连续运行，将控制位置零，进入单步调试模式调试
  //   Reset 
  //   可计数暂停的时钟源
  //   为方便自动评测，需要输出流水线各段保存的PC值，注意是PC不是PC+4，另外ID段寄存器写入信息，Mem段内存写入信息也要输出
  //   使用ERET指令来反向MUX
endmodule

module FinalCPU (
);

  wire and_1_out, and_2_out, and_5_out, and_6_out, and_7_out, and_8_out, and_9_out, and_10_out, and_15_out,
       and_16_out, and_17_out, and_21_out, and_22_out, and_23_out, and_24_out, and_25_out, and_28_out, BJ,
       Branch, BranchTaken, btb_1_hit, CLK, comparator_1_eq, comparator_8_eq, comparator_9_eq,
       comparator_10_eq, comparator_11_eq, comparator_12_eq, comparator_13_eq, d_ff_1_q, d_ff_2_q, d_ff_3_q,
       equ, EX_ALU_SRC, EX_BEQ, EX_BGEZ, EX_BNE, EX_Bubble, EX_ERET, EX_Hit, EX_JAL, EX_JMP, EX_JR,
       EX_MemToReg, EX_MFC0, EX_MTC0, EX_PredictJmp, EX_RegWrite, EX_SRLV, EX_Valid, GEZ, Go, ID_ALU_SRC,
       ID_B, ID_BEQ, ID_BGEZ, ID_BNE, ID_Bubble, ID_ERET, id_ex_1_ex_b, id_ex_1_ex_memreg,
       id_ex_1_ex_syscall, ID_EX_rs, ID_EX_rt, ID_JAL, ID_JMP, ID_JR, ID_MemToReg, ID_MemWrite, ID_MFC0,
       ID_MTC0, ID_PredictJmp, ID_RegDst, ID_RegWrite, ID_SRLV, ID_Syscall, IE, IE_q, if_id_1_id_hit,
       if_id_1_id_valid, INT_SIG, IR1, IR2, IR3, JImm, JR32, LedOut, LoadUse, MEM_B, MEM_EX_rs, MEM_EX_rt,
       MEM_JAL, MEM_MemToReg, MEM_MemWrite, MEM_RegWrite, MEM_Syscall, multiplexer_13_out,
       multiplexer_15_out, not_1_out, not_2_out, not_3_out, not_4_out, not_6_out, not_7_out, not_8_out,
       or_2_out, or_7_out, or_8_out, or_9_out, or_10_out, or_11_out, or_13_out, or_15_out, or_16_out,
       or_20_out, Pause, PredictErr, PredictJ, priority_encoder_1_en_out, RegWrite, rs____0, rs____EX_W_num,
       rs____MEM_W_num, RST, RsUsed, rt____0, rt____EX_W_num, rt____MEM_W_num, RtUsed, sel1, sel2, sel3,
       sel4, SignedExt, W1, W2, W3, WB_JAL, WB_MemToReg, WB_Syscall;
  wire [1:0] EX_Rs_F, EX_Rt_F, ID_Rs_F, ID_Rt_F, INT, INT_TOP, multiplexer_16_out, multiplexer_17_out,
       multiplexer_20_out, multiplexer_22_out, multiplexer_27_out, register_1_q, register_2_q;
  wire [2:0] and_18_out, and_19_out, decoder_1_out1, INM, INM_q, IR1_q, multiplexer_26_out,
       multiplexer_29_out, multiplexer_31_out, multiplexer_33_out, register_4_q, register_6_q;
  wire [3:0] decoder_2_out0, EX_ALU_OP, ID_ALU_OP;
  wire [4:0] EX_sa, EX_W_num, ID_W_num, MEM_W_num, multiplexer_25_out, R1_num, R2_num, WB_W_num;
  wire [7:0] demultiplexer_1_out0, demultiplexer_1_out1, demultiplexer_1_out2, demultiplexer_1_out3, MDin1,
       MDin2, MDin3, MDin4;
  wire [15:0] \LoadUse次数 , \总周期数 , \插入气泡数 , \无条件分支数 , \条件分支成功数 ;
  wire [25:0] EX_Imm26, ID_Imm26;
  wire [31:0] adder_4_out, BAddr, bit_extender_1_out, bit_extender_2_out, BreakPoint, EX_ExtImm, EX_IR,
       EX_MDin, EX_PC, EX_PC_4, EX_R, EX_R1, id_ex_1_ex_r2, ID_ExtImm, ID_MDin, ID_PC, ID_R1, IF_IR, IF_PC,
       LedData, MDin, MEM_IR, MEM_MDout, MEM_PC, MEM_R, MEM_R1, multiplexer_1_out, multiplexer_2_out,
       multiplexer_4_out, multiplexer_5_out, multiplexer_6_out, multiplexer_7_out, multiplexer_8_out,
       multiplexer_9_out, multiplexer_23_out, multiplexer_24_out, multiplexer_28_out, multiplexer_30_out,
       multiplexer_32_out, PC_4, PredictJmp, RDin, RecoverPC, register_3_q, register_5_q, shifter_1_out,
       WB_IR, WB_MDin, WB_MDout, WB_PC, WB_R, WB_R1;
  wire [31:26] ID_IR;

  Button \u_总复位  (.out(RST));
  Button _1 (.out(IR1));
  Button _2 (.out(IR2));
  Button _3 (.out(IR3));
  Button \u_继续运行  (.out(Go));
  LED #(.active("true")) led_1 (.in(W1));
  LED #(.active("true")) led_2 (.in(W2));
  LED #(.active("true")) led_3 (.in(W3));
  Hex_Digit_Display hex_digit_display_1 (.value(LedData[31:28]));  // open: dp
  Multiplexer #(.select(1), .width(32), .disabled("Z"), .enable("false")) multiplexer_1 (
    .in0(PC_4), .in1({EX_PC[31:28], EX_Imm26, 2'b00}), .out(multiplexer_1_out), .sel(JImm));
  Hex_Digit_Display hex_digit_display_2 (.value(LedData[23:20]));  // open: dp
  Hex_Digit_Display hex_digit_display_3 (.value(LedData[27:24]));  // open: dp
  Multiplexer #(.select(1), .width(32), .disabled("Z"), .enable("false")) multiplexer_2 (
    .in0(multiplexer_1_out), .in1(EX_R1), .out(multiplexer_2_out), .sel(JR32));
  Hex_Digit_Display hex_digit_display_4 (.value(LedData[19:16]));  // open: dp
  Hex_Digit_Display hex_digit_display_5 (.value(LedData[15:12]));  // open: dp
  Multiplexer #(.select(1), .width(32), .disabled("Z"), .enable("false")) multiplexer_3 (
    .in0(EX_PC_4), .in1(multiplexer_4_out), .out(RecoverPC), .sel(BranchTaken));
  Multiplexer #(.select(1), .width(32), .disabled("Z"), .enable("false")) multiplexer_4 (
    .in0(multiplexer_2_out), .in1(BAddr), .out(multiplexer_4_out), .sel(BJ));
  and and_1 (and_1_out, ~Pause, ~LoadUse);  // AND_Gate
  Hex_Digit_Display hex_digit_display_6 (.value(LedData[11:8]));  // open: dp
  Hex_Digit_Display hex_digit_display_7 (.value(LedData[7:4]));  // open: dp
  Clock #(.highDuration(1), .lowDuration(1)) clock_1 (.out(CLK));
  Multiplexer #(.select(1), .width(32), .disabled("Z"), .enable("false")) multiplexer_5 (
    .in0(PC_4), .in1(PredictJmp), .out(multiplexer_5_out), .sel(PredictJ));
  Multiplexer #(.select(1), .width(32), .disabled("Z"), .enable("false")) multiplexer_6 (
    .in0(multiplexer_5_out), .in1(RecoverPC), .out(multiplexer_6_out), .sel(PredictErr));
  Multiplexer #(.select(2), .width(32), .disabled("Z"), .enable("false")) multiplexer_7 (
    .in1(32'h30ac), .in2(32'h3158), .in3(32'h3204), .out(multiplexer_7_out), .sel(INT));  // open: in0
  Register #(.width(32), .trigger("rising"), .Select("low")) PC (
    .D(multiplexer_9_out), .en(and_1_out), .Q(IF_PC), .clk(CLK), .clr(RST));
  Hex_Digit_Display hex_digit_display_8 (.value(LedData[3:0]));  // open: dp
  Multiplexer #(.select(1), .width(32), .disabled("Z"), .enable("false")) multiplexer_8 (
    .in0(multiplexer_6_out), .in1(multiplexer_7_out), .out(multiplexer_8_out), .sel(INT_SIG));
  // Probe on \总周期数 
  Multiplexer #(.select(1), .width(32), .disabled("Z"), .enable("false")) multiplexer_9 (
    .in0(multiplexer_8_out), .in1(BreakPoint), .out(multiplexer_9_out), .sel(EX_ERET));
  ROM #(.addrWidth(10), .dataWidth(32), .Select("high")) rom_1 (.addr(IF_PC[11:2]), .data(IF_IR));
  Adder #(.width(32)) adder_1 (.a(IF_PC), .b(32'h4), .out(PC_4));  // open: cin, cout
  // Probe on \总周期数 
  // Probe on \无条件分支数 
  // Probe on \条件分支成功数 
  // Probe on \插入气泡数 
  // Probe on \LoadUse次数 
  Comparator #(.width(32), .mode("twosComplement")) comparator_1 (
    .a({32{1'b0}}), .b(IF_IR), .eq(comparator_1_eq));  // open: gt, lt
  not not_1 (not_1_out, comparator_1_eq);
  and and_2 (and_2_out, ~Pause, ~LoadUse);  // AND_Gate
  // Probe on \总周期数 
  BTB btb_1 (
    .BTin(multiplexer_4_out), .BranchPC(EX_PC), .CLK(CLK), .J(BranchTaken), .BTout(PredictJmp),
    .PredictJmp(PredictJ), .CurrentPC(IF_PC), .Branch(Branch), .Hit(btb_1_hit));
  // Probe on \总周期数 
  Rs_Rt rs_rt_1 (
    .OP0(ID_IR[26]), .OP1(ID_IR[27]), .OP2(ID_IR[28]), .OP3(ID_IR[29]), .OP4(ID_IR[30]), .OP5(ID_IR[31]),
    .F0(ID_Imm26[0]), .F1(ID_Imm26[1]), .F2(ID_Imm26[2]), .F3(ID_Imm26[3]), .F4(ID_Imm26[4]),
    .F5(ID_Imm26[5]), .RsUsed(RsUsed), .RtUsed(RtUsed));
  // Probe on IF_PC[19:0]
  // Mips_Probe mips_probe_1: pin names not known; wires that end beside it: IF_IR
  or or_1 (ID_Bubble, PredictErr, EX_ERET, INT_SIG);
  IF_ID if_id_1 (
    .IF_PC(IF_PC), .IF_IR(IF_IR), .CLK(CLK), .ID_PC(ID_PC), .ID_IR({ID_IR, ID_Imm26}), .RST(RST),
    .RUN(and_2_out), .Bubble(ID_Bubble), .IF_Predict(PredictJ), .ID_Predict(ID_PredictJmp),
    .IF_Valid(not_1_out), .ID_Valid(if_id_1_id_valid), .IF_Hit(btb_1_hit), .ID_Hit(if_id_1_id_hit));
  Comparator #(.width(5), .mode("unsigned")) comparator_2 (.a(R1_num), .b({5{1'b0}}), .eq(rs____0));  // open: gt, lt
  Comparator #(.width(5), .mode("unsigned")) comparator_3 (
    .a(R1_num), .b(EX_W_num), .eq(rs____EX_W_num));  // open: gt, lt
  Comparator #(.width(5), .mode("unsigned")) comparator_4 (
    .a(EX_W_num), .b(R2_num), .eq(rt____EX_W_num));  // open: gt, lt
  Comparator #(.width(5), .mode("unsigned")) comparator_5 (.a({5{1'b0}}), .b(R2_num), .eq(rt____0));  // open: gt, lt
  Comparator #(.width(5), .mode("unsigned")) comparator_6 (
    .a(R2_num), .b(MEM_W_num), .eq(rt____MEM_W_num));  // open: gt, lt
  Comparator #(.width(5), .mode("unsigned")) comparator_7 (
    .a(MEM_W_num), .b(R1_num), .eq(rs____MEM_W_num));  // open: gt, lt
  // Probe on ID_PC[19:0]
  // Mips_Probe mips_probe_2: pin names not known; wires that end beside it: {ID_IR, ID_Imm26}
  or or_2 (or_2_out, JImm, JR32);
  \单周期硬布线控制器  \u_单周期硬布线控制器_1  (
    .Func(ID_Imm26[5:0]), .OP(ID_IR), .ALU_OP(ID_ALU_OP), .MemToReg(ID_MemToReg), .MemWrite(ID_MemWrite),
    .ALU_SRC(ID_ALU_SRC), .RegWrite(ID_RegWrite), .SysCALL(ID_Syscall), .SignedExt(SignedExt),
    .RegDst(ID_RegDst), .JR(ID_JR), .JMP(ID_JMP), .Beq(ID_BEQ), .JAL(ID_JAL), .Bne(ID_BNE), .ERET(ID_ERET),
    .B(ID_B), .BGEZ(ID_BGEZ), .SRLV(ID_SRLV));
  Counter #(.width(16), .max('hffff), .ongoal("wrap"), .trigger("rising"), .behavior("old")) counter_1 (
    .count(or_2_out), .Q(\无条件分支数 ), .clk(CLK), .clr(RST));  // open: load, D, carry, preset
  Counter #(.width(16), .max('hffff), .ongoal("wrap"), .trigger("rising"), .behavior("old")) counter_2 (
    .count(BJ), .Q(\条件分支成功数 ), .clk(CLK), .clr(RST));  // open: load, D, carry, preset
  Comparator #(.width(6), .mode("unsigned")) comparator_8 (
    .a(6'b010000), .b(ID_IR), .eq(comparator_8_eq));  // open: gt, lt
  and and_3 (ID_MTC0, comparator_8_eq, comparator_9_eq);
  Comparator #(.width(5), .mode("unsigned")) comparator_9 (
    .a(ID_Imm26[25:21]), .b(5'b00100), .eq(comparator_9_eq));  // open: gt, lt
  and and_4 (ID_MFC0, comparator_8_eq, comparator_10_eq);
  Comparator #(.width(5), .mode("unsigned")) comparator_10 (
    .a(ID_Imm26[25:21]), .b({5{1'b0}}), .eq(comparator_10_eq));  // open: gt, lt
  and and_5 (and_5_out, ~rs____0, RsUsed, rs____EX_W_num);  // AND_Gate
  and and_6 (and_6_out, rt____EX_W_num, RtUsed, ~rt____0);  // AND_Gate
  and and_7 (and_7_out, ~rs____0, RsUsed, rs____MEM_W_num);  // AND_Gate
  and and_8 (and_8_out, rt____MEM_W_num, RtUsed, ~rt____0);  // AND_Gate
  // Probe on EX_PC[19:0]
  // Mips_Probe mips_probe_3: pin names not known; wires that end beside it: EX_IR
  Multiplexer #(.select(2), .width(5), .disabled("Z"), .enable("false")) multiplexer_10 (
    .in0(ID_Imm26[20:16]), .in1(ID_Imm26[15:11]), .in2({5{1'b1}}), .in3({5{1'b1}}), .out(ID_W_num),
    .sel({ID_JAL, ID_RegDst}));
  or or_3 (W1, IR1_q[0], d_ff_1_q);
  or or_4 (W2, IR1_q[1], d_ff_2_q);
  or or_5 (W3, IR1_q[2], d_ff_3_q);
  // Mips_Probe mips_probe_4: pin names not known; wires that end beside it: MEM_IR
  Multiplexer #(.select(1), .width(5), .disabled("Z"), .enable("false")) multiplexer_11 (
    .in0(ID_Imm26[25:21]), .in1(5'b00010), .out(R1_num), .sel(ID_Syscall));
  Multiplexer #(.select(1), .width(5), .disabled("Z"), .enable("false")) multiplexer_12 (
    .in0(ID_Imm26[20:16]), .in1(5'b00100), .out(R2_num), .sel(ID_Syscall));
  and and_9 (and_9_out, and_5_out, EX_MemToReg);
  and and_10 (and_10_out, EX_MemToReg, and_6_out);
  and and_11 (ID_EX_rt, and_6_out, EX_RegWrite);
  and and_12 (ID_EX_rs, EX_RegWrite, and_5_out);
  and and_13 (MEM_EX_rs, and_7_out, MEM_RegWrite);
  and and_14 (MEM_EX_rt, MEM_RegWrite, and_8_out);
  D_Flip_Flop #(.trigger("rising"), .Pre_Clr_Positions("LEGACY"), .NegatePresetClear("false"), .enable("true"), .NewFFLayout("false")) d_ff_1 (
    .clk(IR1), .D(1'b1), .Q(d_ff_1_q), .reset(IR1_q[0]));  // open: Qn, preset, en
  D_Flip_Flop #(.trigger("rising"), .Pre_Clr_Positions("LEGACY"), .NegatePresetClear("false"), .enable("true"), .NewFFLayout("false")) d_ff_2 (
    .clk(IR2), .D(1'b1), .Q(d_ff_2_q), .reset(IR1_q[1]));  // open: Qn, preset, en
  D_Flip_Flop #(.trigger("rising"), .Pre_Clr_Positions("LEGACY"), .NegatePresetClear("false"), .enable("true"), .NewFFLayout("false")) d_ff_3 (
    .clk(IR3), .D(1'b1), .Q(d_ff_3_q), .reset(IR1_q[2]));  // open: Qn, preset, en
  // Probe on MEM_PC[19:0]
  Comparator #(.width(32), .mode("unsigned")) comparator_11 (
    .a({32{1'b0}}), .b(WB_IR), .eq(comparator_11_eq));  // open: gt, lt
  Counter #(.width(16), .max('hffff), .ongoal("wrap"), .trigger("rising"), .behavior("old")) counter_3 (
    .count(LoadUse), .Q(\LoadUse次数 ), .clk(CLK), .clr(RST));  // open: load, D, carry, preset
  not not_2 (not_2_out, CLK);
  assign bit_extender_1_out = {{16{1'b0}}, ID_Imm26[15:0]};  // Bit_Extender bit_extender_1
  assign bit_extender_2_out = {{16{ID_Imm26[15]}}, ID_Imm26[15:0]};  // Bit_Extender bit_extender_2
  or or_6 (LoadUse, and_9_out, and_10_out);
  or or_7 (or_7_out, EX_MTC0, INT_SIG);
  Multiplexer #(.select(1), .width(1), .disabled("Z"), .enable("false")) multiplexer_13 (
    .in0(IE_q), .in1(1'b1), .out(multiplexer_13_out), .sel(or_7_out));
  or or_8 (or_8_out, d_ff_1_q, IR1_q[0]);
  or or_9 (or_9_out, d_ff_2_q, IR1_q[1]);
  or or_10 (or_10_out, d_ff_3_q, IR1_q[2]);
  // Probe on WB_PC[19:0]
  // Mips_Probe mips_probe_5: pin names not known; wires that end beside it: WB_IR
  Counter #(.width(16), .max('hffff), .ongoal("wrap"), .trigger("rising"), .behavior("old")) counter_4 (
    .count(comparator_11_eq), .Q(\插入气泡数 ), .clk(CLK), .clr(RST));  // open: load, D, carry, preset
  MIPS_Regifile mips_regifile_1 (
    .Din(RDin), .Clk(not_2_out), .R1(ID_R1), .R2(ID_MDin), .WE(RegWrite), .W_num(WB_W_num), .R1_num(R1_num),
    .R2_num(R2_num));
  Multiplexer #(.select(1), .width(32), .disabled("Z"), .enable("false")) multiplexer_14 (
    .in0(bit_extender_1_out), .in1(bit_extender_2_out), .out(ID_ExtImm), .sel(SignedExt));
  Multiplexer #(.select(1), .width(1), .disabled("Z"), .enable("false")) multiplexer_15 (
    .in0(multiplexer_13_out), .in1(1'b0), .out(multiplexer_15_out), .sel(EX_MFC0));
  and and_15 (and_15_out, or_8_out, ~and_19_out[0]);  // AND_Gate
  and and_16 (and_16_out, or_9_out, ~and_19_out[1]);  // AND_Gate
  and and_17 (and_17_out, or_10_out, ~and_19_out[2]);  // AND_Gate
  not not_3 (not_3_out, Pause);
  Multiplexer #(.select(1), .width(2), .disabled("Z"), .enable("false")) multiplexer_16 (
    .in0(2'b00), .in1(2'b01), .out(multiplexer_16_out), .sel(MEM_EX_rs));
  Multiplexer #(.select(1), .width(2), .disabled("Z"), .enable("false")) multiplexer_17 (
    .in0(2'b00), .in1(2'b01), .out(multiplexer_17_out), .sel(MEM_EX_rt));
  D_Flip_Flop #(.trigger("rising"), .Pre_Clr_Positions("ABOVE_BELOW"), .NegatePresetClear("false"), .enable("false"), .NewFFLayout("false")) u_IE (
    .clk(CLK), .D(multiplexer_15_out), .Q(IE_q), .Qn(IE), .reset(or_11_out));  // open: preset
  or or_11 (or_11_out, RST, EX_ERET);
  D_Flip_Flop #(.trigger("rising"), .Pre_Clr_Positions("LEGACY"), .NegatePresetClear("false"), .enable("true"), .NewFFLayout("false")) u_IR1 (
    .clk(CLK), .D(and_15_out), .Q(IR1_q[0]), .reset(RST));  // open: Qn, preset, en
  assign and_18_out = IR1_q & INM;  // AND_Gate and_18, 3 bits wide
  D_Flip_Flop #(.trigger("rising"), .Pre_Clr_Positions("LEGACY"), .NegatePresetClear("false"), .enable("true"), .NewFFLayout("false")) u_IR2 (
    .clk(CLK), .D(and_16_out), .Q(IR1_q[1]), .reset(RST));  // open: Qn, preset, en
  D_Flip_Flop #(.trigger("rising"), .Pre_Clr_Positions("LEGACY"), .NegatePresetClear("false"), .enable("true"), .NewFFLayout("false")) u_IR3 (
    .clk(CLK), .D(and_17_out), .Q(IR1_q[2]), .reset(RST));  // open: Qn, preset, en
  assign and_19_out = decoder_1_out1 & {3{EX_ERET}};  // AND_Gate and_19, 3 bits wide
  or or_12 (EX_Bubble, INT_SIG, LoadUse, PredictErr, EX_ERET);
  ID_EX id_ex_1 (
    .CLK(CLK), .ID_PC(ID_PC), .ID_IR({ID_IR, ID_Imm26}), .RST(RST), .EX_PC(EX_PC), .EX_IR(EX_IR),
    .ID_R1(ID_R1), .ID_R2(ID_MDin), .EX_R1(EX_R1), .EX_R2(id_ex_1_ex_r2), .ID_ExtImm(ID_ExtImm),
    .ID_W_num(ID_W_num), .EX_ExtImm(EX_ExtImm), .EX_W_num(EX_W_num), .ID_B(ID_B), .ID_ERET(ID_ERET),
    .ID_SRLV(ID_SRLV), .ID_JMP(ID_JMP), .ID_JR(ID_JR), .ID_BEQ(ID_BEQ), .ID_BNE(ID_BNE), .ID_BGEZ(ID_BGEZ),
    .ID_JAL(ID_JAL), .ID_MemToReg(ID_MemToReg), .ID_MemWrite(ID_MemWrite), .ID_ALU_SRC(ID_ALU_SRC),
    .ID_RegWrite(ID_RegWrite), .ID_Syscall(ID_Syscall), .ID_AlU_OP(ID_ALU_OP), .EX_B(id_ex_1_ex_b),
    .EX_ERET(EX_ERET), .EX_SRLV(EX_SRLV), .EX_JMP(EX_JMP), .EX_JR(EX_JR), .EX_BEQ(EX_BEQ), .EX_BNE(EX_BNE),
    .EX_BGEZ(EX_BGEZ), .EX_JAL(EX_JAL), .EX_MemToReg(EX_MemToReg), .EX_MemReg(id_ex_1_ex_memreg),
    .EX_ALU_SRC(EX_ALU_SRC), .EX_RegWrite(EX_RegWrite), .EX_Syscall(id_ex_1_ex_syscall),
    .EX_ALU_OP(EX_ALU_OP), .ID_sa(ID_Imm26[10:6]), .EX_sa(EX_sa), .RUN(not_3_out), .Bubble(EX_Bubble),
    .ID_Imm26(ID_Imm26), .EX_Imm26(EX_Imm26), .ID_rs_f(ID_Rs_F), .EX_rs_f(EX_Rs_F), .ID_rt_f(ID_Rt_F),
    .EX_rt_f(EX_Rt_F), .ID_Predict(ID_PredictJmp), .EX_Predict(EX_PredictJmp), .EX_MFC0(EX_MFC0),
    .ID_MFC0(ID_MFC0), .ID_MTC0(ID_MTC0), .EX_MTC0(EX_MTC0), .ID_Valid(if_id_1_id_valid),
    .EX_Valid(EX_Valid), .EX_Hit(EX_Hit), .in_34(if_id_1_id_hit));
  Multiplexer #(.select(1), .width(2), .disabled("Z"), .enable("false")) multiplexer_18 (
    .in0(multiplexer_16_out), .in1(2'b10), .out(ID_Rs_F), .sel(ID_EX_rs));
  Multiplexer #(.select(1), .width(2), .disabled("Z"), .enable("false")) multiplexer_19 (
    .in0(multiplexer_17_out), .in1(2'b10), .out(ID_Rt_F), .sel(ID_EX_rt));
  and and_20 (INT_SIG, IE, EX_Valid, ~priority_encoder_1_en_out);  // AND_Gate
  Priority_Encoder #(.select(2), .disabled("Z")) priority_encoder_1 (
    .in1(and_18_out[0]), .in2(and_18_out[1]), .in3(and_18_out[2]), .out(INT),
    .en_out(priority_encoder_1_en_out));  // open: in0, gs, en_in
  Decoder #(.select(2), .tristate("false"), .disabled("Z"), .enable("false")) decoder_1 (
    .out1(decoder_1_out1[0]), .out2(decoder_1_out1[1]), .out3(decoder_1_out1[2]), .sel(INT_TOP));  // open: out0
  or or_13 (or_13_out, INT_SIG, EX_ERET);
  Multiplexer #(.select(1), .width(2), .disabled("Z"), .enable("false")) multiplexer_20 (
    .in0(INT), .in1(register_1_q), .out(multiplexer_20_out), .sel(EX_ERET));
  Register #(.width(2), .trigger("rising"), .Select("low")) u_INT (
    .D(multiplexer_20_out), .en(or_13_out), .Q(INT_TOP), .clk(CLK), .clr(RST));
  Multiplexer #(.select(2), .width(32), .disabled("Z"), .enable("false")) multiplexer_21 (
    .in0(id_ex_1_ex_r2), .in1(RDin), .in2(MEM_R), .out(EX_MDin), .sel(EX_Rt_F));  // open: in3
  Multiplexer #(.select(1), .width(2), .disabled("Z"), .enable("false")) multiplexer_22 (
    .in0(INT_TOP), .in1(register_2_q), .out(multiplexer_22_out), .sel(EX_ERET));
  Shifter #(.width(32), .shift("ll")) shifter_1 (.in(EX_ExtImm), .\dist (5'b00010), .out(shifter_1_out));
  Adder #(.width(32)) adder_2 (.a(32'h4), .b(EX_PC), .out(EX_PC_4));  // open: cin, cout
  Register #(.width(2), .trigger("rising"), .Select("low")) register_1 (
    .D(multiplexer_22_out), .en(or_13_out), .Q(register_1_q), .clk(CLK), .clr(RST));
  or or_14 (Branch, EX_BEQ, EX_BGEZ, EX_BNE, EX_JMP, EX_JAL, EX_JR);
  Multiplexer #(.select(2), .width(32), .disabled("Z"), .enable("false")) multiplexer_23 (
    .in0(EX_R1), .in1(RDin), .in2(MEM_R), .out(multiplexer_23_out), .sel(EX_Rs_F));  // open: in3
  Multiplexer #(.select(1), .width(32), .disabled("Z"), .enable("false")) multiplexer_24 (
    .in0(EX_MDin), .in1(EX_ExtImm), .out(multiplexer_24_out), .sel(EX_ALU_SRC));
  Multiplexer #(.select(1), .width(5), .disabled("Z"), .enable("false")) multiplexer_25 (
    .in0(EX_sa), .in1(multiplexer_23_out[4:0]), .out(multiplexer_25_out), .sel(EX_SRLV));
  Adder #(.width(32)) adder_3 (.a(shifter_1_out), .b(EX_PC_4), .out(BAddr));  // open: cin, cout
  Multiplexer #(.select(2), .width(3), .disabled("Z"), .enable("false")) multiplexer_26 (
    .in0(3'b000), .in1(3'b001), .in2(3'b011), .in3(3'b111), .out(multiplexer_26_out), .sel(INT));
  Multiplexer #(.select(1), .width(2), .disabled("Z"), .enable("false")) multiplexer_27 (
    .in0(register_1_q), .in1(2'b00), .out(multiplexer_27_out), .sel(EX_ERET));
  Register #(.width(2), .trigger("rising"), .Select("low")) register_2 (
    .D(multiplexer_27_out), .en(or_13_out), .Q(register_2_q), .clk(CLK), .clr(RST));
  and and_21 (and_21_out, equ, EX_BEQ);
  and and_22 (and_22_out, GEZ, EX_BGEZ);
  and and_23 (and_23_out, ~equ, EX_BNE);  // AND_Gate
  and and_24 (and_24_out, ~EX_JAL, ~EX_JR, EX_JMP);  // AND_Gate
  and and_25 (and_25_out, EX_JMP, EX_JAL);
  and and_26 (JR32, EX_JMP, EX_JR);
  MIPS_ALU mips_alu_1 (
    .X(multiplexer_23_out), .Y(multiplexer_24_out), .AluOP(EX_ALU_OP), .Equal(equ), .Result(EX_R),
    .shamt(multiplexer_25_out), .GEZ(GEZ));  // open: Result_2
  Multiplexer #(.select(1), .width(32), .disabled("Z"), .enable("false")) multiplexer_28 (
    .in0(RecoverPC), .in1(register_3_q), .out(multiplexer_28_out), .sel(EX_ERET));
  or or_15 (or_15_out, INT_SIG, EX_ERET);
  Multiplexer #(.select(1), .width(3), .disabled("Z"), .enable("false")) multiplexer_29 (
    .in0(multiplexer_26_out), .in1(register_4_q), .out(multiplexer_29_out), .sel(EX_ERET));
  or or_16 (or_16_out, INT_SIG, EX_ERET);
  or or_17 (BJ, and_21_out, and_22_out, and_23_out);
  or or_18 (JImm, and_24_out, and_25_out);
  not not_4 (not_4_out, Pause);
  EX_MEM ex_mem_1 (
    .CLK(CLK), .EX_PC(EX_PC), .EX_IR(EX_IR), .RST(RST), .EX_R(EX_R), .EX_MDin(EX_MDin), .EX_W_num(EX_W_num),
    .MEM_PC(MEM_PC), .MEM_IR(MEM_IR), .MEM_R(MEM_R), .MEM_MDin(MDin), .MEM_W_num(MEM_W_num),
    .EX_B(id_ex_1_ex_b), .EX_JAL(EX_JAL), .EX_MemToReg(EX_MemToReg), .EX_MemWrite(id_ex_1_ex_memreg),
    .EX_RegWrite(EX_RegWrite), .EX_Syscall(id_ex_1_ex_syscall), .MEM_B(MEM_B), .MEM_JAL(MEM_JAL),
    .MEM_MemToReg(MEM_MemToReg), .MEM_MemWrite(MEM_MemWrite), .MEM_RegWrite(MEM_RegWrite),
    .MEM_Syscall(MEM_Syscall), .RUN(not_4_out), .MEM_R1(MEM_R1), .EX_R1(multiplexer_23_out));
  Register #(.width(32), .trigger("rising"), .Select("low")) EPC_Top (
    .D(multiplexer_28_out), .en(or_15_out), .Q(BreakPoint), .clk(CLK), .clr(RST));
  assign INM = ~INM_q;  // NOT_Gate not_5, 3 bits wide
  Register #(.width(3), .trigger("rising"), .Select("low")) u_INM (
    .D(multiplexer_29_out), .en(or_16_out), .Q(INM_q), .clk(CLK), .clr(RST));
  Register #(.width(32), .trigger("rising"), .Select("low")) register_3 (
    .D(multiplexer_30_out), .en(or_15_out), .Q(register_3_q), .clk(CLK), .clr(RST));
  Multiplexer #(.select(1), .width(32), .disabled("Z"), .enable("false")) multiplexer_30 (
    .in0(BreakPoint), .in1(register_5_q), .out(multiplexer_30_out), .sel(EX_ERET));
  Multiplexer #(.select(1), .width(3), .disabled("Z"), .enable("false")) multiplexer_31 (
    .in0(INM_q), .in1(register_6_q), .out(multiplexer_31_out), .sel(EX_ERET));
  Register #(.width(3), .trigger("rising"), .Select("low")) register_4 (
    .D(multiplexer_31_out), .en(or_16_out), .Q(register_4_q), .clk(CLK), .clr(RST));
  or or_19 (BranchTaken, BJ, JImm, JR32);
  xor xor_1 (PredictErr, EX_PredictJmp, BranchTaken);
  Decoder #(.select(2), .tristate("false"), .disabled("Z"), .enable("false")) decoder_2 (
    .out0(decoder_2_out0[0]), .out1(decoder_2_out0[1]), .out2(decoder_2_out0[2]), .out3(decoder_2_out0[3]),
    .sel(MEM_R[1:0]));
  Demultiplexer #(.select(2), .width(8), .tristate("false"), .disabled("Z"), .enable("false")) demultiplexer_1 (
    .out0(demultiplexer_1_out0), .out1(demultiplexer_1_out1), .out2(demultiplexer_1_out2),
    .out3(demultiplexer_1_out3), .in(MDin[7:0]), .sel(MEM_R[1:0]));
  Multiplexer #(.select(1), .width(32), .disabled("Z"), .enable("false")) multiplexer_32 (
    .in0(register_3_q), .in1({32{1'b0}}), .out(multiplexer_32_out), .sel(EX_ERET));
  Multiplexer #(.select(1), .width(3), .disabled("Z"), .enable("false")) multiplexer_33 (
    .in0(register_4_q), .in1(3'b000), .out(multiplexer_33_out), .sel(EX_ERET));
  assign {sel4, sel3, sel2, sel1} = MEM_B ? decoder_2_out0 : 4'bz;  // Controlled_Buffer controlled_buffer_1
  assign {MDin4, MDin3, MDin2, MDin1} = MEM_B ? {demultiplexer_1_out3, demultiplexer_1_out2, demultiplexer_1_out1, demultiplexer_1_out0} : 32'bz;  // Controlled_Buffer controlled_buffer_2
  Register #(.width(32), .trigger("rising"), .Select("low")) register_5 (
    .D(multiplexer_32_out), .en(or_15_out), .Q(register_5_q), .clk(CLK), .clr(RST));
  Register #(.width(3), .trigger("rising"), .Select("low")) register_6 (
    .D(multiplexer_33_out), .en(or_16_out), .Q(register_6_q), .clk(CLK), .clr(RST));
  assign {sel4, sel3, sel2, sel1} = ~MEM_B ? 4'b1111 : 4'bz;  // Controlled_Buffer controlled_buffer_3
  assign {MDin4, MDin3, MDin2, MDin1} = ~MEM_B ? MDin : 32'bz;  // Controlled_Buffer controlled_buffer_4
  Comparator #(.width(32), .mode("unsigned")) comparator_12 (
    .a(32'h22), .b(WB_R1), .eq(comparator_12_eq));  // open: gt, lt
  Comparator #(.width(32), .mode("unsigned")) comparator_13 (
    .a(WB_R1), .b(32'h32), .eq(comparator_13_eq));  // open: gt, lt
  and and_27 (LedOut, WB_Syscall, comparator_12_eq);
  and and_28 (and_28_out, WB_Syscall, comparator_13_eq);
  D_Flip_Flop #(.trigger("falling"), .Pre_Clr_Positions("ABOVE_BELOW"), .NegatePresetClear("false"), .enable("false"), .NewFFLayout("false")) d_ff_4 (
    .clk(or_20_out), .D(not_6_out), .Q(Pause));  // open: Qn, preset, reset
  or or_20 (or_20_out, Go, and_28_out);
  not not_6 (not_6_out, Pause);
  Register #(.width(32), .trigger("rising"), .Select("low")) register_7 (
    .D(WB_MDin), .en(LedOut), .Q(LedData), .clk(CLK), .clr(RST));
  not not_7 (not_7_out, Pause);
  Counter #(.width(16), .max('hffff), .ongoal("wrap"), .trigger("rising"), .behavior("new")) counter_5 (
    .count(not_7_out), .Q(\总周期数 ), .clk(CLK), .clr(RST));  // open: load, D, carry, preset, down
  RAM #(.addrWidth(10), .dataWidth(8), .bus("separate"), .Select("high")) ram_1 (
    .addr(MEM_R[11:2]), .din(MDin1), .data(MEM_MDout[7:0]), .str(MEM_MemWrite), .sel(sel1), .clk(CLK),
    .clr(RST));  // open: ld
  RAM #(.addrWidth(10), .dataWidth(8), .bus("separate"), .Select("high")) ram_2 (
    .addr(MEM_R[11:2]), .din(MDin2), .data(MEM_MDout[15:8]), .str(MEM_MemWrite), .sel(sel2), .clk(CLK),
    .clr(RST));  // open: ld
  RAM #(.addrWidth(10), .dataWidth(8), .bus("separate"), .Select("high")) ram_3 (
    .addr(MEM_R[11:2]), .din(MDin3), .data(MEM_MDout[23:16]), .str(MEM_MemWrite), .sel(sel3), .clk(CLK),
    .clr(RST));  // open: ld
  RAM #(.addrWidth(10), .dataWidth(8), .bus("separate"), .Select("high")) ram_4 (
    .addr(MEM_R[11:2]), .din(MDin4), .data(MEM_MDout[31:24]), .str(MEM_MemWrite), .sel(sel4), .clk(CLK),
    .clr(RST));  // open: ld
  not not_8 (not_8_out, Pause);
  MEM_WB mem_wb_1 (
    .WB_PC(WB_PC), .WB_IR(WB_IR), .WB_MDout(WB_MDout), .CLK(CLK), .RST(RST), .WB_R(WB_R), .MEM_PC(MEM_PC),
    .MEM_IR(MEM_IR), .MEM_MDout(MEM_MDout), .MEM_R(MEM_R), .MEM_W_num(MEM_W_num), .WB_W_num(WB_W_num),
    .MEM_JAL(MEM_JAL), .MEM_MemToReg(MEM_MemToReg), .MEM_RegWrite(MEM_RegWrite), .WB_JAL(WB_JAL),
    .WB_MemToReg(WB_MemToReg), .WB_RegWrite(RegWrite), .RUN(not_8_out), .MEM_Syscall(MEM_Syscall),
    .WB_Syscall(WB_Syscall), .MEM_R1(MEM_R1), .WB_R1(WB_R1), .MEM_MDin(MDin), .WB_MDin(WB_MDin));
  Adder #(.width(32)) adder_4 (.a(32'h4), .b(WB_PC), .out(adder_4_out));  // open: cin, cout
  Multiplexer #(.select(2), .width(32), .disabled("Z"), .enable("false")) multiplexer_34 (
    .in0(WB_R), .in1(adder_4_out), .in2(WB_MDout), .out(RDin), .sel({WB_MemToReg, WB_JAL}));  // open: in3

  // Other names for the same wires on the sheet: IAddr[31:2] = {EX_PC[31:28], EX_Imm26}; ID_IR[25:0] = ID_Imm26;
  //   Imm16[15:0] = ID_Imm26[15:0]; Imm26[25:0] = ID_Imm26; ID_sa[4:0] = ID_Imm26[10:6]; rd[4:0] = ID_Imm26[15:11];
  //   rt[4:0] = ID_Imm26[20:16]; rs[4:0] = ID_Imm26[25:21]; OP[5:0] = ID_IR; MEM_MDin[31:0] = MDin;
  //   MemAddr[9:0] = MEM_R[11:2]; MemWrite = MEM_MemWrite; PC[31:0] = IF_PC; RAddr[31:0] = EX_R1;
  //   WB_RDin[31:0] = RDin; WB_RegWrite = RegWrite

  // Notes on the sheet:
  //   中断源
  //   中断等待指示
  //   数码管输出
  //   指令存储器
  //   contents of rom_1 (hex, n*v repeats v):
  //   20110001 8000005 20110001 20120002 20130003 8000009 20110001 20120002 20130003 800000d 20110001
  //   20120002 20130003 8000011 20110001 20120002 20130003 c0000f6 20100001 20110001 118fc0 112020
  //   20020022 c 118882 12200001 8000015 112020 20020022 c 20110001 118880 112020 20020022 c 12200001
  //   800001f 20110001 118fc0 112020 20020022 c 1188c3 112020 20020022 c 118903 112020 20020022 c 118903
  //   112020 20020022 c 118903 112020 20020022 c 118903 112020 20020022 c 118903 112020 20020022 c 118903
  //   112020 20020022 c 118903 112020 20020022 c 20100001 109fc0 139fc3 8021 2012000c 24160003 26100001
  //   3210000f 20080008 20090001 139900 2709825 132020 20020022 c 1094022 1500fff9 22100001 2018000f
  //   2188024 108700 20080008 20090001 139902 2709825 132021 20020022 c 1094022 1500fff9 108702 2c9b022
  //   12c00001 8000050 4020 1084027 84400 3508ffff 82021 20020022 c 2010ffff 20110000 ae300000 22100001
  //   22310004 ae300000 22100001 22310004 ae300000 22100001 22310004 ae300000 22100001 22310004 ae300000
  //   22100001 22310004 ae300000 22100001 22310004 ae300000 22100001 22310004 ae300000 22100001 22310004
  //   ae300000 22100001 22310004 ae300000 22100001 22310004 ae300000 22100001 22310004 ae300000 22100001
  //   22310004 ae300000 22100001 22310004 ae300000 22100001 22310004 ae300000 22100001 22310004 ae300000
  //   22100001 22310004 22100001 8020 2011003c 8e130000 8e340000 274402a 11000002 ae330000 ae140000
  //   2231fffc 1611fff8 102020 20020022 c 22100004 2011003c 1611fff2 20020032 c 20080001 20090003 20110876
  //   118d00 112020 20020022 c 200b0008 1118806 1318806 112020 20020022 c 216bffff 1560fff9 20020032 c
  //   2008ffff 20117777 112020 20020022 c 200b0010 2288826 112020 20020022 c 216bffff 1560fffa 20020032 c
  //   20090000 200b0020 20110000 20120001 a1310000 112020 20020022 c 2328820 21290001 216bffff 1560fff8
  //   200b0008 20090000 8d310000 112020 20020022 c 21290004 216bffff 1560fff9 20020032 c 2011000f 112020
  //   20020022 c 2231ffff 621fffb 20020032 c 20100000 22100001 102020 20020022 c 22100002 102020 20020022
  //   c 22100003 102020 20020022 c 22100004 102020 20020022 c 22100005 102020 20020022 c 22100006 102020
  //   20020022 c 22100007 102020 20020022 c 22100008 102020 20020022 20020022 c 3e00008
  //   OP
  //   Func
  //   rs
  //   rt
  //   rd
  //   sa
  //   Imm16
  //   Imm26
  //   v0
  //   t0
  //   ra
  //   Reset 
  //   使用ERET指令来反向MUX
endmodule
module \中断按键参考电路  (
  input  \同步清零信号 ,
  output \与中断屏蔽位与 
);

  wire \_1号中断_out , and_1_out, clock_1_out, d_ff_1_q, or_1_out, or_2_out;

  Clock #(.highDuration(1), .lowDuration(1)) clock_1 (.out(clock_1_out));
  Button \_1号中断  (.out(\_1号中断_out ));
  or or_1 (or_1_out, \与中断屏蔽位与 , d_ff_1_q);
  LED #(.active("true")) \_1号中断等待指示灯  (.in(or_1_out));
  D_Flip_Flop #(.trigger("rising"), .Pre_Clr_Positions("LEGACY"), .NegatePresetClear("false"), .enable("true"), .NewFFLayout("false")) d_ff_1 (
    .clk(\_1号中断_out ), .D(1'b1), .Q(d_ff_1_q), .reset(\与中断屏蔽位与 ));  // open: Qn, preset, en
  or or_2 (or_2_out, d_ff_1_q, \与中断屏蔽位与 );
  and and_1 (and_1_out, or_2_out, ~\同步清零信号 );  // AND_Gate
  D_Flip_Flop #(.trigger("rising"), .Pre_Clr_Positions("LEGACY"), .NegatePresetClear("false"), .enable("true"), .NewFFLayout("false")) IR1 (
    .clk(clock_1_out), .D(and_1_out), .Q(\与中断屏蔽位与 ));  // open: Qn, preset, en, reset

  // Notes on the sheet:
  //   中断信号采样参考电路
  //   Reset 
endmodule

module \单周期MIPS_单级中断  (
  input  IR1,
  input  IR2,
  input  IR3,
  output RegWrite,
  output MemWrite,
  output [31:0] PC,
  output [31:0] IR,
  output [31:0] RDin,
  output [31:0] MDin,
  output [31:0] LedData
);

  wire and_2_out, and_3_out, and_6_out, and_7_out, and_8_out, and_9_out, and_10_out, branch, CLK,
       comparator_1_eq, comparator_2_eq, comparator_3_eq, comparator_4_eq, comparator_5_eq, d_ff_1_q,
       d_ff_2_q, d_ff_3_q, equ, ERET, Go, hangUp, IE, IE_q, INT_SIG, IR1_t, IR2_t, IR3_t, IRA, IRB, IRC, JAL,
       JMP, JR, LedOut, multiplexer_11_out, not_1_out, not_2_out, not_4_out, or_6_out, or_10_out, or_11_out,
       or_12_out, or_13_out, or_14_out, priority_encoder_1_en_out, rst, SignedExt, syscall, W1, W2, W3,
       \单周期硬布线控制器_1_alu_src , \单周期硬布线控制器_1_beq , \单周期硬布线控制器_1_bne ;
  wire [0:0] \单周期硬布线控制器_1_regdst ;
  wire [1:0] INT, register_2_q;
  wire [1:1] \单周期硬布线控制器_1_memtoreg ;
  wire [2:0] and_11_out, and_13_out, decoder_1_out1, INM, INM_q, IR1_q, multiplexer_12_out;
  wire [2:1] or_1_out;
  wire [3:0] \单周期硬布线控制器_1_alu_op ;
  wire [4:0] multiplexer_5_out, multiplexer_6_out, multiplexer_7_out;
  wire [15:0] \总周期数 ;
  wire [27:2] IAddr;
  wire [31:0] BAddr, bit_extender_1_out, bit_extender_2_out, BreakPoint, mips_alu_1_result,
       multiplexer_1_out, multiplexer_2_out, multiplexer_4_out, multiplexer_8_out, multiplexer_9_out, nextPC,
       PC_4, R1out, ram_1_data, shifter_1_out;
  wire [31:26] mips_probe_1_p2;

  Clock #(.highDuration(1), .lowDuration(1)) clock_1 (.out(CLK));
  Button _1 ();  // open: out
  Button _2 ();  // open: out
  Button _3 ();  // open: out
  Button \u_继续运行  (.out(Go));
  LED #(.active("true")) led_1 (.in(W1));
  LED #(.active("true")) led_2 (.in(W2));
  LED #(.active("true")) led_3 (.in(W3));
  Multiplexer #(.select(2), .width(32), .disabled("Z"), .enable("false")) multiplexer_1 (
    .in1(32'h30ac), .in2(32'h3150), .in3(32'h31f4), .out(multiplexer_1_out), .sel(INT));  // open: in0
  and and_1 (or_1_out[2], JR, JMP);
  and and_2 (and_2_out, JAL, JMP);
  or or_1 (or_1_out[1], and_2_out, and_3_out);
  Hex_Digit_Display hex_digit_display_1 (.value(LedData[31:28]));  // open: dp
  Button button_1 (.out(rst));
  Multiplexer #(.select(1), .width(32), .disabled("Z"), .enable("false")) multiplexer_2 (
    .in0(nextPC), .in1(multiplexer_1_out), .out(multiplexer_2_out), .sel(INT_SIG));
  and and_3 (and_3_out, ~JR, ~JAL, JMP);  // AND_Gate
  Multiplexer #(.select(3), .width(32), .disabled("Z"), .enable("false")) multiplexer_3 (
    .in0(PC_4), .in1(BAddr), .in2({4'b0000, IAddr, 2'b00}), .in4(R1out), .out(nextPC),
    .sel({or_1_out, branch}));  // open: in3, in5, in6, in7
  Hex_Digit_Display hex_digit_display_2 (.value(LedData[23:20]));  // open: dp
  Hex_Digit_Display hex_digit_display_3 (.value(LedData[27:24]));  // open: dp
  Hex_Digit_Display hex_digit_display_4 (.value(LedData[19:16]));  // open: dp
  Hex_Digit_Display hex_digit_display_5 (.value(LedData[15:12]));  // open: dp
  Multiplexer #(.select(1), .width(32), .disabled("Z"), .enable("false")) multiplexer_4 (
    .in0(multiplexer_2_out), .in1(BreakPoint), .out(multiplexer_4_out), .sel(ERET));
  not not_1 (not_1_out, hangUp);
  not not_2 (not_2_out, hangUp);
  Counter #(.width(16), .max('hffff), .ongoal("wrap"), .trigger("rising"), .behavior("new")) counter_1 (
    .count(not_2_out), .Q(\总周期数 ), .clk(CLK), .clr(rst));  // open: load, D, carry, preset, down
  Hex_Digit_Display hex_digit_display_6 (.value(LedData[7:4]));  // open: dp
  Hex_Digit_Display hex_digit_display_7 (.value(LedData[11:8]));  // open: dp
  // Probe on \总周期数 
  Register #(.width(32), .trigger("rising"), .Select("low")) u_PC (
    .D(multiplexer_4_out), .en(not_1_out), .Q(PC), .clk(CLK), .clr(rst));
  Hex_Digit_Display hex_digit_display_8 (.value(LedData[3:0]));  // open: dp
  Adder #(.width(32)) adder_1 (.a(PC), .b(32'h4), .out(PC_4));  // open: cin, cout
  and and_4 (LedOut, syscall, comparator_1_eq);
  Comparator #(.width(32), .mode("twosComplement")) comparator_1 (
    .a(32'h22), .b(R1out), .eq(comparator_1_eq));  // open: gt, lt
  and and_5 (hangUp, syscall, ~comparator_1_eq);  // AND_Gate
  // Mips_Probe mips_probe_1: pin names not known; wires that end beside it: PC[11:2], {mips_probe_1_p2, IAddr}
  ROM #(.addrWidth(10), .dataWidth(32), .Select("high")) rom_1 (.addr(PC[11:2]), .data({mips_probe_1_p2, IAddr}));
  Register #(.width(32), .trigger("rising"), .Select("low")) register_1 (
    .D(MDin), .en(LedOut), .Q(LedData), .clk(CLK), .clr(rst));
  or or_2 (IR1_t, IR1, IRA);
  or or_3 (IR2_t, IR2, IRB);
  \单周期硬布线控制器  \u_单周期硬布线控制器_1  (
    .Func(IAddr[7:2]), .OP(mips_probe_1_p2), .ALU_OP(\单周期硬布线控制器_1_alu_op ),
    .MemToReg(\单周期硬布线控制器_1_memtoreg [1]), .MemWrite(MemWrite), .ALU_SRC(\单周期硬布线控制器_1_alu_src ),
    .RegWrite(RegWrite), .SysCALL(syscall), .SignedExt(SignedExt), .RegDst(\单周期硬布线控制器_1_regdst [0]), .JR(JR),
    .JMP(JMP), .Beq(\单周期硬布线控制器_1_beq ), .JAL(JAL), .Bne(\单周期硬布线控制器_1_bne ), .ERET(ERET));  // open: B, BGEZ, SRLV
  Multiplexer #(.select(1), .width(5), .disabled("Z"), .enable("false")) multiplexer_5 (
    .in0(IAddr[27:23]), .in1(5'b00010), .out(multiplexer_5_out), .sel(syscall));
  Multiplexer #(.select(1), .width(5), .disabled("Z"), .enable("false")) multiplexer_6 (
    .in0(IAddr[22:18]), .in1(5'b00100), .out(multiplexer_6_out), .sel(syscall));
  Multiplexer #(.select(2), .width(5), .disabled("Z"), .enable("false")) multiplexer_7 (
    .in0(IAddr[22:18]), .in1(IAddr[17:13]), .in2({5{1'b1}}), .in3({5{1'b1}}), .out(multiplexer_7_out),
    .sel({JAL, \单周期硬布线控制器_1_regdst [0]}));
  or or_4 (IR3_t, IR3, IRC);
  assign bit_extender_1_out = {{16{1'b0}}, IAddr[17:2]};  // Bit_Extender bit_extender_1
  assign bit_extender_2_out = {{16{IAddr[17]}}, IAddr[17:2]};  // Bit_Extender bit_extender_2
  and and_6 (and_6_out, equ, \单周期硬布线控制器_1_beq );
  or or_5 (branch, and_6_out, and_7_out);
  and and_7 (and_7_out, ~equ, \单周期硬布线控制器_1_bne );  // AND_Gate
  MIPS_Regifile mips_regifile_1 (
    .Din(RDin), .Clk(CLK), .R1(R1out), .R2(MDin), .WE(RegWrite), .W_num(multiplexer_7_out),
    .R1_num(multiplexer_5_out), .R2_num(multiplexer_6_out));
  Multiplexer #(.select(1), .width(32), .disabled("Z"), .enable("false")) multiplexer_8 (
    .in0(bit_extender_1_out), .in1(bit_extender_2_out), .out(multiplexer_8_out), .sel(SignedExt));
  Multiplexer #(.select(1), .width(32), .disabled("Z"), .enable("false")) multiplexer_9 (
    .in0(MDin), .in1(multiplexer_8_out), .out(multiplexer_9_out), .sel(\单周期硬布线控制器_1_alu_src ));
  MIPS_ALU mips_alu_1 (
    .X(R1out), .Y(multiplexer_9_out), .AluOP(\单周期硬布线控制器_1_alu_op ), .Equal(equ), .Result(mips_alu_1_result),
    .shamt(IAddr[12:8]));  // open: Result_2, GEZ
  Shifter #(.width(32), .shift("ll")) shifter_1 (.in(bit_extender_2_out), .\dist (5'b00010), .out(shifter_1_out));
  Adder #(.width(32)) adder_2 (.a(shifter_1_out), .b(PC_4), .out(BAddr));  // open: cin, cout
  RAM #(.addrWidth(10), .dataWidth(32), .bus("separate"), .Select("high")) ram_1 (
    .addr(mips_alu_1_result[11:2]), .din(MDin), .data(ram_1_data), .str(MemWrite), .clk(CLK), .clr(rst));  // open: sel, ld
  Multiplexer #(.select(2), .width(32), .disabled("Z"), .enable("false")) multiplexer_10 (
    .in0(mips_alu_1_result), .in1(PC_4), .in2(ram_1_data), .out(RDin), .sel({\单周期硬布线控制器_1_memtoreg [1], JAL}));  // open: in3
  Comparator #(.width(16), .mode("twosComplement")) comparator_2 (
    .a(16'h23b), .b(\总周期数 ), .eq(comparator_2_eq));  // open: gt, lt
  Comparator #(.width(16), .mode("twosComplement")) comparator_3 (
    .a(\总周期数 ), .b(16'h1), .eq(comparator_3_eq));  // open: gt, lt
  Comparator #(.width(16), .mode("twosComplement")) comparator_4 (
    .a(\总周期数 ), .b(16'h4), .eq(comparator_4_eq));  // open: gt, lt
  Comparator #(.width(16), .mode("twosComplement")) comparator_5 (
    .a(\总周期数 ), .b(16'h7), .eq(comparator_5_eq));  // open: gt, lt
  or or_6 (or_6_out, comparator_2_eq, comparator_3_eq);
  Pull_Resistor #(.pull(0)) pull_resistor_1 (.node(IRA));
  assign IRA = or_6_out ? ~CLK : 1'bz;  // Controlled_Inverter controlled_inverter_1
  Pull_Resistor #(.pull(0)) pull_resistor_2 (.node(IRB));
  assign IRB = comparator_4_eq ? ~CLK : 1'bz;  // Controlled_Inverter controlled_inverter_2
  Pull_Resistor #(.pull(0)) pull_resistor_3 (.node(IRC));
  assign IRC = comparator_5_eq ? ~CLK : 1'bz;  // Controlled_Inverter controlled_inverter_3
  or or_7 (W1, IR1_q[0], d_ff_1_q);
  or or_8 (W2, IR1_q[1], d_ff_2_q);
  or or_9 (W3, IR1_q[2], d_ff_3_q);
  D_Flip_Flop #(.trigger("rising"), .Pre_Clr_Positions("LEGACY"), .NegatePresetClear("false"), .enable("true"), .NewFFLayout("false")) d_ff_1 (
    .clk(IR1_t), .D(1'b1), .Q(d_ff_1_q), .reset(IR1_q[0]));  // open: Qn, preset, en
  D_Flip_Flop #(.trigger("rising"), .Pre_Clr_Positions("LEGACY"), .NegatePresetClear("false"), .enable("true"), .NewFFLayout("false")) d_ff_2 (
    .clk(IR2_t), .D(1'b1), .Q(d_ff_2_q), .reset(IR1_q[1]));  // open: Qn, preset, en
  D_Flip_Flop #(.trigger("rising"), .Pre_Clr_Positions("LEGACY"), .NegatePresetClear("false"), .enable("true"), .NewFFLayout("false")) d_ff_3 (
    .clk(IR3_t), .D(1'b1), .Q(d_ff_3_q), .reset(IR1_q[2]));  // open: Qn, preset, en
  Register #(.width(32), .trigger("rising"), .Select("low")) EPC (
    .D(nextPC), .en(INT_SIG), .Q(BreakPoint), .clk(CLK), .clr(rst));
  or or_10 (or_10_out, d_ff_1_q, IR1_q[0]);
  or or_11 (or_11_out, d_ff_2_q, IR1_q[1]);
  or or_12 (or_12_out, d_ff_3_q, IR1_q[2]);
  Multiplexer #(.select(1), .width(1), .disabled("Z"), .enable("false")) multiplexer_11 (
    .in0(IE_q), .in1(1'b1), .out(multiplexer_11_out), .sel(INT_SIG));
  and and_8 (and_8_out, or_10_out, ~and_11_out[0]);  // AND_Gate
  and and_9 (and_9_out, or_11_out, ~and_11_out[1]);  // AND_Gate
  and and_10 (and_10_out, or_12_out, ~and_11_out[2]);  // AND_Gate
  Multiplexer #(.select(2), .width(3), .disabled("Z"), .enable("false")) multiplexer_12 (
    .in0(3'b000), .in1(3'b001), .in2(3'b011), .in3(3'b111), .out(multiplexer_12_out), .sel(INT));
  or or_13 (or_13_out, rst, ERET);
  D_Flip_Flop #(.trigger("rising"), .Pre_Clr_Positions("LEGACY"), .NegatePresetClear("false"), .enable("true"), .NewFFLayout("false")) u_IR1 (
    .clk(CLK), .D(and_8_out), .Q(IR1_q[0]), .reset(rst));  // open: Qn, preset, en
  D_Flip_Flop #(.trigger("rising"), .Pre_Clr_Positions("LEGACY"), .NegatePresetClear("false"), .enable("true"), .NewFFLayout("false")) u_IR2 (
    .clk(CLK), .D(and_9_out), .Q(IR1_q[1]), .reset(rst));  // open: Qn, preset, en
  D_Flip_Flop #(.trigger("rising"), .Pre_Clr_Positions("LEGACY"), .NegatePresetClear("false"), .enable("true"), .NewFFLayout("false")) u_IR3 (
    .clk(CLK), .D(and_10_out), .Q(IR1_q[2]), .reset(rst));  // open: Qn, preset, en
  assign and_11_out = decoder_1_out1 & {3{ERET}};  // AND_Gate and_11, 3 bits wide
  assign INM = ~INM_q;  // NOT_Gate not_3, 3 bits wide
  Register #(.width(3), .trigger("rising"), .Select("low")) u_INM (
    .D(multiplexer_12_out), .en(IE), .Q(INM_q), .clk(CLK), .clr(or_14_out));
  and and_12 (INT_SIG, IE, not_4_out);
  D_Flip_Flop #(.trigger("rising"), .Pre_Clr_Positions("ABOVE_BELOW"), .NegatePresetClear("false"), .enable("false"), .NewFFLayout("false")) u_IE (
    .clk(CLK), .D(multiplexer_11_out), .Q(IE_q), .Qn(IE), .reset(or_13_out));  // open: preset
  not not_4 (not_4_out, priority_encoder_1_en_out);
  assign and_13_out = IR1_q & INM;  // AND_Gate and_13, 3 bits wide
  Priority_Encoder #(.select(2), .disabled("Z")) priority_encoder_1 (
    .in1(and_13_out[0]), .in2(and_13_out[1]), .in3(and_13_out[2]), .out(INT),
    .en_out(priority_encoder_1_en_out));  // open: in0, gs, en_in
  Register #(.width(2), .trigger("rising"), .Select("low")) register_2 (
    .D(INT), .en(INT_SIG), .Q(register_2_q), .clk(CLK));  // open: clr
  Decoder #(.select(2), .tristate("false"), .disabled("Z"), .enable("false")) decoder_1 (
    .out1(decoder_1_out1[0]), .out2(decoder_1_out1[1]), .out3(decoder_1_out1[2]), .sel(register_2_q));  // open: out0
  or or_14 (or_14_out, ERET, rst);

  // Other names for the same wires on the sheet: RAddr[31:0] = R1out

  // Notes on the sheet:
  //   中断源
  //   中断等待指示
  //   总复位信号应将除ROM以外所有存储组件全部清零
  //   异步置位
  //   数码管输出
  //   display
  //   数码管输出应该用寄存器锁存，否则显示数据只能一闪而过
  //   指令存储器
  //   指令字
  //   contents of rom_1 (hex, n*v repeats v):
  //   201d07d0 20100001 109fc0 139fc3 8021 2012000c 24160008 26100001 3210000f 20080008 20090001 139900
  //   2709825 132020 20020022 c 1094022 1500fff9 22100001 2018000f 2188024 108700 20080008 20090001 139902
  //   2709825 132021 20020022 c 1094022 1500fff9 108702 2c9b022 12c00001 8000c07 4020 1084027 84400
  //   3508ffff 82021 20020022 c 8000c01 afa20000 23bd0004 afa40000 23bd0004 afb00000 23bd0004 afb30000
  //   23bd0004 afb40000 23bd0004 afb50000 23bd0004 afb60000 23bd0004 20160001 20140003 20150001 168020
  //   108100 2149825 132020 20020022 c 1600fffa 295a022 1680fff7 23bdfffc 8fb60000 23bdfffc 8fb50000
  //   23bdfffc 8fb40000 23bdfffc 8fb30000 23bdfffc 8fb00000 23bdfffc 8fa40000 23bdfffc 8fa20000 42000018
  //   afa20000 23bd0004 afa40000 23bd0004 afb00000 23bd0004 afb30000 23bd0004 afb40000 23bd0004 afb50000
  //   23bd0004 afb60000 23bd0004 20160002 20140003 20150001 168020 108100 2149825 132020 20020022 c
  //   1600fffa 295a022 1680fff7 23bdfffc 8fb60000 23bdfffc 8fb50000 23bdfffc 8fb40000 23bdfffc 8fb30000
  //   23bdfffc 8fb00000 23bdfffc 8fa40000 23bdfffc 8fa20000 42000018 afa20000 23bd0004 afa40000 23bd0004
  //   afb00000 23bd0004 afb30000 23bd0004 afb40000 23bd0004 afb50000 23bd0004 afb60000 23bd0004 20160003
  //   20140003 20150001 168020 108100 2149825 132020 20020022 c 1600fffa 295a022 1680fff7 23bdfffc
  //   8fb60000 23bdfffc 8fb50000 23bdfffc 8fb40000 23bdfffc 8fb30000 23bdfffc 8fb00000 23bdfffc 8fa40000
  //   23bdfffc 8fa20000 42000018
  //   JMP
  //   JR
  //   OP
  //   OP
  //   Func
  //   Func
  //   rs
  //   v0
  //   rt
  //   t0
  //   rd
  //   ra
  //   sa
  //   Imm16
  //   Imm26
  //   Beq
  //   Bne
  //   MemToReg
  //   MemWrite
  //   AluOP
  //   AluSrcB
  //   RegWrite
  //   JAL
  //   RegDst
  //   Syscall
  //   为方便自动评测，需要输出PC，IR，寄存器堆写如数据RDin
  //   RAM写使能MemWrite、RAM写入数据MDin等信号
  //   中断优先级 1<2<3
  //   没有实现branch delay slot，因此只加4
  //   单级中断测试信号模拟器
  //   Reset 
endmodule

module \单周期MIPS_多级中断  (
  input  IR1,
  input  IR2,
  input  IR3,
  output RegWrite,
  output MemWrite,
  output [31:0] PC,
  output [31:0] IR,
  output [31:0] RDin,
  output [31:0] MDin,
  output [31:0] LedData
);

  wire and_2_out, and_5_out, and_8_out, and_9_out, and_10_out, and_11_out, and_12_out, branch, CLK,
       comparator_1_eq, comparator_2_eq, comparator_3_eq, comparator_4_eq, comparator_5_eq, comparator_6_eq,
       comparator_7_eq, comparator_8_eq, comparator_9_eq, d_ff_1_q, d_ff_2_q, d_ff_3_q, equ, ERET, Go,
       hangUp, IE, IE_q, INT_SIG, IR1_t, IR2_t, IR3_t, IRA, IRB, IRC, JAL, JMP, JR, LedOut, MFC0, MTC0,
       multiplexer_10_out, multiplexer_11_out, not_1_out, not_2_out, or_2_out, or_3_out, or_11_out,
       or_12_out, or_13_out, or_14_out, or_15_out, or_16_out, or_17_out, or_18_out,
       priority_encoder_1_en_out, rst, SignedExt, syscall, W1, W2, W3, \单周期硬布线控制器_1_alu_src ,
       \单周期硬布线控制器_1_beq , \单周期硬布线控制器_1_bne ;
  wire [0:0] \单周期硬布线控制器_1_regdst ;
  wire [1:0] INT, INT_TOP, multiplexer_13_out, multiplexer_14_out, multiplexer_15_out, register_2_q,
       register_3_q;
  wire [1:1] \单周期硬布线控制器_1_memtoreg ;
  wire [2:0] and_14_out, and_15_out, decoder_1_out1, INM, INM_q, IR1_q, multiplexer_16_out,
       multiplexer_18_out, multiplexer_20_out, multiplexer_22_out, register_5_q, register_7_q;
  wire [2:1] or_1_out;
  wire [3:0] \单周期硬布线控制器_1_alu_op ;
  wire [4:0] multiplexer_5_out, multiplexer_6_out, multiplexer_7_out;
  wire [15:0] \总周期数 ;
  wire [31:0] BAddr, bit_extender_1_out, bit_extender_2_out, BreakPoint, mips_alu_1_result,
       multiplexer_1_out, multiplexer_2_out, multiplexer_4_out, multiplexer_8_out, multiplexer_9_out,
       multiplexer_17_out, multiplexer_19_out, multiplexer_21_out, nextPC, PC_4, R1out, ram_1_data,
       register_4_q, register_6_q, shifter_1_out;

  Clock #(.highDuration(1), .lowDuration(1)) clock_1 (.out(CLK));
  Button _1 ();  // open: out
  Button _2 ();  // open: out
  Button _3 ();  // open: out
  Button \u_继续运行  (.out(Go));
  LED #(.active("true")) led_1 (.in(W1));
  LED #(.active("true")) led_2 (.in(W2));
  LED #(.active("true")) led_3 (.in(W3));
  Multiplexer #(.select(2), .width(32), .disabled("Z"), .enable("false")) multiplexer_1 (
    .in1(32'h30ac), .in2(32'h3158), .in3(32'h3204), .out(multiplexer_1_out), .sel(INT));  // open: in0
  and and_1 (or_1_out[2], JR, JMP);
  and and_2 (and_2_out, JAL, JMP);
  or or_1 (or_1_out[1], and_2_out, and_5_out);
  Hex_Digit_Display hex_digit_display_1 (.value(LedData[31:28]));  // open: dp
  Comparator #(.width(6), .mode("unsigned")) comparator_1 (
    .a(6'b010000), .b(IR[31:26]), .eq(comparator_1_eq));  // open: gt, lt
  and and_3 (MTC0, comparator_1_eq, comparator_2_eq);
  Comparator #(.width(5), .mode("unsigned")) comparator_2 (
    .a(IR[25:21]), .b(5'b00100), .eq(comparator_2_eq));  // open: gt, lt
  and and_4 (MFC0, comparator_1_eq, comparator_3_eq);
  Comparator #(.width(5), .mode("unsigned")) comparator_3 (
    .a(IR[25:21]), .b({5{1'b0}}), .eq(comparator_3_eq));  // open: gt, lt
  Multiplexer #(.select(1), .width(32), .disabled("Z"), .enable("false")) multiplexer_2 (
    .in0(nextPC), .in1(multiplexer_1_out), .out(multiplexer_2_out), .sel(INT_SIG));
  and and_5 (and_5_out, ~JR, ~JAL, JMP);  // AND_Gate
  Multiplexer #(.select(3), .width(32), .disabled("Z"), .enable("false")) multiplexer_3 (
    .in0(PC_4), .in1(BAddr), .in2({4'b0000, IR[25:0], 2'b00}), .in4(R1out), .out(nextPC),
    .sel({or_1_out, branch}));  // open: in3, in5, in6, in7
  Comparator #(.width(16), .mode("twosComplement")) comparator_4 (
    .a(16'h258), .b(\总周期数 ), .eq(comparator_4_eq));  // open: gt, lt
  Comparator #(.width(16), .mode("twosComplement")) comparator_5 (
    .a(\总周期数 ), .b(16'h1), .eq(comparator_5_eq));  // open: gt, lt
  Comparator #(.width(16), .mode("twosComplement")) comparator_6 (
    .a(\总周期数 ), .b(16'h4), .eq(comparator_6_eq));  // open: gt, lt
  Comparator #(.width(16), .mode("twosComplement")) comparator_7 (
    .a(\总周期数 ), .b(16'h7), .eq(comparator_7_eq));  // open: gt, lt
  Comparator #(.width(16), .mode("twosComplement")) comparator_8 (
    .a(\总周期数 ), .b(16'h241), .eq(comparator_8_eq));  // open: gt, lt
  Hex_Digit_Display hex_digit_display_2 (.value(LedData[23:20]));  // open: dp
  Hex_Digit_Display hex_digit_display_3 (.value(LedData[27:24]));  // open: dp
  Comparator #(.width(32), .mode("twosComplement")) comparator_9 (
    .a(32'h22), .b(R1out), .eq(comparator_9_eq));  // open: gt, lt
  or or_2 (or_2_out, comparator_4_eq, comparator_5_eq);
  assign IRA = or_2_out ? ~CLK : 1'bz;  // Controlled_Inverter controlled_inverter_1
  assign IRB = comparator_6_eq ? ~CLK : 1'bz;  // Controlled_Inverter controlled_inverter_2
  or or_3 (or_3_out, comparator_7_eq, comparator_8_eq);
  assign IRC = or_3_out ? ~CLK : 1'bz;  // Controlled_Inverter controlled_inverter_3
  Hex_Digit_Display hex_digit_display_4 (.value(LedData[19:16]));  // open: dp
  Hex_Digit_Display hex_digit_display_5 (.value(LedData[15:12]));  // open: dp
  Multiplexer #(.select(1), .width(32), .disabled("Z"), .enable("false")) multiplexer_4 (
    .in0(multiplexer_2_out), .in1(BreakPoint), .out(multiplexer_4_out), .sel(ERET));
  not not_1 (not_1_out, hangUp);
  not not_2 (not_2_out, hangUp);
  Counter #(.width(16), .max('hffff), .ongoal("wrap"), .trigger("rising"), .behavior("new")) counter_1 (
    .count(not_2_out), .Q(\总周期数 ), .clk(CLK), .clr(rst));  // open: load, D, carry, preset, down
  and and_6 (LedOut, syscall, comparator_9_eq);
  and and_7 (hangUp, syscall, ~comparator_9_eq);  // AND_Gate
  Pull_Resistor #(.pull(0)) pull_resistor_1 (.node(IRA));
  Pull_Resistor #(.pull(0)) pull_resistor_2 (.node(IRB));
  Pull_Resistor #(.pull(0)) pull_resistor_3 (.node(IRC));
  Hex_Digit_Display hex_digit_display_6 (.value(LedData[7:4]));  // open: dp
  Hex_Digit_Display hex_digit_display_7 (.value(LedData[11:8]));  // open: dp
  // Probe on \总周期数 
  Register #(.width(32), .trigger("rising"), .Select("low")) u_PC (
    .D(multiplexer_4_out), .en(not_1_out), .Q(PC), .clk(CLK), .clr(rst));
  Hex_Digit_Display hex_digit_display_8 (.value(LedData[3:0]));  // open: dp
  Adder #(.width(32)) adder_1 (.a(PC), .b(32'h4), .out(PC_4));  // open: cin, cout
  Register #(.width(32), .trigger("rising"), .Select("low")) register_1 (
    .D(MDin), .en(LedOut), .Q(LedData), .clk(CLK), .clr(rst));
  // Mips_Probe mips_probe_1: pin names not known; wires that end beside it: PC[11:2], IR
  ROM #(.addrWidth(10), .dataWidth(32), .Select("high")) rom_1 (.addr(PC[11:2]), .data(IR));
  or or_4 (IR1_t, IR1, IRA);
  or or_5 (IR2_t, IR2, IRB);
  \单周期硬布线控制器  \u_单周期硬布线控制器_1  (
    .Func(IR[5:0]), .OP(IR[31:26]), .ALU_OP(\单周期硬布线控制器_1_alu_op ), .MemToReg(\单周期硬布线控制器_1_memtoreg [1]),
    .MemWrite(MemWrite), .ALU_SRC(\单周期硬布线控制器_1_alu_src ), .RegWrite(RegWrite), .SysCALL(syscall),
    .SignedExt(SignedExt), .RegDst(\单周期硬布线控制器_1_regdst [0]), .JR(JR), .JMP(JMP), .Beq(\单周期硬布线控制器_1_beq ),
    .JAL(JAL), .Bne(\单周期硬布线控制器_1_bne ), .ERET(ERET));  // open: B, BGEZ, SRLV
  Multiplexer #(.select(1), .width(5), .disabled("Z"), .enable("false")) multiplexer_5 (
    .in0(IR[25:21]), .in1(5'b00010), .out(multiplexer_5_out), .sel(syscall));
  Multiplexer #(.select(1), .width(5), .disabled("Z"), .enable("false")) multiplexer_6 (
    .in0(IR[20:16]), .in1(5'b00100), .out(multiplexer_6_out), .sel(syscall));
  Multiplexer #(.select(2), .width(5), .disabled("Z"), .enable("false")) multiplexer_7 (
    .in0(IR[20:16]), .in1(IR[15:11]), .in2({5{1'b1}}), .in3({5{1'b1}}), .out(multiplexer_7_out),
    .sel({JAL, \单周期硬布线控制器_1_regdst [0]}));
  or or_6 (IR3_t, IR3, IRC);
  assign bit_extender_1_out = {{16{1'b0}}, IR[15:0]};  // Bit_Extender bit_extender_1
  assign bit_extender_2_out = {{16{IR[15]}}, IR[15:0]};  // Bit_Extender bit_extender_2
  Button button_1 (.out(rst));
  and and_8 (and_8_out, equ, \单周期硬布线控制器_1_beq );
  or or_7 (branch, and_8_out, and_9_out);
  and and_9 (and_9_out, ~equ, \单周期硬布线控制器_1_bne );  // AND_Gate
  MIPS_Regifile mips_regifile_1 (
    .Din(RDin), .Clk(CLK), .R1(R1out), .R2(MDin), .WE(RegWrite), .W_num(multiplexer_7_out),
    .R1_num(multiplexer_5_out), .R2_num(multiplexer_6_out));
  Multiplexer #(.select(1), .width(32), .disabled("Z"), .enable("false")) multiplexer_8 (
    .in0(bit_extender_1_out), .in1(bit_extender_2_out), .out(multiplexer_8_out), .sel(SignedExt));
  Multiplexer #(.select(1), .width(32), .disabled("Z"), .enable("false")) multiplexer_9 (
    .in0(MDin), .in1(multiplexer_8_out), .out(multiplexer_9_out), .sel(\单周期硬布线控制器_1_alu_src ));
  D_Flip_Flop #(.trigger("rising"), .Pre_Clr_Positions("LEGACY"), .NegatePresetClear("false"), .enable("true"), .NewFFLayout("false")) d_ff_1 (
    .clk(IR1_t), .D(1'b1), .Q(d_ff_1_q), .reset(IR1_q[0]));  // open: Qn, preset, en
  or or_8 (W1, IR1_q[0], d_ff_1_q);
  D_Flip_Flop #(.trigger("rising"), .Pre_Clr_Positions("LEGACY"), .NegatePresetClear("false"), .enable("true"), .NewFFLayout("false")) d_ff_2 (
    .clk(IR2_t), .D(1'b1), .Q(d_ff_2_q), .reset(IR1_q[1]));  // open: Qn, preset, en
  or or_9 (W2, IR1_q[1], d_ff_2_q);
  D_Flip_Flop #(.trigger("rising"), .Pre_Clr_Positions("LEGACY"), .NegatePresetClear("false"), .enable("true"), .NewFFLayout("false")) d_ff_3 (
    .clk(IR3_t), .D(1'b1), .Q(d_ff_3_q), .reset(IR1_q[2]));  // open: Qn, preset, en
  or or_10 (W3, IR1_q[2], d_ff_3_q);
  MIPS_ALU mips_alu_1 (
    .X(R1out), .Y(multiplexer_9_out), .AluOP(\单周期硬布线控制器_1_alu_op ), .Equal(equ), .Result(mips_alu_1_result),
    .shamt(IR[10:6]));  // open: Result_2, GEZ
  Shifter #(.width(32), .shift("ll")) shifter_1 (.in(bit_extender_2_out), .\dist (5'b00010), .out(shifter_1_out));
  or or_11 (or_11_out, MTC0, INT_SIG);
  Adder #(.width(32)) adder_2 (.a(shifter_1_out), .b(PC_4), .out(BAddr));  // open: cin, cout
  Multiplexer #(.select(1), .width(1), .disabled("Z"), .enable("false")) multiplexer_10 (
    .in0(IE_q), .in1(1'b1), .out(multiplexer_10_out), .sel(or_11_out));
  Multiplexer #(.select(1), .width(1), .disabled("Z"), .enable("false")) multiplexer_11 (
    .in0(multiplexer_10_out), .in1(1'b0), .out(multiplexer_11_out), .sel(MFC0));
  or or_12 (or_12_out, d_ff_1_q, IR1_q[0]);
  and and_10 (and_10_out, or_12_out, ~and_15_out[0]);  // AND_Gate
  or or_13 (or_13_out, d_ff_2_q, IR1_q[1]);
  and and_11 (and_11_out, or_13_out, ~and_15_out[1]);  // AND_Gate
  or or_14 (or_14_out, d_ff_3_q, IR1_q[2]);
  and and_12 (and_12_out, or_14_out, ~and_15_out[2]);  // AND_Gate
  D_Flip_Flop #(.trigger("rising"), .Pre_Clr_Positions("LEGACY"), .NegatePresetClear("false"), .enable("true"), .NewFFLayout("false")) u_IR1 (
    .clk(CLK), .D(and_10_out), .Q(IR1_q[0]), .reset(rst));  // open: Qn, preset, en
  D_Flip_Flop #(.trigger("rising"), .Pre_Clr_Positions("LEGACY"), .NegatePresetClear("false"), .enable("true"), .NewFFLayout("false")) u_IR2 (
    .clk(CLK), .D(and_11_out), .Q(IR1_q[1]), .reset(rst));  // open: Qn, preset, en
  D_Flip_Flop #(.trigger("rising"), .Pre_Clr_Positions("LEGACY"), .NegatePresetClear("false"), .enable("true"), .NewFFLayout("false")) u_IR3 (
    .clk(CLK), .D(and_12_out), .Q(IR1_q[2]), .reset(rst));  // open: Qn, preset, en
  RAM #(.addrWidth(10), .dataWidth(32), .bus("separate"), .Select("high")) ram_1 (
    .addr(mips_alu_1_result[11:2]), .din(MDin), .data(ram_1_data), .str(MemWrite), .clk(CLK), .clr(rst));  // open: sel, ld
  and and_13 (INT_SIG, IE, ~priority_encoder_1_en_out);  // AND_Gate
  D_Flip_Flop #(.trigger("rising"), .Pre_Clr_Positions("ABOVE_BELOW"), .NegatePresetClear("false"), .enable("false"), .NewFFLayout("false")) u_IE (
    .clk(CLK), .D(multiplexer_11_out), .Q(IE_q), .Qn(IE), .reset(or_15_out));  // open: preset
  or or_15 (or_15_out, rst, ERET);
  assign and_14_out = IR1_q & INM;  // AND_Gate and_14, 3 bits wide
  assign and_15_out = decoder_1_out1 & {3{ERET}};  // AND_Gate and_15, 3 bits wide
  Multiplexer #(.select(2), .width(32), .disabled("Z"), .enable("false")) multiplexer_12 (
    .in0(mips_alu_1_result), .in1(PC_4), .in2(ram_1_data), .out(RDin), .sel({\单周期硬布线控制器_1_memtoreg [1], JAL}));  // open: in3
  Priority_Encoder #(.select(2), .disabled("Z")) priority_encoder_1 (
    .in1(and_14_out[0]), .in2(and_14_out[1]), .in3(and_14_out[2]), .out(INT),
    .en_out(priority_encoder_1_en_out));  // open: in0, gs, en_in
  Decoder #(.select(2), .tristate("false"), .disabled("Z"), .enable("false")) decoder_1 (
    .out1(decoder_1_out1[0]), .out2(decoder_1_out1[1]), .out3(decoder_1_out1[2]), .sel(INT_TOP));  // open: out0
  Multiplexer #(.select(1), .width(2), .disabled("Z"), .enable("false")) multiplexer_13 (
    .in0(INT), .in1(register_2_q), .out(multiplexer_13_out), .sel(ERET));
  or or_16 (or_16_out, INT_SIG, ERET);
  Register #(.width(2), .trigger("rising"), .Select("low")) u_INT (
    .D(multiplexer_13_out), .en(or_16_out), .Q(INT_TOP), .clk(CLK), .clr(rst));
  Register #(.width(2), .trigger("rising"), .Select("low")) register_2 (
    .D(multiplexer_14_out), .en(or_16_out), .Q(register_2_q), .clk(CLK), .clr(rst));
  Multiplexer #(.select(1), .width(2), .disabled("Z"), .enable("false")) multiplexer_14 (
    .in0(INT_TOP), .in1(register_3_q), .out(multiplexer_14_out), .sel(ERET));
  Multiplexer #(.select(1), .width(2), .disabled("Z"), .enable("false")) multiplexer_15 (
    .in0(register_2_q), .in1(2'b00), .out(multiplexer_15_out), .sel(ERET));
  or or_17 (or_17_out, INT_SIG, ERET);
  Multiplexer #(.select(2), .width(3), .disabled("Z"), .enable("false")) multiplexer_16 (
    .in0(3'b000), .in1(3'b001), .in2(3'b011), .in3(3'b111), .out(multiplexer_16_out), .sel(INT));
  or or_18 (or_18_out, INT_SIG, ERET);
  Register #(.width(2), .trigger("rising"), .Select("low")) register_3 (
    .D(multiplexer_15_out), .en(or_16_out), .Q(register_3_q), .clk(CLK), .clr(rst));
  Multiplexer #(.select(1), .width(32), .disabled("Z"), .enable("false")) multiplexer_17 (
    .in0(nextPC), .in1(register_4_q), .out(multiplexer_17_out), .sel(ERET));
  Register #(.width(32), .trigger("rising"), .Select("low")) EPC_Top (
    .D(multiplexer_17_out), .en(or_17_out), .Q(BreakPoint), .clk(CLK), .clr(rst));
  assign INM = ~INM_q;  // NOT_Gate not_3, 3 bits wide
  Multiplexer #(.select(1), .width(3), .disabled("Z"), .enable("false")) multiplexer_18 (
    .in0(multiplexer_16_out), .in1(register_5_q), .out(multiplexer_18_out), .sel(ERET));
  Register #(.width(3), .trigger("rising"), .Select("low")) u_INM (
    .D(multiplexer_18_out), .en(or_18_out), .Q(INM_q), .clk(CLK), .clr(rst));
  Multiplexer #(.select(1), .width(32), .disabled("Z"), .enable("false")) multiplexer_19 (
    .in0(BreakPoint), .in1(register_6_q), .out(multiplexer_19_out), .sel(ERET));
  Multiplexer #(.select(1), .width(3), .disabled("Z"), .enable("false")) multiplexer_20 (
    .in0(INM_q), .in1(register_7_q), .out(multiplexer_20_out), .sel(ERET));
  Register #(.width(32), .trigger("rising"), .Select("low")) register_4 (
    .D(multiplexer_19_out), .en(or_17_out), .Q(register_4_q), .clk(CLK), .clr(rst));
  Register #(.width(3), .trigger("rising"), .Select("low")) register_5 (
    .D(multiplexer_20_out), .en(or_18_out), .Q(register_5_q), .clk(CLK), .clr(rst));
  Register #(.width(32), .trigger("rising"), .Select("low")) register_6 (
    .D(multiplexer_21_out), .en(or_17_out), .Q(register_6_q), .clk(CLK), .clr(rst));
  Multiplexer #(.select(1), .width(32), .disabled("Z"), .enable("false")) multiplexer_21 (
    .in0(register_4_q), .in1({32{1'b0}}), .out(multiplexer_21_out), .sel(ERET));
  Multiplexer #(.select(1), .width(3), .disabled("Z"), .enable("false")) multiplexer_22 (
    .in0(register_5_q), .in1(3'b000), .out(multiplexer_22_out), .sel(ERET));
  Register #(.width(3), .trigger("rising"), .Select("low")) register_7 (
    .D(multiplexer_22_out), .en(or_18_out), .Q(register_7_q), .clk(CLK), .clr(rst));

  // Other names for the same wires on the sheet: IAddr[27:2] = IR[25:0]; rs[4:0] = IR[25:21]; OP[5:0] = IR[31:26];
  //   RAddr[31:0] = R1out

  // Notes on the sheet:
  //   中断源
  //   注意入口变了
  //   中断等待指示
  //   总复位信号应将除ROM以外所有存储组件全部清零
  //   多级中断测试信号模拟器
  //   display
  //   数码管输出
  //   数码管输出应该用寄存器锁存，否则显示数据只能一闪而过
  //   指令存储器
  //   指令字
  //   contents of rom_1 (hex, n*v repeats v):
  //   201d07d0 20100001 109fc0 139fc3 8021 2012000c 24160008 26100001 3210000f 20080008 20090001 139900
  //   2709825 132020 20020022 c 1094022 1500fff9 22100001 2018000f 2188024 108700 20080008 20090001 139902
  //   2709825 132021 20020022 c 1094022 1500fff9 108702 2c9b022 12c00001 8000c07 4020 1084027 84400
  //   3508ffff 82021 20020022 c 8000c01 afa20000 23bd0004 afa40000 23bd0004 afb00000 23bd0004 afb30000
  //   23bd0004 afb40000 23bd0004 afb50000 23bd0004 afb60000 23bd0004 40000000 20160001 20140003 20150001
  //   168020 108100 2149825 132020 20020022 c 1600fffa 295a022 1680fff7 40800000 23bdfffc 8fb60000
  //   23bdfffc 8fb50000 23bdfffc 8fb40000 23bdfffc 8fb30000 23bdfffc 8fb00000 23bdfffc 8fa40000 23bdfffc
  //   8fa20000 42000018 afa20000 23bd0004 afa40000 23bd0004 afb00000 23bd0004 afb30000 23bd0004 afb40000
  //   23bd0004 afb50000 23bd0004 afb60000 23bd0004 40000000 20160002 20140003 20150001 168020 108100
  //   2149825 132020 20020022 c 1600fffa 295a022 1680fff7 40800000 23bdfffc 8fb60000 23bdfffc 8fb50000
  //   23bdfffc 8fb40000 23bdfffc 8fb30000 23bdfffc 8fb00000 23bdfffc 8fa40000 23bdfffc 8fa20000 42000018
  //   afa20000 23bd0004 afa40000 23bd0004 afb00000 23bd0004 afb30000 23bd0004 afb40000 23bd0004 afb50000
  //   23bd0004 afb60000 23bd0004 40000000 20160003 20140003 20150001 168020 108100 2149825 132020 20020022
  //   c 1600fffa 295a022 1680fff7 40800000 23bdfffc 8fb60000 23bdfffc 8fb50000 23bdfffc 8fb40000 23bdfffc
  //   8fb30000 23bdfffc 8fb00000 23bdfffc 8fa40000 23bdfffc 8fa20000 42000018
  //   JMP
  //   JR
  //   OP
  //   OP
  //   Func
  //   Func
  //   v0
  //   rt
  //   t0
  //   rd
  //   ra
  //   sa
  //   Imm16
  //   Imm26
  //   Beq
  //   Bne
  //   MemToReg
  //   MemWrite
  //   AluOP
  //   AluSrcB
  //   RegWrite
  //   JAL
  //   RegDst
  //   Syscall
  //   rs
  //   为方便自动评测，需要输出PC，IR，寄存器堆写如数据RDin
  //   RAM写使能MemWrite、RAM写入数据MDin等信号
  //   Reset 
  //   没有实现branch delay slot，因此只加4
  //   使用ERET指令来反向MUX
endmodule

module \封装正确性测试  (
);

  wire IR1, IR2, IR3, MemW, RegW;
  wire [31:0] EX_PC, ID_PC, IF_PC, IR, LED, MDin, MDinr, MEM_PC, PC, RDin, RDinr, WB_PC;

  \单周期MIPS  \u_单周期mips_1  (
    .RegWrite(RegW), .MemWrite(MemW), .PC(PC), .IR(IR), .RDin(RDin), .MDin(MDin), .LedData(LED));  // open: IR1, IR2, IR3
  \气泡流水线  \u_气泡流水线_1  (
    .RegWrite(RegW), .MemWrite(MemW), .IF_PC(IF_PC), .ID_PC(ID_PC), .EX_PC(EX_PC), .M_PC(MEM_PC),
    .WB_PC(WB_PC), .RDin(RDinr), .MDin(MDinr), .LedData(LED));
  \单周期MIPS_单级中断  \u_单周期mips_单级中断_1  (
    .IR1(IR1), .IR2(IR2), .IR3(IR3), .RegWrite(RegW), .MemWrite(MemW), .PC(PC), .IR(IR), .RDin(RDin),
    .MDin(MDin), .LedData(LED));
  \理想流水线  \u_理想流水线_1  (
    .RegWrite(RegW), .MemWrite(MemW), .IF_PC(IF_PC), .ID_PC(ID_PC), .EX_PC(EX_PC), .M_PC(MEM_PC),
    .WB_PC(WB_PC), .RDin(RDinr), .MDin(MDinr), .LedData(LED));
  \重定向流水线  \u_重定向流水线_1  (
    .RegWrite(RegW), .MemWrite(MemW), .IF_PC(IF_PC), .ID_PC(ID_PC), .EX_PC(EX_PC), .M_PC(MEM_PC),
    .WB_PC(WB_PC), .RDin(RDinr), .MDin(MDinr), .LedData(LED));
  \单周期MIPS_多级中断  \u_单周期mips_多级中断_1  (
    .IR1(IR1), .IR2(IR2), .IR3(IR3), .RegWrite(RegW), .MemWrite(MemW), .PC(PC), .IR(IR), .RDin(RDin),
    .MDin(MDin), .LedData(LED));

  // Notes on the sheet:
  //   单周期封装测试
  //   气泡流水封装测试
  //   单周期+单级中断封装测试
  //   请检查上面封装有无位宽不匹配，引脚标签是否和连接的标签相对应，否则无法在educoder平台上正确测试
  //   理想流水封装测试
  //   重定向流水封装测试
  //   单周期+多级中断封装测试
endmodule

module IF_ID (
  input  CLK,
  input  [31:0] IF_PC,
  input  [31:0] IF_IR,
  input  RST,
  input  IF_Predict,
  input  RUN,
  input  Bubble,
  input  IF_Valid,
  input  IF_Hit,
  output [31:0] ID_PC,
  output [31:0] ID_IR,
  output ID_Predict,
  output ID_Valid,
  output ID_Hit
);

  wire multiplexer_3_out, multiplexer_4_out, multiplexer_5_out;
  wire [31:0] multiplexer_1_out, multiplexer_2_out;

  Multiplexer #(.select(1), .width(32), .disabled("Z"), .enable("false")) multiplexer_1 (
    .in0(IF_PC), .in1({32{1'b0}}), .out(multiplexer_1_out), .sel(Bubble));
  Multiplexer #(.select(1), .width(32), .disabled("Z"), .enable("false")) multiplexer_2 (
    .in0(IF_IR), .in1({32{1'b0}}), .out(multiplexer_2_out), .sel(Bubble));
  Multiplexer #(.select(1), .width(1), .disabled("Z"), .enable("false")) multiplexer_3 (
    .in0(IF_Predict), .in1(1'b0), .out(multiplexer_3_out), .sel(Bubble));
  Multiplexer #(.select(1), .width(1), .disabled("Z"), .enable("false")) multiplexer_4 (
    .in0(IF_Valid), .in1(1'b0), .out(multiplexer_4_out), .sel(Bubble));
  Multiplexer #(.select(1), .width(1), .disabled("Z"), .enable("false")) multiplexer_5 (
    .in0(IF_Hit), .in1(1'b0), .out(multiplexer_5_out), .sel(Bubble));
  Register #(.width(32), .trigger("rising"), .Select("low")) register_1 (
    .D(multiplexer_1_out), .en(RUN), .Q(ID_PC), .clk(CLK), .clr(RST));
  Register #(.width(32), .trigger("rising"), .Select("low")) register_2 (
    .D(multiplexer_2_out), .en(RUN), .Q(ID_IR), .clk(CLK), .clr(RST));
  Register #(.width(1), .trigger("rising"), .Select("low")) register_3 (
    .D(multiplexer_3_out), .en(RUN), .Q(ID_Predict), .clk(CLK), .clr(RST));
  Register #(.width(1), .trigger("rising"), .Select("low")) register_4 (
    .D(multiplexer_4_out), .en(RUN), .Q(ID_Valid), .clk(CLK), .clr(RST));
  Register #(.width(1), .trigger("rising"), .Select("low")) register_5 (
    .D(multiplexer_5_out), .en(RUN), .Q(ID_Hit), .clk(CLK), .clr(RST));
endmodule

module ID_EX (
  input  ID_B,
  input  CLK,
  input  ID_ERET,
  input  [31:0] ID_PC,
  input  [31:0] ID_IR,
  input  ID_SRLV,
  input  RST,
  input  ID_JMP,
  input  ID_JR,
  input  RUN,
  input  ID_BEQ,
  input  ID_BNE,
  input  ID_BGEZ,
  input  [31:0] ID_R1,
  input  [31:0] ID_R2,
  input  ID_JAL,
  input  ID_MemToReg,
  input  ID_MemWrite,
  input  ID_ALU_SRC,
  input  [4:0] ID_W_num,
  input  ID_RegWrite,
  input  [31:0] ID_ExtImm,
  input  ID_Syscall,
  input  [4:0] ID_sa,
  input  [3:0] ID_AlU_OP,
  input  ID_Predict,
  input  Bubble,
  input  [25:0] ID_Imm26,
  input  ID_MFC0,
  input  ID_MTC0,
  input  [1:0] ID_rs_f,
  input  ID_Valid,
  input  [1:0] ID_rt_f,
  input  in_34,
  output EX_B,
  output EX_ERET,
  output [31:0] EX_PC,
  output [31:0] EX_IR,
  output EX_SRLV,
  output EX_JMP,
  output EX_JR,
  output EX_BEQ,
  output EX_BNE,
  output EX_BGEZ,
  output [31:0] EX_R1,
  output [31:0] EX_R2,
  output EX_JAL,
  output EX_MemToReg,
  output EX_MemReg,
  output EX_ALU_SRC,
  output [4:0] EX_W_num,
  output EX_RegWrite,
  output [31:0] EX_ExtImm,
  output EX_Syscall,
  output [4:0] EX_sa,
  output [3:0] EX_ALU_OP,
  output EX_Predict,
  output [25:0] EX_Imm26,
  output EX_MFC0,
  output EX_MTC0,
  output [1:0] EX_rs_f,
  output [1:0] EX_rt_f,
  output EX_Valid,
  output EX_Hit
);

  wire multiplexer_12_out, multiplexer_13_out, multiplexer_14_out, multiplexer_15_out, multiplexer_16_out;
  wire [1:0] multiplexer_10_out, multiplexer_11_out;
  wire [3:0] multiplexer_7_out;
  wire [4:0] multiplexer_5_out, multiplexer_8_out;
  wire [13:0] multiplexer_17_out;
  wire [25:0] multiplexer_9_out;
  wire [31:0] multiplexer_1_out, multiplexer_2_out, multiplexer_3_out, multiplexer_4_out, multiplexer_6_out;

  Multiplexer #(.select(1), .width(32), .disabled("Z"), .enable("false")) multiplexer_1 (
    .in0(ID_PC), .in1({32{1'b0}}), .out(multiplexer_1_out), .sel(Bubble));
  Multiplexer #(.select(1), .width(32), .disabled("Z"), .enable("false")) multiplexer_2 (
    .in0(ID_IR), .in1({32{1'b0}}), .out(multiplexer_2_out), .sel(Bubble));
  Multiplexer #(.select(1), .width(32), .disabled("Z"), .enable("false")) multiplexer_3 (
    .in0(ID_R1), .in1({32{1'b0}}), .out(multiplexer_3_out), .sel(Bubble));
  Multiplexer #(.select(1), .width(32), .disabled("Z"), .enable("false")) multiplexer_4 (
    .in0(ID_R2), .in1({32{1'b0}}), .out(multiplexer_4_out), .sel(Bubble));
  Multiplexer #(.select(1), .width(5), .disabled("Z"), .enable("false")) multiplexer_5 (
    .in0(ID_W_num), .in1({5{1'b0}}), .out(multiplexer_5_out), .sel(Bubble));
  Multiplexer #(.select(1), .width(32), .disabled("Z"), .enable("false")) multiplexer_6 (
    .in0(ID_ExtImm), .in1({32{1'b0}}), .out(multiplexer_6_out), .sel(Bubble));
  Multiplexer #(.select(1), .width(4), .disabled("Z"), .enable("false")) multiplexer_7 (
    .in0(ID_AlU_OP), .in1(4'b0000), .out(multiplexer_7_out), .sel(Bubble));
  Multiplexer #(.select(1), .width(5), .disabled("Z"), .enable("false")) multiplexer_8 (
    .in0(ID_sa), .in1({5{1'b0}}), .out(multiplexer_8_out), .sel(Bubble));
  Multiplexer #(.select(1), .width(26), .disabled("Z"), .enable("false")) multiplexer_9 (
    .in0(ID_Imm26), .in1({26{1'b0}}), .out(multiplexer_9_out), .sel(Bubble));
  Multiplexer #(.select(1), .width(2), .disabled("Z"), .enable("false")) multiplexer_10 (
    .in0(ID_rs_f), .in1(2'b00), .out(multiplexer_10_out), .sel(Bubble));
  Multiplexer #(.select(1), .width(2), .disabled("Z"), .enable("false")) multiplexer_11 (
    .in0(ID_rt_f), .in1(2'b00), .out(multiplexer_11_out), .sel(Bubble));
  Multiplexer #(.select(1), .width(1), .disabled("Z"), .enable("false")) multiplexer_12 (
    .in0(ID_Predict), .in1(1'b0), .out(multiplexer_12_out), .sel(Bubble));
  Multiplexer #(.select(1), .width(1), .disabled("Z"), .enable("false")) multiplexer_13 (
    .in0(ID_MTC0), .in1(1'b0), .out(multiplexer_13_out), .sel(Bubble));
  Multiplexer #(.select(1), .width(1), .disabled("Z"), .enable("false")) multiplexer_14 (
    .in0(ID_MFC0), .in1(1'b0), .out(multiplexer_14_out), .sel(Bubble));
  Multiplexer #(.select(1), .width(1), .disabled("Z"), .enable("false")) multiplexer_15 (
    .in0(ID_Valid), .in1(1'b0), .out(multiplexer_15_out), .sel(Bubble));
  Multiplexer #(.select(1), .width(1), .disabled("Z"), .enable("false")) multiplexer_16 (
    .in0(in_34), .in1(1'b0), .out(multiplexer_16_out), .sel(Bubble));
  Multiplexer #(.select(1), .width(14), .disabled("Z"), .enable("false")) multiplexer_17 (
    .in0({ID_Syscall, ID_RegWrite, ID_ALU_SRC, ID_MemWrite, ID_MemToReg, ID_JAL, ID_BGEZ, ID_BNE, ID_BEQ, ID_JR, ID_JMP, ID_SRLV, ID_ERET, ID_B}),
    .in1({14{1'b0}}), .out(multiplexer_17_out), .sel(Bubble));
  Register #(.width(32), .trigger("rising"), .Select("low")) register_1 (
    .D(multiplexer_1_out), .en(RUN), .Q(EX_PC), .clk(CLK), .clr(RST));
  Register #(.width(32), .trigger("rising"), .Select("low")) register_2 (
    .D(multiplexer_2_out), .en(RUN), .Q(EX_IR), .clk(CLK), .clr(RST));
  Register #(.width(32), .trigger("rising"), .Select("low")) register_3 (
    .D(multiplexer_3_out), .en(RUN), .Q(EX_R1), .clk(CLK), .clr(RST));
  Register #(.width(32), .trigger("rising"), .Select("low")) register_4 (
    .D(multiplexer_4_out), .en(RUN), .Q(EX_R2), .clk(CLK), .clr(RST));
  Register #(.width(5), .trigger("rising"), .Select("low")) register_5 (
    .D(multiplexer_5_out), .en(RUN), .Q(EX_W_num), .clk(CLK), .clr(RST));
  Register #(.width(32), .trigger("rising"), .Select("low")) register_6 (
    .D(multiplexer_6_out), .en(RUN), .Q(EX_ExtImm), .clk(CLK), .clr(RST));
  Register #(.width(4), .trigger("rising"), .Select("low")) register_7 (
    .D(multiplexer_7_out), .en(RUN), .Q(EX_ALU_OP), .clk(CLK), .clr(RST));
  Register #(.width(5), .trigger("rising"), .Select("low")) register_8 (
    .D(multiplexer_8_out), .en(RUN), .Q(EX_sa), .clk(CLK), .clr(RST));
  Register #(.width(26), .trigger("rising"), .Select("low")) register_9 (
    .D(multiplexer_9_out), .en(RUN), .Q(EX_Imm26), .clk(CLK), .clr(RST));
  Register #(.width(2), .trigger("rising"), .Select("low")) register_10 (
    .D(multiplexer_10_out), .en(RUN), .Q(EX_rs_f), .clk(CLK), .clr(RST));
  Register #(.width(2), .trigger("rising"), .Select("low")) register_11 (
    .D(multiplexer_11_out), .en(RUN), .Q(EX_rt_f), .clk(CLK), .clr(RST));
  Register #(.width(1), .trigger("rising"), .Select("low")) register_12 (
    .D(multiplexer_12_out), .en(RUN), .Q(EX_Predict), .clk(CLK), .clr(RST));
  Register #(.width(1), .trigger("rising"), .Select("low")) register_13 (
    .D(multiplexer_13_out), .en(RUN), .Q(EX_MTC0), .clk(CLK), .clr(RST));
  Register #(.width(1), .trigger("rising"), .Select("low")) register_14 (
    .D(multiplexer_14_out), .en(RUN), .Q(EX_MFC0), .clk(CLK), .clr(RST));
  Register #(.width(1), .trigger("rising"), .Select("low")) register_15 (
    .D(multiplexer_15_out), .en(RUN), .Q(EX_Valid), .clk(CLK), .clr(RST));
  Register #(.width(1), .trigger("rising"), .Select("low")) register_16 (
    .D(multiplexer_16_out), .en(RUN), .Q(EX_Hit), .clk(CLK), .clr(RST));
  Register #(.width(14), .trigger("rising"), .Select("low")) register_17 (
    .D(multiplexer_17_out), .en(RUN),
    .Q({EX_Syscall, EX_RegWrite, EX_ALU_SRC, EX_MemReg, EX_MemToReg, EX_JAL, EX_BGEZ, EX_BNE, EX_BEQ, EX_JR, EX_JMP, EX_SRLV, EX_ERET, EX_B}),
    .clk(CLK), .clr(RST));

  // Other names for the same wires on the sheet: EX_MemWrite = EX_MemReg; ID_Hit = in_34
endmodule

module EX_MEM (
  input  CLK,
  input  [31:0] EX_PC,
  input  [31:0] EX_IR,
  input  EX_B,
  input  RST,
  input  EX_JAL,
  input  RUN,
  input  EX_MemToReg,
  input  EX_MemWrite,
  input  EX_RegWrite,
  input  [31:0] EX_R,
  input  [31:0] EX_MDin,
  input  EX_Syscall,
  input  [4:0] EX_W_num,
  input  [31:0] EX_R1,
  output [31:0] MEM_PC,
  output [31:0] MEM_IR,
  output MEM_B,
  output MEM_JAL,
  output MEM_MemToReg,
  output MEM_MemWrite,
  output MEM_RegWrite,
  output [31:0] MEM_R,
  output [31:0] MEM_MDin,
  output MEM_Syscall,
  output [4:0] MEM_W_num,
  output [31:0] MEM_R1
);

  Register #(.width(32), .trigger("rising"), .Select("low")) register_1 (
    .D(EX_R1), .en(RUN), .Q(MEM_R1), .clk(CLK), .clr(RST));
  Register #(.width(32), .trigger("rising"), .Select("low")) register_2 (
    .D(EX_PC), .en(RUN), .Q(MEM_PC), .clk(CLK), .clr(RST));
  Register #(.width(32), .trigger("rising"), .Select("low")) register_3 (
    .D(EX_IR), .en(RUN), .Q(MEM_IR), .clk(CLK), .clr(RST));
  Register #(.width(32), .trigger("rising"), .Select("low")) register_4 (
    .D(EX_R), .en(RUN), .Q(MEM_R), .clk(CLK), .clr(RST));
  Register #(.width(32), .trigger("rising"), .Select("low")) register_5 (
    .D(EX_MDin), .en(RUN), .Q(MEM_MDin), .clk(CLK), .clr(RST));
  Register #(.width(5), .trigger("rising"), .Select("low")) register_6 (
    .D(EX_W_num), .en(RUN), .Q(MEM_W_num), .clk(CLK), .clr(RST));
  Register #(.width(6), .trigger("rising"), .Select("low")) register_7 (
    .D({EX_Syscall, EX_RegWrite, EX_MemWrite, EX_MemToReg, EX_JAL, EX_B}), .en(RUN),
    .Q({MEM_Syscall, MEM_RegWrite, MEM_MemWrite, MEM_MemToReg, MEM_JAL, MEM_B}), .clk(CLK), .clr(RST));
endmodule

module MEM_WB (
  input  [31:0] MEM_PC,
  input  [31:0] MEM_IR,
  input  [31:0] MEM_MDin,
  input  RUN,
  input  [31:0] MEM_MDout,
  input  CLK,
  input  RST,
  input  [31:0] MEM_R,
  input  MEM_JAL,
  input  [4:0] MEM_W_num,
  input  MEM_MemToReg,
  input  MEM_RegWrite,
  input  MEM_Syscall,
  input  [31:0] MEM_R1,
  output [31:0] WB_PC,
  output [31:0] WB_IR,
  output [31:0] WB_MDin,
  output [31:0] WB_MDout,
  output [31:0] WB_R,
  output WB_JAL,
  output [4:0] WB_W_num,
  output WB_MemToReg,
  output WB_RegWrite,
  output WB_Syscall,
  output [31:0] WB_R1
);

  Register #(.width(32), .trigger("rising"), .Select("low")) register_1 (
    .D(MEM_PC), .en(RUN), .Q(WB_PC), .clk(CLK), .clr(RST));
  Register #(.width(32), .trigger("rising"), .Select("low")) register_2 (
    .D(MEM_IR), .en(RUN), .Q(WB_IR), .clk(CLK), .clr(RST));
  Register #(.width(32), .trigger("rising"), .Select("low")) register_3 (
    .D(MEM_MDout), .en(RUN), .Q(WB_MDout), .clk(CLK), .clr(RST));
  Register #(.width(32), .trigger("rising"), .Select("low")) register_4 (
    .D(MEM_R), .en(RUN), .Q(WB_R), .clk(CLK), .clr(RST));
  Register #(.width(5), .trigger("rising"), .Select("low")) register_5 (
    .D(MEM_W_num), .en(RUN), .Q(WB_W_num), .clk(CLK), .clr(RST));
  Register #(.width(3), .trigger("rising"), .Select("low")) register_6 (
    .D({MEM_RegWrite, MEM_JAL, MEM_MemToReg}), .en(RUN), .Q({WB_RegWrite, WB_JAL, WB_MemToReg}), .clk(CLK),
    .clr(RST));
  Register #(.width(1), .trigger("rising"), .Select("low")) register_7 (
    .D(MEM_Syscall), .en(RUN), .Q(WB_Syscall), .clk(CLK), .clr(RST));
  Register #(.width(32), .trigger("rising"), .Select("low")) register_8 (
    .D(MEM_R1), .en(RUN), .Q(WB_R1), .clk(CLK), .clr(RST));
  Register #(.width(32), .trigger("rising"), .Select("low")) register_9 (
    .D(MEM_MDin), .en(RUN), .Q(WB_MDin), .clk(CLK), .clr(RST));
endmodule

// Rs&Rt-Used
module Rs_Rt (
  input  OP0,
  input  OP1,
  input  OP2,
  input  OP3,
  input  OP4,
  input  OP5,
  input  F0,
  input  F1,
  input  F2,
  input  F3,
  input  F4,
  input  F5,
  output RsUsed,
  output RtUsed
);

  wire and_1_out, and_2_out, and_3_out, and_4_out, and_5_out, and_6_out, and_7_out, and_8_out, and_9_out,
       and_10_out, and_11_out, and_12_out, and_13_out, and_14_out, and_15_out, and_16_out, and_17_out,
       and_18_out, and_19_out, and_20_out, and_21_out, and_22_out, and_23_out, and_24_out, and_25_out,
       and_26_out, and_27_out, and_28_out, and_29_out, and_30_out, and_31_out, and_32_out, and_33_out,
       and_34_out, and_35_out, and_36_out, and_37_out, and_38_out, and_39_out, and_40_out, and_41_out,
       and_42_out, and_43_out, and_44_out, not_1_out, not_2_out, not_3_out, not_4_out, not_5_out, not_6_out,
       not_7_out, not_8_out, not_9_out, not_10_out, not_11_out, not_12_out, not_13_out, not_14_out,
       not_15_out, not_16_out, not_17_out, not_18_out, not_19_out, not_20_out, not_21_out, not_22_out,
       not_23_out, not_24_out, not_25_out, not_26_out, not_27_out, not_28_out, not_29_out, not_30_out,
       not_31_out, not_32_out, not_33_out, not_34_out, not_35_out, not_36_out, not_37_out, not_38_out,
       not_39_out, not_40_out, not_41_out, not_42_out, not_43_out, not_44_out, not_45_out, not_46_out,
       not_47_out, not_48_out, not_49_out, not_50_out, not_51_out, not_52_out, not_53_out, not_54_out,
       not_55_out, not_56_out, not_57_out, not_58_out, not_59_out, not_60_out, not_61_out, not_62_out,
       not_63_out, not_64_out, not_65_out, not_66_out, not_67_out, not_68_out, not_69_out, not_70_out,
       not_71_out, not_72_out, not_73_out, not_74_out, not_75_out, not_76_out, not_77_out, not_78_out,
       not_79_out, not_80_out, not_81_out, not_82_out, not_83_out, not_84_out, not_85_out, not_86_out,
       not_87_out, not_88_out, not_89_out, not_90_out, not_91_out, not_92_out, not_93_out, not_94_out,
       not_95_out, not_96_out, not_97_out, not_98_out, not_99_out, not_100_out, not_101_out, not_102_out,
       not_103_out, not_104_out, not_105_out, not_106_out, not_107_out, not_108_out, not_109_out,
       not_110_out, not_111_out, not_112_out, not_113_out, not_114_out, not_115_out, not_116_out,
       not_117_out, not_118_out, not_119_out, not_120_out, not_121_out, not_122_out, not_123_out,
       not_124_out, not_125_out, not_126_out, not_127_out, not_128_out, not_129_out, not_130_out,
       not_131_out, not_132_out, not_133_out, not_134_out, not_135_out, not_136_out, not_137_out,
       not_138_out, not_139_out, not_140_out, not_141_out, not_142_out, not_143_out, not_144_out,
       not_145_out, not_146_out, not_147_out, not_148_out, not_149_out, not_150_out, not_151_out,
       not_152_out, not_153_out, not_154_out, not_155_out, not_156_out, not_157_out, not_158_out,
       not_159_out, not_160_out, not_161_out, not_162_out, not_163_out, not_164_out, not_165_out,
       not_166_out, not_167_out, not_168_out, not_169_out, not_170_out, not_171_out, not_172_out,
       not_173_out, not_174_out, not_175_out, not_176_out, not_177_out, not_178_out, not_179_out,
       not_180_out, not_181_out, not_182_out, not_183_out, not_184_out, not_185_out, not_186_out,
       not_187_out, not_188_out, not_189_out, not_190_out, not_191_out, not_192_out, not_193_out,
       not_194_out, not_195_out, not_196_out, not_197_out, not_198_out, not_199_out, not_200_out,
       not_201_out, not_202_out, not_203_out, not_204_out, not_205_out, not_206_out, not_207_out,
       not_208_out, not_209_out, not_210_out, not_211_out, not_212_out, not_213_out, not_214_out,
       not_215_out, not_216_out, not_217_out, not_218_out, not_219_out, not_220_out, not_221_out,
       not_222_out, not_223_out, not_224_out, not_225_out, not_226_out, not_227_out, not_228_out,
       not_229_out, not_230_out, not_231_out, not_232_out, not_233_out, not_234_out, not_235_out,
       not_236_out, not_237_out, not_238_out, not_239_out, not_240_out, not_241_out, not_242_out,
       not_243_out, not_244_out, not_245_out, not_246_out, not_247_out, not_248_out, not_249_out,
       not_250_out, not_251_out, not_252_out, not_253_out, not_254_out, not_255_out, not_256_out,
       not_257_out, not_258_out, not_259_out, not_260_out, not_261_out, not_262_out, not_263_out,
       not_264_out, not_265_out, not_266_out, not_267_out, not_268_out, not_269_out, not_270_out,
       not_271_out, not_272_out, not_273_out, not_274_out, not_275_out, not_276_out, not_277_out,
       not_278_out, not_279_out, not_280_out, not_281_out, not_282_out, not_283_out, not_284_out,
       not_285_out, not_286_out, not_287_out, not_288_out, not_289_out, not_290_out, not_291_out,
       not_292_out, not_293_out, not_294_out, not_295_out, not_296_out, not_297_out, not_298_out,
       not_299_out, not_300_out, not_301_out, not_302_out, not_303_out, not_304_out, not_305_out,
       not_306_out, not_307_out, not_308_out, not_309_out, not_310_out, not_311_out, not_312_out,
       not_313_out, not_314_out, not_315_out, not_316_out, not_317_out, not_318_out, not_319_out,
       not_320_out, not_321_out, not_322_out, not_323_out, not_324_out, not_325_out, not_326_out,
       not_327_out, not_328_out, not_329_out, not_330_out, not_331_out, not_332_out, not_333_out,
       not_334_out, not_335_out, not_336_out, not_337_out, not_338_out, not_339_out, not_340_out,
       not_341_out, not_342_out, not_343_out;

  not not_1 (not_1_out, OP5);
  not not_2 (not_2_out, OP4);
  not not_3 (not_3_out, OP3);
  not not_4 (not_4_out, OP2);
  not not_5 (not_5_out, OP1);
  not not_6 (not_6_out, OP0);
  not not_7 (not_7_out, F5);
  not not_8 (not_8_out, F4);
  not not_9 (not_9_out, F3);
  not not_10 (not_10_out, F2);
  not not_11 (not_11_out, F1);
  not not_12 (not_12_out, F0);
  not not_13 (not_13_out, OP5);
  not not_14 (not_14_out, OP4);
  not not_15 (not_15_out, OP3);
  not not_16 (not_16_out, OP2);
  not not_17 (not_17_out, OP1);
  not not_18 (not_18_out, OP0);
  not not_19 (not_19_out, F5);
  not not_20 (not_20_out, F4);
  not not_21 (not_21_out, F3);
  not not_22 (not_22_out, F2);
  not not_23 (not_23_out, OP5);
  not not_24 (not_24_out, OP4);
  not not_25 (not_25_out, OP3);
  not not_26 (not_26_out, OP2);
  not not_27 (not_27_out, OP1);
  not not_28 (not_28_out, OP0);
  not not_29 (not_29_out, F5);
  not not_30 (not_30_out, F4);
  not not_31 (not_31_out, F3);
  not not_32 (not_32_out, F2);
  not not_33 (not_33_out, F0);
  not not_34 (not_34_out, OP5);
  not not_35 (not_35_out, OP4);
  not not_36 (not_36_out, OP3);
  not not_37 (not_37_out, OP2);
  not not_38 (not_38_out, OP1);
  not not_39 (not_39_out, OP0);
  not not_40 (not_40_out, F4);
  not not_41 (not_41_out, F3);
  not not_42 (not_42_out, F2);
  not not_43 (not_43_out, F1);
  not not_44 (not_44_out, F0);
  not not_45 (not_45_out, OP5);
  not not_46 (not_46_out, OP4);
  not not_47 (not_47_out, OP3);
  not not_48 (not_48_out, OP2);
  not not_49 (not_49_out, OP1);
  not not_50 (not_50_out, OP0);
  not not_51 (not_51_out, F4);
  not not_52 (not_52_out, F3);
  not not_53 (not_53_out, F2);
  not not_54 (not_54_out, F1);
  not not_55 (not_55_out, OP5);
  not not_56 (not_56_out, OP4);
  not not_57 (not_57_out, OP3);
  not not_58 (not_58_out, OP2);
  not not_59 (not_59_out, OP1);
  not not_60 (not_60_out, OP0);
  not not_61 (not_61_out, F4);
  not not_62 (not_62_out, F3);
  not not_63 (not_63_out, F2);
  not not_64 (not_64_out, F0);
  not not_65 (not_65_out, OP5);
  not not_66 (not_66_out, OP4);
  not not_67 (not_67_out, OP3);
  not not_68 (not_68_out, OP2);
  not not_69 (not_69_out, OP1);
  not not_70 (not_70_out, OP0);
  not not_71 (not_71_out, F4);
  not not_72 (not_72_out, F3);
  not not_73 (not_73_out, F1);
  not not_74 (not_74_out, F0);
  not not_75 (not_75_out, OP5);
  not not_76 (not_76_out, OP4);
  not not_77 (not_77_out, OP3);
  not not_78 (not_78_out, OP2);
  not not_79 (not_79_out, OP1);
  not not_80 (not_80_out, OP0);
  not not_81 (not_81_out, F4);
  not not_82 (not_82_out, F3);
  not not_83 (not_83_out, F1);
  not not_84 (not_84_out, OP5);
  not not_85 (not_85_out, OP4);
  not not_86 (not_86_out, OP3);
  not not_87 (not_87_out, OP2);
  not not_88 (not_88_out, OP1);
  not not_89 (not_89_out, OP0);
  not not_90 (not_90_out, F4);
  not not_91 (not_91_out, F3);
  not not_92 (not_92_out, OP5);
  not not_93 (not_93_out, OP4);
  not not_94 (not_94_out, OP3);
  not not_95 (not_95_out, OP2);
  not not_96 (not_96_out, OP1);
  not not_97 (not_97_out, OP0);
  not not_98 (not_98_out, F4);
  not not_99 (not_99_out, F2);
  not not_100 (not_100_out, F0);
  not not_101 (not_101_out, OP5);
  not not_102 (not_102_out, OP4);
  not not_103 (not_103_out, OP3);
  not not_104 (not_104_out, OP2);
  not not_105 (not_105_out, OP1);
  not not_106 (not_106_out, OP0);
  not not_107 (not_107_out, F4);
  not not_108 (not_108_out, F2);
  not not_109 (not_109_out, OP5);
  not not_110 (not_110_out, OP4);
  not not_111 (not_111_out, OP3);
  not not_112 (not_112_out, OP2);
  not not_113 (not_113_out, OP1);
  not not_114 (not_114_out, OP0);
  not not_115 (not_115_out, F5);
  not not_116 (not_116_out, F4);
  not not_117 (not_117_out, F2);
  not not_118 (not_118_out, F1);
  not not_119 (not_119_out, F0);
  not not_120 (not_120_out, OP5);
  not not_121 (not_121_out, OP4);
  not not_122 (not_122_out, OP3);
  not not_123 (not_123_out, OP2);
  not not_124 (not_124_out, OP1);
  not not_125 (not_125_out, OP0);
  not not_126 (not_126_out, F5);
  not not_127 (not_127_out, F4);
  not not_128 (not_128_out, F1);
  not not_129 (not_129_out, F0);
  not not_130 (not_130_out, OP5);
  not not_131 (not_131_out, OP4);
  not not_132 (not_132_out, OP3);
  not not_133 (not_133_out, OP1);
  not not_134 (not_134_out, OP0);
  not not_135 (not_135_out, OP5);
  not not_136 (not_136_out, OP4);
  not not_137 (not_137_out, OP3);
  not not_138 (not_138_out, OP1);
  not not_139 (not_139_out, OP5);
  not not_140 (not_140_out, OP4);
  not not_141 (not_141_out, OP2);
  not not_142 (not_142_out, OP1);
  not not_143 (not_143_out, OP0);
  not not_144 (not_144_out, OP5);
  not not_145 (not_145_out, OP4);
  not not_146 (not_146_out, OP1);
  not not_147 (not_147_out, OP0);
  not not_148 (not_148_out, OP5);
  not not_149 (not_149_out, OP4);
  not not_150 (not_150_out, OP2);
  not not_151 (not_151_out, OP1);
  not not_152 (not_152_out, OP5);
  not not_153 (not_153_out, OP4);
  not not_154 (not_154_out, OP2);
  not not_155 (not_155_out, OP0);
  not not_156 (not_156_out, OP5);
  not not_157 (not_157_out, OP4);
  not not_158 (not_158_out, OP1);
  not not_159 (not_159_out, OP4);
  not not_160 (not_160_out, OP3);
  not not_161 (not_161_out, OP2);
  not not_162 (not_162_out, OP4);
  not not_163 (not_163_out, OP2);
  not not_164 (not_164_out, OP5);
  not not_165 (not_165_out, OP4);
  not not_166 (not_166_out, OP3);
  not not_167 (not_167_out, OP2);
  not not_168 (not_168_out, OP1);
  not not_169 (not_169_out, OP0);
  not not_170 (not_170_out, F5);
  not not_171 (not_171_out, F4);
  not not_172 (not_172_out, F3);
  not not_173 (not_173_out, F0);
  not not_174 (not_174_out, OP5);
  not not_175 (not_175_out, OP4);
  not not_176 (not_176_out, OP3);
  not not_177 (not_177_out, OP2);
  not not_178 (not_178_out, OP1);
  not not_179 (not_179_out, OP0);
  not not_180 (not_180_out, F4);
  not not_181 (not_181_out, F3);
  not not_182 (not_182_out, F0);
  not not_183 (not_183_out, OP4);
  not not_184 (not_184_out, OP2);
  not not_185 (not_185_out, OP1);
  not not_186 (not_186_out, OP0);
  not not_187 (not_187_out, OP5);
  not not_188 (not_188_out, OP4);
  not not_189 (not_189_out, OP3);
  not not_190 (not_190_out, OP2);
  not not_191 (not_191_out, OP1);
  not not_192 (not_192_out, OP5);
  not not_193 (not_193_out, OP4);
  not not_194 (not_194_out, OP3);
  not not_195 (not_195_out, OP2);
  not not_196 (not_196_out, OP1);
  not not_197 (not_197_out, OP0);
  not not_198 (not_198_out, F5);
  not not_199 (not_199_out, F4);
  not not_200 (not_200_out, F3);
  not not_201 (not_201_out, F2);
  not not_202 (not_202_out, F1);
  not not_203 (not_203_out, F0);
  not not_204 (not_204_out, OP5);
  not not_205 (not_205_out, OP4);
  not not_206 (not_206_out, OP3);
  not not_207 (not_207_out, OP2);
  not not_208 (not_208_out, OP1);
  not not_209 (not_209_out, OP0);
  not not_210 (not_210_out, F5);
  not not_211 (not_211_out, F4);
  not not_212 (not_212_out, F3);
  not not_213 (not_213_out, F2);
  not not_214 (not_214_out, OP5);
  not not_215 (not_215_out, OP4);
  not not_216 (not_216_out, OP3);
  not not_217 (not_217_out, OP2);
  not not_218 (not_218_out, OP1);
  not not_219 (not_219_out, OP0);
  not not_220 (not_220_out, F5);
  not not_221 (not_221_out, F4);
  not not_222 (not_222_out, F3);
  not not_223 (not_223_out, F2);
  not not_224 (not_224_out, F0);
  not not_225 (not_225_out, OP5);
  not not_226 (not_226_out, OP4);
  not not_227 (not_227_out, OP3);
  not not_228 (not_228_out, OP2);
  not not_229 (not_229_out, OP1);
  not not_230 (not_230_out, OP0);
  not not_231 (not_231_out, F4);
  not not_232 (not_232_out, F3);
  not not_233 (not_233_out, F2);
  not not_234 (not_234_out, F1);
  not not_235 (not_235_out, F0);
  not not_236 (not_236_out, OP5);
  not not_237 (not_237_out, OP4);
  not not_238 (not_238_out, OP3);
  not not_239 (not_239_out, OP2);
  not not_240 (not_240_out, OP1);
  not not_241 (not_241_out, OP0);
  not not_242 (not_242_out, F4);
  not not_243 (not_243_out, F3);
  not not_244 (not_244_out, F2);
  not not_245 (not_245_out, F1);
  not not_246 (not_246_out, OP5);
  not not_247 (not_247_out, OP4);
  not not_248 (not_248_out, OP3);
  not not_249 (not_249_out, OP2);
  not not_250 (not_250_out, OP1);
  not not_251 (not_251_out, OP0);
  not not_252 (not_252_out, F4);
  not not_253 (not_253_out, F3);
  not not_254 (not_254_out, F2);
  not not_255 (not_255_out, F0);
  not not_256 (not_256_out, OP5);
  not not_257 (not_257_out, OP4);
  not not_258 (not_258_out, OP3);
  not not_259 (not_259_out, OP2);
  not not_260 (not_260_out, OP1);
  not not_261 (not_261_out, OP0);
  not not_262 (not_262_out, F4);
  not not_263 (not_263_out, F3);
  not not_264 (not_264_out, F1);
  not not_265 (not_265_out, F0);
  not not_266 (not_266_out, OP5);
  not not_267 (not_267_out, OP4);
  not not_268 (not_268_out, OP3);
  not not_269 (not_269_out, OP2);
  not not_270 (not_270_out, OP1);
  not not_271 (not_271_out, OP0);
  not not_272 (not_272_out, F4);
  not not_273 (not_273_out, F3);
  not not_274 (not_274_out, F1);
  not not_275 (not_275_out, OP5);
  not not_276 (not_276_out, OP4);
  not not_277 (not_277_out, OP3);
  not not_278 (not_278_out, OP2);
  not not_279 (not_279_out, OP1);
  not not_280 (not_280_out, OP0);
  not not_281 (not_281_out, F4);
  not not_282 (not_282_out, F3);
  not not_283 (not_283_out, OP5);
  not not_284 (not_284_out, OP4);
  not not_285 (not_285_out, OP3);
  not not_286 (not_286_out, OP2);
  not not_287 (not_287_out, OP1);
  not not_288 (not_288_out, OP0);
  not not_289 (not_289_out, F4);
  not not_290 (not_290_out, F2);
  not not_291 (not_291_out, F0);
  not not_292 (not_292_out, OP5);
  not not_293 (not_293_out, OP4);
  not not_294 (not_294_out, OP3);
  not not_295 (not_295_out, OP2);
  not not_296 (not_296_out, OP1);
  not not_297 (not_297_out, OP0);
  not not_298 (not_298_out, F4);
  not not_299 (not_299_out, F2);
  not not_300 (not_300_out, OP5);
  not not_301 (not_301_out, OP4);
  not not_302 (not_302_out, OP3);
  not not_303 (not_303_out, OP2);
  not not_304 (not_304_out, OP1);
  not not_305 (not_305_out, OP0);
  not not_306 (not_306_out, F5);
  not not_307 (not_307_out, F4);
  not not_308 (not_308_out, F1);
  not not_309 (not_309_out, F0);
  not not_310 (not_310_out, OP5);
  not not_311 (not_311_out, OP4);
  not not_312 (not_312_out, OP3);
  not not_313 (not_313_out, OP1);
  not not_314 (not_314_out, OP0);
  not not_315 (not_315_out, OP5);
  not not_316 (not_316_out, OP4);
  not not_317 (not_317_out, OP3);
  not not_318 (not_318_out, OP1);
  not not_319 (not_319_out, OP4);
  not not_320 (not_320_out, OP2);
  not not_321 (not_321_out, OP5);
  not not_322 (not_322_out, OP4);
  not not_323 (not_323_out, OP3);
  not not_324 (not_324_out, OP2);
  not not_325 (not_325_out, OP1);
  not not_326 (not_326_out, OP0);
  not not_327 (not_327_out, F5);
  not not_328 (not_328_out, F4);
  not not_329 (not_329_out, F3);
  not not_330 (not_330_out, F0);
  not not_331 (not_331_out, OP5);
  not not_332 (not_332_out, OP4);
  not not_333 (not_333_out, OP3);
  not not_334 (not_334_out, OP2);
  not not_335 (not_335_out, OP1);
  not not_336 (not_336_out, OP0);
  not not_337 (not_337_out, F4);
  not not_338 (not_338_out, F3);
  not not_339 (not_339_out, F0);
  not not_340 (not_340_out, OP4);
  not not_341 (not_341_out, OP2);
  not not_342 (not_342_out, OP1);
  not not_343 (not_343_out, OP0);
  and and_1 (and_1_out, not_1_out, not_2_out, not_3_out, not_4_out, not_5_out, not_6_out, not_7_out, not_8_out, not_9_out, not_10_out, not_11_out, not_12_out);
  and and_2 (and_2_out, not_13_out, not_14_out, not_15_out, not_16_out, not_17_out, not_18_out, not_19_out, not_20_out, not_21_out, not_22_out, F1, F0);
  and and_3 (and_3_out, not_23_out, not_24_out, not_25_out, not_26_out, not_27_out, not_28_out, not_29_out, not_30_out, not_31_out, not_32_out, F1, not_33_out);
  and and_4 (and_4_out, not_34_out, not_35_out, not_36_out, not_37_out, not_38_out, not_39_out, F5, not_40_out, not_41_out, not_42_out, not_43_out, not_44_out);
  and and_5 (and_5_out, not_45_out, not_46_out, not_47_out, not_48_out, not_49_out, not_50_out, F5, not_51_out, not_52_out, not_53_out, not_54_out, F0);
  and and_6 (and_6_out, not_55_out, not_56_out, not_57_out, not_58_out, not_59_out, not_60_out, F5, not_61_out, not_62_out, not_63_out, F1, not_64_out);
  and and_7 (and_7_out, not_65_out, not_66_out, not_67_out, not_68_out, not_69_out, not_70_out, F5, not_71_out, not_72_out, F2, not_73_out, not_74_out);
  and and_8 (and_8_out, not_75_out, not_76_out, not_77_out, not_78_out, not_79_out, not_80_out, F5, not_81_out, not_82_out, F2, not_83_out, F0);
  and and_9 (and_9_out, not_84_out, not_85_out, not_86_out, not_87_out, not_88_out, not_89_out, F5, not_90_out, not_91_out, F2, F1, F0);
  and and_10 (and_10_out, not_92_out, not_93_out, not_94_out, not_95_out, not_96_out, not_97_out, F5, not_98_out, F3, not_99_out, F1, not_100_out);
  and and_11 (and_11_out, not_101_out, not_102_out, not_103_out, not_104_out, not_105_out, not_106_out, F5, not_107_out, F3, not_108_out, F1, F0);
  and and_12 (and_12_out, not_109_out, not_110_out, not_111_out, not_112_out, not_113_out, not_114_out, not_115_out, not_116_out, F3, not_117_out, not_118_out, not_119_out);
  and and_13 (and_13_out, not_120_out, not_121_out, not_122_out, not_123_out, not_124_out, not_125_out, not_126_out, not_127_out, F3, F2, not_128_out, not_129_out);
  and and_14 (and_14_out, not_130_out, not_131_out, not_132_out, OP2, not_133_out, not_134_out);
  and and_15 (and_15_out, not_135_out, not_136_out, not_137_out, OP2, not_138_out, OP0);
  and and_16 (and_16_out, not_139_out, not_140_out, OP3, not_141_out, not_142_out, not_143_out);
  and and_17 (and_17_out, not_144_out, not_145_out, OP3, OP2, not_146_out, not_147_out);
  and and_18 (and_18_out, not_148_out, not_149_out, OP3, not_150_out, not_151_out, OP0);
  and and_19 (and_19_out, not_152_out, not_153_out, OP3, not_154_out, OP1, not_155_out);
  and and_20 (and_20_out, not_156_out, not_157_out, OP3, OP2, not_158_out, OP0);
  and and_21 (and_21_out, OP5, not_159_out, not_160_out, not_161_out, OP1, OP0);
  and and_22 (and_22_out, OP5, not_162_out, OP3, not_163_out, OP1, OP0);
  and and_23 (and_23_out, not_164_out, not_165_out, not_166_out, not_167_out, not_168_out, not_169_out, not_170_out, not_171_out, not_172_out, F2, F1, not_173_out);
  and and_24 (and_24_out, not_174_out, not_175_out, not_176_out, not_177_out, not_178_out, not_179_out, F5, not_180_out, not_181_out, F2, F1, not_182_out);
  and and_25 (and_25_out, OP5, not_183_out, OP3, not_184_out, not_185_out, not_186_out);
  and and_26 (and_26_out, not_187_out, not_188_out, not_189_out, not_190_out, not_191_out, OP0);
  and and_27 (and_27_out, not_192_out, not_193_out, not_194_out, not_195_out, not_196_out, not_197_out, not_198_out, not_199_out, not_200_out, not_201_out, not_202_out, not_203_out);
  and and_28 (and_28_out, not_204_out, not_205_out, not_206_out, not_207_out, not_208_out, not_209_out, not_210_out, not_211_out, not_212_out, not_213_out, F1, F0);
  and and_29 (and_29_out, not_214_out, not_215_out, not_216_out, not_217_out, not_218_out, not_219_out, not_220_out, not_221_out, not_222_out, not_223_out, F1, not_224_out);
  and and_30 (and_30_out, not_225_out, not_226_out, not_227_out, not_228_out, not_229_out, not_230_out, F5, not_231_out, not_232_out, not_233_out, not_234_out, not_235_out);
  and and_31 (and_31_out, not_236_out, not_237_out, not_238_out, not_239_out, not_240_out, not_241_out, F5, not_242_out, not_243_out, not_244_out, not_245_out, F0);
  and and_32 (and_32_out, not_246_out, not_247_out, not_248_out, not_249_out, not_250_out, not_251_out, F5, not_252_out, not_253_out, not_254_out, F1, not_255_out);
  and and_33 (and_33_out, not_256_out, not_257_out, not_258_out, not_259_out, not_260_out, not_261_out, F5, not_262_out, not_263_out, F2, not_264_out, not_265_out);
  and and_34 (and_34_out, not_266_out, not_267_out, not_268_out, not_269_out, not_270_out, not_271_out, F5, not_272_out, not_273_out, F2, not_274_out, F0);
  and and_35 (and_35_out, not_275_out, not_276_out, not_277_out, not_278_out, not_279_out, not_280_out, F5, not_281_out, not_282_out, F2, F1, F0);
  and and_36 (and_36_out, not_283_out, not_284_out, not_285_out, not_286_out, not_287_out, not_288_out, F5, not_289_out, F3, not_290_out, F1, not_291_out);
  and and_37 (and_37_out, not_292_out, not_293_out, not_294_out, not_295_out, not_296_out, not_297_out, F5, not_298_out, F3, not_299_out, F1, F0);
  and and_38 (and_38_out, not_300_out, not_301_out, not_302_out, not_303_out, not_304_out, not_305_out, not_306_out, not_307_out, F3, F2, not_308_out, not_309_out);
  and and_39 (and_39_out, not_310_out, not_311_out, not_312_out, OP2, not_313_out, not_314_out);
  and and_40 (and_40_out, not_315_out, not_316_out, not_317_out, OP2, not_318_out, OP0);
  and and_41 (and_41_out, OP5, not_319_out, OP3, not_320_out, OP1, OP0);
  and and_42 (and_42_out, not_321_out, not_322_out, not_323_out, not_324_out, not_325_out, not_326_out, not_327_out, not_328_out, not_329_out, F2, F1, not_330_out);
  and and_43 (and_43_out, not_331_out, not_332_out, not_333_out, not_334_out, not_335_out, not_336_out, F5, not_337_out, not_338_out, F2, F1, not_339_out);
  and and_44 (and_44_out, OP5, not_340_out, OP3, not_341_out, not_342_out, not_343_out);
  or or_1 (RsUsed, and_1_out, and_2_out, and_3_out, and_4_out, and_5_out, and_6_out, and_7_out, and_8_out, and_9_out, and_10_out, and_11_out, and_12_out, and_13_out, and_14_out, and_15_out, and_16_out, and_17_out, and_18_out, and_19_out, and_20_out, and_21_out, and_22_out, and_23_out, and_24_out, and_25_out, and_26_out);
  or or_2 (RtUsed, and_27_out, and_28_out, and_29_out, and_30_out, and_31_out, and_32_out, and_33_out, and_34_out, and_35_out, and_36_out, and_37_out, and_38_out, and_39_out, and_40_out, and_41_out, and_42_out, and_43_out, and_44_out);
endmodule

module BTB (
  input  [31:0] BTin,
  input  [31:0] BranchPC,
  input  CLK,
  input  Branch,
  input  J,
  input  [31:0] CurrentPC,
  output [31:0] BTout,
  output PredictJmp,
  output Hit
);

  wire and_17_out, and_18_out, and_19_out, and_20_out, and_21_out, and_22_out, and_23_out, and_24_out,
       and_25_out, and_26_out, and_27_out, and_28_out, and_29_out, and_30_out, and_31_out, and_32_out,
       and_33_out, comparator_1_eq, comparator_2_eq, comparator_3_eq, comparator_4_eq, comparator_5_eq,
       comparator_6_eq, comparator_7_eq, comparator_8_eq, comparator_9_eq, comparator_10_eq,
       comparator_11_eq, comparator_12_eq, comparator_13_eq, comparator_14_eq, comparator_15_eq,
       comparator_16_eq, d_ff_1_q, d_ff_2_q, d_ff_3_q, d_ff_4_q, d_ff_5_q, d_ff_6_q, d_ff_7_q, d_ff_8_q,
       full, line0, line0p, line1, line1p, line2, line2p, line3, line3p, line4, line4p, line5, line5p, line6,
       line6p, line7, line7p, Miss, multiplexer_3_out, not_1_out, not_2_out, not_3_out, not_4_out, not_5_out,
       not_6_out, not_7_out, not_8_out, or_1_out, or_2_out, or_3_out, or_4_out, or_5_out, or_6_out, or_7_out,
       or_8_out, or_9_out, PredictJmp0, PredictJmp1, PredictJmp2, PredictJmp3, PredictJmp4, PredictJmp5,
       PredictJmp6, PredictJmp7, priority_encoder_1_en_out, v0, v1, v2, v3, v4, v5, v6, v7, Write0, Write1,
       Write2, Write3, Write4, Write5, Write6, Write7;
  wire [2:0] emptyRow, max3merge_1_max_num, max3merge_2_max_num, max3merge_3_max_num, max3merge_4_max_num,
       max3merge_5_max_num, max3merge_6_max_num, multiplexer_4_out, obsRow, priority_encoder_1_out;
  wire [15:0] c0, c1, c2, c3, c4, c5, c6, c7, max3merge_1_max, max3merge_2_max, max3merge_3_max,
       max3merge_4_max, max3merge_5_max, max3merge_6_max;
  wire [31:0] multiplexer_1_out, multiplexer_2_out, SlotData0, SlotData1, SlotData2, SlotData3, SlotData4,
       SlotData5, SlotData6, SlotData7, tag_2_q, tag_3_q, tag_4_q, tag_5_q, tag_6_q, tag_7_q, tag_8_q, tag_q;

  Multiplexer #(.select(1), .width(32), .disabled("Z"), .enable("false")) multiplexer_1 (
    .in0(CurrentPC), .in1(BranchPC), .out(multiplexer_1_out), .sel(Branch));
  Register #(.width(1), .trigger("rising"), .Select("low")) valid (
    .D(Write0), .en(Write0), .Q(v0), .clk(CLK));  // open: clr
  Register #(.width(1), .trigger("rising"), .Select("low")) valid_2 (
    .D(Write1), .en(Write1), .Q(v1), .clk(CLK));  // open: clr
  Register #(.width(1), .trigger("rising"), .Select("low")) valid_3 (
    .D(Write2), .en(Write2), .Q(v2), .clk(CLK));  // open: clr
  Register #(.width(1), .trigger("rising"), .Select("low")) valid_4 (
    .D(Write3), .en(Write3), .Q(v3), .clk(CLK));  // open: clr
  Register #(.width(1), .trigger("rising"), .Select("low")) valid_5 (
    .D(Write4), .en(Write4), .Q(v4), .clk(CLK));  // open: clr
  Register #(.width(1), .trigger("rising"), .Select("low")) valid_6 (
    .D(Write5), .en(Write5), .Q(v5), .clk(CLK));  // open: clr
  Register #(.width(1), .trigger("rising"), .Select("low")) valid_7 (
    .D(Write6), .en(Write6), .Q(v6), .clk(CLK));  // open: clr
  Register #(.width(1), .trigger("rising"), .Select("low")) valid_8 (
    .D(Write7), .en(Write7), .Q(v7), .clk(CLK));  // open: clr
  Register #(.width(32), .trigger("rising"), .Select("low")) tag (
    .D(multiplexer_1_out), .en(Write0), .Q(tag_q), .clk(CLK));  // open: clr
  Register #(.width(32), .trigger("rising"), .Select("low")) tag_2 (
    .D(multiplexer_1_out), .en(Write1), .Q(tag_2_q), .clk(CLK));  // open: clr
  Register #(.width(32), .trigger("rising"), .Select("low")) tag_3 (
    .D(multiplexer_1_out), .en(Write2), .Q(tag_3_q), .clk(CLK));  // open: clr
  Register #(.width(32), .trigger("rising"), .Select("low")) tag_4 (
    .D(multiplexer_1_out), .en(Write3), .Q(tag_4_q), .clk(CLK));  // open: clr
  Register #(.width(32), .trigger("rising"), .Select("low")) tag_5 (
    .D(multiplexer_1_out), .en(Write4), .Q(tag_5_q), .clk(CLK));  // open: clr
  Register #(.width(32), .trigger("rising"), .Select("low")) tag_6 (
    .D(multiplexer_1_out), .en(Write5), .Q(tag_6_q), .clk(CLK));  // open: clr
  Register #(.width(32), .trigger("rising"), .Select("low")) tag_7 (
    .D(multiplexer_1_out), .en(Write6), .Q(tag_7_q), .clk(CLK));  // open: clr
  Register #(.width(32), .trigger("rising"), .Select("low")) tag_8 (
    .D(multiplexer_1_out), .en(Write7), .Q(tag_8_q), .clk(CLK));  // open: clr
  Comparator #(.width(32), .mode("unsigned")) comparator_1 (
    .a(tag_q), .b(BranchPC), .eq(comparator_1_eq));  // open: gt, lt
  Comparator #(.width(32), .mode("unsigned")) comparator_2 (
    .a(tag_q), .b(CurrentPC), .eq(comparator_2_eq));  // open: gt, lt
  Comparator #(.width(32), .mode("unsigned")) comparator_3 (
    .a(tag_2_q), .b(BranchPC), .eq(comparator_3_eq));  // open: gt, lt
  Comparator #(.width(32), .mode("unsigned")) comparator_4 (
    .a(tag_2_q), .b(CurrentPC), .eq(comparator_4_eq));  // open: gt, lt
  Comparator #(.width(32), .mode("unsigned")) comparator_5 (
    .a(tag_3_q), .b(BranchPC), .eq(comparator_5_eq));  // open: gt, lt
  Comparator #(.width(32), .mode("unsigned")) comparator_6 (
    .a(tag_3_q), .b(CurrentPC), .eq(comparator_6_eq));  // open: gt, lt
  Comparator #(.width(32), .mode("unsigned")) comparator_7 (
    .a(tag_4_q), .b(BranchPC), .eq(comparator_7_eq));  // open: gt, lt
  Comparator #(.width(32), .mode("unsigned")) comparator_8 (
    .a(tag_4_q), .b(CurrentPC), .eq(comparator_8_eq));  // open: gt, lt
  Comparator #(.width(32), .mode("unsigned")) comparator_9 (
    .a(tag_5_q), .b(BranchPC), .eq(comparator_9_eq));  // open: gt, lt
  Comparator #(.width(32), .mode("unsigned")) comparator_10 (
    .a(tag_5_q), .b(CurrentPC), .eq(comparator_10_eq));  // open: gt, lt
  Comparator #(.width(32), .mode("unsigned")) comparator_11 (
    .a(tag_6_q), .b(BranchPC), .eq(comparator_11_eq));  // open: gt, lt
  Comparator #(.width(32), .mode("unsigned")) comparator_12 (
    .a(tag_6_q), .b(CurrentPC), .eq(comparator_12_eq));  // open: gt, lt
  Comparator #(.width(32), .mode("unsigned")) comparator_13 (
    .a(tag_7_q), .b(BranchPC), .eq(comparator_13_eq));  // open: gt, lt
  Comparator #(.width(32), .mode("unsigned")) comparator_14 (
    .a(tag_7_q), .b(CurrentPC), .eq(comparator_14_eq));  // open: gt, lt
  Comparator #(.width(32), .mode("unsigned")) comparator_15 (
    .a(tag_8_q), .b(BranchPC), .eq(comparator_15_eq));  // open: gt, lt
  Comparator #(.width(32), .mode("unsigned")) comparator_16 (
    .a(tag_8_q), .b(CurrentPC), .eq(comparator_16_eq));  // open: gt, lt
  and and_1 (line0, v0, comparator_1_eq);
  and and_2 (line0p, v0, comparator_2_eq);
  and and_3 (line1, v1, comparator_3_eq);
  and and_4 (line1p, v1, comparator_4_eq);
  and and_5 (line2, v2, comparator_5_eq);
  and and_6 (line2p, v2, comparator_6_eq);
  and and_7 (line3, v3, comparator_7_eq);
  and and_8 (line3p, v3, comparator_8_eq);
  and and_9 (line4, v4, comparator_9_eq);
  and and_10 (line4p, v4, comparator_10_eq);
  and and_11 (line5, v5, comparator_11_eq);
  and and_12 (line5p, v5, comparator_12_eq);
  and and_13 (line6, v6, comparator_13_eq);
  and and_14 (line6p, v6, comparator_14_eq);
  and and_15 (line7, v7, comparator_15_eq);
  and and_16 (line7p, v7, comparator_16_eq);
  Register #(.width(32), .trigger("rising"), .Select("low")) BT (
    .D(BTin), .en(Write0), .Q(SlotData0), .clk(CLK));  // open: clr
  Register #(.width(32), .trigger("rising"), .Select("low")) BT_2 (
    .D(BTin), .en(Write1), .Q(SlotData1), .clk(CLK));  // open: clr
  Register #(.width(32), .trigger("rising"), .Select("low")) BT_3 (
    .D(BTin), .en(Write2), .Q(SlotData2), .clk(CLK));  // open: clr
  Register #(.width(32), .trigger("rising"), .Select("low")) BT_4 (
    .D(BTin), .en(Write3), .Q(SlotData3), .clk(CLK));  // open: clr
  Register #(.width(32), .trigger("rising"), .Select("low")) BT_5 (
    .D(BTin), .en(Write4), .Q(SlotData4), .clk(CLK));  // open: clr
  Register #(.width(32), .trigger("rising"), .Select("low")) BT_6 (
    .D(BTin), .en(Write5), .Q(SlotData5), .clk(CLK));  // open: clr
  Register #(.width(32), .trigger("rising"), .Select("low")) BT_7 (
    .D(BTin), .en(Write6), .Q(SlotData6), .clk(CLK));  // open: clr
  Register #(.width(32), .trigger("rising"), .Select("low")) BT_8 (
    .D(BTin), .en(Write7), .Q(SlotData7), .clk(CLK));  // open: clr
  or or_1 (or_1_out, Write0, line0p, line0);
  or or_2 (or_2_out, Write1, line1p, line1);
  or or_3 (or_3_out, Write2, line2p, line2);
  or or_4 (or_4_out, Write3, line3p, line3);
  or or_5 (or_5_out, Write4, line4p, line4);
  or or_6 (or_6_out, Write5, line5p, line5);
  or or_7 (or_7_out, Write6, line6p, line6);
  or or_8 (or_8_out, Write7, line7p, line7);
  D_Flip_Flop #(.trigger("rising"), .Pre_Clr_Positions("ABOVE_BELOW"), .NegatePresetClear("false"), .enable("false"), .NewFFLayout("false")) d_ff_1 (
    .clk(CLK), .D(or_1_out), .Q(d_ff_1_q));  // open: Qn, preset, reset
  D_Flip_Flop #(.trigger("rising"), .Pre_Clr_Positions("ABOVE_BELOW"), .NegatePresetClear("false"), .enable("false"), .NewFFLayout("false")) d_ff_2 (
    .clk(CLK), .D(or_2_out), .Q(d_ff_2_q));  // open: Qn, preset, reset
  D_Flip_Flop #(.trigger("rising"), .Pre_Clr_Positions("ABOVE_BELOW"), .NegatePresetClear("false"), .enable("false"), .NewFFLayout("false")) d_ff_3 (
    .clk(CLK), .D(or_3_out), .Q(d_ff_3_q));  // open: Qn, preset, reset
  D_Flip_Flop #(.trigger("rising"), .Pre_Clr_Positions("ABOVE_BELOW"), .NegatePresetClear("false"), .enable("false"), .NewFFLayout("false")) d_ff_4 (
    .clk(CLK), .D(or_4_out), .Q(d_ff_4_q));  // open: Qn, preset, reset
  D_Flip_Flop #(.trigger("rising"), .Pre_Clr_Positions("ABOVE_BELOW"), .NegatePresetClear("false"), .enable("false"), .NewFFLayout("false")) d_ff_5 (
    .clk(CLK), .D(or_5_out), .Q(d_ff_5_q));  // open: Qn, preset, reset
  D_Flip_Flop #(.trigger("rising"), .Pre_Clr_Positions("ABOVE_BELOW"), .NegatePresetClear("false"), .enable("false"), .NewFFLayout("false")) d_ff_6 (
    .clk(CLK), .D(or_6_out), .Q(d_ff_6_q));  // open: Qn, preset, reset
  D_Flip_Flop #(.trigger("rising"), .Pre_Clr_Positions("ABOVE_BELOW"), .NegatePresetClear("false"), .enable("false"), .NewFFLayout("false")) d_ff_7 (
    .clk(CLK), .D(or_7_out), .Q(d_ff_7_q));  // open: Qn, preset, reset
  D_Flip_Flop #(.trigger("rising"), .Pre_Clr_Positions("ABOVE_BELOW"), .NegatePresetClear("false"), .enable("false"), .NewFFLayout("false")) d_ff_8 (
    .clk(CLK), .D(or_8_out), .Q(d_ff_8_q));  // open: Qn, preset, reset
  Counter #(.width(16), .max('hffff), .ongoal("wrap"), .trigger("rising"), .behavior("new")) cnt (
    .count(v0), .Q(c0), .clk(CLK), .clr(d_ff_1_q));  // open: load, D, carry, preset, down
  Counter #(.width(16), .max('hffff), .ongoal("wrap"), .trigger("rising"), .behavior("new")) cnt_2 (
    .count(v1), .Q(c1), .clk(CLK), .clr(d_ff_2_q));  // open: load, D, carry, preset, down
  Counter #(.width(16), .max('hffff), .ongoal("wrap"), .trigger("rising"), .behavior("new")) cnt_3 (
    .count(v2), .Q(c2), .clk(CLK), .clr(d_ff_3_q));  // open: load, D, carry, preset, down
  Counter #(.width(16), .max('hffff), .ongoal("wrap"), .trigger("rising"), .behavior("new")) cnt_4 (
    .count(v3), .Q(c3), .clk(CLK), .clr(d_ff_4_q));  // open: load, D, carry, preset, down
  Counter #(.width(16), .max('hffff), .ongoal("wrap"), .trigger("rising"), .behavior("new")) cnt_5 (
    .count(v4), .Q(c4), .clk(CLK), .clr(d_ff_5_q));  // open: load, D, carry, preset, down
  Counter #(.width(16), .max('hffff), .ongoal("wrap"), .trigger("rising"), .behavior("new")) cnt_6 (
    .count(v5), .Q(c5), .clk(CLK), .clr(d_ff_6_q));  // open: load, D, carry, preset, down
  Counter #(.width(16), .max('hffff), .ongoal("wrap"), .trigger("rising"), .behavior("new")) cnt_7 (
    .count(v6), .Q(c6), .clk(CLK), .clr(d_ff_7_q));  // open: load, D, carry, preset, down
  Counter #(.width(16), .max('hffff), .ongoal("wrap"), .trigger("rising"), .behavior("new")) cnt_8 (
    .count(v7), .Q(c7), .clk(CLK), .clr(d_ff_8_q));  // open: load, D, carry, preset, down
  and and_17 (and_17_out, J, line0);
  and and_18 (and_18_out, line0, Branch);
  and and_19 (and_19_out, J, line1);
  and and_20 (and_20_out, line1, Branch);
  and and_21 (and_21_out, J, line2);
  and and_22 (and_22_out, line2, Branch);
  and and_23 (and_23_out, J, line3);
  and and_24 (and_24_out, line3, Branch);
  and and_25 (and_25_out, J, line4);
  and and_26 (and_26_out, line4, Branch);
  and and_27 (and_27_out, J, line5);
  and and_28 (and_28_out, line5, Branch);
  and and_29 (and_29_out, J, line6);
  and and_30 (and_30_out, line6, Branch);
  and and_31 (and_31_out, J, line7);
  and and_32 (and_32_out, line7, Branch);
  Predict predict_1 (.J(and_17_out), .CLK(CLK), .PreSet(Write0), .Predict(PredictJmp0), .Branch(and_18_out));
  Predict predict_2 (.J(and_19_out), .CLK(CLK), .PreSet(Write1), .Predict(PredictJmp1), .Branch(and_20_out));
  Predict predict_3 (.J(and_21_out), .CLK(CLK), .PreSet(Write2), .Predict(PredictJmp2), .Branch(and_22_out));
  Predict predict_4 (.J(and_23_out), .CLK(CLK), .PreSet(Write3), .Predict(PredictJmp3), .Branch(and_24_out));
  Predict predict_5 (.J(and_25_out), .CLK(CLK), .PreSet(Write4), .Predict(PredictJmp4), .Branch(and_26_out));
  Predict predict_6 (.J(and_27_out), .CLK(CLK), .PreSet(Write5), .Predict(PredictJmp5), .Branch(and_28_out));
  Predict predict_7 (.J(and_29_out), .CLK(CLK), .PreSet(Write6), .Predict(PredictJmp6), .Branch(and_30_out));
  Predict predict_8 (.J(and_31_out), .CLK(CLK), .PreSet(Write7), .Predict(PredictJmp7), .Branch(and_32_out));
  not not_1 (not_1_out, v0);
  not not_2 (not_2_out, v1);
  not not_3 (not_3_out, v2);
  not not_4 (not_4_out, v3);
  not not_5 (not_5_out, v4);
  not not_6 (not_6_out, v5);
  not not_7 (not_7_out, v6);
  not not_8 (not_8_out, v7);
  Multiplexer #(.select(3), .width(32), .disabled("Z"), .enable("false")) multiplexer_2 (
    .in0(SlotData0), .in1(SlotData1), .in2(SlotData2), .in3(SlotData3), .in4(SlotData4), .in5(SlotData5),
    .in6(SlotData6), .in7(SlotData7), .out(multiplexer_2_out), .sel(priority_encoder_1_out));
  Priority_Encoder #(.select(3), .disabled(0)) priority_encoder_1 (
    .in0(line0p), .in1(line1p), .in2(line2p), .in3(line3p), .in4(line4p), .in5(line5p), .in6(line6p),
    .in7(line7p), .out(priority_encoder_1_out), .en_out(priority_encoder_1_en_out), .en_in(1'b1));  // open: gs
  Multiplexer #(.select(3), .width(1), .disabled("Z"), .enable("false")) multiplexer_3 (
    .in0(PredictJmp0), .in1(PredictJmp1), .in2(PredictJmp2), .in3(PredictJmp3), .in4(PredictJmp4),
    .in5(PredictJmp5), .in6(PredictJmp6), .in7(PredictJmp7), .out(multiplexer_3_out),
    .sel(priority_encoder_1_out));
  Demultiplexer #(.select(3), .width(1), .tristate("false"), .disabled("Z"), .enable("false")) demultiplexer_1 (
    .out0(Write0), .out1(Write1), .out2(Write2), .out3(Write3), .out4(Write4), .out5(Write5), .out6(Write6),
    .out7(Write7), .in(and_33_out), .sel(multiplexer_4_out));
  and and_33 (and_33_out, Miss, J, Branch);
  Multiplexer #(.select(1), .width(3), .disabled("Z"), .enable("false")) multiplexer_4 (
    .in0(emptyRow), .in1(obsRow), .out(multiplexer_4_out), .sel(full));
  Priority_Encoder #(.select(3), .disabled("Z")) priority_encoder_2 (
    .in0(not_1_out), .in1(not_2_out), .in2(not_3_out), .in3(not_4_out), .in4(not_5_out), .in5(not_6_out),
    .in6(not_7_out), .in7(not_8_out), .out(emptyRow), .en_out(full), .en_in(1'b1));  // open: gs
  Max3Merge max3merge_1 (
    .Y(c0), .X(c1), .Y_num(3'b000), .X_num(3'b001), .MAX(max3merge_1_max), .Max_num(max3merge_1_max_num));
  Max3Merge max3merge_2 (
    .Y(c2), .X(c3), .Y_num(3'b010), .X_num(3'b011), .MAX(max3merge_2_max), .Max_num(max3merge_2_max_num));
  Max3Merge max3merge_3 (
    .Y(c4), .X(c5), .Y_num(3'b100), .X_num(3'b101), .MAX(max3merge_3_max), .Max_num(max3merge_3_max_num));
  Max3Merge max3merge_4 (
    .Y(c6), .X(c7), .Y_num(3'b110), .X_num(3'b111), .MAX(max3merge_4_max), .Max_num(max3merge_4_max_num));
  Multiplexer #(.select(1), .width(32), .disabled("Z"), .enable("false")) multiplexer_5 (
    .in0(multiplexer_2_out), .in1({32{1'b0}}), .out(BTout), .sel(priority_encoder_1_en_out));
  not not_9 (Hit, priority_encoder_1_en_out);
  Multiplexer #(.select(1), .width(1), .disabled("Z"), .enable("false")) multiplexer_6 (
    .in0(multiplexer_3_out), .in1(1'b0), .out(PredictJmp), .sel(priority_encoder_1_en_out));
  Max3Merge max3merge_5 (
    .Y(max3merge_1_max), .X(max3merge_2_max), .Y_num(max3merge_1_max_num), .X_num(max3merge_2_max_num),
    .MAX(max3merge_5_max), .Max_num(max3merge_5_max_num));
  Max3Merge max3merge_6 (
    .Y(max3merge_3_max), .X(max3merge_4_max), .Y_num(max3merge_3_max_num), .X_num(max3merge_4_max_num),
    .MAX(max3merge_6_max), .Max_num(max3merge_6_max_num));
  or or_9 (or_9_out, line0, line2, line1, line3, line4, line5, line6, line7);
  Max3Merge max3merge_7 (
    .Y(max3merge_5_max), .X(max3merge_6_max), .Y_num(max3merge_5_max_num), .X_num(max3merge_6_max_num),
    .Max_num(obsRow));  // open: MAX
  not not_10 (Miss, or_9_out);

  // Notes on the sheet:
  //   满了就选淘汰行，没满就选空行
endmodule

// Max3
module Max3Merge (
  input  [15:0] Y,
  input  [15:0] X,
  input  [2:0] Y_num,
  input  [2:0] X_num,
  output [15:0] MAX,
  output [2:0] Max_num
);

  wire comparator_1_eq, comparator_1_gt, or_1_out;

  Multiplexer #(.select(1), .width(16), .disabled("Z"), .enable("false")) multiplexer_1 (
    .in0(Y), .in1(X), .out(MAX), .sel(or_1_out));
  Comparator #(.width(16), .mode("unsigned")) comparator_1 (
    .a(X), .b(Y), .gt(comparator_1_gt), .eq(comparator_1_eq));  // open: lt
  or or_1 (or_1_out, comparator_1_gt, comparator_1_eq);
  Multiplexer #(.select(1), .width(3), .disabled("Z"), .enable("false")) multiplexer_2 (
    .in0(Y_num), .in1(X_num), .out(Max_num), .sel(or_1_out));
endmodule

module Predict (
  input  PreSet,
  input  Branch,
  input  CLK,
  input  J,
  output Predict
);

  wire and_1_out, and_2_out, and_3_out, and_4_out, decoder_1_out2, decoder_1_out3, multiplexer_1_out,
       multiplexer_2_out, not_1_out, not_2_out, not_3_out, not_4_out, not_5_out, or_1_out, or_2_out, or_3_out;
  wire [1:0] d_ff_2_q;

  not not_1 (not_1_out, d_ff_2_q[0]);
  not not_2 (not_2_out, J);
  not not_3 (not_3_out, d_ff_2_q[0]);
  not not_4 (not_4_out, d_ff_2_q[1]);
  not not_5 (not_5_out, d_ff_2_q[0]);
  and and_1 (and_1_out, d_ff_2_q[1], not_1_out);
  and and_2 (and_2_out, J, d_ff_2_q[0]);
  and and_3 (and_3_out, not_2_out, d_ff_2_q[1], not_3_out);
  and and_4 (and_4_out, J, not_4_out, not_5_out);
  or or_1 (or_1_out, and_1_out, and_2_out);
  or or_2 (or_2_out, and_3_out, and_4_out);
  or or_3 (or_3_out, PreSet, Branch);
  Multiplexer #(.select(1), .width(1), .disabled("Z"), .enable("false")) multiplexer_1 (
    .in0(or_1_out), .in1(1'b1), .out(multiplexer_1_out), .sel(PreSet));
  Multiplexer #(.select(1), .width(1), .disabled("Z"), .enable("false")) multiplexer_2 (
    .in0(or_2_out), .in1(1'b0), .out(multiplexer_2_out), .sel(PreSet));
  D_Flip_Flop #(.trigger("rising"), .Pre_Clr_Positions("ABOVE_BELOW"), .NegatePresetClear("false"), .enable("true"), .NewFFLayout("false")) d_ff_1 (
    .clk(CLK), .D(multiplexer_1_out), .Q(d_ff_2_q[1]), .en(or_3_out));  // open: Qn, preset, reset
  D_Flip_Flop #(.trigger("rising"), .Pre_Clr_Positions("ABOVE_BELOW"), .NegatePresetClear("false"), .enable("true"), .NewFFLayout("false")) d_ff_2 (
    .clk(CLK), .D(multiplexer_2_out), .Q(d_ff_2_q[0]), .en(or_3_out));  // open: Qn, preset, reset
  Decoder #(.select(2), .tristate("false"), .disabled("Z"), .enable("false")) decoder_1 (
    .out2(decoder_1_out2), .out3(decoder_1_out3), .sel(d_ff_2_q));  // open: out0, out1
  or or_4 (Predict, decoder_1_out2, decoder_1_out3);
endmodule
